// Logisim project ALU.circ as structural Verilog: 1 circuit, main circuit main
module main (
  input  [5:0] in_1,
  input  [7:0] in_2,
  input  [7:0] in_3,
  input  in_4
);

  wire pull_resistor_9_node, pull_resistor_10_node, pull_resistor_11_node, pull_resistor_12_node,
       pull_resistor_13_node, pull_resistor_14_node, pull_resistor_17_node, pull_resistor_18_node,
       pull_resistor_21_node, pull_resistor_25_node, pull_resistor_26_node, pull_resistor_27_node,
       pull_resistor_31_node, pull_resistor_32_node, pull_resistor_35_node, pull_resistor_54_node,
       pull_resistor_55_node, pull_resistor_56_node, pull_resistor_58_node, pull_resistor_62_node,
       pull_resistor_63_node, pull_resistor_66_node, pull_resistor_71_node, pull_resistor_83_node,
       pull_resistor_84_node, pull_resistor_86_node, pull_resistor_87_node, pull_resistor_89_node,
       pull_resistor_97_node, pull_resistor_99_node, pull_resistor_100_node, pull_resistor_101_node,
       pull_resistor_109_node, pull_resistor_119_node, pull_resistor_121_node, pull_resistor_122_node,
       pull_resistor_124_node, pull_resistor_125_node, pull_resistor_126_node, pull_resistor_127_node,
       pull_resistor_128_node, pull_resistor_129_node, pull_resistor_130_node, pull_resistor_131_node,
       pull_resistor_132_node, transistor_5_out, transistor_7_out, transistor_9_out, transistor_10_out,
       transistor_11_out, transistor_15_out, transistor_16_out, transistor_18_out, transistor_19_out,
       transistor_20_out, transistor_21_out, transistor_22_out, transistor_23_out, transistor_27_out,
       transistor_29_out, transistor_30_out, transistor_31_out, transistor_32_out, transistor_33_out,
       transistor_34_out, transistor_35_out, transistor_39_out, transistor_40_out, transistor_42_out,
       transistor_43_out, transistor_44_out, transistor_45_out, transistor_46_out, transistor_47_out,
       transistor_48_out, transistor_50_out, transistor_51_out, transistor_52_out, transistor_53_out,
       transistor_54_out, transistor_55_out, transistor_56_out, transistor_57_out, transistor_58_out,
       transistor_59_out, transistor_60_out, transistor_61_out, transistor_62_out, transistor_63_out,
       transistor_64_out, transistor_65_out, transistor_71_out, transistor_72_out, transistor_74_out,
       transistor_75_out, transistor_76_out, transistor_77_out, transistor_78_out, transistor_83_out,
       transistor_84_out, transistor_86_out, transistor_87_out, transistor_88_out, transistor_89_out,
       transistor_92_out, transistor_95_out, transistor_96_out, transistor_97_out, transistor_98_out,
       transistor_99_out, transistor_100_out, transistor_101_out, transistor_104_out, transistor_106_out,
       transistor_107_out, transistor_108_out, transistor_109_out, transistor_110_out, transistor_111_out,
       transistor_112_out, transistor_115_out, transistor_119_out, transistor_121_out, transistor_122_out,
       transistor_124_out, transistor_125_out, transistor_126_out, transistor_127_out, transistor_128_out,
       transistor_129_out, transistor_130_out, transistor_131_out, transistor_132_out, transistor_134_out,
       transistor_137_out, transistor_138_out, transistor_139_out, transistor_141_out, transistor_142_out,
       transistor_143_out, transistor_144_out, transistor_145_out, transistor_146_out, transistor_148_out,
       transistor_149_out, transistor_151_out, transistor_152_out, transistor_156_out, transistor_157_out,
       transistor_160_out, transistor_161_out, transistor_162_out, transistor_163_out, transistor_165_out,
       transistor_166_out, transistor_167_out, transistor_168_out, transistor_169_out, transistor_171_out,
       transistor_172_out, transistor_173_out, transistor_174_out, transistor_175_out, transistor_176_out,
       transistor_177_out, transistor_178_out, transistor_180_out, transistor_181_out, transistor_187_out,
       transistor_188_out, transistor_193_out, transistor_195_out, transistor_197_out, transistor_199_out,
       transistor_201_out, transistor_203_out, transistor_206_out, transistor_207_out, transistor_210_out,
       transistor_211_out, transistor_214_out, transistor_215_out, transistor_218_out, transistor_219_out,
       transistor_222_out, transistor_223_out, transistor_226_out, transistor_227_out, transistor_230_out,
       transistor_231_out, transistor_234_out, transistor_235_out, transistor_238_out, transistor_239_out,
       transistor_242_out, transistor_243_out, transistor_246_out, transistor_247_out, transistor_250_out,
       transistor_251_out, transistor_254_out, transistor_255_out, transistor_258_out, transistor_259_out,
       transistor_262_out, transistor_263_out, transistor_266_out, transistor_267_out, transistor_270_out,
       transistor_271_out, transistor_274_out, transistor_275_out, transistor_277_out, transistor_279_out,
       transistor_281_out, transistor_283_out, transistor_285_out;
  wire [3:0] pull_resistor_3_node, pull_resistor_5_node;

  Hex_Digit_Display hex_digit_display_1 (.value(pull_resistor_5_node));  // open: dp
  Hex_Digit_Display hex_digit_display_2 (.value(in_3[7:4]));  // open: dp
  Hex_Digit_Display hex_digit_display_3 (.value(pull_resistor_3_node));  // open: dp
  Pull_Resistor #(.pull(1)) pull_resistor_1 (.node(pull_resistor_3_node[3]));
  Pull_Resistor #(.pull(1)) pull_resistor_2 (.node(pull_resistor_3_node[2]));
  Pull_Resistor #(.pull(1)) pull_resistor_3 (.node(pull_resistor_3_node[0]));
  Pull_Resistor #(.pull(1)) pull_resistor_4 (.node(pull_resistor_5_node[2]));
  Pull_Resistor #(.pull(1)) pull_resistor_5 (.node(pull_resistor_5_node[0]));
  Pull_Resistor #(.pull(1)) pull_resistor_6 (.node(pull_resistor_5_node[1]));
  Pull_Resistor #(.pull(1)) pull_resistor_7 (.node(pull_resistor_3_node[1]));
  Hex_Digit_Display hex_digit_display_4 (.value(in_2[7:4]));  // open: dp
  Hex_Digit_Display hex_digit_display_5 (.value(in_3[3:0]));  // open: dp
  Pull_Resistor #(.pull(1)) pull_resistor_8 (.node(pull_resistor_5_node[3]));
  Hex_Digit_Display hex_digit_display_6 (.value(in_2[3:0]));  // open: dp
  Pull_Resistor #(.pull(1)) pull_resistor_9 (.node(pull_resistor_9_node));
  Transistor #(.\type ("n")) transistor_1 (.in(1'b0), .out(pull_resistor_9_node), .gate(in_3[7]));
  Pull_Resistor #(.pull(1)) pull_resistor_10 (.node(pull_resistor_10_node));
  Transistor #(.\type ("n")) transistor_2 (.in(1'b0), .out(pull_resistor_10_node), .gate(in_2[7]));
  Pull_Resistor #(.pull(1)) pull_resistor_11 (.node(pull_resistor_11_node));
  Transistor #(.\type ("n")) transistor_3 (.in(1'b0), .out(pull_resistor_11_node), .gate(pull_resistor_17_node));
  Pull_Resistor #(.pull(1)) pull_resistor_12 (.node(pull_resistor_12_node));
  Transistor #(.\type ("n"), .gate("br")) transistor_4 (
    .in(transistor_15_out), .out(pull_resistor_12_node), .gate(transistor_16_out));
  Transistor #(.\type ("n"), .gate("br")) transistor_5 (
    .in(1'b0), .out(transistor_5_out), .gate(pull_resistor_12_node));
  Pull_Resistor #(.pull(1)) pull_resistor_13 (.node(pull_resistor_13_node));
  Transistor #(.\type ("n"), .gate("br")) transistor_6 (
    .in(transistor_5_out), .out(pull_resistor_13_node), .gate(transistor_18_out));
  Transistor #(.\type ("n"), .gate("br")) transistor_7 (.in(1'b0), .out(transistor_7_out), .gate(in_4));
  Pull_Resistor #(.pull(1)) pull_resistor_14 (.node(pull_resistor_14_node));
  Transistor #(.\type ("n"), .gate("br")) transistor_8 (
    .in(transistor_7_out), .out(pull_resistor_14_node), .gate(transistor_19_out));
  Transistor #(.\type ("n"), .gate("br")) transistor_9 (
    .in(transistor_20_out), .out(transistor_9_out), .gate(transistor_16_out));
  Pull_Resistor #(.pull(1)) pull_resistor_15 (.node(transistor_9_out));
  Transistor #(.\type ("n"), .gate("br")) transistor_10 (
    .in(1'b0), .out(transistor_10_out), .gate(pull_resistor_14_node));
  Transistor #(.\type ("n"), .gate("br")) transistor_11 (
    .in(transistor_10_out), .out(transistor_11_out), .gate(transistor_21_out));
  Pull_Resistor #(.pull(1)) pull_resistor_16 (.node(transistor_11_out));
  Pull_Resistor #(.pull(1)) pull_resistor_17 (.node(pull_resistor_17_node));
  Transistor #(.\type ("n")) transistor_12 (
    .in(transistor_22_out), .out(pull_resistor_17_node), .gate(pull_resistor_5_node[3]));
  Transistor #(.\type ("n")) transistor_13 (
    .in(transistor_23_out), .out(pull_resistor_17_node), .gate(pull_resistor_31_node));
  Pull_Resistor #(.pull(1)) pull_resistor_18 (.node(pull_resistor_18_node));
  Transistor #(.\type ("n")) transistor_14 (.in(1'b0), .out(pull_resistor_18_node), .gate(in_2[0]));
  Transistor #(.\type ("n"), .gate("br")) transistor_15 (.in(1'b0), .out(transistor_15_out), .gate(in_2[0]));
  Pull_Resistor #(.pull(1)) pull_resistor_19 (.node(transistor_15_out));
  Transistor #(.\type ("n"), .gate("br")) transistor_16 (
    .in(transistor_15_out), .out(transistor_16_out), .gate(in_3[0]));
  Pull_Resistor #(.pull(1)) pull_resistor_20 (.node(transistor_16_out));
  Pull_Resistor #(.pull(1)) pull_resistor_21 (.node(pull_resistor_21_node));
  Transistor #(.\type ("n"), .gate("br")) transistor_17 (
    .in(1'b0), .out(pull_resistor_21_node), .gate(transistor_16_out));
  Transistor #(.\type ("n"), .gate("br")) transistor_18 (
    .in(pull_resistor_21_node), .out(transistor_18_out), .gate(in_3[0]));
  Pull_Resistor #(.pull(1)) pull_resistor_22 (.node(transistor_18_out));
  Transistor #(.\type ("n"), .gate("br")) transistor_19 (
    .in(transistor_7_out), .out(transistor_19_out), .gate(pull_resistor_13_node));
  Pull_Resistor #(.pull(1)) pull_resistor_23 (.node(transistor_19_out));
  Transistor #(.\type ("n"), .gate("br")) transistor_20 (.in(1'b0), .out(transistor_20_out), .gate(transistor_19_out));
  Transistor #(.\type ("n"), .gate("br")) transistor_21 (
    .in(transistor_20_out), .out(transistor_21_out), .gate(pull_resistor_13_node));
  Pull_Resistor #(.pull(1)) pull_resistor_24 (.node(transistor_21_out));
  Transistor #(.\type ("n")) transistor_22 (
    .in(transistor_34_out), .out(transistor_22_out), .gate(pull_resistor_9_node));
  Transistor #(.\type ("n")) transistor_23 (.in(transistor_35_out), .out(transistor_23_out), .gate(in_3[7]));
  Pull_Resistor #(.pull(1)) pull_resistor_25 (.node(pull_resistor_25_node));
  Transistor #(.\type ("n")) transistor_24 (.in(1'b0), .out(pull_resistor_25_node), .gate(pull_resistor_18_node));
  Transistor #(.\type ("n")) transistor_25 (.in(1'b0), .out(pull_resistor_18_node), .gate(in_3[0]));
  Pull_Resistor #(.pull(1)) pull_resistor_26 (.node(pull_resistor_26_node));
  Transistor #(.\type ("n"), .gate("br")) transistor_26 (
    .in(transistor_39_out), .out(pull_resistor_26_node), .gate(transistor_40_out));
  Transistor #(.\type ("n"), .gate("br")) transistor_27 (
    .in(1'b0), .out(transistor_27_out), .gate(pull_resistor_26_node));
  Pull_Resistor #(.pull(1)) pull_resistor_27 (.node(pull_resistor_27_node));
  Transistor #(.\type ("n"), .gate("br")) transistor_28 (
    .in(transistor_27_out), .out(pull_resistor_27_node), .gate(transistor_42_out));
  Transistor #(.\type ("n"), .gate("br")) transistor_29 (.in(1'b0), .out(transistor_29_out), .gate(transistor_9_out));
  Transistor #(.\type ("n"), .gate("br")) transistor_30 (
    .in(transistor_29_out), .out(transistor_30_out), .gate(transistor_43_out));
  Pull_Resistor #(.pull(1)) pull_resistor_28 (.node(transistor_30_out));
  Transistor #(.\type ("n"), .gate("br")) transistor_31 (
    .in(transistor_44_out), .out(transistor_31_out), .gate(transistor_40_out));
  Pull_Resistor #(.pull(1)) pull_resistor_29 (.node(transistor_31_out));
  Transistor #(.\type ("n"), .gate("br")) transistor_32 (.in(1'b0), .out(transistor_32_out), .gate(transistor_30_out));
  Transistor #(.\type ("n"), .gate("br")) transistor_33 (
    .in(transistor_32_out), .out(transistor_33_out), .gate(transistor_45_out));
  Pull_Resistor #(.pull(1)) pull_resistor_30 (.node(transistor_33_out));
  Transistor #(.\type ("n")) transistor_34 (.in(1'b0), .out(transistor_34_out), .gate(pull_resistor_10_node));
  Transistor #(.\type ("n")) transistor_35 (.in(1'b0), .out(transistor_35_out), .gate(in_2[7]));
  Pull_Resistor #(.pull(1)) pull_resistor_31 (.node(pull_resistor_31_node));
  Transistor #(.\type ("n")) transistor_36 (.in(1'b0), .out(pull_resistor_31_node), .gate(pull_resistor_5_node[3]));
  Pull_Resistor #(.pull(1)) pull_resistor_32 (.node(pull_resistor_32_node));
  Transistor #(.\type ("n")) transistor_37 (.in(1'b0), .out(pull_resistor_32_node), .gate(in_3[1]));
  Transistor #(.\type ("n")) transistor_38 (.in(1'b0), .out(pull_resistor_32_node), .gate(in_2[1]));
  Transistor #(.\type ("n"), .gate("br")) transistor_39 (.in(1'b0), .out(transistor_39_out), .gate(in_2[1]));
  Pull_Resistor #(.pull(1)) pull_resistor_33 (.node(transistor_39_out));
  Transistor #(.\type ("n"), .gate("br")) transistor_40 (
    .in(transistor_39_out), .out(transistor_40_out), .gate(in_3[1]));
  Pull_Resistor #(.pull(1)) pull_resistor_34 (.node(transistor_40_out));
  Pull_Resistor #(.pull(1)) pull_resistor_35 (.node(pull_resistor_35_node));
  Transistor #(.\type ("n"), .gate("br")) transistor_41 (
    .in(1'b0), .out(pull_resistor_35_node), .gate(transistor_40_out));
  Transistor #(.\type ("n"), .gate("br")) transistor_42 (
    .in(pull_resistor_35_node), .out(transistor_42_out), .gate(in_3[1]));
  Pull_Resistor #(.pull(1)) pull_resistor_36 (.node(transistor_42_out));
  Transistor #(.\type ("n"), .gate("br")) transistor_43 (
    .in(transistor_29_out), .out(transistor_43_out), .gate(pull_resistor_27_node));
  Pull_Resistor #(.pull(1)) pull_resistor_37 (.node(transistor_43_out));
  Transistor #(.\type ("n"), .gate("br")) transistor_44 (.in(1'b0), .out(transistor_44_out), .gate(transistor_43_out));
  Transistor #(.\type ("n"), .gate("br")) transistor_45 (
    .in(transistor_44_out), .out(transistor_45_out), .gate(pull_resistor_27_node));
  Pull_Resistor #(.pull(1)) pull_resistor_38 (.node(transistor_45_out));
  Transistor #(.\type ("n")) transistor_46 (.in(1'b0), .out(transistor_46_out), .gate(pull_resistor_32_node));
  Pull_Resistor #(.pull(1)) pull_resistor_39 (.node(transistor_46_out));
  Transistor #(.\type ("n")) transistor_47 (.in(1'b0), .out(transistor_47_out), .gate(in_2[2]));
  Transistor #(.\type ("n")) transistor_48 (.in(1'b0), .out(transistor_48_out), .gate(transistor_47_out));
  Pull_Resistor #(.pull(1)) pull_resistor_40 (.node(transistor_48_out));
  Transistor #(.\type ("n")) transistor_49 (.in(1'b0), .out(transistor_47_out), .gate(in_3[2]));
  Pull_Resistor #(.pull(1)) pull_resistor_41 (.node(transistor_47_out));
  Transistor #(.\type ("n"), .gate("br")) transistor_50 (
    .in(transistor_59_out), .out(transistor_50_out), .gate(transistor_60_out));
  Pull_Resistor #(.pull(1)) pull_resistor_42 (.node(transistor_50_out));
  Transistor #(.\type ("n"), .gate("br")) transistor_51 (.in(1'b0), .out(transistor_51_out), .gate(transistor_50_out));
  Transistor #(.\type ("n"), .gate("br")) transistor_52 (
    .in(transistor_51_out), .out(transistor_52_out), .gate(transistor_62_out));
  Pull_Resistor #(.pull(1)) pull_resistor_43 (.node(transistor_52_out));
  Transistor #(.\type ("n"), .gate("br")) transistor_53 (.in(1'b0), .out(transistor_53_out), .gate(transistor_31_out));
  Transistor #(.\type ("n"), .gate("br")) transistor_54 (
    .in(transistor_53_out), .out(transistor_54_out), .gate(transistor_63_out));
  Pull_Resistor #(.pull(1)) pull_resistor_44 (.node(transistor_54_out));
  Transistor #(.\type ("n"), .gate("br")) transistor_55 (
    .in(transistor_64_out), .out(transistor_55_out), .gate(transistor_60_out));
  Pull_Resistor #(.pull(1)) pull_resistor_45 (.node(transistor_55_out));
  Transistor #(.\type ("n"), .gate("br")) transistor_56 (.in(1'b0), .out(transistor_56_out), .gate(transistor_54_out));
  Transistor #(.\type ("n"), .gate("br")) transistor_57 (
    .in(transistor_56_out), .out(transistor_57_out), .gate(transistor_65_out));
  Pull_Resistor #(.pull(1)) pull_resistor_46 (.node(transistor_57_out));
  Transistor #(.\type ("n")) transistor_58 (.in(1'b0), .out(transistor_58_out), .gate(in_2[3]));
  Pull_Resistor #(.pull(1)) pull_resistor_47 (.node(transistor_58_out));
  Transistor #(.\type ("n"), .gate("br")) transistor_59 (.in(1'b0), .out(transistor_59_out), .gate(in_2[2]));
  Pull_Resistor #(.pull(1)) pull_resistor_48 (.node(transistor_59_out));
  Transistor #(.\type ("n"), .gate("br")) transistor_60 (
    .in(transistor_59_out), .out(transistor_60_out), .gate(in_3[2]));
  Pull_Resistor #(.pull(1)) pull_resistor_49 (.node(transistor_60_out));
  Transistor #(.\type ("n"), .gate("br")) transistor_61 (.in(1'b0), .out(transistor_61_out), .gate(transistor_60_out));
  Pull_Resistor #(.pull(1)) pull_resistor_50 (.node(transistor_61_out));
  Transistor #(.\type ("n"), .gate("br")) transistor_62 (
    .in(transistor_61_out), .out(transistor_62_out), .gate(in_3[2]));
  Pull_Resistor #(.pull(1)) pull_resistor_51 (.node(transistor_62_out));
  Transistor #(.\type ("n"), .gate("br")) transistor_63 (
    .in(transistor_53_out), .out(transistor_63_out), .gate(transistor_52_out));
  Pull_Resistor #(.pull(1)) pull_resistor_52 (.node(transistor_63_out));
  Transistor #(.\type ("n"), .gate("br")) transistor_64 (.in(1'b0), .out(transistor_64_out), .gate(transistor_63_out));
  Transistor #(.\type ("n"), .gate("br")) transistor_65 (
    .in(transistor_64_out), .out(transistor_65_out), .gate(transistor_52_out));
  Pull_Resistor #(.pull(1)) pull_resistor_53 (.node(transistor_65_out));
  Pull_Resistor #(.pull(1)) pull_resistor_54 (.node(pull_resistor_54_node));
  Pull_Resistor #(.pull(1)) pull_resistor_55 (.node(pull_resistor_55_node));
  Transistor #(.\type ("n")) transistor_66 (.in(1'b0), .out(transistor_58_out), .gate(in_3[3]));
  Transistor #(.\type ("n")) transistor_67 (.in(1'b0), .out(pull_resistor_55_node), .gate(transistor_58_out));
  Transistor #(.\type ("n")) transistor_68 (.in(1'b0), .out(pull_resistor_54_node), .gate(pull_resistor_3_node[0]));
  Pull_Resistor #(.pull(1)) pull_resistor_56 (.node(pull_resistor_56_node));
  Transistor #(.\type ("n")) transistor_69 (.in(1'b0), .out(pull_resistor_56_node), .gate(in_2[4]));
  Transistor #(.\type ("n")) transistor_70 (.in(1'b0), .out(pull_resistor_56_node), .gate(in_3[4]));
  Transistor #(.\type ("n"), .gate("br")) transistor_71 (
    .in(transistor_83_out), .out(transistor_71_out), .gate(transistor_84_out));
  Pull_Resistor #(.pull(1)) pull_resistor_57 (.node(transistor_71_out));
  Transistor #(.\type ("n"), .gate("br")) transistor_72 (.in(1'b0), .out(transistor_72_out), .gate(transistor_71_out));
  Pull_Resistor #(.pull(1)) pull_resistor_58 (.node(pull_resistor_58_node));
  Transistor #(.\type ("n"), .gate("br")) transistor_73 (
    .in(transistor_72_out), .out(pull_resistor_58_node), .gate(transistor_86_out));
  Transistor #(.\type ("n"), .gate("br")) transistor_74 (.in(1'b0), .out(transistor_74_out), .gate(transistor_55_out));
  Transistor #(.\type ("n"), .gate("br")) transistor_75 (
    .in(transistor_74_out), .out(transistor_75_out), .gate(transistor_87_out));
  Pull_Resistor #(.pull(1)) pull_resistor_59 (.node(transistor_75_out));
  Transistor #(.\type ("n"), .gate("br")) transistor_76 (
    .in(transistor_88_out), .out(transistor_76_out), .gate(transistor_84_out));
  Pull_Resistor #(.pull(1)) pull_resistor_60 (.node(transistor_76_out));
  Transistor #(.\type ("n"), .gate("br")) transistor_77 (.in(1'b0), .out(transistor_77_out), .gate(transistor_75_out));
  Transistor #(.\type ("n"), .gate("br")) transistor_78 (
    .in(transistor_77_out), .out(transistor_78_out), .gate(transistor_89_out));
  Pull_Resistor #(.pull(1)) pull_resistor_61 (.node(transistor_78_out));
  Transistor #(.\type ("n")) transistor_79 (.in(1'b0), .out(pull_resistor_54_node), .gate(pull_resistor_3_node[1]));
  Transistor #(.\type ("n")) transistor_80 (.in(1'b0), .out(pull_resistor_54_node), .gate(pull_resistor_3_node[2]));
  Pull_Resistor #(.pull(1)) pull_resistor_62 (.node(pull_resistor_62_node));
  Pull_Resistor #(.pull(1)) pull_resistor_63 (.node(pull_resistor_63_node));
  Transistor #(.\type ("n")) transistor_81 (.in(1'b0), .out(pull_resistor_62_node), .gate(pull_resistor_56_node));
  Transistor #(.\type ("n")) transistor_82 (.in(1'b0), .out(pull_resistor_63_node), .gate(in_2[5]));
  Transistor #(.\type ("n"), .gate("br")) transistor_83 (.in(1'b0), .out(transistor_83_out), .gate(in_2[3]));
  Pull_Resistor #(.pull(1)) pull_resistor_64 (.node(transistor_83_out));
  Transistor #(.\type ("n"), .gate("br")) transistor_84 (
    .in(transistor_83_out), .out(transistor_84_out), .gate(in_3[3]));
  Pull_Resistor #(.pull(1)) pull_resistor_65 (.node(transistor_84_out));
  Pull_Resistor #(.pull(1)) pull_resistor_66 (.node(pull_resistor_66_node));
  Transistor #(.\type ("n"), .gate("br")) transistor_85 (
    .in(1'b0), .out(pull_resistor_66_node), .gate(transistor_84_out));
  Transistor #(.\type ("n"), .gate("br")) transistor_86 (
    .in(pull_resistor_66_node), .out(transistor_86_out), .gate(in_3[3]));
  Pull_Resistor #(.pull(1)) pull_resistor_67 (.node(transistor_86_out));
  Transistor #(.\type ("n"), .gate("br")) transistor_87 (
    .in(transistor_74_out), .out(transistor_87_out), .gate(pull_resistor_58_node));
  Pull_Resistor #(.pull(1)) pull_resistor_68 (.node(transistor_87_out));
  Transistor #(.\type ("n"), .gate("br")) transistor_88 (.in(1'b0), .out(transistor_88_out), .gate(transistor_87_out));
  Transistor #(.\type ("n"), .gate("br")) transistor_89 (
    .in(transistor_88_out), .out(transistor_89_out), .gate(pull_resistor_58_node));
  Pull_Resistor #(.pull(1)) pull_resistor_69 (.node(transistor_89_out));
  Transistor #(.\type ("n")) transistor_90 (.in(1'b0), .out(pull_resistor_54_node), .gate(pull_resistor_5_node[0]));
  Transistor #(.\type ("n")) transistor_91 (.in(1'b0), .out(pull_resistor_54_node), .gate(pull_resistor_3_node[3]));
  Transistor #(.\type ("n")) transistor_92 (.in(1'b0), .out(transistor_92_out), .gate(pull_resistor_63_node));
  Transistor #(.\type ("n")) transistor_93 (.in(1'b0), .out(pull_resistor_63_node), .gate(in_3[5]));
  Pull_Resistor #(.pull(1)) pull_resistor_70 (.node(transistor_92_out));
  Pull_Resistor #(.pull(1)) pull_resistor_71 (.node(pull_resistor_71_node));
  Transistor #(.\type ("n"), .gate("br")) transistor_94 (
    .in(transistor_106_out), .out(pull_resistor_71_node), .gate(transistor_107_out));
  Transistor #(.\type ("n"), .gate("br")) transistor_95 (
    .in(1'b0), .out(transistor_95_out), .gate(pull_resistor_71_node));
  Transistor #(.\type ("n"), .gate("br")) transistor_96 (
    .in(transistor_95_out), .out(transistor_96_out), .gate(transistor_109_out));
  Pull_Resistor #(.pull(1)) pull_resistor_72 (.node(transistor_96_out));
  Transistor #(.\type ("n"), .gate("br")) transistor_97 (.in(1'b0), .out(transistor_97_out), .gate(transistor_76_out));
  Transistor #(.\type ("n"), .gate("br")) transistor_98 (
    .in(transistor_97_out), .out(transistor_98_out), .gate(transistor_110_out));
  Pull_Resistor #(.pull(1)) pull_resistor_73 (.node(transistor_98_out));
  Transistor #(.\type ("n"), .gate("br")) transistor_99 (
    .in(transistor_111_out), .out(transistor_99_out), .gate(transistor_107_out));
  Pull_Resistor #(.pull(1)) pull_resistor_74 (.node(transistor_99_out));
  Transistor #(.\type ("n"), .gate("br")) transistor_100 (
    .in(1'b0), .out(transistor_100_out), .gate(transistor_98_out));
  Transistor #(.\type ("n"), .gate("br")) transistor_101 (
    .in(transistor_100_out), .out(transistor_101_out), .gate(transistor_112_out));
  Pull_Resistor #(.pull(1)) pull_resistor_75 (.node(transistor_101_out));
  Transistor #(.\type ("n")) transistor_102 (.in(1'b0), .out(pull_resistor_54_node), .gate(pull_resistor_5_node[1]));
  Transistor #(.\type ("n")) transistor_103 (.in(1'b0), .out(pull_resistor_54_node), .gate(pull_resistor_5_node[2]));
  Transistor #(.\type ("n")) transistor_104 (.in(1'b0), .out(transistor_104_out), .gate(in_2[6]));
  Pull_Resistor #(.pull(1)) pull_resistor_76 (.node(transistor_104_out));
  Transistor #(.\type ("n")) transistor_105 (.in(1'b0), .out(transistor_104_out), .gate(in_3[6]));
  Transistor #(.\type ("n"), .gate("br")) transistor_106 (.in(1'b0), .out(transistor_106_out), .gate(in_2[4]));
  Pull_Resistor #(.pull(1)) pull_resistor_77 (.node(transistor_106_out));
  Transistor #(.\type ("n"), .gate("br")) transistor_107 (
    .in(transistor_106_out), .out(transistor_107_out), .gate(in_3[4]));
  Pull_Resistor #(.pull(1)) pull_resistor_78 (.node(transistor_107_out));
  Transistor #(.\type ("n"), .gate("br")) transistor_108 (
    .in(1'b0), .out(transistor_108_out), .gate(transistor_107_out));
  Pull_Resistor #(.pull(1)) pull_resistor_79 (.node(transistor_108_out));
  Transistor #(.\type ("n"), .gate("br")) transistor_109 (
    .in(transistor_108_out), .out(transistor_109_out), .gate(in_3[4]));
  Pull_Resistor #(.pull(1)) pull_resistor_80 (.node(transistor_109_out));
  Transistor #(.\type ("n"), .gate("br")) transistor_110 (
    .in(transistor_97_out), .out(transistor_110_out), .gate(transistor_96_out));
  Pull_Resistor #(.pull(1)) pull_resistor_81 (.node(transistor_110_out));
  Transistor #(.\type ("n"), .gate("br")) transistor_111 (
    .in(1'b0), .out(transistor_111_out), .gate(transistor_110_out));
  Transistor #(.\type ("n"), .gate("br")) transistor_112 (
    .in(transistor_111_out), .out(transistor_112_out), .gate(transistor_96_out));
  Pull_Resistor #(.pull(1)) pull_resistor_82 (.node(transistor_112_out));
  Transistor #(.\type ("n")) transistor_113 (.in(1'b0), .out(pull_resistor_54_node), .gate(pull_resistor_5_node[3]));
  Pull_Resistor #(.pull(1)) pull_resistor_83 (.node(pull_resistor_83_node));
  Transistor #(.\type ("n")) transistor_114 (.in(1'b0), .out(pull_resistor_83_node), .gate(transistor_104_out));
  Transistor #(.\type ("n")) transistor_115 (.in(1'b0), .out(transistor_115_out), .gate(in_3[7]));
  Pull_Resistor #(.pull(1)) pull_resistor_84 (.node(pull_resistor_84_node));
  Transistor #(.\type ("n")) transistor_116 (.in(1'b0), .out(transistor_115_out), .gate(in_2[7]));
  Pull_Resistor #(.pull(1)) pull_resistor_85 (.node(transistor_115_out));
  Transistor #(.\type ("n")) transistor_117 (.in(1'b0), .out(pull_resistor_84_node), .gate(transistor_115_out));
  Pull_Resistor #(.pull(1)) pull_resistor_86 (.node(pull_resistor_86_node));
  Transistor #(.\type ("n"), .gate("br")) transistor_118 (
    .in(transistor_126_out), .out(pull_resistor_86_node), .gate(transistor_127_out));
  Transistor #(.\type ("n"), .gate("br")) transistor_119 (
    .in(1'b0), .out(transistor_119_out), .gate(pull_resistor_86_node));
  Pull_Resistor #(.pull(1)) pull_resistor_87 (.node(pull_resistor_87_node));
  Transistor #(.\type ("n"), .gate("br")) transistor_120 (
    .in(transistor_119_out), .out(pull_resistor_87_node), .gate(transistor_129_out));
  Transistor #(.\type ("n"), .gate("br")) transistor_121 (
    .in(1'b0), .out(transistor_121_out), .gate(transistor_99_out));
  Transistor #(.\type ("n"), .gate("br")) transistor_122 (
    .in(transistor_121_out), .out(transistor_122_out), .gate(transistor_130_out));
  Pull_Resistor #(.pull(1)) pull_resistor_88 (.node(transistor_122_out));
  Pull_Resistor #(.pull(1)) pull_resistor_89 (.node(pull_resistor_89_node));
  Transistor #(.\type ("n"), .gate("br")) transistor_123 (
    .in(transistor_131_out), .out(pull_resistor_89_node), .gate(transistor_127_out));
  Transistor #(.\type ("n"), .gate("br")) transistor_124 (
    .in(1'b0), .out(transistor_124_out), .gate(transistor_122_out));
  Transistor #(.\type ("n"), .gate("br")) transistor_125 (
    .in(transistor_124_out), .out(transistor_125_out), .gate(transistor_132_out));
  Pull_Resistor #(.pull(1)) pull_resistor_90 (.node(transistor_125_out));
  Transistor #(.\type ("n"), .gate("br")) transistor_126 (.in(1'b0), .out(transistor_126_out), .gate(in_2[5]));
  Pull_Resistor #(.pull(1)) pull_resistor_91 (.node(transistor_126_out));
  Transistor #(.\type ("n"), .gate("br")) transistor_127 (
    .in(transistor_126_out), .out(transistor_127_out), .gate(in_3[5]));
  Pull_Resistor #(.pull(1)) pull_resistor_92 (.node(transistor_127_out));
  Transistor #(.\type ("n"), .gate("br")) transistor_128 (
    .in(1'b0), .out(transistor_128_out), .gate(transistor_127_out));
  Pull_Resistor #(.pull(1)) pull_resistor_93 (.node(transistor_128_out));
  Transistor #(.\type ("n"), .gate("br")) transistor_129 (
    .in(transistor_128_out), .out(transistor_129_out), .gate(in_3[5]));
  Pull_Resistor #(.pull(1)) pull_resistor_94 (.node(transistor_129_out));
  Transistor #(.\type ("n"), .gate("br")) transistor_130 (
    .in(transistor_121_out), .out(transistor_130_out), .gate(pull_resistor_87_node));
  Pull_Resistor #(.pull(1)) pull_resistor_95 (.node(transistor_130_out));
  Transistor #(.\type ("n"), .gate("br")) transistor_131 (
    .in(1'b0), .out(transistor_131_out), .gate(transistor_130_out));
  Transistor #(.\type ("n"), .gate("br")) transistor_132 (
    .in(transistor_131_out), .out(transistor_132_out), .gate(pull_resistor_87_node));
  Pull_Resistor #(.pull(1)) pull_resistor_96 (.node(transistor_132_out));
  Transistor #(.\type ("n")) transistor_133 (
    .in(transistor_134_out), .out(pull_resistor_3_node[0]), .gate(pull_resistor_130_node));
  Transistor #(.\type ("n")) transistor_134 (.in(1'b0), .out(transistor_134_out), .gate(pull_resistor_121_node));
  Transistor #(.\type ("n")) transistor_135 (
    .in(transistor_138_out), .out(pull_resistor_3_node[2]), .gate(pull_resistor_128_node));
  Transistor #(.\type ("n")) transistor_136 (
    .in(transistor_137_out), .out(pull_resistor_3_node[1]), .gate(pull_resistor_126_node));
  Transistor #(.\type ("n")) transistor_137 (.in(1'b0), .out(transistor_137_out), .gate(pull_resistor_121_node));
  Transistor #(.\type ("n")) transistor_138 (.in(1'b0), .out(transistor_138_out), .gate(pull_resistor_121_node));
  Transistor #(.\type ("n"), .gate("br")) transistor_139 (.in(1'b0), .out(transistor_139_out), .gate(in_2[6]));
  Pull_Resistor #(.pull(1)) pull_resistor_97 (.node(pull_resistor_97_node));
  Transistor #(.\type ("n"), .gate("br")) transistor_140 (
    .in(transistor_139_out), .out(pull_resistor_97_node), .gate(transistor_141_out));
  Transistor #(.\type ("n"), .gate("br")) transistor_141 (
    .in(transistor_139_out), .out(transistor_141_out), .gate(in_3[6]));
  Transistor #(.\type ("n"), .gate("br")) transistor_142 (
    .in(1'b0), .out(transistor_142_out), .gate(pull_resistor_97_node));
  Transistor #(.\type ("n"), .gate("br")) transistor_143 (
    .in(transistor_142_out), .out(transistor_143_out), .gate(transistor_146_out));
  Pull_Resistor #(.pull(1)) pull_resistor_98 (.node(transistor_143_out));
  Transistor #(.\type ("n"), .gate("br")) transistor_144 (
    .in(1'b0), .out(transistor_144_out), .gate(transistor_141_out));
  Transistor #(.\type ("n"), .gate("br")) transistor_145 (
    .in(1'b0), .out(transistor_145_out), .gate(pull_resistor_89_node));
  Transistor #(.\type ("n"), .gate("br")) transistor_146 (
    .in(transistor_144_out), .out(transistor_146_out), .gate(in_3[6]));
  Pull_Resistor #(.pull(1)) pull_resistor_99 (.node(pull_resistor_99_node));
  Transistor #(.\type ("n"), .gate("br")) transistor_147 (
    .in(transistor_145_out), .out(pull_resistor_99_node), .gate(transistor_148_out));
  Transistor #(.\type ("n"), .gate("br")) transistor_148 (
    .in(transistor_145_out), .out(transistor_148_out), .gate(transistor_143_out));
  Transistor #(.\type ("n"), .gate("br")) transistor_149 (
    .in(1'b0), .out(transistor_149_out), .gate(transistor_148_out));
  Pull_Resistor #(.pull(1)) pull_resistor_100 (.node(pull_resistor_100_node));
  Transistor #(.\type ("n"), .gate("br")) transistor_150 (
    .in(transistor_149_out), .out(pull_resistor_100_node), .gate(transistor_141_out));
  Transistor #(.\type ("n"), .gate("br")) transistor_151 (
    .in(transistor_149_out), .out(transistor_151_out), .gate(transistor_143_out));
  Transistor #(.\type ("n"), .gate("br")) transistor_152 (
    .in(1'b0), .out(transistor_152_out), .gate(pull_resistor_99_node));
  Pull_Resistor #(.pull(1)) pull_resistor_101 (.node(pull_resistor_101_node));
  Transistor #(.\type ("n"), .gate("br")) transistor_153 (
    .in(transistor_152_out), .out(pull_resistor_101_node), .gate(transistor_151_out));
  Transistor #(.\type ("n")) transistor_154 (
    .in(transistor_157_out), .out(pull_resistor_5_node[0]), .gate(pull_resistor_131_node));
  Transistor #(.\type ("n")) transistor_155 (
    .in(transistor_156_out), .out(pull_resistor_3_node[3]), .gate(pull_resistor_127_node));
  Transistor #(.\type ("n")) transistor_156 (.in(1'b0), .out(transistor_156_out), .gate(pull_resistor_121_node));
  Transistor #(.\type ("n")) transistor_157 (.in(1'b0), .out(transistor_157_out), .gate(pull_resistor_121_node));
  Pull_Resistor #(.pull(1)) pull_resistor_102 (.node(transistor_139_out));
  Pull_Resistor #(.pull(1)) pull_resistor_103 (.node(transistor_141_out));
  Pull_Resistor #(.pull(1)) pull_resistor_104 (.node(transistor_144_out));
  Pull_Resistor #(.pull(1)) pull_resistor_105 (.node(transistor_146_out));
  Pull_Resistor #(.pull(1)) pull_resistor_106 (.node(transistor_148_out));
  Pull_Resistor #(.pull(1)) pull_resistor_107 (.node(transistor_151_out));
  Transistor #(.\type ("n")) transistor_158 (
    .in(transistor_161_out), .out(pull_resistor_5_node[1]), .gate(pull_resistor_132_node));
  Transistor #(.\type ("n")) transistor_159 (
    .in(transistor_160_out), .out(pull_resistor_5_node[2]), .gate(pull_resistor_129_node));
  Transistor #(.\type ("n")) transistor_160 (.in(1'b0), .out(transistor_160_out), .gate(pull_resistor_121_node));
  Transistor #(.\type ("n")) transistor_161 (.in(1'b0), .out(transistor_161_out), .gate(pull_resistor_121_node));
  Transistor #(.\type ("n"), .gate("br")) transistor_162 (
    .in(transistor_172_out), .out(transistor_162_out), .gate(transistor_173_out));
  Pull_Resistor #(.pull(1)) pull_resistor_108 (.node(transistor_162_out));
  Transistor #(.\type ("n"), .gate("br")) transistor_163 (
    .in(1'b0), .out(transistor_163_out), .gate(transistor_162_out));
  Pull_Resistor #(.pull(1)) pull_resistor_109 (.node(pull_resistor_109_node));
  Transistor #(.\type ("n"), .gate("br")) transistor_164 (
    .in(transistor_163_out), .out(pull_resistor_109_node), .gate(transistor_175_out));
  Transistor #(.\type ("n"), .gate("br")) transistor_165 (
    .in(1'b0), .out(transistor_165_out), .gate(pull_resistor_100_node));
  Transistor #(.\type ("n"), .gate("br")) transistor_166 (
    .in(transistor_165_out), .out(transistor_166_out), .gate(transistor_176_out));
  Pull_Resistor #(.pull(1)) pull_resistor_110 (.node(transistor_166_out));
  Transistor #(.\type ("n"), .gate("br")) transistor_167 (
    .in(transistor_177_out), .out(transistor_167_out), .gate(transistor_173_out));
  Pull_Resistor #(.pull(1)) pull_resistor_111 (.node(transistor_167_out));
  Transistor #(.\type ("n"), .gate("br")) transistor_168 (
    .in(1'b0), .out(transistor_168_out), .gate(transistor_166_out));
  Transistor #(.\type ("n"), .gate("br")) transistor_169 (
    .in(transistor_168_out), .out(transistor_169_out), .gate(transistor_178_out));
  Pull_Resistor #(.pull(1)) pull_resistor_112 (.node(transistor_169_out));
  Transistor #(.\type ("n")) transistor_170 (
    .in(transistor_171_out), .out(pull_resistor_5_node[3]), .gate(pull_resistor_125_node));
  Transistor #(.\type ("n")) transistor_171 (.in(1'b0), .out(transistor_171_out), .gate(pull_resistor_121_node));
  Transistor #(.\type ("n"), .gate("br")) transistor_172 (.in(1'b0), .out(transistor_172_out), .gate(in_2[7]));
  Pull_Resistor #(.pull(1)) pull_resistor_113 (.node(transistor_172_out));
  Transistor #(.\type ("n"), .gate("br")) transistor_173 (
    .in(transistor_172_out), .out(transistor_173_out), .gate(in_3[7]));
  Pull_Resistor #(.pull(1)) pull_resistor_114 (.node(transistor_173_out));
  Transistor #(.\type ("n"), .gate("br")) transistor_174 (
    .in(1'b0), .out(transistor_174_out), .gate(transistor_173_out));
  Pull_Resistor #(.pull(1)) pull_resistor_115 (.node(transistor_174_out));
  Transistor #(.\type ("n"), .gate("br")) transistor_175 (
    .in(transistor_174_out), .out(transistor_175_out), .gate(in_3[7]));
  Pull_Resistor #(.pull(1)) pull_resistor_116 (.node(transistor_175_out));
  Transistor #(.\type ("n"), .gate("br")) transistor_176 (
    .in(transistor_165_out), .out(transistor_176_out), .gate(pull_resistor_109_node));
  Pull_Resistor #(.pull(1)) pull_resistor_117 (.node(transistor_176_out));
  Transistor #(.\type ("n"), .gate("br")) transistor_177 (
    .in(1'b0), .out(transistor_177_out), .gate(transistor_176_out));
  Transistor #(.\type ("n"), .gate("br")) transistor_178 (
    .in(transistor_177_out), .out(transistor_178_out), .gate(pull_resistor_109_node));
  Pull_Resistor #(.pull(1)) pull_resistor_118 (.node(transistor_178_out));
  Pull_Resistor #(.pull(1)) pull_resistor_119 (.node(pull_resistor_119_node));
  Transistor #(.\type ("n")) transistor_179 (
    .in(transistor_181_out), .out(pull_resistor_119_node), .gate(transistor_167_out));
  Transistor #(.\type ("n")) transistor_180 (.in(1'b0), .out(transistor_180_out), .gate(pull_resistor_119_node));
  Pull_Resistor #(.pull(1)) pull_resistor_120 (.node(transistor_180_out));
  Transistor #(.\type ("n")) transistor_181 (.in(1'b0), .out(transistor_181_out), .gate(in_1[0]));
  Pull_Resistor #(.pull(1)) pull_resistor_121 (.node(pull_resistor_121_node));
  Transistor #(.\type ("n")) transistor_182 (.in(1'b0), .out(pull_resistor_121_node), .gate(pull_resistor_122_node));
  Pull_Resistor #(.pull(1)) pull_resistor_122 (.node(pull_resistor_122_node));
  Transistor #(.\type ("n")) transistor_183 (.in(1'b0), .out(pull_resistor_122_node), .gate(in_1[5]));
  Transistor #(.\type ("n")) transistor_184 (.in(1'b0), .out(pull_resistor_122_node), .gate(in_1[4]));
  Transistor #(.\type ("n")) transistor_185 (.in(1'b0), .out(pull_resistor_122_node), .gate(in_1[3]));
  Transistor #(.\type ("n")) transistor_186 (.in(1'b0), .out(pull_resistor_122_node), .gate(in_1[2]));
  Transistor #(.\type ("n")) transistor_187 (.in(transistor_188_out), .out(transistor_187_out), .gate(in_2[0]));
  Pull_Resistor #(.pull(1)) pull_resistor_123 (.node(transistor_187_out));
  Pull_Resistor #(.pull(1)) pull_resistor_124 (.node(pull_resistor_124_node));
  Transistor #(.\type ("n")) transistor_188 (.in(1'b0), .out(transistor_188_out), .gate(in_1[3]));
  Transistor #(.\type ("n")) transistor_189 (.in(1'b0), .out(pull_resistor_124_node), .gate(transistor_187_out));
  Transistor #(.\type ("n")) transistor_190 (.in(1'b0), .out(pull_resistor_122_node), .gate(in_1[0]));
  Transistor #(.\type ("n")) transistor_191 (.in(1'b0), .out(pull_resistor_122_node), .gate(in_1[1]));
  Pull_Resistor #(.pull(1)) pull_resistor_125 (.node(pull_resistor_125_node));
  Pull_Resistor #(.pull(1)) pull_resistor_126 (.node(pull_resistor_126_node));
  Pull_Resistor #(.pull(1)) pull_resistor_127 (.node(pull_resistor_127_node));
  Pull_Resistor #(.pull(1)) pull_resistor_128 (.node(pull_resistor_128_node));
  Pull_Resistor #(.pull(1)) pull_resistor_129 (.node(pull_resistor_129_node));
  Pull_Resistor #(.pull(1)) pull_resistor_130 (.node(pull_resistor_130_node));
  Pull_Resistor #(.pull(1)) pull_resistor_131 (.node(pull_resistor_131_node));
  Pull_Resistor #(.pull(1)) pull_resistor_132 (.node(pull_resistor_132_node));
  Transistor #(.\type ("n")) transistor_192 (
    .in(transistor_193_out), .out(pull_resistor_130_node), .gate(pull_resistor_25_node));
  Transistor #(.\type ("n")) transistor_193 (.in(1'b0), .out(transistor_193_out), .gate(in_1[5]));
  Transistor #(.\type ("n")) transistor_194 (
    .in(transistor_195_out), .out(pull_resistor_130_node), .gate(pull_resistor_21_node));
  Transistor #(.\type ("n")) transistor_195 (.in(1'b0), .out(transistor_195_out), .gate(in_1[4]));
  Transistor #(.\type ("n")) transistor_196 (.in(transistor_197_out), .out(pull_resistor_130_node), .gate(in_2[1]));
  Transistor #(.\type ("n")) transistor_197 (.in(1'b0), .out(transistor_197_out), .gate(in_1[3]));
  Transistor #(.\type ("n")) transistor_198 (
    .in(transistor_199_out), .out(pull_resistor_130_node), .gate(transistor_15_out));
  Transistor #(.\type ("n")) transistor_199 (.in(1'b0), .out(transistor_199_out), .gate(in_1[2]));
  Transistor #(.\type ("n")) transistor_200 (
    .in(transistor_201_out), .out(pull_resistor_130_node), .gate(pull_resistor_13_node));
  Transistor #(.\type ("n")) transistor_201 (.in(1'b0), .out(transistor_201_out), .gate(in_1[1]));
  Transistor #(.\type ("n")) transistor_202 (
    .in(transistor_203_out), .out(pull_resistor_130_node), .gate(transistor_11_out));
  Transistor #(.\type ("n")) transistor_203 (.in(1'b0), .out(transistor_203_out), .gate(in_1[0]));
  Transistor #(.\type ("n")) transistor_204 (
    .in(transistor_206_out), .out(pull_resistor_126_node), .gate(transistor_46_out));
  Transistor #(.\type ("n")) transistor_205 (
    .in(transistor_207_out), .out(pull_resistor_128_node), .gate(transistor_48_out));
  Transistor #(.\type ("n")) transistor_206 (.in(1'b0), .out(transistor_206_out), .gate(in_1[5]));
  Transistor #(.\type ("n")) transistor_207 (.in(1'b0), .out(transistor_207_out), .gate(in_1[5]));
  Transistor #(.\type ("n")) transistor_208 (
    .in(transistor_210_out), .out(pull_resistor_126_node), .gate(pull_resistor_35_node));
  Transistor #(.\type ("n")) transistor_209 (
    .in(transistor_211_out), .out(pull_resistor_128_node), .gate(transistor_61_out));
  Transistor #(.\type ("n")) transistor_210 (.in(1'b0), .out(transistor_210_out), .gate(in_1[4]));
  Transistor #(.\type ("n")) transistor_211 (.in(1'b0), .out(transistor_211_out), .gate(in_1[4]));
  Transistor #(.\type ("n")) transistor_212 (.in(transistor_214_out), .out(pull_resistor_126_node), .gate(in_2[2]));
  Transistor #(.\type ("n")) transistor_213 (.in(transistor_215_out), .out(pull_resistor_128_node), .gate(in_2[3]));
  Transistor #(.\type ("n")) transistor_214 (.in(1'b0), .out(transistor_214_out), .gate(in_1[3]));
  Transistor #(.\type ("n")) transistor_215 (.in(1'b0), .out(transistor_215_out), .gate(in_1[3]));
  Transistor #(.\type ("n")) transistor_216 (
    .in(transistor_219_out), .out(pull_resistor_128_node), .gate(transistor_59_out));
  Transistor #(.\type ("n")) transistor_217 (
    .in(transistor_218_out), .out(pull_resistor_126_node), .gate(transistor_39_out));
  Transistor #(.\type ("n")) transistor_218 (.in(1'b0), .out(transistor_218_out), .gate(in_1[2]));
  Transistor #(.\type ("n")) transistor_219 (.in(1'b0), .out(transistor_219_out), .gate(in_1[2]));
  Transistor #(.\type ("n")) transistor_220 (
    .in(transistor_223_out), .out(pull_resistor_126_node), .gate(pull_resistor_27_node));
  Transistor #(.\type ("n")) transistor_221 (
    .in(transistor_222_out), .out(pull_resistor_128_node), .gate(transistor_52_out));
  Transistor #(.\type ("n")) transistor_222 (.in(1'b0), .out(transistor_222_out), .gate(in_1[1]));
  Transistor #(.\type ("n")) transistor_223 (.in(1'b0), .out(transistor_223_out), .gate(in_1[1]));
  Transistor #(.\type ("n")) transistor_224 (
    .in(transistor_226_out), .out(pull_resistor_128_node), .gate(transistor_57_out));
  Transistor #(.\type ("n")) transistor_225 (
    .in(transistor_227_out), .out(pull_resistor_126_node), .gate(transistor_33_out));
  Transistor #(.\type ("n")) transistor_226 (.in(1'b0), .out(transistor_226_out), .gate(in_1[0]));
  Transistor #(.\type ("n")) transistor_227 (.in(1'b0), .out(transistor_227_out), .gate(in_1[0]));
  Transistor #(.\type ("n")) transistor_228 (
    .in(transistor_230_out), .out(pull_resistor_131_node), .gate(pull_resistor_62_node));
  Transistor #(.\type ("n")) transistor_229 (
    .in(transistor_231_out), .out(pull_resistor_127_node), .gate(pull_resistor_55_node));
  Transistor #(.\type ("n")) transistor_230 (.in(1'b0), .out(transistor_230_out), .gate(in_1[5]));
  Transistor #(.\type ("n")) transistor_231 (.in(1'b0), .out(transistor_231_out), .gate(in_1[5]));
  Transistor #(.\type ("n")) transistor_232 (
    .in(transistor_235_out), .out(pull_resistor_131_node), .gate(transistor_108_out));
  Transistor #(.\type ("n")) transistor_233 (
    .in(transistor_234_out), .out(pull_resistor_127_node), .gate(pull_resistor_66_node));
  Transistor #(.\type ("n")) transistor_234 (.in(1'b0), .out(transistor_234_out), .gate(in_1[4]));
  Transistor #(.\type ("n")) transistor_235 (.in(1'b0), .out(transistor_235_out), .gate(in_1[4]));
  Transistor #(.\type ("n")) transistor_236 (.in(transistor_239_out), .out(pull_resistor_131_node), .gate(in_2[5]));
  Transistor #(.\type ("n")) transistor_237 (.in(transistor_238_out), .out(pull_resistor_127_node), .gate(in_2[4]));
  Transistor #(.\type ("n")) transistor_238 (.in(1'b0), .out(transistor_238_out), .gate(in_1[3]));
  Transistor #(.\type ("n")) transistor_239 (.in(1'b0), .out(transistor_239_out), .gate(in_1[3]));
  Transistor #(.\type ("n")) transistor_240 (
    .in(transistor_243_out), .out(pull_resistor_127_node), .gate(transistor_83_out));
  Transistor #(.\type ("n")) transistor_241 (
    .in(transistor_242_out), .out(pull_resistor_131_node), .gate(transistor_106_out));
  Transistor #(.\type ("n")) transistor_242 (.in(1'b0), .out(transistor_242_out), .gate(in_1[2]));
  Transistor #(.\type ("n")) transistor_243 (.in(1'b0), .out(transistor_243_out), .gate(in_1[2]));
  Transistor #(.\type ("n")) transistor_244 (
    .in(transistor_246_out), .out(pull_resistor_131_node), .gate(transistor_96_out));
  Transistor #(.\type ("n")) transistor_245 (
    .in(transistor_247_out), .out(pull_resistor_127_node), .gate(pull_resistor_58_node));
  Transistor #(.\type ("n")) transistor_246 (.in(1'b0), .out(transistor_246_out), .gate(in_1[1]));
  Transistor #(.\type ("n")) transistor_247 (.in(1'b0), .out(transistor_247_out), .gate(in_1[1]));
  Transistor #(.\type ("n")) transistor_248 (
    .in(transistor_251_out), .out(pull_resistor_131_node), .gate(transistor_101_out));
  Transistor #(.\type ("n")) transistor_249 (
    .in(transistor_250_out), .out(pull_resistor_127_node), .gate(transistor_78_out));
  Transistor #(.\type ("n")) transistor_250 (.in(1'b0), .out(transistor_250_out), .gate(in_1[0]));
  Transistor #(.\type ("n")) transistor_251 (.in(1'b0), .out(transistor_251_out), .gate(in_1[0]));
  Transistor #(.\type ("n")) transistor_252 (
    .in(transistor_255_out), .out(pull_resistor_132_node), .gate(transistor_92_out));
  Transistor #(.\type ("n")) transistor_253 (
    .in(transistor_254_out), .out(pull_resistor_129_node), .gate(pull_resistor_83_node));
  Transistor #(.\type ("n")) transistor_254 (.in(1'b0), .out(transistor_254_out), .gate(in_1[5]));
  Transistor #(.\type ("n")) transistor_255 (.in(1'b0), .out(transistor_255_out), .gate(in_1[5]));
  Transistor #(.\type ("n")) transistor_256 (
    .in(transistor_259_out), .out(pull_resistor_132_node), .gate(transistor_128_out));
  Transistor #(.\type ("n")) transistor_257 (
    .in(transistor_258_out), .out(pull_resistor_129_node), .gate(transistor_144_out));
  Transistor #(.\type ("n")) transistor_258 (.in(1'b0), .out(transistor_258_out), .gate(in_1[4]));
  Transistor #(.\type ("n")) transistor_259 (.in(1'b0), .out(transistor_259_out), .gate(in_1[4]));
  Transistor #(.\type ("n")) transistor_260 (.in(transistor_262_out), .out(pull_resistor_132_node), .gate(in_2[6]));
  Transistor #(.\type ("n")) transistor_261 (.in(transistor_263_out), .out(pull_resistor_129_node), .gate(in_2[7]));
  Transistor #(.\type ("n")) transistor_262 (.in(1'b0), .out(transistor_262_out), .gate(in_1[3]));
  Transistor #(.\type ("n")) transistor_263 (.in(1'b0), .out(transistor_263_out), .gate(in_1[3]));
  Transistor #(.\type ("n")) transistor_264 (
    .in(transistor_266_out), .out(pull_resistor_129_node), .gate(transistor_139_out));
  Transistor #(.\type ("n")) transistor_265 (
    .in(transistor_267_out), .out(pull_resistor_132_node), .gate(transistor_126_out));
  Transistor #(.\type ("n")) transistor_266 (.in(1'b0), .out(transistor_266_out), .gate(in_1[2]));
  Transistor #(.\type ("n")) transistor_267 (.in(1'b0), .out(transistor_267_out), .gate(in_1[2]));
  Transistor #(.\type ("n")) transistor_268 (
    .in(transistor_270_out), .out(pull_resistor_132_node), .gate(pull_resistor_87_node));
  Transistor #(.\type ("n")) transistor_269 (
    .in(transistor_271_out), .out(pull_resistor_129_node), .gate(transistor_143_out));
  Transistor #(.\type ("n")) transistor_270 (.in(1'b0), .out(transistor_270_out), .gate(in_1[1]));
  Transistor #(.\type ("n")) transistor_271 (.in(1'b0), .out(transistor_271_out), .gate(in_1[1]));
  Transistor #(.\type ("n")) transistor_272 (
    .in(transistor_274_out), .out(pull_resistor_129_node), .gate(pull_resistor_101_node));
  Transistor #(.\type ("n")) transistor_273 (
    .in(transistor_275_out), .out(pull_resistor_132_node), .gate(transistor_125_out));
  Transistor #(.\type ("n")) transistor_274 (.in(1'b0), .out(transistor_274_out), .gate(in_1[0]));
  Transistor #(.\type ("n")) transistor_275 (.in(1'b0), .out(transistor_275_out), .gate(in_1[0]));
  Transistor #(.\type ("n")) transistor_276 (
    .in(transistor_277_out), .out(pull_resistor_125_node), .gate(pull_resistor_84_node));
  Transistor #(.\type ("n")) transistor_277 (.in(1'b0), .out(transistor_277_out), .gate(in_1[5]));
  Transistor #(.\type ("n")) transistor_278 (
    .in(transistor_279_out), .out(pull_resistor_125_node), .gate(transistor_174_out));
  Transistor #(.\type ("n")) transistor_279 (.in(1'b0), .out(transistor_279_out), .gate(in_1[4]));
  Transistor #(.\type ("n")) transistor_280 (
    .in(transistor_281_out), .out(pull_resistor_125_node), .gate(transistor_172_out));
  Transistor #(.\type ("n")) transistor_281 (.in(1'b0), .out(transistor_281_out), .gate(in_1[2]));
  Transistor #(.\type ("n")) transistor_282 (
    .in(transistor_283_out), .out(pull_resistor_125_node), .gate(pull_resistor_109_node));
  Transistor #(.\type ("n")) transistor_283 (.in(1'b0), .out(transistor_283_out), .gate(in_1[1]));
  Transistor #(.\type ("n")) transistor_284 (
    .in(transistor_285_out), .out(pull_resistor_125_node), .gate(transistor_169_out));
  Transistor #(.\type ("n")) transistor_285 (.in(1'b0), .out(transistor_285_out), .gate(in_1[0]));
  Bit_Extender bit_extender_1 ();  // open: in, out

  // Notes on the sheet:
  //   OR
  //   AND
  //   Right Shift
  //   NOT
  //   ADD
endmodule
