// Logisim project Controller unit v1.0 sim.circ as structural Verilog: 1 circuit, main circuit main
module main (
  input  in_1,
  input  in_2,
  input  in_3,
  input  in_4,
  input  in_5,
  input  [7:0] in_6,
  input  in_7,
  input  in_8
);

  wire A___ALU_A, A___ALU_B, ADD, ADR_0, ADR_1, ADR_2, ADR_3, ADR_4, ADR_5, ADR_6, ADR_7, ADR_8, ADR_9,
       ADR_10, ADR_11, ADR_12, ADR_13, ADR_14, ADR_15, ADR___0, ADR___1, ADR___2, ADR___3, ADR___4, ADR___5,
       ADR___6, ADR___7, ADR___8, ADR___9, ADR___10, ADR___11, ADR___12, ADR___13, ADR___14, ADR___15,
       ALU_B___FF, AND, B___ALU_A, B___ALU_B, bus_out____Main_bus, C___ALU_A, C___ALU_B, Carry_in,
       clock_1_out, clock_4_out, clock_5_out, clock_6_out, clock_7_out, clock_8_out, Commit_jump, D___ALU_A,
       D___ALU_B, FLAG_C, FLAG_N, FLAG_O, FLAG_STORE_C, FLAG_STORE_N, FLAG_STORE_O, FLAG_STORE_U,
       FLAG_STORE_Z, FLAG_U, FLAG_Z, jump_type_instruction, Main_bus____bus_out, nADC, nADD, nAND, nBNC,
       nBNO, nBNU, nBNZ, nBOC, nBON, nBOO, nBOP, nBOU, nBOZ, nClear, nDEC, NEXT_ADR_0, NEXT_ADR_1,
       NEXT_ADR_2, NEXT_ADR_3, NEXT_ADR_4, NEXT_ADR_5, NEXT_ADR_6, NEXT_ADR_7, NEXT_ADR_8, NEXT_ADR_9,
       NEXT_ADR_10, NEXT_ADR_11, NEXT_ADR_12, NEXT_ADR_13, NEXT_ADR_14, NEXT_ADR_15, nINC, nJMP, nLoad, nMOV,
       nNOT, nOR, NOT, not_1_out, not_2_out, not_3_out, not_4_out, not_5_out, not_6_out, not_7_out,
       not_8_out, not_9_out, not_10_out, not_11_out, not_12_out, not_13_out, not_14_out, not_15_out,
       not_16_out, not_17_out, not_18_out, not_19_out, not_20_out, not_21_out, not_22_out, not_23_out,
       not_24_out, not_25_out, not_26_out, not_27_out, not_28_out, not_29_out, not_30_out, not_31_out,
       not_32_out, not_33_out, not_34_out, not_35_out, not_36_out, nRS, nStore, nTIME_STEP_0, nXOR, OR,
       pull_resistor_33_node, pull_resistor_40_node, pull_resistor_41_node, pull_resistor_42_node,
       pull_resistor_43_node, pull_resistor_44_node, pull_resistor_73_node, pull_resistor_79_node,
       pull_resistor_88_node, pull_resistor_91_node, pull_resistor_95_node, pull_resistor_98_node,
       pull_resistor_102_node, pull_resistor_105_node, pull_resistor_107_node, pull_resistor_112_node,
       pull_resistor_113_node, pull_resistor_114_node, pull_resistor_115_node, pull_resistor_118_node,
       pull_resistor_119_node, pull_resistor_120_node, pull_resistor_123_node, pull_resistor_124_node,
       pull_resistor_126_node, pull_resistor_139_node, pull_resistor_140_node, pull_resistor_142_node,
       pull_resistor_143_node, pull_resistor_144_node, pull_resistor_145_node, pull_resistor_147_node,
       pull_resistor_156_node, pull_resistor_158_node, pull_resistor_166_node, pull_resistor_169_node,
       pull_resistor_170_node, pull_resistor_175_node, pull_resistor_178_node, pull_resistor_179_node,
       pull_resistor_181_node, pull_resistor_185_node, pull_resistor_187_node, pull_resistor_189_node,
       pull_resistor_194_node, pull_resistor_196_node, pull_resistor_197_node, pull_resistor_201_node,
       pull_resistor_203_node, pull_resistor_206_node, pull_resistor_210_node, pull_resistor_212_node,
       pull_resistor_214_node, pull_resistor_216_node, pull_resistor_220_node, pull_resistor_221_node,
       pull_resistor_222_node, pull_resistor_232_node, pull_resistor_234_node, pull_resistor_237_node,
       pull_resistor_238_node, pull_resistor_241_node, pull_resistor_242_node, pull_resistor_245_node,
       pull_resistor_247_node, pull_resistor_249_node, pull_resistor_251_node, pull_resistor_253_node,
       pull_resistor_255_node, pull_resistor_256_node, pull_resistor_258_node, pull_resistor_261_node,
       pull_resistor_263_node, pull_resistor_264_node, R_W_out, READ_A, READ_B, READ_C, READ_D, READ_FALG,
       Read_From_stored_Address, Read_New_Instruction, Read_Write_ins, REG____ALU_A, REG____ALU_B, REG_Read,
       RS, Store_Address_plus_plus, STORED_ADR_0, STORED_ADR_1, STORED_ADR_2, STORED_ADR_3, STORED_ADR_4,
       STORED_ADR_5, STORED_ADR_6, STORED_ADR_7, STORED_ADR_8, STORED_ADR_9, STORED_ADR_10, STORED_ADR_11,
       STORED_ADR_12, STORED_ADR_13, STORED_ADR_14, STORED_ADR_15, TEMP_ADR_0, TEMP_ADR_1, TEMP_ADR_2,
       TEMP_ADR_3, TEMP_ADR_4, TEMP_ADR_5, TEMP_ADR_6, TEMP_ADR_7, TEMP_ADR_8, TEMP_ADR_9, TEMP_ADR_10,
       TEMP_ADR_11, TEMP_ADR_12, TEMP_ADR_13, TEMP_ADR_14, TEMP_ADR_15, TIME_STEP_0, TIME_STEP_0or1,
       TIME_STEP_0or1or2, TIME_STEP_1, TIME_STEP_2, TIME_STEP_IN_0, TIME_STEP_IN_1, TIME_STEP_IN_2,
       transistor_6_out, transistor_7_out, transistor_8_out, transistor_9_out, transistor_10_out,
       transistor_12_out, transistor_13_out, transistor_14_out, transistor_15_out, transistor_16_out,
       transistor_19_out, transistor_22_out, transistor_24_out, transistor_28_out, transistor_29_out,
       transistor_30_out, transistor_31_out, transistor_32_out, transistor_33_out, transistor_34_out,
       transistor_38_out, transistor_41_out, transistor_43_out, transistor_45_out, transistor_46_out,
       transistor_47_out, transistor_48_out, transistor_52_out, transistor_55_out, transistor_58_out,
       transistor_60_out, transistor_63_out, transistor_65_out, transistor_67_out, transistor_68_out,
       transistor_69_out, transistor_70_out, transistor_71_out, transistor_72_out, transistor_73_out,
       transistor_74_out, transistor_75_out, transistor_77_out, transistor_81_out, transistor_95_out,
       transistor_96_out, transistor_97_out, transistor_98_out, transistor_99_out, transistor_100_out,
       transistor_101_out, transistor_102_out, transistor_103_out, transistor_104_out, transistor_105_out,
       transistor_106_out, transistor_107_out, transistor_109_out, transistor_110_out, transistor_111_out,
       transistor_112_out, transistor_113_out, transistor_114_out, transistor_115_out, transistor_116_out,
       transistor_117_out, transistor_118_out, transistor_119_out, transistor_122_out, transistor_124_out,
       transistor_126_out, transistor_127_out, transistor_128_out, transistor_129_out, transistor_131_out,
       transistor_132_out, transistor_133_out, transistor_134_out, transistor_135_out, transistor_136_out,
       transistor_137_out, transistor_138_out, transistor_139_out, transistor_144_out, transistor_145_out,
       transistor_146_out, transistor_147_out, transistor_149_out, transistor_150_out, transistor_152_out,
       transistor_153_out, transistor_157_out, transistor_159_out, transistor_160_out, transistor_161_out,
       transistor_162_out, transistor_164_out, transistor_165_out, transistor_166_out, transistor_169_out,
       transistor_171_out, transistor_175_out, transistor_182_out, transistor_187_out, transistor_190_out,
       transistor_194_out, transistor_195_out, transistor_197_out, transistor_199_out, transistor_202_out,
       transistor_203_out, transistor_211_out, transistor_212_out, transistor_215_out, transistor_218_out,
       transistor_222_out, transistor_224_out, transistor_225_out, transistor_230_out, transistor_232_out,
       transistor_233_out, transistor_234_out, transistor_237_out, transistor_240_out, transistor_245_out,
       transistor_247_out, transistor_249_out, transistor_250_out, transistor_252_out, transistor_253_out,
       transistor_255_out, transistor_258_out, transistor_261_out, transistor_264_out, transistor_265_out,
       transistor_267_out, transistor_270_out, transistor_273_out, transistor_276_out, transistor_277_out,
       transistor_279_out, transistor_280_out, transistor_282_out, transistor_284_out, transistor_285_out,
       transistor_287_out, transistor_289_out, transistor_291_out, transistor_292_out, transistor_294_out,
       transistor_295_out, transistor_296_out, transistor_298_out, transistor_301_out, transistor_303_out,
       transistor_306_out, transistor_308_out, transistor_310_out, transistor_311_out, transistor_313_out,
       transistor_315_out, transistor_316_out, transistor_318_out, transistor_320_out, transistor_321_out,
       transistor_323_out, transistor_326_out, transistor_328_out, transistor_330_out, transistor_331_out,
       transistor_333_out, transistor_335_out, transistor_337_out, transistor_339_out, transistor_341_out,
       transistor_343_out, transistor_344_out, transistor_346_out, transistor_348_out, transistor_349_out,
       transistor_351_out, transistor_353_out, transistor_357_out, transistor_358_out, transistor_361_out,
       transistor_362_out, transistor_363_out, transistor_365_out, transistor_373_out, transistor_375_out,
       transistor_380_out, transistor_382_out, transistor_386_out, transistor_387_out, transistor_390_out,
       transistor_391_out, transistor_393_out, transistor_394_out, transistor_396_out, transistor_399_out,
       transistor_401_out, transistor_404_out, transistor_406_out, transistor_410_out, transistor_412_out,
       transistor_414_out, transistor_415_out, transistor_417_out, transistor_420_out, transistor_422_out,
       transistor_425_out, transistor_427_out, transistor_430_out, transistor_432_out, transistor_435_out,
       transistor_437_out, transistor_439_out, transistor_440_out, transistor_442_out, transistor_445_out,
       transistor_447_out, transistor_449_out, transistor_451_out, transistor_453_out, transistor_455_out,
       transistor_457_out, transistor_458_out, transistor_460_out, transistor_462_out, transistor_463_out,
       transistor_465_out, transistor_467_out, transistor_468_out, transistor_470_out, transistor_475_out,
       transistor_477_out, transistor_479_out, transistor_481_out, transistor_482_out, transistor_483_out,
       transistor_485_out, transistor_486_out, transistor_487_out, transistor_489_out, transistor_490_out,
       transistor_491_out, transistor_493_out, transistor_494_out, transistor_495_out, transistor_497_out,
       transistor_498_out, transistor_499_out, transistor_501_out, transistor_502_out, transistor_503_out,
       transistor_505_out, transistor_506_out, transistor_507_out, transistor_509_out, transistor_510_out,
       transistor_511_out, transistor_513_out, transistor_514_out, transistor_515_out, transistor_517_out,
       transistor_518_out, transistor_519_out, transistor_521_out, transistor_522_out, transistor_523_out,
       transistor_525_out, transistor_526_out, transistor_527_out, transistor_529_out, transistor_530_out,
       transistor_531_out, transistor_533_out, transistor_534_out, transistor_535_out, transistor_537_out,
       transistor_538_out, transistor_539_out, transistor_541_out, transistor_542_out, XOR;
  wire [7:0] Main_bus, register_1_q, transistor_26_out;

  Register #(.trigger("falling")) register_1 (
    .D(in_6), .en(Read_New_Instruction), .Q(register_1_q), .clk(clock_1_out), .clr(in_7));
  Clock clock_1 (.out(clock_1_out));
  Pull_Resistor #(.pull(1)) pull_resistor_1 (.node(transistor_26_out[7]));
  Transistor #(.\type ("n")) transistor_1 (.in(1'b0), .out(transistor_26_out[7]), .gate(register_1_q[0]));
  Transistor #(.\type ("n")) transistor_2 (.in(1'b0), .out(transistor_26_out[6]), .gate(register_1_q[1]));
  Pull_Resistor #(.pull(1)) pull_resistor_2 (.node(transistor_26_out[6]));
  Hex_Digit_Display hex_digit_display_1 (.value(register_1_q[3:0]));  // open: dp
  Hex_Digit_Display hex_digit_display_2 (.value(register_1_q[7:4]));  // open: dp
  Transistor #(.\type ("n")) transistor_3 (.in(1'b0), .out(transistor_26_out[5]), .gate(register_1_q[2]));
  Pull_Resistor #(.pull(1)) pull_resistor_3 (.node(transistor_26_out[4]));
  Pull_Resistor #(.pull(1)) pull_resistor_4 (.node(transistor_26_out[5]));
  Transistor #(.\type ("n")) transistor_4 (.in(1'b0), .out(transistor_26_out[4]), .gate(register_1_q[3]));
  Transistor #(.\type ("n")) transistor_5 (.in(1'b0), .out(transistor_26_out[3]), .gate(register_1_q[4]));
  Pull_Resistor #(.pull(1)) pull_resistor_5 (.node(transistor_26_out[3]));
  Transistor #(.\type ("n")) transistor_6 (.in(transistor_7_out), .out(transistor_6_out), .gate(transistor_26_out[1]));
  Transistor #(.\type ("n")) transistor_7 (.in(1'b0), .out(transistor_7_out), .gate(transistor_26_out[0]));
  Transistor #(.\type ("n")) transistor_8 (.in(transistor_7_out), .out(transistor_8_out), .gate(register_1_q[6]));
  Transistor #(.\type ("n")) transistor_9 (.in(1'b0), .out(transistor_9_out), .gate(register_1_q[7]));
  Transistor #(.\type ("n")) transistor_10 (
    .in(transistor_9_out), .out(transistor_10_out), .gate(transistor_26_out[1]));
  Transistor #(.\type ("n")) transistor_11 (.in(1'b0), .out(transistor_26_out[2]), .gate(register_1_q[5]));
  Pull_Resistor #(.pull(1)) pull_resistor_6 (.node(transistor_26_out[2]));
  Transistor #(.\type ("n")) transistor_12 (
    .in(transistor_6_out), .out(transistor_12_out), .gate(transistor_26_out[2]));
  Transistor #(.\type ("n")) transistor_13 (
    .in(transistor_12_out), .out(transistor_13_out), .gate(transistor_26_out[3]));
  Transistor #(.\type ("n")) transistor_14 (.in(transistor_12_out), .out(transistor_14_out), .gate(register_1_q[4]));
  Transistor #(.\type ("n")) transistor_15 (
    .in(transistor_16_out), .out(transistor_15_out), .gate(transistor_26_out[3]));
  Transistor #(.\type ("n")) transistor_16 (.in(transistor_6_out), .out(transistor_16_out), .gate(register_1_q[5]));
  Transistor #(.\type ("n")) transistor_17 (.in(transistor_16_out), .out(nAND), .gate(register_1_q[4]));
  Pull_Resistor #(.pull(1)) pull_resistor_7 (.node(nAND));
  Transistor #(.\type ("n")) transistor_18 (.in(transistor_19_out), .out(nOR), .gate(transistor_26_out[3]));
  Transistor #(.\type ("n")) transistor_19 (
    .in(transistor_8_out), .out(transistor_19_out), .gate(transistor_26_out[2]));
  Pull_Resistor #(.pull(1)) pull_resistor_8 (.node(nOR));
  Transistor #(.\type ("n")) transistor_20 (.in(transistor_19_out), .out(nXOR), .gate(register_1_q[4]));
  Pull_Resistor #(.pull(1)) pull_resistor_9 (.node(nXOR));
  Transistor #(.\type ("n")) transistor_21 (.in(transistor_22_out), .out(nADD), .gate(transistor_26_out[3]));
  Pull_Resistor #(.pull(1)) pull_resistor_10 (.node(nADD));
  Transistor #(.\type ("n")) transistor_22 (.in(transistor_8_out), .out(transistor_22_out), .gate(register_1_q[5]));
  Transistor #(.\type ("n")) transistor_23 (.in(transistor_22_out), .out(nADC), .gate(register_1_q[4]));
  Pull_Resistor #(.pull(1)) pull_resistor_11 (.node(nADC));
  Transistor #(.\type ("n")) transistor_24 (
    .in(transistor_10_out), .out(transistor_24_out), .gate(transistor_26_out[2]));
  Pull_Resistor #(.pull(1)) pull_resistor_12 (.node(nMOV));
  Transistor #(.\type ("n")) transistor_25 (.in(transistor_24_out), .out(nMOV), .gate(transistor_26_out[3]));
  Pull_Resistor #(.pull(1)) pull_resistor_13 (.node(transistor_26_out[1]));
  Transistor #(.\type ("n")) transistor_26 (.in(1'b0), .out(transistor_26_out[0]), .gate(register_1_q[7]));
  Pull_Resistor #(.pull(1)) pull_resistor_14 (.node(transistor_26_out[0]));
  Transistor #(.\type ("n")) transistor_27 (.in(1'b0), .out(transistor_26_out[1]), .gate(register_1_q[6]));
  Transistor #(.\type ("n")) transistor_28 (
    .in(transistor_29_out), .out(transistor_28_out), .gate(transistor_26_out[5]));
  Transistor #(.\type ("n")) transistor_29 (
    .in(transistor_13_out), .out(transistor_29_out), .gate(transistor_26_out[4]));
  Transistor #(.\type ("n")) transistor_30 (.in(transistor_29_out), .out(transistor_30_out), .gate(register_1_q[2]));
  Transistor #(.\type ("n")) transistor_31 (
    .in(transistor_32_out), .out(transistor_31_out), .gate(transistor_26_out[5]));
  Transistor #(.\type ("n")) transistor_32 (.in(transistor_13_out), .out(transistor_32_out), .gate(register_1_q[3]));
  Transistor #(.\type ("n")) transistor_33 (.in(transistor_32_out), .out(transistor_33_out), .gate(register_1_q[2]));
  Transistor #(.\type ("n")) transistor_34 (
    .in(transistor_14_out), .out(transistor_34_out), .gate(transistor_26_out[4]));
  Pull_Resistor #(.pull(1)) pull_resistor_15 (.node(nClear));
  Transistor #(.\type ("n")) transistor_35 (.in(transistor_34_out), .out(nClear), .gate(transistor_26_out[5]));
  Pull_Resistor #(.pull(1)) pull_resistor_16 (.node(nLoad));
  Transistor #(.\type ("n")) transistor_36 (.in(transistor_34_out), .out(nLoad), .gate(register_1_q[2]));
  Pull_Resistor #(.pull(1)) pull_resistor_17 (.node(nStore));
  Transistor #(.\type ("n")) transistor_37 (.in(transistor_38_out), .out(nStore), .gate(transistor_26_out[5]));
  Transistor #(.\type ("n")) transistor_38 (.in(transistor_14_out), .out(transistor_38_out), .gate(register_1_q[3]));
  Transistor #(.\type ("n")) transistor_39 (.in(transistor_38_out), .out(nINC), .gate(register_1_q[2]));
  Pull_Resistor #(.pull(1)) pull_resistor_18 (.node(nINC));
  Transistor #(.\type ("n")) transistor_40 (.in(transistor_41_out), .out(nDEC), .gate(transistor_26_out[5]));
  Transistor #(.\type ("n")) transistor_41 (
    .in(transistor_15_out), .out(transistor_41_out), .gate(transistor_26_out[4]));
  Pull_Resistor #(.pull(1)) pull_resistor_19 (.node(nDEC));
  Pull_Resistor #(.pull(1)) pull_resistor_20 (.node(nRS));
  Transistor #(.\type ("n")) transistor_42 (.in(transistor_41_out), .out(nRS), .gate(register_1_q[2]));
  Pull_Resistor #(.pull(1)) pull_resistor_21 (.node(nNOT));
  Transistor #(.\type ("n")) transistor_43 (.in(transistor_15_out), .out(transistor_43_out), .gate(register_1_q[3]));
  Transistor #(.\type ("n")) transistor_44 (.in(transistor_43_out), .out(nNOT), .gate(transistor_26_out[5]));
  Transistor #(.\type ("n")) transistor_45 (.in(1'b0), .out(transistor_45_out), .gate(REG_Read));
  Transistor #(.\type ("n")) transistor_46 (.in(1'b0), .out(transistor_46_out), .gate(REG____ALU_A));
  Transistor #(.\type ("n")) transistor_47 (.in(1'b0), .out(transistor_47_out), .gate(REG____ALU_B));
  Transistor #(.\type ("n")) transistor_48 (.in(transistor_28_out), .out(transistor_48_out), .gate(register_1_q[1]));
  Transistor #(.\type ("n")) transistor_49 (.in(transistor_48_out), .out(nJMP), .gate(transistor_26_out[7]));
  Pull_Resistor #(.pull(1)) pull_resistor_22 (.node(nJMP));
  Pull_Resistor #(.pull(1)) pull_resistor_23 (.node(nBOP));
  Transistor #(.\type ("n")) transistor_50 (.in(transistor_48_out), .out(nBOP), .gate(register_1_q[0]));
  Transistor #(.\type ("n")) transistor_51 (.in(transistor_52_out), .out(nBON), .gate(transistor_26_out[7]));
  Transistor #(.\type ("n")) transistor_52 (
    .in(transistor_30_out), .out(transistor_52_out), .gate(transistor_26_out[6]));
  Pull_Resistor #(.pull(1)) pull_resistor_24 (.node(nBON));
  Pull_Resistor #(.pull(1)) pull_resistor_25 (.node(nBOZ));
  Transistor #(.\type ("n")) transistor_53 (.in(transistor_52_out), .out(nBOZ), .gate(register_1_q[0]));
  Transistor #(.\type ("n")) transistor_54 (.in(transistor_55_out), .out(nBNZ), .gate(transistor_26_out[7]));
  Pull_Resistor #(.pull(1)) pull_resistor_26 (.node(nBNZ));
  Transistor #(.\type ("n")) transistor_55 (.in(transistor_30_out), .out(transistor_55_out), .gate(register_1_q[1]));
  Pull_Resistor #(.pull(1)) pull_resistor_27 (.node(nBOO));
  Transistor #(.\type ("n")) transistor_56 (.in(transistor_55_out), .out(nBOO), .gate(register_1_q[0]));
  Transistor #(.\type ("n")) transistor_57 (.in(transistor_58_out), .out(nBNO), .gate(transistor_26_out[7]));
  Pull_Resistor #(.pull(1)) pull_resistor_28 (.node(nBNO));
  Transistor #(.\type ("n")) transistor_58 (
    .in(transistor_31_out), .out(transistor_58_out), .gate(transistor_26_out[6]));
  Pull_Resistor #(.pull(1)) pull_resistor_29 (.node(nBOU));
  Transistor #(.\type ("n")) transistor_59 (.in(transistor_58_out), .out(nBOU), .gate(register_1_q[0]));
  Transistor #(.\type ("n")) transistor_60 (.in(transistor_31_out), .out(transistor_60_out), .gate(register_1_q[1]));
  Transistor #(.\type ("n")) transistor_61 (.in(transistor_60_out), .out(nBNU), .gate(transistor_26_out[7]));
  Pull_Resistor #(.pull(1)) pull_resistor_30 (.node(nBNU));
  Pull_Resistor #(.pull(1)) pull_resistor_31 (.node(nBOC));
  Transistor #(.\type ("n")) transistor_62 (.in(transistor_60_out), .out(nBOC), .gate(register_1_q[0]));
  Transistor #(.\type ("n")) transistor_63 (
    .in(transistor_33_out), .out(transistor_63_out), .gate(transistor_26_out[6]));
  Pull_Resistor #(.pull(1)) pull_resistor_32 (.node(nBNC));
  Transistor #(.\type ("n")) transistor_64 (.in(transistor_63_out), .out(nBNC), .gate(transistor_26_out[7]));
  Transistor #(.\type ("n")) transistor_65 (
    .in(transistor_45_out), .out(transistor_65_out), .gate(transistor_26_out[6]));
  Pull_Resistor #(.pull(1)) pull_resistor_33 (.node(pull_resistor_33_node));
  Transistor #(.\type ("n")) transistor_66 (
    .in(transistor_65_out), .out(pull_resistor_33_node), .gate(transistor_26_out[7]));
  Transistor #(.\type ("n")) transistor_67 (.in(transistor_65_out), .out(transistor_67_out), .gate(register_1_q[0]));
  Pull_Resistor #(.pull(1)) pull_resistor_34 (.node(transistor_67_out));
  Transistor #(.\type ("n")) transistor_68 (.in(transistor_45_out), .out(transistor_68_out), .gate(register_1_q[1]));
  Transistor #(.\type ("n")) transistor_69 (
    .in(transistor_68_out), .out(transistor_69_out), .gate(transistor_26_out[7]));
  Pull_Resistor #(.pull(1)) pull_resistor_35 (.node(transistor_69_out));
  Transistor #(.\type ("n")) transistor_70 (.in(transistor_68_out), .out(transistor_70_out), .gate(register_1_q[0]));
  Pull_Resistor #(.pull(1)) pull_resistor_36 (.node(transistor_70_out));
  Transistor #(.\type ("n")) transistor_71 (
    .in(transistor_72_out), .out(transistor_71_out), .gate(transistor_26_out[7]));
  Transistor #(.\type ("n")) transistor_72 (
    .in(transistor_46_out), .out(transistor_72_out), .gate(transistor_26_out[6]));
  Pull_Resistor #(.pull(1)) pull_resistor_37 (.node(transistor_71_out));
  Transistor #(.\type ("n")) transistor_73 (.in(transistor_72_out), .out(transistor_73_out), .gate(register_1_q[0]));
  Pull_Resistor #(.pull(1)) pull_resistor_38 (.node(transistor_73_out));
  Transistor #(.\type ("n")) transistor_74 (
    .in(transistor_75_out), .out(transistor_74_out), .gate(transistor_26_out[7]));
  Pull_Resistor #(.pull(1)) pull_resistor_39 (.node(transistor_74_out));
  Transistor #(.\type ("n")) transistor_75 (.in(transistor_46_out), .out(transistor_75_out), .gate(register_1_q[1]));
  Pull_Resistor #(.pull(1)) pull_resistor_40 (.node(pull_resistor_40_node));
  Transistor #(.\type ("n")) transistor_76 (
    .in(transistor_75_out), .out(pull_resistor_40_node), .gate(register_1_q[0]));
  Transistor #(.\type ("n")) transistor_77 (
    .in(transistor_47_out), .out(transistor_77_out), .gate(transistor_26_out[4]));
  Pull_Resistor #(.pull(1)) pull_resistor_41 (.node(pull_resistor_41_node));
  Transistor #(.\type ("n")) transistor_78 (
    .in(transistor_77_out), .out(pull_resistor_41_node), .gate(transistor_26_out[5]));
  Pull_Resistor #(.pull(1)) pull_resistor_42 (.node(pull_resistor_42_node));
  Transistor #(.\type ("n")) transistor_79 (
    .in(transistor_77_out), .out(pull_resistor_42_node), .gate(register_1_q[2]));
  Pull_Resistor #(.pull(1)) pull_resistor_43 (.node(pull_resistor_43_node));
  Transistor #(.\type ("n")) transistor_80 (
    .in(transistor_81_out), .out(pull_resistor_43_node), .gate(transistor_26_out[5]));
  Transistor #(.\type ("n")) transistor_81 (.in(transistor_47_out), .out(transistor_81_out), .gate(register_1_q[3]));
  Pull_Resistor #(.pull(1)) pull_resistor_44 (.node(pull_resistor_44_node));
  Transistor #(.\type ("n")) transistor_82 (
    .in(transistor_81_out), .out(pull_resistor_44_node), .gate(register_1_q[2]));
  not not_1 (not_1_out, nJMP);
  LED led_1 (.in(not_1_out));
  LED led_2 (.in(not_2_out));
  not not_2 (not_2_out, nBOP);
  LED led_3 (.in(not_3_out));
  not not_3 (not_3_out, nBON);
  LED led_4 (.in(not_4_out));
  not not_4 (not_4_out, nBOZ);
  not not_5 (not_5_out, nBNZ);
  LED led_5 (.in(not_5_out));
  LED led_6 (.in(not_6_out));
  not not_6 (not_6_out, nBOO);
  LED led_7 (.in(not_7_out));
  not not_7 (not_7_out, nBNO);
  LED led_8 (.in(not_8_out));
  not not_8 (not_8_out, nBOU);
  not not_9 (not_9_out, nBNU);
  LED led_9 (.in(not_9_out));
  not not_10 (not_10_out, nBOC);
  LED led_10 (.in(not_10_out));
  LED led_11 (.in(not_11_out));
  not not_11 (not_11_out, nBNC);
  not not_12 (not_12_out, nClear);
  LED led_12 (.in(not_12_out));
  LED led_13 (.in(not_13_out));
  not not_13 (not_13_out, nLoad);
  not not_14 (not_14_out, nStore);
  LED led_14 (.in(not_14_out));
  not not_15 (not_15_out, nINC);
  LED led_15 (.in(not_15_out));
  not not_16 (not_16_out, nDEC);
  LED led_16 (.in(not_16_out));
  LED led_17 (.in(not_17_out));
  not not_17 (not_17_out, nRS);
  not not_18 (not_18_out, nNOT);
  LED led_18 (.in(not_18_out));
  LED led_19 (.in(not_19_out));
  not not_19 (not_19_out, nAND);
  not not_20 (not_20_out, nOR);
  LED led_20 (.in(not_20_out));
  not not_21 (not_21_out, nXOR);
  LED led_21 (.in(not_21_out));
  not not_22 (not_22_out, nADD);
  LED led_22 (.in(not_22_out));
  LED led_23 (.in(not_23_out));
  not not_23 (not_23_out, nADC);
  LED led_24 (.in(not_24_out));
  not not_24 (not_24_out, nMOV);
  not not_25 (not_25_out, pull_resistor_33_node);
  LED led_25 (.in(not_25_out));
  Transistor #(.\type ("n")) transistor_83 (.in(1'b0), .out(READ_A), .gate(pull_resistor_33_node));
  Pull_Resistor #(.pull(1)) pull_resistor_45 (.node(READ_A));
  LED led_26 (.in(not_26_out));
  not not_26 (not_26_out, transistor_67_out);
  Pull_Resistor #(.pull(1)) pull_resistor_46 (.node(READ_B));
  Transistor #(.\type ("n")) transistor_84 (.in(1'b0), .out(READ_B), .gate(transistor_67_out));
  LED led_27 (.in(not_27_out));
  not not_27 (not_27_out, transistor_69_out);
  Transistor #(.\type ("n")) transistor_85 (.in(1'b0), .out(READ_C), .gate(transistor_69_out));
  Pull_Resistor #(.pull(1)) pull_resistor_47 (.node(READ_C));
  not not_28 (not_28_out, transistor_70_out);
  LED led_28 (.in(not_28_out));
  Pull_Resistor #(.pull(1)) pull_resistor_48 (.node(READ_D));
  Transistor #(.\type ("n")) transistor_86 (.in(1'b0), .out(READ_D), .gate(transistor_70_out));
  not not_29 (not_29_out, transistor_71_out);
  LED led_29 (.in(not_29_out));
  Pull_Resistor #(.pull(1)) pull_resistor_49 (.node(A___ALU_A));
  Transistor #(.\type ("n")) transistor_87 (.in(1'b0), .out(A___ALU_A), .gate(transistor_71_out));
  not not_30 (not_30_out, transistor_73_out);
  LED led_30 (.in(not_30_out));
  Transistor #(.\type ("n")) transistor_88 (.in(1'b0), .out(B___ALU_A), .gate(transistor_73_out));
  Pull_Resistor #(.pull(1)) pull_resistor_50 (.node(B___ALU_A));
  not not_31 (not_31_out, transistor_74_out);
  LED led_31 (.in(not_31_out));
  Pull_Resistor #(.pull(1)) pull_resistor_51 (.node(C___ALU_A));
  Transistor #(.\type ("n")) transistor_89 (.in(1'b0), .out(C___ALU_A), .gate(transistor_74_out));
  LED led_32 (.in(not_32_out));
  not not_32 (not_32_out, pull_resistor_40_node);
  Pull_Resistor #(.pull(1)) pull_resistor_52 (.node(D___ALU_A));
  Transistor #(.\type ("n")) transistor_90 (.in(1'b0), .out(D___ALU_A), .gate(pull_resistor_40_node));
  not not_33 (not_33_out, pull_resistor_41_node);
  LED led_33 (.in(not_33_out));
  Transistor #(.\type ("n")) transistor_91 (.in(1'b0), .out(A___ALU_B), .gate(pull_resistor_41_node));
  Pull_Resistor #(.pull(1)) pull_resistor_53 (.node(A___ALU_B));
  LED led_34 (.in(not_34_out));
  not not_34 (not_34_out, pull_resistor_42_node);
  Pull_Resistor #(.pull(1)) pull_resistor_54 (.node(B___ALU_B));
  Transistor #(.\type ("n")) transistor_92 (.in(1'b0), .out(B___ALU_B), .gate(pull_resistor_42_node));
  not not_35 (not_35_out, pull_resistor_43_node);
  LED led_35 (.in(not_35_out));
  Pull_Resistor #(.pull(1)) pull_resistor_55 (.node(C___ALU_B));
  Transistor #(.\type ("n")) transistor_93 (.in(1'b0), .out(C___ALU_B), .gate(pull_resistor_43_node));
  LED led_36 (.in(not_36_out));
  not not_36 (not_36_out, pull_resistor_44_node);
  Pull_Resistor #(.pull(1)) pull_resistor_56 (.node(D___ALU_B));
  Transistor #(.\type ("n")) transistor_94 (.in(1'b0), .out(D___ALU_B), .gate(pull_resistor_44_node));
  Clock clock_2 ();  // open: out
  Transistor #(.\type ("n")) transistor_95 (.in(1'b0), .out(transistor_95_out), .gate(nClear));
  Transistor #(.\type ("n")) transistor_96 (.in(1'b0), .out(transistor_96_out), .gate(nStore));
  Transistor #(.\type ("n")) transistor_97 (.in(1'b0), .out(transistor_97_out), .gate(nAND));
  Transistor #(.\type ("n")) transistor_98 (.in(1'b0), .out(transistor_98_out), .gate(nINC));
  Pull_Resistor #(.pull(1)) pull_resistor_57 (.node(in_6[7]));
  Pull_Resistor #(.pull(1)) pull_resistor_58 (.node(in_6[6]));
  Pull_Resistor #(.pull(1)) pull_resistor_59 (.node(in_6[5]));
  Pull_Resistor #(.pull(1)) pull_resistor_60 (.node(in_6[4]));
  Pull_Resistor #(.pull(1)) pull_resistor_61 (.node(in_6[3]));
  Pull_Resistor #(.pull(1)) pull_resistor_62 (.node(in_6[2]));
  Pull_Resistor #(.pull(1)) pull_resistor_63 (.node(in_6[1]));
  Pull_Resistor #(.pull(1)) pull_resistor_64 (.node(in_6[0]));
  Pull_Resistor #(.pull(1)) pull_resistor_65 (.node(Main_bus[7]));
  Pull_Resistor #(.pull(1)) pull_resistor_66 (.node(Main_bus[6]));
  Pull_Resistor #(.pull(1)) pull_resistor_67 (.node(Main_bus[5]));
  Pull_Resistor #(.pull(1)) pull_resistor_68 (.node(Main_bus[4]));
  Pull_Resistor #(.pull(1)) pull_resistor_69 (.node(Main_bus[3]));
  Pull_Resistor #(.pull(1)) pull_resistor_70 (.node(Main_bus[2]));
  Pull_Resistor #(.pull(1)) pull_resistor_71 (.node(Main_bus[1]));
  Pull_Resistor #(.pull(1)) pull_resistor_72 (.node(Main_bus[0]));
  Transistor #(.\type ("n")) transistor_99 (.in(transistor_95_out), .out(transistor_99_out), .gate(nLoad));
  Transistor #(.\type ("n")) transistor_100 (.in(transistor_99_out), .out(transistor_100_out), .gate(nINC));
  Transistor #(.\type ("n")) transistor_101 (.in(transistor_102_out), .out(transistor_101_out), .gate(nDEC));
  Transistor #(.\type ("n")) transistor_102 (.in(transistor_96_out), .out(transistor_102_out), .gate(nINC));
  Transistor #(.\type ("n")) transistor_103 (.in(transistor_97_out), .out(transistor_103_out), .gate(nOR));
  Transistor #(.\type ("n")) transistor_104 (.in(transistor_103_out), .out(transistor_104_out), .gate(nXOR));
  Transistor #(.\type ("n")) transistor_105 (.in(transistor_98_out), .out(transistor_105_out), .gate(nDEC));
  Transistor #(.\type ("n")) transistor_106 (.in(transistor_105_out), .out(transistor_106_out), .gate(nRS));
  Transistor #(.\type ("n")) transistor_107 (.in(1'b0), .out(transistor_107_out), .gate(nBOP));
  Pull_Resistor #(.pull(1)) pull_resistor_73 (.node(pull_resistor_73_node));
  Transistor #(.\type ("n")) transistor_108 (
    .in(transistor_110_out), .out(pull_resistor_73_node), .gate(transistor_109_out));
  Transistor #(.\type ("n")) transistor_109 (.in(1'b0), .out(transistor_109_out), .gate(nLoad));
  Pull_Resistor #(.pull(1)) pull_resistor_74 (.node(transistor_109_out));
  Transistor #(.\type ("n")) transistor_110 (.in(1'b0), .out(transistor_110_out), .gate(TIME_STEP_2));
  Transistor #(.\type ("n")) transistor_111 (.in(transistor_112_out), .out(transistor_111_out), .gate(nRS));
  Transistor #(.\type ("n")) transistor_112 (.in(transistor_100_out), .out(transistor_112_out), .gate(nDEC));
  Transistor #(.\type ("n")) transistor_113 (.in(transistor_101_out), .out(transistor_113_out), .gate(nRS));
  Transistor #(.\type ("n")) transistor_114 (.in(transistor_113_out), .out(transistor_114_out), .gate(nNOT));
  Transistor #(.\type ("n")) transistor_115 (.in(transistor_116_out), .out(transistor_115_out), .gate(nADC));
  Transistor #(.\type ("n")) transistor_116 (.in(transistor_104_out), .out(transistor_116_out), .gate(nADD));
  Transistor #(.\type ("n")) transistor_117 (.in(transistor_106_out), .out(transistor_117_out), .gate(nNOT));
  Transistor #(.\type ("n")) transistor_118 (.in(transistor_117_out), .out(transistor_118_out), .gate(nAND));
  Transistor #(.\type ("n")) transistor_119 (.in(1'b0), .out(transistor_119_out), .gate(transistor_107_out));
  Transistor #(.\type ("n"), .gate("br")) transistor_120 (.in(1'b0), .out(transistor_107_out), .gate(FLAG_N));
  Pull_Resistor #(.pull(1)) pull_resistor_75 (.node(transistor_107_out));
  Transistor #(.\type ("n"), .gate("br")) transistor_121 (.in(1'b0), .out(transistor_107_out), .gate(FLAG_Z));
  Transistor #(.\type ("n")) transistor_122 (.in(1'b0), .out(transistor_122_out), .gate(nJMP));
  Pull_Resistor #(.pull(1)) pull_resistor_76 (.node(Read_Write_ins));
  Transistor #(.\type ("n")) transistor_123 (.in(transistor_124_out), .out(Read_Write_ins), .gate(nStore));
  Transistor #(.\type ("n")) transistor_124 (.in(1'b0), .out(transistor_124_out), .gate(nLoad));
  Pull_Resistor #(.pull(1)) pull_resistor_77 (.node(bus_out____Main_bus));
  Transistor #(.\type ("n")) transistor_125 (.in(1'b0), .out(bus_out____Main_bus), .gate(pull_resistor_73_node));
  Transistor #(.\type ("n")) transistor_126 (.in(transistor_111_out), .out(transistor_126_out), .gate(nNOT));
  Transistor #(.\type ("n")) transistor_127 (.in(transistor_126_out), .out(transistor_127_out), .gate(nAND));
  Transistor #(.\type ("n")) transistor_128 (.in(transistor_129_out), .out(transistor_128_out), .gate(nOR));
  Transistor #(.\type ("n")) transistor_129 (.in(transistor_114_out), .out(transistor_129_out), .gate(nAND));
  Transistor #(.\type ("n")) transistor_130 (.in(transistor_115_out), .out(REG____ALU_B), .gate(nMOV));
  Transistor #(.\type ("n")) transistor_131 (.in(transistor_132_out), .out(transistor_131_out), .gate(nXOR));
  Transistor #(.\type ("n")) transistor_132 (.in(transistor_118_out), .out(transistor_132_out), .gate(nOR));
  Transistor #(.\type ("n")) transistor_133 (.in(transistor_122_out), .out(transistor_133_out), .gate(nBOP));
  Transistor #(.\type ("n")) transistor_134 (.in(transistor_133_out), .out(transistor_134_out), .gate(nBON));
  Transistor #(.\type ("n")) transistor_135 (.in(transistor_136_out), .out(transistor_135_out), .gate(nXOR));
  Transistor #(.\type ("n")) transistor_136 (.in(transistor_127_out), .out(transistor_136_out), .gate(nOR));
  Transistor #(.\type ("n")) transistor_137 (.in(transistor_138_out), .out(transistor_137_out), .gate(nADD));
  Transistor #(.\type ("n")) transistor_138 (.in(transistor_128_out), .out(transistor_138_out), .gate(nXOR));
  Pull_Resistor #(.pull(1)) pull_resistor_78 (.node(REG____ALU_B));
  Transistor #(.\type ("n")) transistor_139 (.in(transistor_131_out), .out(transistor_139_out), .gate(nADD));
  Transistor #(.\type ("n")) transistor_140 (.in(transistor_139_out), .out(READ_FALG), .gate(nADC));
  Transistor #(.\type ("n")) transistor_141 (.in(1'b0), .out(transistor_119_out), .gate(pull_resistor_79_node));
  Pull_Resistor #(.pull(1)) pull_resistor_79 (.node(pull_resistor_79_node));
  Transistor #(.\type ("n"), .gate("br")) transistor_142 (
    .in(1'b0), .out(pull_resistor_79_node), .gate(transistor_144_out));
  Transistor #(.\type ("n")) transistor_143 (.in(1'b0), .out(pull_resistor_79_node), .gate(nBON));
  Transistor #(.\type ("n")) transistor_144 (.in(1'b0), .out(transistor_144_out), .gate(FLAG_N));
  Pull_Resistor #(.pull(1)) pull_resistor_80 (.node(transistor_144_out));
  Transistor #(.\type ("n")) transistor_145 (.in(transistor_146_out), .out(transistor_145_out), .gate(nBNZ));
  Transistor #(.\type ("n")) transistor_146 (.in(transistor_134_out), .out(transistor_146_out), .gate(nBOZ));
  Transistor #(.\type ("n")) transistor_147 (.in(1'b0), .out(transistor_147_out), .gate(TIME_STEP_0));
  Transistor #(.\type ("n")) transistor_148 (.in(1'b0), .out(transistor_147_out), .gate(TIME_STEP_1));
  Pull_Resistor #(.pull(1)) pull_resistor_81 (.node(transistor_147_out));
  Transistor #(.\type ("n")) transistor_149 (.in(transistor_135_out), .out(transistor_149_out), .gate(nADD));
  Transistor #(.\type ("n")) transistor_150 (.in(transistor_149_out), .out(transistor_150_out), .gate(nADC));
  Transistor #(.\type ("n")) transistor_151 (.in(transistor_137_out), .out(REG____ALU_A), .gate(nADC));
  Pull_Resistor #(.pull(1)) pull_resistor_82 (.node(READ_FALG));
  Transistor #(.\type ("n")) transistor_152 (.in(transistor_145_out), .out(transistor_152_out), .gate(nBOO));
  Transistor #(.\type ("n")) transistor_153 (.in(transistor_152_out), .out(transistor_153_out), .gate(nBNO));
  Pull_Resistor #(.pull(1)) pull_resistor_83 (.node(TIME_STEP_0or1));
  Transistor #(.\type ("n")) transistor_154 (.in(1'b0), .out(TIME_STEP_0or1), .gate(transistor_147_out));
  Transistor #(.\type ("n")) transistor_155 (.in(transistor_150_out), .out(REG_Read), .gate(nMOV));
  Pull_Resistor #(.pull(1)) pull_resistor_84 (.node(REG_Read));
  Pull_Resistor #(.pull(1)) pull_resistor_85 (.node(REG____ALU_A));
  Hex_Digit_Display hex_digit_display_3 (.value({ADR_15, ADR_14, ADR_13, ADR_12}));  // open: dp
  Transistor #(.\type ("n")) transistor_156 (.in(1'b0), .out(transistor_119_out), .gate(transistor_157_out));
  Transistor #(.\type ("n")) transistor_157 (.in(1'b0), .out(transistor_157_out), .gate(nBOZ));
  Transistor #(.\type ("n"), .gate("br")) transistor_158 (
    .in(1'b0), .out(transistor_157_out), .gate(transistor_164_out));
  Pull_Resistor #(.pull(1)) pull_resistor_86 (.node(transistor_157_out));
  Transistor #(.\type ("n")) transistor_159 (.in(transistor_153_out), .out(transistor_159_out), .gate(nBOU));
  Transistor #(.\type ("n")) transistor_160 (.in(transistor_159_out), .out(transistor_160_out), .gate(nBOU));
  Transistor #(.\type ("n")) transistor_161 (
    .in(transistor_162_out), .out(transistor_161_out), .gate(jump_type_instruction));
  Pull_Resistor #(.pull(1)) pull_resistor_87 (.node(transistor_161_out));
  Transistor #(.\type ("n")) transistor_162 (.in(1'b0), .out(transistor_162_out), .gate(transistor_147_out));
  Hex_Digit_Display hex_digit_display_4 (.value({ADR_11, ADR_10, ADR_9, ADR_8}));  // open: dp
  Hex_Digit_Display hex_digit_display_5 (.value({ADR_7, ADR_6, ADR_5, ADR_4}));  // open: dp
  Pull_Resistor #(.pull(1)) pull_resistor_88 (.node(pull_resistor_88_node));
  Transistor #(.\type ("n")) transistor_163 (.in(1'b0), .out(pull_resistor_88_node), .gate(nBNZ));
  Transistor #(.\type ("n")) transistor_164 (.in(1'b0), .out(transistor_164_out), .gate(FLAG_Z));
  Pull_Resistor #(.pull(1)) pull_resistor_89 (.node(transistor_164_out));
  Transistor #(.\type ("n")) transistor_165 (.in(transistor_166_out), .out(transistor_165_out), .gate(nBOC));
  Transistor #(.\type ("n")) transistor_166 (.in(transistor_160_out), .out(transistor_166_out), .gate(nBNU));
  Pull_Resistor #(.pull(1)) pull_resistor_90 (.node(TIME_STEP_IN_0));
  Transistor #(.\type ("n")) transistor_167 (.in(1'b0), .out(TIME_STEP_IN_0), .gate(transistor_161_out));
  Transistor #(.\type ("n"), .gate("br")) transistor_168 (
    .in(transistor_169_out), .out(transistor_161_out), .gate(Read_Write_ins));
  Transistor #(.\type ("n"), .gate("br")) transistor_169 (
    .in(1'b0), .out(transistor_169_out), .gate(transistor_175_out));
  Pull_Resistor #(.pull(1)) pull_resistor_91 (.node(pull_resistor_91_node));
  Transistor #(.\type ("n")) transistor_170 (
    .in(transistor_110_out), .out(pull_resistor_91_node), .gate(transistor_171_out));
  Transistor #(.\type ("n")) transistor_171 (.in(1'b0), .out(transistor_171_out), .gate(nStore));
  Pull_Resistor #(.pull(1)) pull_resistor_92 (.node(transistor_171_out));
  Hex_Digit_Display hex_digit_display_6 (.value({ADR_3, ADR_2, ADR_1, ADR_0}));  // open: dp
  Transistor #(.\type ("n")) transistor_172 (.in(1'b0), .out(transistor_119_out), .gate(pull_resistor_88_node));
  Transistor #(.\type ("n"), .gate("br")) transistor_173 (.in(1'b0), .out(pull_resistor_88_node), .gate(FLAG_Z));
  Pull_Resistor #(.pull(1)) pull_resistor_93 (.node(jump_type_instruction));
  Transistor #(.\type ("n")) transistor_174 (.in(transistor_165_out), .out(jump_type_instruction), .gate(nBNC));
  Transistor #(.\type ("n")) transistor_175 (.in(1'b0), .out(transistor_175_out), .gate(TIME_STEP_2));
  Pull_Resistor #(.pull(1)) pull_resistor_94 (.node(Main_bus____bus_out));
  Transistor #(.\type ("n")) transistor_176 (.in(1'b0), .out(Main_bus____bus_out), .gate(pull_resistor_91_node));
  Clock clock_3 ();  // open: out
  Transistor #(.\type ("n")) transistor_177 (.in(1'b0), .out(transistor_119_out), .gate(pull_resistor_95_node));
  Pull_Resistor #(.pull(1)) pull_resistor_95 (.node(pull_resistor_95_node));
  Transistor #(.\type ("n"), .gate("br")) transistor_178 (
    .in(1'b0), .out(pull_resistor_95_node), .gate(pull_resistor_98_node));
  Transistor #(.\type ("n")) transistor_179 (.in(1'b0), .out(pull_resistor_95_node), .gate(nBOO));
  Pull_Resistor #(.pull(1)) pull_resistor_96 (.node(transistor_175_out));
  Transistor #(.\type ("n")) transistor_180 (.in(1'b0), .out(transistor_175_out), .gate(TIME_STEP_0));
  Transistor #(.\type ("n")) transistor_181 (.in(1'b0), .out(transistor_175_out), .gate(TIME_STEP_1));
  Transistor #(.\type ("n")) transistor_182 (.in(1'b0), .out(transistor_182_out), .gate(nBNO));
  Pull_Resistor #(.pull(1)) pull_resistor_97 (.node(transistor_182_out));
  Pull_Resistor #(.pull(1)) pull_resistor_98 (.node(pull_resistor_98_node));
  Transistor #(.\type ("n")) transistor_183 (.in(1'b0), .out(pull_resistor_98_node), .gate(FLAG_O));
  Pull_Resistor #(.pull(1)) pull_resistor_99 (.node(TIME_STEP_0or1or2));
  Transistor #(.\type ("n")) transistor_184 (.in(1'b0), .out(TIME_STEP_0or1or2), .gate(transistor_175_out));
  Transistor #(.\type ("n")) transistor_185 (.in(1'b0), .out(transistor_119_out), .gate(transistor_182_out));
  Transistor #(.\type ("n"), .gate("br")) transistor_186 (.in(1'b0), .out(transistor_182_out), .gate(FLAG_O));
  Transistor #(.\type ("n")) transistor_187 (.in(1'b0), .out(transistor_187_out), .gate(nDEC));
  Transistor #(.\type ("n")) transistor_188 (.in(1'b0), .out(ALU_B___FF), .gate(nDEC));
  Pull_Resistor #(.pull(1)) pull_resistor_100 (.node(ALU_B___FF));
  Pull_Resistor #(.pull(1)) pull_resistor_101 (.node(NOT));
  Transistor #(.\type ("n")) transistor_189 (.in(1'b0), .out(NOT), .gate(nNOT));
  Transistor #(.\type ("n")) transistor_190 (.in(1'b0), .out(transistor_190_out), .gate(nAND));
  LED led_37 (.in(FLAG_C));
  LED led_38 (.in(FLAG_O));
  LED led_39 (.in(FLAG_U));
  LED led_40 (.in(FLAG_Z));
  LED led_41 (.in(FLAG_N));
  Transistor #(.\type ("n")) transistor_191 (.in(1'b0), .out(transistor_119_out), .gate(pull_resistor_102_node));
  Pull_Resistor #(.pull(1)) pull_resistor_102 (.node(pull_resistor_102_node));
  Transistor #(.\type ("n"), .gate("br")) transistor_192 (
    .in(1'b0), .out(pull_resistor_102_node), .gate(pull_resistor_107_node));
  Transistor #(.\type ("n")) transistor_193 (.in(1'b0), .out(pull_resistor_102_node), .gate(nBOU));
  Transistor #(.\type ("n")) transistor_194 (.in(transistor_187_out), .out(transistor_194_out), .gate(nINC));
  Transistor #(.\type ("n")) transistor_195 (.in(transistor_194_out), .out(transistor_195_out), .gate(nADD));
  Pull_Resistor #(.pull(1)) pull_resistor_103 (.node(AND));
  Transistor #(.\type ("n")) transistor_196 (.in(transistor_190_out), .out(AND), .gate(nClear));
  Transistor #(.\type ("n")) transistor_197 (.in(1'b0), .out(transistor_197_out), .gate(Main_bus[0]));
  Transistor #(.\type ("n")) transistor_198 (.in(transistor_199_out), .out(in_6[0]), .gate(transistor_197_out));
  Pull_Resistor #(.pull(1)) pull_resistor_104 (.node(transistor_197_out));
  Transistor #(.\type ("n")) transistor_199 (.in(1'b0), .out(transistor_199_out), .gate(Main_bus____bus_out));
  Pull_Resistor #(.pull(1)) pull_resistor_105 (.node(pull_resistor_105_node));
  Transistor #(.\type ("n")) transistor_200 (.in(transistor_202_out), .out(Main_bus[0]), .gate(pull_resistor_105_node));
  Transistor #(.\type ("n")) transistor_201 (.in(1'b0), .out(pull_resistor_105_node), .gate(in_6[0]));
  Transistor #(.\type ("n")) transistor_202 (.in(1'b0), .out(transistor_202_out), .gate(bus_out____Main_bus));
  Transistor #(.\type ("n")) transistor_203 (.in(1'b0), .out(transistor_203_out), .gate(nBNU));
  Pull_Resistor #(.pull(1)) pull_resistor_106 (.node(transistor_203_out));
  Pull_Resistor #(.pull(1)) pull_resistor_107 (.node(pull_resistor_107_node));
  Transistor #(.\type ("n")) transistor_204 (.in(1'b0), .out(pull_resistor_107_node), .gate(FLAG_U));
  Transistor #(.\type ("n")) transistor_205 (.in(transistor_195_out), .out(ADD), .gate(nADC));
  Pull_Resistor #(.pull(1)) pull_resistor_108 (.node(ADD));
  Transistor #(.\type ("n")) transistor_206 (.in(1'b0), .out(transistor_119_out), .gate(transistor_203_out));
  Transistor #(.\type ("n"), .gate("br")) transistor_207 (.in(1'b0), .out(transistor_203_out), .gate(FLAG_U));
  Transistor #(.\type ("n")) transistor_208 (.in(transistor_232_out), .out(R_W_out), .gate(nStore));
  Pull_Resistor #(.pull(1)) pull_resistor_109 (.node(R_W_out));
  Transistor #(.\type ("n")) transistor_209 (.in(1'b0), .out(XOR), .gate(nXOR));
  Pull_Resistor #(.pull(1)) pull_resistor_110 (.node(XOR));
  Transistor #(.\type ("n")) transistor_210 (.in(1'b0), .out(RS), .gate(nRS));
  Pull_Resistor #(.pull(1)) pull_resistor_111 (.node(RS));
  Transistor #(.\type ("n")) transistor_211 (.in(1'b0), .out(transistor_211_out), .gate(nStore));
  Transistor #(.\type ("n")) transistor_212 (.in(transistor_211_out), .out(transistor_212_out), .gate(nMOV));
  Pull_Resistor #(.pull(1)) pull_resistor_112 (.node(pull_resistor_112_node));
  Transistor #(.\type ("n")) transistor_213 (.in(transistor_215_out), .out(in_6[1]), .gate(pull_resistor_112_node));
  Transistor #(.\type ("n")) transistor_214 (.in(1'b0), .out(pull_resistor_112_node), .gate(Main_bus[1]));
  Transistor #(.\type ("n")) transistor_215 (.in(1'b0), .out(transistor_215_out), .gate(Main_bus____bus_out));
  Transistor #(.\type ("n")) transistor_216 (.in(transistor_218_out), .out(Main_bus[1]), .gate(pull_resistor_113_node));
  Pull_Resistor #(.pull(1)) pull_resistor_113 (.node(pull_resistor_113_node));
  Transistor #(.\type ("n")) transistor_217 (.in(1'b0), .out(pull_resistor_113_node), .gate(in_6[1]));
  Transistor #(.\type ("n")) transistor_218 (.in(1'b0), .out(transistor_218_out), .gate(bus_out____Main_bus));
  Transistor #(.\type ("n")) transistor_219 (.in(1'b0), .out(transistor_119_out), .gate(pull_resistor_114_node));
  Pull_Resistor #(.pull(1)) pull_resistor_114 (.node(pull_resistor_114_node));
  Transistor #(.\type ("n"), .gate("br")) transistor_220 (
    .in(1'b0), .out(pull_resistor_114_node), .gate(pull_resistor_119_node));
  Transistor #(.\type ("n")) transistor_221 (.in(1'b0), .out(pull_resistor_114_node), .gate(nBOC));
  Pull_Resistor #(.pull(1)) pull_resistor_115 (.node(pull_resistor_115_node));
  Transistor #(.\type ("n"), .gate("br")) transistor_222 (
    .in(transistor_224_out), .out(transistor_222_out), .gate(TIME_STEP_0or1or2));
  Transistor #(.\type ("n")) transistor_223 (.in(transistor_225_out), .out(transistor_222_out), .gate(TIME_STEP_0or1));
  Pull_Resistor #(.pull(1)) pull_resistor_116 (.node(transistor_222_out));
  Transistor #(.\type ("n"), .gate("br")) transistor_224 (.in(1'b0), .out(transistor_224_out), .gate(Read_Write_ins));
  Transistor #(.\type ("n")) transistor_225 (.in(1'b0), .out(transistor_225_out), .gate(jump_type_instruction));
  Pull_Resistor #(.pull(1)) pull_resistor_117 (.node(OR));
  Transistor #(.\type ("n")) transistor_226 (.in(transistor_212_out), .out(OR), .gate(nOR));
  Pull_Resistor #(.pull(1)) pull_resistor_118 (.node(pull_resistor_118_node));
  Transistor #(.\type ("n")) transistor_227 (.in(1'b0), .out(pull_resistor_118_node), .gate(nBNC));
  Pull_Resistor #(.pull(1)) pull_resistor_119 (.node(pull_resistor_119_node));
  Transistor #(.\type ("n")) transistor_228 (.in(1'b0), .out(pull_resistor_119_node), .gate(FLAG_C));
  Pull_Resistor #(.pull(1)) pull_resistor_120 (.node(pull_resistor_120_node));
  Transistor #(.\type ("n")) transistor_229 (
    .in(transistor_230_out), .out(pull_resistor_120_node), .gate(pull_resistor_115_node));
  Transistor #(.\type ("n")) transistor_230 (.in(1'b0), .out(transistor_230_out), .gate(transistor_222_out));
  Transistor #(.\type ("n")) transistor_231 (
    .in(transistor_232_out), .out(Read_From_stored_Address), .gate(Read_Write_ins));
  Pull_Resistor #(.pull(1)) pull_resistor_121 (.node(Read_From_stored_Address));
  Transistor #(.\type ("n")) transistor_232 (.in(transistor_233_out), .out(transistor_232_out), .gate(nTIME_STEP_0));
  Transistor #(.\type ("n")) transistor_233 (.in(1'b0), .out(transistor_233_out), .gate(TIME_STEP_2));
  Transistor #(.\type ("n")) transistor_234 (.in(1'b0), .out(transistor_234_out), .gate(nADC));
  Pull_Resistor #(.pull(1)) pull_resistor_122 (.node(transistor_234_out));
  Pull_Resistor #(.pull(1)) pull_resistor_123 (.node(pull_resistor_123_node));
  Transistor #(.\type ("n")) transistor_235 (.in(transistor_237_out), .out(in_6[2]), .gate(pull_resistor_123_node));
  Transistor #(.\type ("n")) transistor_236 (.in(1'b0), .out(pull_resistor_123_node), .gate(Main_bus[2]));
  Transistor #(.\type ("n")) transistor_237 (.in(1'b0), .out(transistor_237_out), .gate(Main_bus____bus_out));
  Transistor #(.\type ("n")) transistor_238 (.in(transistor_240_out), .out(Main_bus[2]), .gate(pull_resistor_124_node));
  Pull_Resistor #(.pull(1)) pull_resistor_124 (.node(pull_resistor_124_node));
  Transistor #(.\type ("n")) transistor_239 (.in(1'b0), .out(pull_resistor_124_node), .gate(in_6[2]));
  Transistor #(.\type ("n")) transistor_240 (.in(1'b0), .out(transistor_240_out), .gate(bus_out____Main_bus));
  Transistor #(.\type ("n")) transistor_241 (.in(1'b0), .out(transistor_119_out), .gate(pull_resistor_118_node));
  Transistor #(.\type ("n"), .gate("br")) transistor_242 (.in(1'b0), .out(pull_resistor_118_node), .gate(FLAG_C));
  Pull_Resistor #(.pull(1)) pull_resistor_125 (.node(Read_New_Instruction));
  Transistor #(.\type ("n")) transistor_243 (.in(1'b0), .out(Read_New_Instruction), .gate(pull_resistor_120_node));
  Pull_Resistor #(.pull(1)) pull_resistor_126 (.node(pull_resistor_126_node));
  Transistor #(.\type ("n")) transistor_244 (
    .in(transistor_245_out), .out(pull_resistor_126_node), .gate(transistor_234_out));
  Transistor #(.\type ("n")) transistor_245 (.in(1'b0), .out(transistor_245_out), .gate(FLAG_C));
  Pull_Resistor pull_resistor_127 (.node(in_1));
  Pull_Resistor pull_resistor_128 (.node(in_2));
  Pull_Resistor pull_resistor_129 (.node(in_3));
  Pull_Resistor pull_resistor_130 (.node(in_4));
  Pull_Resistor pull_resistor_131 (.node(in_5));
  Pull_Resistor #(.pull(1)) pull_resistor_132 (.node(transistor_119_out));
  Transistor #(.\type ("n")) transistor_246 (.in(1'b0), .out(transistor_119_out), .gate(transistor_247_out));
  Transistor #(.\type ("n")) transistor_247 (.in(1'b0), .out(transistor_247_out), .gate(nJMP));
  Pull_Resistor #(.pull(1)) pull_resistor_133 (.node(transistor_247_out));
  Transistor #(.\type ("n")) transistor_248 (.in(transistor_249_out), .out(Carry_in), .gate(nINC));
  Pull_Resistor #(.pull(1)) pull_resistor_134 (.node(Carry_in));
  Transistor #(.\type ("n")) transistor_249 (.in(1'b0), .out(transistor_249_out), .gate(pull_resistor_126_node));
  Transistor #(.\type ("n")) transistor_250 (.in(1'b0), .out(transistor_250_out), .gate(Main_bus[3]));
  Pull_Resistor #(.pull(1)) pull_resistor_135 (.node(transistor_250_out));
  Transistor #(.\type ("n")) transistor_251 (.in(transistor_252_out), .out(in_6[3]), .gate(transistor_250_out));
  Transistor #(.\type ("n")) transistor_252 (.in(1'b0), .out(transistor_252_out), .gate(Main_bus____bus_out));
  Transistor #(.\type ("n")) transistor_253 (.in(1'b0), .out(transistor_253_out), .gate(in_6[3]));
  Pull_Resistor #(.pull(1)) pull_resistor_136 (.node(transistor_253_out));
  Transistor #(.\type ("n")) transistor_254 (.in(transistor_255_out), .out(Main_bus[3]), .gate(transistor_253_out));
  Transistor #(.\type ("n")) transistor_255 (.in(1'b0), .out(transistor_255_out), .gate(bus_out____Main_bus));
  Transistor #(.\type ("n")) transistor_256 (.in(1'b0), .out(Commit_jump), .gate(transistor_119_out));
  Pull_Resistor #(.pull(1)) pull_resistor_137 (.node(Commit_jump));
  Transistor #(.\type ("n")) transistor_257 (
    .in(transistor_258_out), .out(Store_Address_plus_plus), .gate(TIME_STEP_IN_2));
  Pull_Resistor #(.pull(1)) pull_resistor_138 (.node(Store_Address_plus_plus));
  Transistor #(.\type ("n")) transistor_258 (.in(1'b0), .out(transistor_258_out), .gate(Commit_jump));
  Pull_Resistor #(.pull(1)) pull_resistor_139 (.node(pull_resistor_139_node));
  Transistor #(.\type ("n")) transistor_259 (.in(transistor_261_out), .out(in_6[4]), .gate(pull_resistor_139_node));
  Transistor #(.\type ("n")) transistor_260 (.in(1'b0), .out(pull_resistor_139_node), .gate(Main_bus[4]));
  Transistor #(.\type ("n")) transistor_261 (.in(1'b0), .out(transistor_261_out), .gate(Main_bus____bus_out));
  Pull_Resistor #(.pull(1)) pull_resistor_140 (.node(pull_resistor_140_node));
  Transistor #(.\type ("n")) transistor_262 (.in(1'b0), .out(pull_resistor_140_node), .gate(in_6[4]));
  Transistor #(.\type ("n")) transistor_263 (.in(transistor_264_out), .out(Main_bus[4]), .gate(pull_resistor_140_node));
  Transistor #(.\type ("n")) transistor_264 (.in(1'b0), .out(transistor_264_out), .gate(bus_out____Main_bus));
  Transistor #(.\type ("n")) transistor_265 (.in(1'b0), .out(transistor_265_out), .gate(Main_bus[5]));
  Transistor #(.\type ("n")) transistor_266 (.in(transistor_267_out), .out(in_6[5]), .gate(transistor_265_out));
  Pull_Resistor #(.pull(1)) pull_resistor_141 (.node(transistor_265_out));
  Transistor #(.\type ("n")) transistor_267 (.in(1'b0), .out(transistor_267_out), .gate(Main_bus____bus_out));
  Transistor #(.\type ("n")) transistor_268 (.in(transistor_270_out), .out(Main_bus[5]), .gate(pull_resistor_142_node));
  Pull_Resistor #(.pull(1)) pull_resistor_142 (.node(pull_resistor_142_node));
  Transistor #(.\type ("n")) transistor_269 (.in(1'b0), .out(pull_resistor_142_node), .gate(in_6[5]));
  Transistor #(.\type ("n")) transistor_270 (.in(1'b0), .out(transistor_270_out), .gate(bus_out____Main_bus));
  Register register_2 (
    .D({NEXT_ADR_7, NEXT_ADR_6, NEXT_ADR_5, NEXT_ADR_4, NEXT_ADR_3, NEXT_ADR_2, NEXT_ADR_1, NEXT_ADR_0}),
    .en(pull_resistor_143_node),
    .Q({STORED_ADR_7, STORED_ADR_6, STORED_ADR_5, STORED_ADR_4, STORED_ADR_3, STORED_ADR_2, STORED_ADR_1, STORED_ADR_0}),
    .clk(clock_4_out), .clr(in_7));
  Pull_Resistor #(.pull(1)) pull_resistor_143 (.node(pull_resistor_143_node));
  Clock clock_4 (.out(clock_4_out));
  Transistor #(.\type ("n")) transistor_271 (.in(transistor_273_out), .out(in_6[6]), .gate(pull_resistor_144_node));
  Pull_Resistor #(.pull(1)) pull_resistor_144 (.node(pull_resistor_144_node));
  Transistor #(.\type ("n")) transistor_272 (.in(1'b0), .out(pull_resistor_144_node), .gate(Main_bus[6]));
  Transistor #(.\type ("n")) transistor_273 (.in(1'b0), .out(transistor_273_out), .gate(Main_bus____bus_out));
  Pull_Resistor #(.pull(1)) pull_resistor_145 (.node(pull_resistor_145_node));
  Transistor #(.\type ("n")) transistor_274 (.in(1'b0), .out(pull_resistor_145_node), .gate(in_6[6]));
  Transistor #(.\type ("n")) transistor_275 (.in(transistor_276_out), .out(Main_bus[6]), .gate(pull_resistor_145_node));
  Transistor #(.\type ("n")) transistor_276 (.in(1'b0), .out(transistor_276_out), .gate(bus_out____Main_bus));
  Transistor #(.\type ("n")) transistor_277 (.in(1'b0), .out(transistor_277_out), .gate(Store_Address_plus_plus));
  Pull_Resistor #(.pull(1)) pull_resistor_146 (.node(transistor_277_out));
  Pull_Resistor #(.pull(1)) pull_resistor_147 (.node(pull_resistor_147_node));
  Transistor #(.\type ("n")) transistor_278 (.in(1'b0), .out(pull_resistor_147_node), .gate(Read_From_stored_Address));
  Register #(.trigger("falling")) register_3 (
    .D(in_6), .en(TIME_STEP_1),
    .Q({TEMP_ADR_7, TEMP_ADR_6, TEMP_ADR_5, TEMP_ADR_4, TEMP_ADR_3, TEMP_ADR_2, TEMP_ADR_1, TEMP_ADR_0}),
    .clk(clock_5_out), .clr(in_7));
  Clock clock_5 (.out(clock_5_out));
  Transistor #(.\type ("n")) transistor_279 (.in(transistor_280_out), .out(transistor_279_out), .gate(ADR___0));
  Pull_Resistor #(.pull(1)) pull_resistor_148 (.node(transistor_279_out));
  Transistor #(.\type ("n")) transistor_280 (.in(1'b0), .out(transistor_280_out), .gate(Store_Address_plus_plus));
  Transistor #(.\type ("n")) transistor_281 (.in(transistor_282_out), .out(transistor_279_out), .gate(TEMP_ADR_0));
  Transistor #(.\type ("n")) transistor_282 (.in(1'b0), .out(transistor_282_out), .gate(transistor_277_out));
  Pull_Resistor #(.pull(1)) pull_resistor_149 (.node(NEXT_ADR_0));
  Transistor #(.\type ("n")) transistor_283 (.in(1'b0), .out(NEXT_ADR_0), .gate(transistor_279_out));
  Transistor #(.\type ("n")) transistor_284 (.in(transistor_285_out), .out(transistor_284_out), .gate(STORED_ADR_0));
  Pull_Resistor #(.pull(1)) pull_resistor_150 (.node(transistor_284_out));
  Transistor #(.\type ("n")) transistor_285 (.in(1'b0), .out(transistor_285_out), .gate(Read_From_stored_Address));
  Transistor #(.\type ("n")) transistor_286 (.in(transistor_287_out), .out(transistor_284_out), .gate(TEMP_ADR_0));
  Transistor #(.\type ("n")) transistor_287 (.in(1'b0), .out(transistor_287_out), .gate(pull_resistor_147_node));
  Transistor #(.\type ("n")) transistor_288 (.in(1'b0), .out(ADR_0), .gate(transistor_284_out));
  Pull_Resistor #(.pull(1)) pull_resistor_151 (.node(ADR_0));
  Transistor #(.\type ("n")) transistor_289 (.in(1'b0), .out(transistor_289_out), .gate(Main_bus[7]));
  Pull_Resistor #(.pull(1)) pull_resistor_152 (.node(transistor_289_out));
  Transistor #(.\type ("n")) transistor_290 (.in(transistor_291_out), .out(in_6[7]), .gate(transistor_289_out));
  Transistor #(.\type ("n")) transistor_291 (.in(1'b0), .out(transistor_291_out), .gate(Main_bus____bus_out));
  Transistor #(.\type ("n")) transistor_292 (.in(1'b0), .out(transistor_292_out), .gate(in_6[7]));
  Transistor #(.\type ("n")) transistor_293 (.in(transistor_294_out), .out(Main_bus[7]), .gate(transistor_292_out));
  Pull_Resistor #(.pull(1)) pull_resistor_153 (.node(transistor_292_out));
  Transistor #(.\type ("n")) transistor_294 (.in(1'b0), .out(transistor_294_out), .gate(bus_out____Main_bus));
  Transistor #(.\type ("n")) transistor_295 (.in(transistor_296_out), .out(transistor_295_out), .gate(ADR___1));
  Pull_Resistor #(.pull(1)) pull_resistor_154 (.node(transistor_295_out));
  Transistor #(.\type ("n")) transistor_296 (.in(1'b0), .out(transistor_296_out), .gate(Store_Address_plus_plus));
  Transistor #(.\type ("n")) transistor_297 (.in(transistor_298_out), .out(transistor_295_out), .gate(TEMP_ADR_1));
  Transistor #(.\type ("n")) transistor_298 (.in(1'b0), .out(transistor_298_out), .gate(transistor_277_out));
  Transistor #(.\type ("n")) transistor_299 (.in(1'b0), .out(NEXT_ADR_1), .gate(transistor_295_out));
  Pull_Resistor #(.pull(1)) pull_resistor_155 (.node(NEXT_ADR_1));
  Pull_Resistor #(.pull(1)) pull_resistor_156 (.node(pull_resistor_156_node));
  Transistor #(.\type ("n")) transistor_300 (
    .in(transistor_301_out), .out(pull_resistor_156_node), .gate(STORED_ADR_1));
  Transistor #(.\type ("n")) transistor_301 (.in(1'b0), .out(transistor_301_out), .gate(Read_From_stored_Address));
  Transistor #(.\type ("n")) transistor_302 (.in(transistor_303_out), .out(pull_resistor_156_node), .gate(TEMP_ADR_1));
  Transistor #(.\type ("n")) transistor_303 (.in(1'b0), .out(transistor_303_out), .gate(pull_resistor_147_node));
  Transistor #(.\type ("n")) transistor_304 (.in(1'b0), .out(ADR_1), .gate(pull_resistor_156_node));
  Pull_Resistor #(.pull(1)) pull_resistor_157 (.node(ADR_1));
  Pull_Resistor #(.pull(1)) pull_resistor_158 (.node(pull_resistor_158_node));
  Transistor #(.\type ("n")) transistor_305 (.in(transistor_306_out), .out(pull_resistor_158_node), .gate(ADR___2));
  Transistor #(.\type ("n")) transistor_306 (.in(1'b0), .out(transistor_306_out), .gate(Store_Address_plus_plus));
  Transistor #(.\type ("n")) transistor_307 (.in(transistor_308_out), .out(pull_resistor_158_node), .gate(TEMP_ADR_2));
  Transistor #(.\type ("n")) transistor_308 (.in(1'b0), .out(transistor_308_out), .gate(transistor_277_out));
  Pull_Resistor #(.pull(1)) pull_resistor_159 (.node(NEXT_ADR_2));
  Transistor #(.\type ("n")) transistor_309 (.in(1'b0), .out(NEXT_ADR_2), .gate(pull_resistor_158_node));
  Transistor #(.\type ("n")) transistor_310 (.in(transistor_311_out), .out(transistor_310_out), .gate(STORED_ADR_2));
  Pull_Resistor #(.pull(1)) pull_resistor_160 (.node(transistor_310_out));
  Transistor #(.\type ("n")) transistor_311 (.in(1'b0), .out(transistor_311_out), .gate(Read_From_stored_Address));
  Transistor #(.\type ("n")) transistor_312 (.in(transistor_313_out), .out(transistor_310_out), .gate(TEMP_ADR_2));
  Transistor #(.\type ("n")) transistor_313 (.in(1'b0), .out(transistor_313_out), .gate(pull_resistor_147_node));
  Transistor #(.\type ("n")) transistor_314 (.in(1'b0), .out(ADR_2), .gate(transistor_310_out));
  Pull_Resistor #(.pull(1)) pull_resistor_161 (.node(ADR_2));
  Transistor #(.\type ("n")) transistor_315 (.in(transistor_316_out), .out(transistor_315_out), .gate(ADR___3));
  Pull_Resistor #(.pull(1)) pull_resistor_162 (.node(transistor_315_out));
  Transistor #(.\type ("n")) transistor_316 (.in(1'b0), .out(transistor_316_out), .gate(Store_Address_plus_plus));
  Transistor #(.\type ("n")) transistor_317 (.in(transistor_318_out), .out(transistor_315_out), .gate(TEMP_ADR_3));
  Transistor #(.\type ("n")) transistor_318 (.in(1'b0), .out(transistor_318_out), .gate(transistor_277_out));
  Pull_Resistor #(.pull(1)) pull_resistor_163 (.node(NEXT_ADR_3));
  Transistor #(.\type ("n")) transistor_319 (.in(1'b0), .out(NEXT_ADR_3), .gate(transistor_315_out));
  Transistor #(.\type ("n")) transistor_320 (.in(transistor_321_out), .out(transistor_320_out), .gate(STORED_ADR_3));
  Pull_Resistor #(.pull(1)) pull_resistor_164 (.node(transistor_320_out));
  Transistor #(.\type ("n")) transistor_321 (.in(1'b0), .out(transistor_321_out), .gate(Read_From_stored_Address));
  Transistor #(.\type ("n")) transistor_322 (.in(transistor_323_out), .out(transistor_320_out), .gate(TEMP_ADR_3));
  Transistor #(.\type ("n")) transistor_323 (.in(1'b0), .out(transistor_323_out), .gate(pull_resistor_147_node));
  Pull_Resistor #(.pull(1)) pull_resistor_165 (.node(ADR_3));
  Transistor #(.\type ("n")) transistor_324 (.in(1'b0), .out(ADR_3), .gate(transistor_320_out));
  Pull_Resistor #(.pull(1)) pull_resistor_166 (.node(pull_resistor_166_node));
  Transistor #(.\type ("n")) transistor_325 (.in(transistor_326_out), .out(pull_resistor_166_node), .gate(ADR___4));
  Transistor #(.\type ("n")) transistor_326 (.in(1'b0), .out(transistor_326_out), .gate(Store_Address_plus_plus));
  Transistor #(.\type ("n")) transistor_327 (.in(transistor_328_out), .out(pull_resistor_166_node), .gate(TEMP_ADR_4));
  Transistor #(.\type ("n")) transistor_328 (.in(1'b0), .out(transistor_328_out), .gate(transistor_277_out));
  Transistor #(.\type ("n")) transistor_329 (.in(1'b0), .out(NEXT_ADR_4), .gate(pull_resistor_166_node));
  Pull_Resistor #(.pull(1)) pull_resistor_167 (.node(NEXT_ADR_4));
  Transistor #(.\type ("n")) transistor_330 (.in(transistor_331_out), .out(transistor_330_out), .gate(STORED_ADR_4));
  Pull_Resistor #(.pull(1)) pull_resistor_168 (.node(transistor_330_out));
  Transistor #(.\type ("n")) transistor_331 (.in(1'b0), .out(transistor_331_out), .gate(Read_From_stored_Address));
  Transistor #(.\type ("n")) transistor_332 (.in(transistor_333_out), .out(transistor_330_out), .gate(TEMP_ADR_4));
  Transistor #(.\type ("n")) transistor_333 (.in(1'b0), .out(transistor_333_out), .gate(pull_resistor_147_node));
  Register register_4 (
    .D({FLAG_STORE_C, FLAG_STORE_O, FLAG_STORE_U, FLAG_STORE_Z, FLAG_STORE_N, TIME_STEP_IN_2, TIME_STEP_IN_1, TIME_STEP_IN_0}),
    .en(1'b1), .Q({FLAG_C, FLAG_O, FLAG_U, FLAG_Z, FLAG_N, TIME_STEP_2, TIME_STEP_1, TIME_STEP_0}),
    .clk(clock_6_out), .clr(in_7));
  Clock clock_6 (.out(clock_6_out));
  Pull_Resistor #(.pull(1)) pull_resistor_169 (.node(pull_resistor_169_node));
  Transistor #(.\type ("n")) transistor_334 (.in(transistor_335_out), .out(pull_resistor_169_node), .gate(ADR___5));
  Transistor #(.\type ("n")) transistor_335 (.in(1'b0), .out(transistor_335_out), .gate(Store_Address_plus_plus));
  Transistor #(.\type ("n")) transistor_336 (.in(transistor_337_out), .out(pull_resistor_169_node), .gate(TEMP_ADR_5));
  Transistor #(.\type ("n")) transistor_337 (.in(1'b0), .out(transistor_337_out), .gate(transistor_277_out));
  Pull_Resistor #(.pull(1)) pull_resistor_170 (.node(pull_resistor_170_node));
  Transistor #(.\type ("n")) transistor_338 (
    .in(transistor_339_out), .out(pull_resistor_170_node), .gate(STORED_ADR_5));
  Transistor #(.\type ("n")) transistor_339 (.in(1'b0), .out(transistor_339_out), .gate(Read_From_stored_Address));
  Transistor #(.\type ("n")) transistor_340 (.in(transistor_341_out), .out(pull_resistor_170_node), .gate(TEMP_ADR_5));
  Transistor #(.\type ("n")) transistor_341 (.in(1'b0), .out(transistor_341_out), .gate(pull_resistor_147_node));
  Transistor #(.\type ("n")) transistor_342 (.in(1'b0), .out(ADR_4), .gate(transistor_330_out));
  Pull_Resistor #(.pull(1)) pull_resistor_171 (.node(ADR_4));
  Transistor #(.\type ("n")) transistor_343 (.in(transistor_344_out), .out(transistor_343_out), .gate(ADR___6));
  Pull_Resistor #(.pull(1)) pull_resistor_172 (.node(transistor_343_out));
  Transistor #(.\type ("n")) transistor_344 (.in(1'b0), .out(transistor_344_out), .gate(Store_Address_plus_plus));
  Transistor #(.\type ("n")) transistor_345 (.in(transistor_346_out), .out(transistor_343_out), .gate(TEMP_ADR_6));
  Transistor #(.\type ("n")) transistor_346 (.in(1'b0), .out(transistor_346_out), .gate(transistor_277_out));
  Transistor #(.\type ("n")) transistor_347 (.in(1'b0), .out(NEXT_ADR_5), .gate(pull_resistor_169_node));
  Pull_Resistor #(.pull(1)) pull_resistor_173 (.node(NEXT_ADR_5));
  Transistor #(.\type ("n")) transistor_348 (.in(transistor_349_out), .out(transistor_348_out), .gate(STORED_ADR_6));
  Transistor #(.\type ("n")) transistor_349 (.in(1'b0), .out(transistor_349_out), .gate(Read_From_stored_Address));
  Transistor #(.\type ("n")) transistor_350 (.in(transistor_351_out), .out(transistor_348_out), .gate(TEMP_ADR_6));
  Transistor #(.\type ("n")) transistor_351 (.in(1'b0), .out(transistor_351_out), .gate(pull_resistor_147_node));
  Transistor #(.\type ("n")) transistor_352 (.in(1'b0), .out(ADR_5), .gate(pull_resistor_170_node));
  Pull_Resistor #(.pull(1)) pull_resistor_174 (.node(ADR_5));
  Pull_Resistor #(.pull(1)) pull_resistor_175 (.node(pull_resistor_175_node));
  Clock clock_7 (.out(clock_7_out));
  Transistor #(.\type ("n")) transistor_353 (.in(1'b0), .out(transistor_353_out), .gate(nTIME_STEP_0));
  Pull_Resistor #(.pull(1)) pull_resistor_176 (.node(transistor_353_out));
  Transistor #(.\type ("n")) transistor_354 (.in(1'b0), .out(nTIME_STEP_0), .gate(TIME_STEP_0));
  Pull_Resistor #(.pull(1)) pull_resistor_177 (.node(nTIME_STEP_0));
  Pull_Resistor #(.pull(1)) pull_resistor_178 (.node(pull_resistor_178_node));
  Pull_Resistor #(.pull(1)) pull_resistor_179 (.node(pull_resistor_179_node));
  Transistor #(.\type ("n")) transistor_355 (.in(1'b0), .out(pull_resistor_178_node), .gate(pull_resistor_179_node));
  Transistor #(.\type ("n")) transistor_356 (.in(1'b0), .out(pull_resistor_179_node), .gate(TIME_STEP_1));
  Transistor #(.\type ("n")) transistor_357 (.in(transistor_358_out), .out(transistor_357_out), .gate(FLAG_N));
  Pull_Resistor #(.pull(1)) pull_resistor_180 (.node(transistor_357_out));
  Transistor #(.\type ("n")) transistor_358 (.in(1'b0), .out(transistor_358_out), .gate(pull_resistor_181_node));
  Pull_Resistor #(.pull(1)) pull_resistor_181 (.node(pull_resistor_181_node));
  Transistor #(.\type ("n")) transistor_359 (.in(1'b0), .out(pull_resistor_181_node), .gate(READ_FALG));
  Transistor #(.\type ("n")) transistor_360 (.in(transistor_361_out), .out(transistor_357_out), .gate(in_5));
  Transistor #(.\type ("n")) transistor_361 (.in(1'b0), .out(transistor_361_out), .gate(READ_FALG));
  Transistor #(.\type ("n")) transistor_362 (.in(transistor_363_out), .out(transistor_362_out), .gate(ADR___7));
  Transistor #(.\type ("n")) transistor_363 (.in(1'b0), .out(transistor_363_out), .gate(Store_Address_plus_plus));
  Transistor #(.\type ("n")) transistor_364 (.in(transistor_365_out), .out(transistor_362_out), .gate(TEMP_ADR_7));
  Transistor #(.\type ("n")) transistor_365 (.in(1'b0), .out(transistor_365_out), .gate(transistor_277_out));
  Transistor #(.\type ("n")) transistor_366 (.in(1'b0), .out(NEXT_ADR_6), .gate(transistor_343_out));
  Pull_Resistor #(.pull(1)) pull_resistor_182 (.node(NEXT_ADR_6));
  Pull_Resistor #(.pull(1)) pull_resistor_183 (.node(transistor_348_out));
  Pull_Resistor #(.pull(1)) pull_resistor_184 (.node(ADR_6));
  Transistor #(.\type ("n")) transistor_367 (.in(1'b0), .out(ADR_6), .gate(transistor_348_out));
  Register register_5 (
    .D({NEXT_ADR_15, NEXT_ADR_14, NEXT_ADR_13, NEXT_ADR_12, NEXT_ADR_11, NEXT_ADR_10, NEXT_ADR_9, NEXT_ADR_8}),
    .en(pull_resistor_175_node),
    .Q({STORED_ADR_15, STORED_ADR_14, STORED_ADR_13, STORED_ADR_12, STORED_ADR_11, STORED_ADR_10, STORED_ADR_9, STORED_ADR_8}),
    .clk(clock_7_out), .clr(in_7));
  Pull_Resistor #(.pull(1)) pull_resistor_185 (.node(pull_resistor_185_node));
  Transistor #(.\type ("n")) transistor_368 (.in(1'b0), .out(pull_resistor_185_node), .gate(transistor_353_out));
  Transistor #(.\type ("n")) transistor_369 (.in(1'b0), .out(TIME_STEP_IN_1), .gate(pull_resistor_185_node));
  Pull_Resistor #(.pull(1)) pull_resistor_186 (.node(TIME_STEP_IN_1));
  Pull_Resistor #(.pull(1)) pull_resistor_187 (.node(pull_resistor_187_node));
  Transistor #(.\type ("n")) transistor_370 (.in(1'b0), .out(TIME_STEP_IN_2), .gate(pull_resistor_187_node));
  Pull_Resistor #(.pull(1)) pull_resistor_188 (.node(TIME_STEP_IN_2));
  Transistor #(.\type ("n")) transistor_371 (.in(1'b0), .out(pull_resistor_187_node), .gate(pull_resistor_178_node));
  Pull_Resistor #(.pull(1)) pull_resistor_189 (.node(pull_resistor_189_node));
  Transistor #(.\type ("n")) transistor_372 (.in(transistor_373_out), .out(pull_resistor_189_node), .gate(FLAG_Z));
  Transistor #(.\type ("n")) transistor_373 (.in(1'b0), .out(transistor_373_out), .gate(pull_resistor_181_node));
  Transistor #(.\type ("n")) transistor_374 (.in(transistor_375_out), .out(pull_resistor_189_node), .gate(in_4));
  Transistor #(.\type ("n")) transistor_375 (.in(1'b0), .out(transistor_375_out), .gate(READ_FALG));
  Transistor #(.\type ("n")) transistor_376 (.in(1'b0), .out(FLAG_STORE_Z), .gate(pull_resistor_189_node));
  Pull_Resistor #(.pull(1)) pull_resistor_190 (.node(FLAG_STORE_Z));
  Pull_Resistor #(.pull(1)) pull_resistor_191 (.node(FLAG_STORE_N));
  Transistor #(.\type ("n")) transistor_377 (.in(1'b0), .out(FLAG_STORE_N), .gate(transistor_357_out));
  Pull_Resistor #(.pull(1)) pull_resistor_192 (.node(transistor_362_out));
  Transistor #(.\type ("n")) transistor_378 (.in(1'b0), .out(NEXT_ADR_7), .gate(transistor_362_out));
  Pull_Resistor #(.pull(1)) pull_resistor_193 (.node(NEXT_ADR_7));
  Pull_Resistor #(.pull(1)) pull_resistor_194 (.node(pull_resistor_194_node));
  Transistor #(.\type ("n")) transistor_379 (
    .in(transistor_380_out), .out(pull_resistor_194_node), .gate(STORED_ADR_7));
  Transistor #(.\type ("n")) transistor_380 (.in(1'b0), .out(transistor_380_out), .gate(Read_From_stored_Address));
  Transistor #(.\type ("n")) transistor_381 (.in(transistor_382_out), .out(pull_resistor_194_node), .gate(TEMP_ADR_7));
  Transistor #(.\type ("n")) transistor_382 (.in(1'b0), .out(transistor_382_out), .gate(pull_resistor_147_node));
  Pull_Resistor #(.pull(1)) pull_resistor_195 (.node(ADR_7));
  Transistor #(.\type ("n")) transistor_383 (.in(1'b0), .out(ADR_7), .gate(pull_resistor_194_node));
  Clock clock_8 (.out(clock_8_out));
  Pull_Resistor #(.pull(1)) pull_resistor_196 (.node(pull_resistor_196_node));
  Pull_Resistor #(.pull(1)) pull_resistor_197 (.node(pull_resistor_197_node));
  Transistor #(.\type ("n")) transistor_384 (.in(transistor_387_out), .out(pull_resistor_196_node), .gate(FLAG_U));
  Transistor #(.\type ("n")) transistor_385 (.in(transistor_386_out), .out(pull_resistor_197_node), .gate(FLAG_O));
  Transistor #(.\type ("n")) transistor_386 (.in(1'b0), .out(transistor_386_out), .gate(pull_resistor_181_node));
  Transistor #(.\type ("n")) transistor_387 (.in(1'b0), .out(transistor_387_out), .gate(pull_resistor_181_node));
  Transistor #(.\type ("n")) transistor_388 (.in(transistor_390_out), .out(pull_resistor_196_node), .gate(in_3));
  Transistor #(.\type ("n")) transistor_389 (.in(transistor_391_out), .out(pull_resistor_197_node), .gate(in_2));
  Transistor #(.\type ("n")) transistor_390 (.in(1'b0), .out(transistor_390_out), .gate(READ_FALG));
  Transistor #(.\type ("n")) transistor_391 (.in(1'b0), .out(transistor_391_out), .gate(READ_FALG));
  Transistor #(.\type ("n")) transistor_392 (.in(1'b0), .out(FLAG_STORE_U), .gate(pull_resistor_196_node));
  Pull_Resistor #(.pull(1)) pull_resistor_198 (.node(FLAG_STORE_U));
  Transistor #(.\type ("n")) transistor_393 (.in(transistor_394_out), .out(transistor_393_out), .gate(ADR___8));
  Pull_Resistor #(.pull(1)) pull_resistor_199 (.node(transistor_393_out));
  Transistor #(.\type ("n")) transistor_394 (.in(1'b0), .out(transistor_394_out), .gate(Store_Address_plus_plus));
  Transistor #(.\type ("n")) transistor_395 (.in(transistor_396_out), .out(transistor_393_out), .gate(TEMP_ADR_8));
  Transistor #(.\type ("n")) transistor_396 (.in(1'b0), .out(transistor_396_out), .gate(transistor_277_out));
  Pull_Resistor #(.pull(1)) pull_resistor_200 (.node(NEXT_ADR_8));
  Transistor #(.\type ("n")) transistor_397 (.in(1'b0), .out(NEXT_ADR_8), .gate(transistor_393_out));
  Pull_Resistor #(.pull(1)) pull_resistor_201 (.node(pull_resistor_201_node));
  Transistor #(.\type ("n")) transistor_398 (
    .in(transistor_399_out), .out(pull_resistor_201_node), .gate(STORED_ADR_8));
  Transistor #(.\type ("n")) transistor_399 (.in(1'b0), .out(transistor_399_out), .gate(Read_From_stored_Address));
  Transistor #(.\type ("n")) transistor_400 (.in(transistor_401_out), .out(pull_resistor_201_node), .gate(TEMP_ADR_8));
  Transistor #(.\type ("n")) transistor_401 (.in(1'b0), .out(transistor_401_out), .gate(pull_resistor_147_node));
  Transistor #(.\type ("n")) transistor_402 (.in(1'b0), .out(ADR_8), .gate(pull_resistor_201_node));
  Pull_Resistor #(.pull(1)) pull_resistor_202 (.node(ADR_8));
  Register #(.trigger("falling")) register_6 (
    .D(in_6), .en(TIME_STEP_0),
    .Q({TEMP_ADR_15, TEMP_ADR_14, TEMP_ADR_13, TEMP_ADR_12, TEMP_ADR_11, TEMP_ADR_10, TEMP_ADR_9, TEMP_ADR_8}),
    .clk(clock_8_out), .clr(in_7));
  Pull_Resistor #(.pull(1)) pull_resistor_203 (.node(pull_resistor_203_node));
  Transistor #(.\type ("n")) transistor_403 (.in(transistor_404_out), .out(pull_resistor_203_node), .gate(FLAG_C));
  Transistor #(.\type ("n")) transistor_404 (.in(1'b0), .out(transistor_404_out), .gate(pull_resistor_181_node));
  Transistor #(.\type ("n")) transistor_405 (.in(transistor_406_out), .out(pull_resistor_203_node), .gate(in_1));
  Transistor #(.\type ("n")) transistor_406 (.in(1'b0), .out(transistor_406_out), .gate(READ_FALG));
  Pull_Resistor #(.pull(1)) pull_resistor_204 (.node(FLAG_STORE_O));
  Pull_Resistor #(.pull(1)) pull_resistor_205 (.node(FLAG_STORE_C));
  Transistor #(.\type ("n")) transistor_407 (.in(1'b0), .out(FLAG_STORE_O), .gate(pull_resistor_197_node));
  Transistor #(.\type ("n")) transistor_408 (.in(1'b0), .out(FLAG_STORE_C), .gate(pull_resistor_203_node));
  Pull_Resistor #(.pull(1)) pull_resistor_206 (.node(pull_resistor_206_node));
  Transistor #(.\type ("n")) transistor_409 (.in(transistor_410_out), .out(pull_resistor_206_node), .gate(ADR___9));
  Transistor #(.\type ("n")) transistor_410 (.in(1'b0), .out(transistor_410_out), .gate(Store_Address_plus_plus));
  Transistor #(.\type ("n")) transistor_411 (.in(transistor_412_out), .out(pull_resistor_206_node), .gate(TEMP_ADR_9));
  Transistor #(.\type ("n")) transistor_412 (.in(1'b0), .out(transistor_412_out), .gate(transistor_277_out));
  Pull_Resistor #(.pull(1)) pull_resistor_207 (.node(NEXT_ADR_9));
  Transistor #(.\type ("n")) transistor_413 (.in(1'b0), .out(NEXT_ADR_9), .gate(pull_resistor_206_node));
  Transistor #(.\type ("n")) transistor_414 (.in(transistor_415_out), .out(transistor_414_out), .gate(STORED_ADR_9));
  Pull_Resistor #(.pull(1)) pull_resistor_208 (.node(transistor_414_out));
  Transistor #(.\type ("n")) transistor_415 (.in(1'b0), .out(transistor_415_out), .gate(Read_From_stored_Address));
  Transistor #(.\type ("n")) transistor_416 (.in(transistor_417_out), .out(transistor_414_out), .gate(TEMP_ADR_9));
  Transistor #(.\type ("n")) transistor_417 (.in(1'b0), .out(transistor_417_out), .gate(pull_resistor_147_node));
  Pull_Resistor #(.pull(1)) pull_resistor_209 (.node(ADR_9));
  Transistor #(.\type ("n")) transistor_418 (.in(1'b0), .out(ADR_9), .gate(transistor_414_out));
  Pull_Resistor #(.pull(1)) pull_resistor_210 (.node(pull_resistor_210_node));
  Transistor #(.\type ("n")) transistor_419 (.in(transistor_420_out), .out(pull_resistor_210_node), .gate(ADR___10));
  Transistor #(.\type ("n")) transistor_420 (.in(1'b0), .out(transistor_420_out), .gate(Store_Address_plus_plus));
  Transistor #(.\type ("n")) transistor_421 (.in(transistor_422_out), .out(pull_resistor_210_node), .gate(TEMP_ADR_10));
  Transistor #(.\type ("n")) transistor_422 (.in(1'b0), .out(transistor_422_out), .gate(transistor_277_out));
  Transistor #(.\type ("n")) transistor_423 (.in(1'b0), .out(NEXT_ADR_10), .gate(pull_resistor_210_node));
  Pull_Resistor #(.pull(1)) pull_resistor_211 (.node(NEXT_ADR_10));
  Pull_Resistor #(.pull(1)) pull_resistor_212 (.node(pull_resistor_212_node));
  Transistor #(.\type ("n")) transistor_424 (
    .in(transistor_425_out), .out(pull_resistor_212_node), .gate(STORED_ADR_10));
  Transistor #(.\type ("n")) transistor_425 (.in(1'b0), .out(transistor_425_out), .gate(Read_From_stored_Address));
  Transistor #(.\type ("n")) transistor_426 (.in(transistor_427_out), .out(pull_resistor_212_node), .gate(TEMP_ADR_10));
  Transistor #(.\type ("n")) transistor_427 (.in(1'b0), .out(transistor_427_out), .gate(pull_resistor_147_node));
  Pull_Resistor #(.pull(1)) pull_resistor_213 (.node(ADR_10));
  Transistor #(.\type ("n")) transistor_428 (.in(1'b0), .out(ADR_10), .gate(pull_resistor_212_node));
  Pull_Resistor #(.pull(1)) pull_resistor_214 (.node(pull_resistor_214_node));
  Transistor #(.\type ("n")) transistor_429 (.in(transistor_430_out), .out(pull_resistor_214_node), .gate(ADR___11));
  Transistor #(.\type ("n")) transistor_430 (.in(1'b0), .out(transistor_430_out), .gate(Store_Address_plus_plus));
  Transistor #(.\type ("n")) transistor_431 (.in(transistor_432_out), .out(pull_resistor_214_node), .gate(TEMP_ADR_11));
  Transistor #(.\type ("n")) transistor_432 (.in(1'b0), .out(transistor_432_out), .gate(transistor_277_out));
  Transistor #(.\type ("n")) transistor_433 (.in(1'b0), .out(NEXT_ADR_11), .gate(pull_resistor_214_node));
  Pull_Resistor #(.pull(1)) pull_resistor_215 (.node(NEXT_ADR_11));
  Pull_Resistor #(.pull(1)) pull_resistor_216 (.node(pull_resistor_216_node));
  Transistor #(.\type ("n")) transistor_434 (
    .in(transistor_435_out), .out(pull_resistor_216_node), .gate(STORED_ADR_11));
  Transistor #(.\type ("n")) transistor_435 (.in(1'b0), .out(transistor_435_out), .gate(Read_From_stored_Address));
  Transistor #(.\type ("n")) transistor_436 (.in(transistor_437_out), .out(pull_resistor_216_node), .gate(TEMP_ADR_11));
  Transistor #(.\type ("n")) transistor_437 (.in(1'b0), .out(transistor_437_out), .gate(pull_resistor_147_node));
  Transistor #(.\type ("n")) transistor_438 (.in(1'b0), .out(ADR_11), .gate(pull_resistor_216_node));
  Pull_Resistor #(.pull(1)) pull_resistor_217 (.node(ADR_11));
  Transistor #(.\type ("n")) transistor_439 (.in(transistor_440_out), .out(transistor_439_out), .gate(ADR___12));
  Pull_Resistor #(.pull(1)) pull_resistor_218 (.node(transistor_439_out));
  Transistor #(.\type ("n")) transistor_440 (.in(1'b0), .out(transistor_440_out), .gate(Store_Address_plus_plus));
  Transistor #(.\type ("n")) transistor_441 (.in(transistor_442_out), .out(transistor_439_out), .gate(TEMP_ADR_12));
  Transistor #(.\type ("n")) transistor_442 (.in(1'b0), .out(transistor_442_out), .gate(transistor_277_out));
  Transistor #(.\type ("n")) transistor_443 (.in(1'b0), .out(NEXT_ADR_12), .gate(transistor_439_out));
  Pull_Resistor #(.pull(1)) pull_resistor_219 (.node(NEXT_ADR_12));
  Pull_Resistor #(.pull(1)) pull_resistor_220 (.node(pull_resistor_220_node));
  Transistor #(.\type ("n")) transistor_444 (
    .in(transistor_445_out), .out(pull_resistor_220_node), .gate(STORED_ADR_12));
  Transistor #(.\type ("n")) transistor_445 (.in(1'b0), .out(transistor_445_out), .gate(Read_From_stored_Address));
  Transistor #(.\type ("n")) transistor_446 (.in(transistor_447_out), .out(pull_resistor_220_node), .gate(TEMP_ADR_12));
  Transistor #(.\type ("n")) transistor_447 (.in(1'b0), .out(transistor_447_out), .gate(pull_resistor_147_node));
  Pull_Resistor #(.pull(1)) pull_resistor_221 (.node(pull_resistor_221_node));
  Transistor #(.\type ("n")) transistor_448 (.in(transistor_449_out), .out(pull_resistor_221_node), .gate(ADR___13));
  Transistor #(.\type ("n")) transistor_449 (.in(1'b0), .out(transistor_449_out), .gate(Store_Address_plus_plus));
  Transistor #(.\type ("n")) transistor_450 (.in(transistor_451_out), .out(pull_resistor_221_node), .gate(TEMP_ADR_13));
  Transistor #(.\type ("n")) transistor_451 (.in(1'b0), .out(transistor_451_out), .gate(transistor_277_out));
  Pull_Resistor #(.pull(1)) pull_resistor_222 (.node(pull_resistor_222_node));
  Transistor #(.\type ("n")) transistor_452 (
    .in(transistor_453_out), .out(pull_resistor_222_node), .gate(STORED_ADR_13));
  Transistor #(.\type ("n")) transistor_453 (.in(1'b0), .out(transistor_453_out), .gate(Read_From_stored_Address));
  Transistor #(.\type ("n")) transistor_454 (.in(transistor_455_out), .out(pull_resistor_222_node), .gate(TEMP_ADR_13));
  Transistor #(.\type ("n")) transistor_455 (.in(1'b0), .out(transistor_455_out), .gate(pull_resistor_147_node));
  Pull_Resistor #(.pull(1)) pull_resistor_223 (.node(ADR_12));
  Transistor #(.\type ("n")) transistor_456 (.in(1'b0), .out(ADR_12), .gate(pull_resistor_220_node));
  Transistor #(.\type ("n")) transistor_457 (.in(transistor_458_out), .out(transistor_457_out), .gate(ADR___14));
  Pull_Resistor #(.pull(1)) pull_resistor_224 (.node(transistor_457_out));
  Transistor #(.\type ("n")) transistor_458 (.in(1'b0), .out(transistor_458_out), .gate(Store_Address_plus_plus));
  Transistor #(.\type ("n")) transistor_459 (.in(transistor_460_out), .out(transistor_457_out), .gate(TEMP_ADR_14));
  Transistor #(.\type ("n")) transistor_460 (.in(1'b0), .out(transistor_460_out), .gate(transistor_277_out));
  Pull_Resistor #(.pull(1)) pull_resistor_225 (.node(NEXT_ADR_13));
  Transistor #(.\type ("n")) transistor_461 (.in(1'b0), .out(NEXT_ADR_13), .gate(pull_resistor_221_node));
  Transistor #(.\type ("n")) transistor_462 (.in(transistor_463_out), .out(transistor_462_out), .gate(STORED_ADR_14));
  Transistor #(.\type ("n")) transistor_463 (.in(1'b0), .out(transistor_463_out), .gate(Read_From_stored_Address));
  Transistor #(.\type ("n")) transistor_464 (.in(transistor_465_out), .out(transistor_462_out), .gate(TEMP_ADR_14));
  Transistor #(.\type ("n")) transistor_465 (.in(1'b0), .out(transistor_465_out), .gate(pull_resistor_147_node));
  Pull_Resistor #(.pull(1)) pull_resistor_226 (.node(ADR_13));
  Transistor #(.\type ("n")) transistor_466 (.in(1'b0), .out(ADR_13), .gate(pull_resistor_222_node));
  Transistor #(.\type ("n")) transistor_467 (.in(transistor_468_out), .out(transistor_467_out), .gate(ADR___15));
  Transistor #(.\type ("n")) transistor_468 (.in(1'b0), .out(transistor_468_out), .gate(Store_Address_plus_plus));
  Transistor #(.\type ("n")) transistor_469 (.in(transistor_470_out), .out(transistor_467_out), .gate(TEMP_ADR_15));
  Transistor #(.\type ("n")) transistor_470 (.in(1'b0), .out(transistor_470_out), .gate(transistor_277_out));
  Transistor #(.\type ("n")) transistor_471 (.in(1'b0), .out(NEXT_ADR_14), .gate(transistor_457_out));
  Pull_Resistor #(.pull(1)) pull_resistor_227 (.node(NEXT_ADR_14));
  Pull_Resistor #(.pull(1)) pull_resistor_228 (.node(transistor_462_out));
  Transistor #(.\type ("n")) transistor_472 (.in(1'b0), .out(ADR_14), .gate(transistor_462_out));
  Pull_Resistor #(.pull(1)) pull_resistor_229 (.node(ADR_14));
  Pull_Resistor #(.pull(1)) pull_resistor_230 (.node(transistor_467_out));
  Pull_Resistor #(.pull(1)) pull_resistor_231 (.node(NEXT_ADR_15));
  Transistor #(.\type ("n")) transistor_473 (.in(1'b0), .out(NEXT_ADR_15), .gate(transistor_467_out));
  Pull_Resistor #(.pull(1)) pull_resistor_232 (.node(pull_resistor_232_node));
  Transistor #(.\type ("n")) transistor_474 (
    .in(transistor_475_out), .out(pull_resistor_232_node), .gate(STORED_ADR_15));
  Transistor #(.\type ("n")) transistor_475 (.in(1'b0), .out(transistor_475_out), .gate(Read_From_stored_Address));
  Transistor #(.\type ("n")) transistor_476 (.in(transistor_477_out), .out(pull_resistor_232_node), .gate(TEMP_ADR_15));
  Transistor #(.\type ("n")) transistor_477 (.in(1'b0), .out(transistor_477_out), .gate(pull_resistor_147_node));
  Pull_Resistor #(.pull(1)) pull_resistor_233 (.node(ADR_15));
  Transistor #(.\type ("n")) transistor_478 (.in(1'b0), .out(ADR_15), .gate(pull_resistor_232_node));
  Transistor #(.\type ("n")) transistor_479 (.in(1'b0), .out(transistor_479_out), .gate(STORED_ADR_15));
  Transistor #(.\type ("n")) transistor_480 (.in(1'b0), .out(transistor_479_out), .gate(pull_resistor_237_node));
  Transistor #(.\type ("n")) transistor_481 (.in(1'b0), .out(transistor_481_out), .gate(STORED_ADR_15));
  Transistor #(.\type ("n")) transistor_482 (
    .in(transistor_481_out), .out(transistor_482_out), .gate(pull_resistor_237_node));
  Transistor #(.\type ("n")) transistor_483 (.in(1'b0), .out(transistor_483_out), .gate(STORED_ADR_14));
  Transistor #(.\type ("n")) transistor_484 (.in(1'b0), .out(transistor_483_out), .gate(pull_resistor_238_node));
  Transistor #(.\type ("n")) transistor_485 (
    .in(transistor_486_out), .out(transistor_485_out), .gate(pull_resistor_238_node));
  Transistor #(.\type ("n")) transistor_486 (.in(1'b0), .out(transistor_486_out), .gate(STORED_ADR_14));
  Transistor #(.\type ("n")) transistor_487 (.in(1'b0), .out(transistor_487_out), .gate(pull_resistor_241_node));
  Transistor #(.\type ("n")) transistor_488 (.in(1'b0), .out(transistor_487_out), .gate(STORED_ADR_13));
  Transistor #(.\type ("n")) transistor_489 (
    .in(transistor_490_out), .out(transistor_489_out), .gate(pull_resistor_241_node));
  Transistor #(.\type ("n")) transistor_490 (.in(1'b0), .out(transistor_490_out), .gate(STORED_ADR_13));
  Transistor #(.\type ("n")) transistor_491 (.in(1'b0), .out(transistor_491_out), .gate(STORED_ADR_12));
  Transistor #(.\type ("n")) transistor_492 (.in(1'b0), .out(transistor_491_out), .gate(pull_resistor_242_node));
  Transistor #(.\type ("n")) transistor_493 (
    .in(transistor_494_out), .out(transistor_493_out), .gate(pull_resistor_242_node));
  Transistor #(.\type ("n")) transistor_494 (.in(1'b0), .out(transistor_494_out), .gate(STORED_ADR_12));
  Transistor #(.\type ("n")) transistor_495 (.in(1'b0), .out(transistor_495_out), .gate(STORED_ADR_11));
  Transistor #(.\type ("n")) transistor_496 (.in(1'b0), .out(transistor_495_out), .gate(pull_resistor_245_node));
  Transistor #(.\type ("n")) transistor_497 (.in(1'b0), .out(transistor_497_out), .gate(STORED_ADR_11));
  Transistor #(.\type ("n")) transistor_498 (
    .in(transistor_497_out), .out(transistor_498_out), .gate(pull_resistor_245_node));
  Transistor #(.\type ("n")) transistor_499 (.in(1'b0), .out(transistor_499_out), .gate(STORED_ADR_10));
  Transistor #(.\type ("n")) transistor_500 (.in(1'b0), .out(transistor_499_out), .gate(pull_resistor_247_node));
  Transistor #(.\type ("n")) transistor_501 (
    .in(transistor_502_out), .out(transistor_501_out), .gate(pull_resistor_247_node));
  Transistor #(.\type ("n")) transistor_502 (.in(1'b0), .out(transistor_502_out), .gate(STORED_ADR_10));
  Transistor #(.\type ("n")) transistor_503 (.in(1'b0), .out(transistor_503_out), .gate(STORED_ADR_9));
  Transistor #(.\type ("n")) transistor_504 (.in(1'b0), .out(transistor_503_out), .gate(pull_resistor_249_node));
  Transistor #(.\type ("n")) transistor_505 (
    .in(transistor_506_out), .out(transistor_505_out), .gate(pull_resistor_249_node));
  Transistor #(.\type ("n")) transistor_506 (.in(1'b0), .out(transistor_506_out), .gate(STORED_ADR_9));
  Transistor #(.\type ("n")) transistor_507 (.in(1'b0), .out(transistor_507_out), .gate(pull_resistor_251_node));
  Transistor #(.\type ("n")) transistor_508 (.in(1'b0), .out(transistor_507_out), .gate(STORED_ADR_8));
  Transistor #(.\type ("n")) transistor_509 (
    .in(transistor_510_out), .out(transistor_509_out), .gate(pull_resistor_251_node));
  Transistor #(.\type ("n")) transistor_510 (.in(1'b0), .out(transistor_510_out), .gate(STORED_ADR_8));
  Transistor #(.\type ("n")) transistor_511 (.in(1'b0), .out(transistor_511_out), .gate(STORED_ADR_7));
  Transistor #(.\type ("n")) transistor_512 (.in(1'b0), .out(transistor_511_out), .gate(pull_resistor_253_node));
  Transistor #(.\type ("n")) transistor_513 (.in(1'b0), .out(transistor_513_out), .gate(STORED_ADR_7));
  Transistor #(.\type ("n")) transistor_514 (
    .in(transistor_513_out), .out(transistor_514_out), .gate(pull_resistor_253_node));
  Transistor #(.\type ("n")) transistor_515 (.in(1'b0), .out(transistor_515_out), .gate(STORED_ADR_6));
  Transistor #(.\type ("n")) transistor_516 (.in(1'b0), .out(transistor_515_out), .gate(pull_resistor_255_node));
  Transistor #(.\type ("n")) transistor_517 (.in(1'b0), .out(transistor_517_out), .gate(STORED_ADR_6));
  Transistor #(.\type ("n")) transistor_518 (
    .in(transistor_517_out), .out(transistor_518_out), .gate(pull_resistor_255_node));
  Transistor #(.\type ("n")) transistor_519 (.in(1'b0), .out(transistor_519_out), .gate(pull_resistor_256_node));
  Transistor #(.\type ("n")) transistor_520 (.in(1'b0), .out(transistor_519_out), .gate(STORED_ADR_5));
  Transistor #(.\type ("n")) transistor_521 (
    .in(transistor_522_out), .out(transistor_521_out), .gate(pull_resistor_256_node));
  Transistor #(.\type ("n")) transistor_522 (.in(1'b0), .out(transistor_522_out), .gate(STORED_ADR_5));
  Transistor #(.\type ("n")) transistor_523 (.in(1'b0), .out(transistor_523_out), .gate(STORED_ADR_4));
  Transistor #(.\type ("n")) transistor_524 (.in(1'b0), .out(transistor_523_out), .gate(pull_resistor_258_node));
  Transistor #(.\type ("n")) transistor_525 (
    .in(transistor_526_out), .out(transistor_525_out), .gate(pull_resistor_258_node));
  Transistor #(.\type ("n")) transistor_526 (.in(1'b0), .out(transistor_526_out), .gate(STORED_ADR_4));
  Transistor #(.\type ("n")) transistor_527 (.in(1'b0), .out(transistor_527_out), .gate(pull_resistor_261_node));
  Transistor #(.\type ("n")) transistor_528 (.in(1'b0), .out(transistor_527_out), .gate(STORED_ADR_3));
  Transistor #(.\type ("n")) transistor_529 (.in(1'b0), .out(transistor_529_out), .gate(STORED_ADR_3));
  Transistor #(.\type ("n")) transistor_530 (
    .in(transistor_529_out), .out(transistor_530_out), .gate(pull_resistor_261_node));
  Transistor #(.\type ("n")) transistor_531 (.in(1'b0), .out(transistor_531_out), .gate(STORED_ADR_2));
  Transistor #(.\type ("n")) transistor_532 (.in(1'b0), .out(transistor_531_out), .gate(pull_resistor_263_node));
  Transistor #(.\type ("n")) transistor_533 (.in(1'b0), .out(transistor_533_out), .gate(STORED_ADR_2));
  Transistor #(.\type ("n")) transistor_534 (
    .in(transistor_533_out), .out(transistor_534_out), .gate(pull_resistor_263_node));
  Transistor #(.\type ("n")) transistor_535 (.in(1'b0), .out(transistor_535_out), .gate(pull_resistor_264_node));
  Transistor #(.\type ("n")) transistor_536 (.in(1'b0), .out(transistor_535_out), .gate(STORED_ADR_1));
  Transistor #(.\type ("n")) transistor_537 (.in(1'b0), .out(transistor_537_out), .gate(STORED_ADR_1));
  Transistor #(.\type ("n")) transistor_538 (
    .in(transistor_537_out), .out(transistor_538_out), .gate(pull_resistor_264_node));
  Transistor #(.\type ("n")) transistor_539 (.in(1'b0), .out(transistor_539_out), .gate(STORED_ADR_0));
  Transistor #(.\type ("n")) transistor_540 (.in(1'b0), .out(transistor_539_out), .gate(1'b1));
  Transistor #(.\type ("n")) transistor_541 (.in(transistor_542_out), .out(transistor_541_out), .gate(1'b1));
  Transistor #(.\type ("n")) transistor_542 (.in(1'b0), .out(transistor_542_out), .gate(STORED_ADR_0));
  Pull_Resistor #(.pull(1)) pull_resistor_234 (.node(pull_resistor_234_node));
  Pull_Resistor #(.pull(1)) pull_resistor_235 (.node(transistor_482_out));
  Transistor #(.\type ("n")) transistor_543 (.in(1'b0), .out(pull_resistor_234_node), .gate(transistor_482_out));
  Pull_Resistor #(.pull(1)) pull_resistor_236 (.node(transistor_485_out));
  Pull_Resistor #(.pull(1)) pull_resistor_237 (.node(pull_resistor_237_node));
  Transistor #(.\type ("n")) transistor_544 (.in(1'b0), .out(pull_resistor_237_node), .gate(transistor_485_out));
  Pull_Resistor #(.pull(1)) pull_resistor_238 (.node(pull_resistor_238_node));
  Pull_Resistor #(.pull(1)) pull_resistor_239 (.node(transistor_489_out));
  Transistor #(.\type ("n")) transistor_545 (.in(1'b0), .out(pull_resistor_238_node), .gate(transistor_489_out));
  Pull_Resistor #(.pull(1)) pull_resistor_240 (.node(transistor_493_out));
  Pull_Resistor #(.pull(1)) pull_resistor_241 (.node(pull_resistor_241_node));
  Transistor #(.\type ("n")) transistor_546 (.in(1'b0), .out(pull_resistor_241_node), .gate(transistor_493_out));
  Pull_Resistor #(.pull(1)) pull_resistor_242 (.node(pull_resistor_242_node));
  Pull_Resistor #(.pull(1)) pull_resistor_243 (.node(transistor_498_out));
  Transistor #(.\type ("n")) transistor_547 (.in(1'b0), .out(pull_resistor_242_node), .gate(transistor_498_out));
  Pull_Resistor #(.pull(1)) pull_resistor_244 (.node(transistor_501_out));
  Pull_Resistor #(.pull(1)) pull_resistor_245 (.node(pull_resistor_245_node));
  Transistor #(.\type ("n")) transistor_548 (.in(1'b0), .out(pull_resistor_245_node), .gate(transistor_501_out));
  Pull_Resistor #(.pull(1)) pull_resistor_246 (.node(transistor_505_out));
  Pull_Resistor #(.pull(1)) pull_resistor_247 (.node(pull_resistor_247_node));
  Transistor #(.\type ("n")) transistor_549 (.in(1'b0), .out(pull_resistor_247_node), .gate(transistor_505_out));
  Pull_Resistor #(.pull(1)) pull_resistor_248 (.node(transistor_509_out));
  Pull_Resistor #(.pull(1)) pull_resistor_249 (.node(pull_resistor_249_node));
  Transistor #(.\type ("n")) transistor_550 (.in(1'b0), .out(pull_resistor_249_node), .gate(transistor_509_out));
  Pull_Resistor #(.pull(1)) pull_resistor_250 (.node(transistor_514_out));
  Pull_Resistor #(.pull(1)) pull_resistor_251 (.node(pull_resistor_251_node));
  Transistor #(.\type ("n")) transistor_551 (.in(1'b0), .out(pull_resistor_251_node), .gate(transistor_514_out));
  Pull_Resistor #(.pull(1)) pull_resistor_252 (.node(transistor_518_out));
  Pull_Resistor #(.pull(1)) pull_resistor_253 (.node(pull_resistor_253_node));
  Transistor #(.\type ("n")) transistor_552 (.in(1'b0), .out(pull_resistor_253_node), .gate(transistor_518_out));
  Pull_Resistor #(.pull(1)) pull_resistor_254 (.node(transistor_521_out));
  Pull_Resistor #(.pull(1)) pull_resistor_255 (.node(pull_resistor_255_node));
  Transistor #(.\type ("n")) transistor_553 (.in(1'b0), .out(pull_resistor_255_node), .gate(transistor_521_out));
  Pull_Resistor #(.pull(1)) pull_resistor_256 (.node(pull_resistor_256_node));
  Pull_Resistor #(.pull(1)) pull_resistor_257 (.node(transistor_525_out));
  Transistor #(.\type ("n")) transistor_554 (.in(1'b0), .out(pull_resistor_256_node), .gate(transistor_525_out));
  Pull_Resistor #(.pull(1)) pull_resistor_258 (.node(pull_resistor_258_node));
  Pull_Resistor #(.pull(1)) pull_resistor_259 (.node(transistor_530_out));
  Transistor #(.\type ("n")) transistor_555 (.in(1'b0), .out(pull_resistor_258_node), .gate(transistor_530_out));
  Pull_Resistor #(.pull(1)) pull_resistor_260 (.node(transistor_534_out));
  Pull_Resistor #(.pull(1)) pull_resistor_261 (.node(pull_resistor_261_node));
  Transistor #(.\type ("n")) transistor_556 (.in(1'b0), .out(pull_resistor_261_node), .gate(transistor_534_out));
  Pull_Resistor #(.pull(1)) pull_resistor_262 (.node(transistor_538_out));
  Pull_Resistor #(.pull(1)) pull_resistor_263 (.node(pull_resistor_263_node));
  Transistor #(.\type ("n")) transistor_557 (.in(1'b0), .out(pull_resistor_263_node), .gate(transistor_538_out));
  Pull_Resistor #(.pull(1)) pull_resistor_264 (.node(pull_resistor_264_node));
  Pull_Resistor #(.pull(1)) pull_resistor_265 (.node(transistor_541_out));
  Transistor #(.\type ("n")) transistor_558 (.in(1'b0), .out(pull_resistor_264_node), .gate(transistor_541_out));
  Transistor #(.\type ("n")) transistor_559 (.in(1'b0), .out(ADR___15), .gate(transistor_479_out));
  Pull_Resistor #(.pull(1)) pull_resistor_266 (.node(transistor_479_out));
  Transistor #(.\type ("n")) transistor_560 (.in(1'b0), .out(ADR___14), .gate(transistor_483_out));
  Pull_Resistor #(.pull(1)) pull_resistor_267 (.node(transistor_483_out));
  Transistor #(.\type ("n")) transistor_561 (.in(1'b0), .out(ADR___13), .gate(transistor_487_out));
  Pull_Resistor #(.pull(1)) pull_resistor_268 (.node(transistor_487_out));
  Transistor #(.\type ("n")) transistor_562 (.in(1'b0), .out(ADR___12), .gate(transistor_491_out));
  Pull_Resistor #(.pull(1)) pull_resistor_269 (.node(transistor_491_out));
  Transistor #(.\type ("n")) transistor_563 (.in(1'b0), .out(ADR___11), .gate(transistor_495_out));
  Pull_Resistor #(.pull(1)) pull_resistor_270 (.node(transistor_495_out));
  Transistor #(.\type ("n")) transistor_564 (.in(1'b0), .out(ADR___10), .gate(transistor_499_out));
  Pull_Resistor #(.pull(1)) pull_resistor_271 (.node(transistor_499_out));
  Transistor #(.\type ("n")) transistor_565 (.in(1'b0), .out(ADR___9), .gate(transistor_503_out));
  Pull_Resistor #(.pull(1)) pull_resistor_272 (.node(transistor_503_out));
  Transistor #(.\type ("n")) transistor_566 (.in(1'b0), .out(ADR___8), .gate(transistor_507_out));
  Pull_Resistor #(.pull(1)) pull_resistor_273 (.node(transistor_507_out));
  Transistor #(.\type ("n")) transistor_567 (.in(1'b0), .out(ADR___7), .gate(transistor_511_out));
  Pull_Resistor #(.pull(1)) pull_resistor_274 (.node(transistor_511_out));
  Transistor #(.\type ("n")) transistor_568 (.in(1'b0), .out(ADR___6), .gate(transistor_515_out));
  Pull_Resistor #(.pull(1)) pull_resistor_275 (.node(transistor_515_out));
  Transistor #(.\type ("n")) transistor_569 (.in(1'b0), .out(ADR___5), .gate(transistor_519_out));
  Pull_Resistor #(.pull(1)) pull_resistor_276 (.node(transistor_519_out));
  Transistor #(.\type ("n")) transistor_570 (.in(1'b0), .out(ADR___4), .gate(transistor_523_out));
  Pull_Resistor #(.pull(1)) pull_resistor_277 (.node(transistor_523_out));
  Transistor #(.\type ("n")) transistor_571 (.in(1'b0), .out(ADR___3), .gate(transistor_527_out));
  Pull_Resistor #(.pull(1)) pull_resistor_278 (.node(transistor_527_out));
  Transistor #(.\type ("n")) transistor_572 (.in(1'b0), .out(ADR___2), .gate(transistor_531_out));
  Pull_Resistor #(.pull(1)) pull_resistor_279 (.node(transistor_531_out));
  Transistor #(.\type ("n")) transistor_573 (.in(1'b0), .out(ADR___1), .gate(transistor_535_out));
  Pull_Resistor #(.pull(1)) pull_resistor_280 (.node(transistor_535_out));
  Transistor #(.\type ("n")) transistor_574 (.in(1'b0), .out(ADR___0), .gate(transistor_539_out));
  Pull_Resistor #(.pull(1)) pull_resistor_281 (.node(transistor_539_out));
  Transistor #(.\type ("n")) transistor_575 (.in(1'b0), .out(ADR___15), .gate(pull_resistor_234_node));
  Pull_Resistor #(.pull(1)) pull_resistor_282 (.node(ADR___15));
  Transistor #(.\type ("n")) transistor_576 (.in(1'b0), .out(ADR___14), .gate(pull_resistor_237_node));
  Pull_Resistor #(.pull(1)) pull_resistor_283 (.node(ADR___14));
  Transistor #(.\type ("n")) transistor_577 (.in(1'b0), .out(ADR___13), .gate(pull_resistor_238_node));
  Pull_Resistor #(.pull(1)) pull_resistor_284 (.node(ADR___13));
  Pull_Resistor #(.pull(1)) pull_resistor_285 (.node(ADR___12));
  Transistor #(.\type ("n")) transistor_578 (.in(1'b0), .out(ADR___12), .gate(pull_resistor_241_node));
  Pull_Resistor #(.pull(1)) pull_resistor_286 (.node(ADR___11));
  Transistor #(.\type ("n")) transistor_579 (.in(1'b0), .out(ADR___11), .gate(pull_resistor_242_node));
  Pull_Resistor #(.pull(1)) pull_resistor_287 (.node(ADR___10));
  Transistor #(.\type ("n")) transistor_580 (.in(1'b0), .out(ADR___10), .gate(pull_resistor_245_node));
  Transistor #(.\type ("n")) transistor_581 (.in(1'b0), .out(ADR___9), .gate(pull_resistor_247_node));
  Pull_Resistor #(.pull(1)) pull_resistor_288 (.node(ADR___9));
  Pull_Resistor #(.pull(1)) pull_resistor_289 (.node(ADR___8));
  Transistor #(.\type ("n")) transistor_582 (.in(1'b0), .out(ADR___8), .gate(pull_resistor_249_node));
  Pull_Resistor #(.pull(1)) pull_resistor_290 (.node(ADR___7));
  Transistor #(.\type ("n")) transistor_583 (.in(1'b0), .out(ADR___7), .gate(pull_resistor_251_node));
  Pull_Resistor #(.pull(1)) pull_resistor_291 (.node(ADR___6));
  Transistor #(.\type ("n")) transistor_584 (.in(1'b0), .out(ADR___6), .gate(pull_resistor_253_node));
  Transistor #(.\type ("n")) transistor_585 (.in(1'b0), .out(ADR___5), .gate(pull_resistor_255_node));
  Pull_Resistor #(.pull(1)) pull_resistor_292 (.node(ADR___5));
  Transistor #(.\type ("n")) transistor_586 (.in(1'b0), .out(ADR___4), .gate(pull_resistor_256_node));
  Pull_Resistor #(.pull(1)) pull_resistor_293 (.node(ADR___4));
  Transistor #(.\type ("n")) transistor_587 (.in(1'b0), .out(ADR___3), .gate(pull_resistor_258_node));
  Pull_Resistor #(.pull(1)) pull_resistor_294 (.node(ADR___3));
  Transistor #(.\type ("n")) transistor_588 (.in(1'b0), .out(ADR___2), .gate(pull_resistor_261_node));
  Pull_Resistor #(.pull(1)) pull_resistor_295 (.node(ADR___2));
  Transistor #(.\type ("n")) transistor_589 (.in(1'b0), .out(ADR___1), .gate(pull_resistor_263_node));
  Pull_Resistor #(.pull(1)) pull_resistor_296 (.node(ADR___1));
  Transistor #(.\type ("n")) transistor_590 (.in(1'b0), .out(ADR___0), .gate(pull_resistor_264_node));
  Pull_Resistor #(.pull(1)) pull_resistor_297 (.node(ADR___0));
  Pull_Resistor #(.pull(1)) pull_resistor_298 ();  // open: node

  // Other names for the same wires on the sheet: ADR_out[15:0] = {ADR_15, ADR_14, ADR_13, ADR_12, ADR_11, ADR_10, ADR_9, ADR_8, ADR_7, ADR_6, ADR_5, ADR_4, ADR_3, ADR_2, ADR_1, ADR_0};
  //   Buss[7:0] = in_6; Buss0 = in_6[0]; Buss1 = in_6[1]; Buss2 = in_6[2]; Buss3 = in_6[3]; Buss4 = in_6[4];
  //   Buss5 = in_6[5]; Buss6 = in_6[6]; Buss7 = in_6[7]; ALU_FLAG_C = in_1; ALU_FLAG_N = in_5; ALU_FLAG_O = in_2;
  //   ALU_FLAG_U = in_3; ALU_FLAG_Z = in_4; Main_bus_0 = Main_bus[0]; Main_bus_1 = Main_bus[1];
  //   Main_bus_2 = Main_bus[2]; Main_bus_3 = Main_bus[3]; Main_bus_4 = Main_bus[4]; Main_bus_5 = Main_bus[5];
  //   Main_bus_6 = Main_bus[6]; Main_bus_7 = Main_bus[7]; rst = in_7

  // Notes on the sheet:
  //   its all inverted
endmodule
