// Logisim project FullAdder.circ as structural Verilog: 1 circuit, main circuit main
module main (
  input  [2:0] in_1,
  input  [2:0] in_2
);

  wire pull_resistor_3_node, pull_resistor_4_node, pull_resistor_6_node, pull_resistor_7_node,
       pull_resistor_8_node, pull_resistor_9_node, pull_resistor_10_node, pull_resistor_11_node,
       pull_resistor_14_node, pull_resistor_16_node, pull_resistor_19_node, pull_resistor_20_node,
       pull_resistor_21_node, pull_resistor_23_node, pull_resistor_26_node, pull_resistor_28_node,
       pull_resistor_30_node, pull_resistor_31_node, pull_resistor_32_node, pull_resistor_33_node,
       pull_resistor_35_node, pull_resistor_36_node, pull_resistor_38_node, pull_resistor_39_node,
       pull_resistor_41_node, pull_resistor_46_node, pull_resistor_47_node, pull_resistor_48_node,
       transistor_1_out, transistor_2_out, transistor_3_out, transistor_4_out, transistor_5_out,
       transistor_8_out, transistor_9_out, transistor_10_out, transistor_11_out, transistor_14_out,
       transistor_15_out, transistor_16_out, transistor_17_out, transistor_18_out, transistor_20_out,
       transistor_21_out, transistor_25_out, transistor_26_out, transistor_27_out, transistor_28_out,
       transistor_30_out, transistor_31_out, transistor_32_out, transistor_33_out, transistor_35_out,
       transistor_36_out, transistor_38_out, transistor_39_out, transistor_42_out, transistor_44_out,
       transistor_45_out, transistor_46_out, transistor_47_out, transistor_49_out, transistor_50_out,
       transistor_52_out, transistor_53_out, transistor_54_out, transistor_56_out, transistor_59_out,
       transistor_60_out, transistor_62_out, transistor_63_out, transistor_64_out, transistor_67_out,
       transistor_70_out, transistor_71_out, transistor_73_out, transistor_74_out, transistor_75_out,
       transistor_76_out, transistor_77_out, transistor_78_out, transistor_79_out, transistor_80_out,
       transistor_82_out, transistor_85_out, undriven, undriven_2;

  Transistor #(.\type ("n")) transistor_1 (.in(transistor_2_out), .out(transistor_1_out), .gate(in_1[0]));
  Transistor #(.\type ("n")) transistor_2 (.in(1'b0), .out(transistor_2_out), .gate(in_1[1]));
  Pull_Resistor #(.pull(1)) pull_resistor_1 (.node(transistor_1_out));
  Transistor #(.\type ("n")) transistor_3 (.in(transistor_4_out), .out(transistor_3_out), .gate(in_1[0]));
  Pull_Resistor #(.pull(1)) pull_resistor_2 (.node(transistor_3_out));
  Transistor #(.\type ("n")) transistor_4 (.in(1'b0), .out(transistor_4_out), .gate(in_1[1]));
  Pull_Resistor #(.pull(1)) pull_resistor_3 (.node(pull_resistor_3_node));
  Transistor #(.\type ("n")) transistor_5 (.in(1'b0), .out(transistor_5_out), .gate(in_1[1]));
  Transistor #(.\type ("n")) transistor_6 (.in(transistor_5_out), .out(pull_resistor_3_node), .gate(transistor_3_out));
  Pull_Resistor #(.pull(1)) pull_resistor_4 (.node(pull_resistor_4_node));
  Transistor #(.\type ("n")) transistor_7 (.in(transistor_8_out), .out(pull_resistor_4_node), .gate(in_1[0]));
  Transistor #(.\type ("n")) transistor_8 (.in(1'b0), .out(transistor_8_out), .gate(in_1[1]));
  Transistor #(.\type ("n")) transistor_9 (.in(transistor_8_out), .out(transistor_9_out), .gate(pull_resistor_4_node));
  Pull_Resistor #(.pull(1)) pull_resistor_5 (.node(transistor_9_out));
  Transistor #(.\type ("n")) transistor_10 (.in(1'b0), .out(transistor_10_out), .gate(transistor_9_out));
  Transistor #(.\type ("n")) transistor_11 (.in(1'b0), .out(transistor_11_out), .gate(in_1[1]));
  Pull_Resistor #(.pull(1)) pull_resistor_6 (.node(pull_resistor_6_node));
  Transistor #(.\type ("n")) transistor_12 (.in(transistor_11_out), .out(pull_resistor_6_node), .gate(in_1[0]));
  Pull_Resistor #(.pull(1)) pull_resistor_7 (.node(pull_resistor_7_node));
  Transistor #(.\type ("n")) transistor_13 (
    .in(transistor_11_out), .out(pull_resistor_7_node), .gate(pull_resistor_6_node));
  Transistor #(.\type ("n")) transistor_14 (.in(1'b0), .out(transistor_14_out), .gate(transistor_1_out));
  Transistor #(.\type ("n")) transistor_15 (.in(1'b0), .out(transistor_15_out), .gate(transistor_1_out));
  Transistor #(.\type ("n")) transistor_16 (.in(1'b0), .out(transistor_16_out), .gate(transistor_3_out));
  Transistor #(.\type ("n")) transistor_17 (.in(1'b0), .out(transistor_17_out), .gate(pull_resistor_3_node));
  Transistor #(.\type ("n")) transistor_18 (.in(1'b0), .out(transistor_18_out), .gate(pull_resistor_4_node));
  Pull_Resistor #(.pull(1)) pull_resistor_8 (.node(pull_resistor_8_node));
  Transistor #(.\type ("n")) transistor_19 (
    .in(transistor_10_out), .out(pull_resistor_8_node), .gate(pull_resistor_14_node));
  Transistor #(.\type ("n")) transistor_20 (.in(1'b0), .out(transistor_20_out), .gate(pull_resistor_6_node));
  Pull_Resistor #(.pull(1)) pull_resistor_9 (.node(pull_resistor_9_node));
  Transistor #(.\type ("n")) transistor_21 (.in(1'b0), .out(transistor_21_out), .gate(pull_resistor_7_node));
  Transistor #(.\type ("n")) transistor_22 (
    .in(transistor_21_out), .out(pull_resistor_9_node), .gate(transistor_33_out));
  Pull_Resistor #(.pull(1)) pull_resistor_10 (.node(pull_resistor_10_node));
  Transistor #(.\type ("n")) transistor_23 (.in(transistor_14_out), .out(pull_resistor_10_node), .gate(in_1[0]));
  Pull_Resistor #(.pull(1)) pull_resistor_11 (.node(pull_resistor_11_node));
  Transistor #(.\type ("n")) transistor_24 (.in(transistor_15_out), .out(pull_resistor_11_node), .gate(in_1[1]));
  Transistor #(.\type ("n")) transistor_25 (.in(transistor_16_out), .out(transistor_25_out), .gate(in_1[0]));
  Pull_Resistor #(.pull(1)) pull_resistor_12 (.node(transistor_25_out));
  Transistor #(.\type ("n")) transistor_26 (.in(1'b0), .out(transistor_26_out), .gate(in_1[2]));
  Transistor #(.\type ("n")) transistor_27 (.in(transistor_17_out), .out(transistor_27_out), .gate(transistor_25_out));
  Pull_Resistor #(.pull(1)) pull_resistor_13 (.node(transistor_27_out));
  Transistor #(.\type ("n")) transistor_28 (.in(1'b0), .out(transistor_28_out), .gate(in_1[2]));
  Pull_Resistor #(.pull(1)) pull_resistor_14 (.node(pull_resistor_14_node));
  Transistor #(.\type ("n")) transistor_29 (.in(transistor_18_out), .out(pull_resistor_14_node), .gate(in_1[0]));
  Transistor #(.\type ("n")) transistor_30 (.in(1'b0), .out(transistor_30_out), .gate(in_1[2]));
  Transistor #(.\type ("n")) transistor_31 (
    .in(transistor_30_out), .out(transistor_31_out), .gate(pull_resistor_23_node));
  Transistor #(.\type ("n")) transistor_32 (.in(1'b0), .out(transistor_32_out), .gate(pull_resistor_23_node));
  Pull_Resistor #(.pull(1)) pull_resistor_15 (.node(transistor_31_out));
  Pull_Resistor #(.pull(1)) pull_resistor_16 (.node(pull_resistor_16_node));
  Transistor #(.\type ("n")) transistor_33 (.in(transistor_20_out), .out(transistor_33_out), .gate(in_1[0]));
  Pull_Resistor #(.pull(1)) pull_resistor_17 (.node(transistor_33_out));
  Transistor #(.\type ("n")) transistor_34 (
    .in(transistor_36_out), .out(pull_resistor_16_node), .gate(pull_resistor_9_node));
  Transistor #(.\type ("n")) transistor_35 (
    .in(transistor_36_out), .out(transistor_35_out), .gate(pull_resistor_16_node));
  Transistor #(.\type ("n")) transistor_36 (.in(1'b0), .out(transistor_36_out), .gate(in_1[2]));
  Pull_Resistor #(.pull(1)) pull_resistor_18 (.node(transistor_35_out));
  Pull_Resistor #(.pull(1)) pull_resistor_19 (.node(pull_resistor_19_node));
  Transistor #(.\type ("n")) transistor_37 (
    .in(transistor_38_out), .out(pull_resistor_19_node), .gate(pull_resistor_10_node));
  Transistor #(.\type ("n")) transistor_38 (.in(1'b0), .out(transistor_38_out), .gate(pull_resistor_11_node));
  Pull_Resistor #(.pull(1)) pull_resistor_20 (.node(pull_resistor_20_node));
  Transistor #(.\type ("n")) transistor_39 (.in(1'b0), .out(transistor_39_out), .gate(in_1[2]));
  Transistor #(.\type ("n")) transistor_40 (
    .in(transistor_39_out), .out(pull_resistor_20_node), .gate(pull_resistor_19_node));
  Pull_Resistor #(.pull(1)) pull_resistor_21 (.node(pull_resistor_21_node));
  Transistor #(.\type ("n")) transistor_41 (
    .in(transistor_26_out), .out(pull_resistor_21_node), .gate(transistor_27_out));
  Transistor #(.\type ("n")) transistor_42 (
    .in(transistor_28_out), .out(transistor_42_out), .gate(pull_resistor_21_node));
  Pull_Resistor #(.pull(1)) pull_resistor_22 (.node(transistor_42_out));
  Pull_Resistor #(.pull(1)) pull_resistor_23 (.node(pull_resistor_23_node));
  Transistor #(.\type ("n")) transistor_43 (
    .in(transistor_30_out), .out(pull_resistor_23_node), .gate(pull_resistor_8_node));
  Transistor #(.\type ("n")) transistor_44 (
    .in(transistor_32_out), .out(transistor_44_out), .gate(pull_resistor_8_node));
  Pull_Resistor #(.pull(1)) pull_resistor_24 (.node(transistor_44_out));
  Transistor #(.\type ("n")) transistor_45 (.in(1'b0), .out(transistor_45_out), .gate(pull_resistor_16_node));
  Transistor #(.\type ("n")) transistor_46 (
    .in(transistor_45_out), .out(transistor_46_out), .gate(pull_resistor_6_node));
  Pull_Resistor #(.pull(1)) pull_resistor_25 (.node(transistor_46_out));
  Pull_Resistor #(.pull(1)) pull_resistor_26 (.node(pull_resistor_26_node));
  Transistor #(.\type ("n")) transistor_47 (.in(1'b0), .out(transistor_47_out), .gate(pull_resistor_21_node));
  Transistor #(.\type ("n")) transistor_48 (
    .in(transistor_47_out), .out(pull_resistor_26_node), .gate(transistor_27_out));
  Transistor #(.\type ("n")) transistor_49 (.in(transistor_50_out), .out(transistor_49_out), .gate(transistor_3_out));
  Transistor #(.\type ("n")) transistor_50 (.in(1'b0), .out(transistor_50_out), .gate(pull_resistor_21_node));
  Pull_Resistor #(.pull(1)) pull_resistor_27 (.node(transistor_49_out));
  Pull_Resistor #(.pull(1)) pull_resistor_28 (.node(pull_resistor_28_node));
  Transistor #(.\type ("n")) transistor_51 (
    .in(transistor_32_out), .out(pull_resistor_28_node), .gate(pull_resistor_4_node));
  Transistor #(.\type ("n")) transistor_52 (.in(1'b0), .out(transistor_52_out), .gate(transistor_31_out));
  Transistor #(.\type ("n")) transistor_53 (
    .in(transistor_45_out), .out(transistor_53_out), .gate(pull_resistor_9_node));
  Pull_Resistor #(.pull(1)) pull_resistor_29 (.node(transistor_53_out));
  Pull_Resistor #(.pull(1)) pull_resistor_30 (.node(pull_resistor_30_node));
  Transistor #(.\type ("n")) transistor_54 (.in(1'b0), .out(transistor_54_out), .gate(transistor_35_out));
  Transistor #(.\type ("n")) transistor_55 (
    .in(transistor_54_out), .out(pull_resistor_30_node), .gate(transistor_53_out));
  Transistor #(.\type ("n")) transistor_56 (.in(1'b0), .out(transistor_56_out), .gate(pull_resistor_20_node));
  Pull_Resistor #(.pull(1)) pull_resistor_31 (.node(pull_resistor_31_node));
  Transistor #(.\type ("n")) transistor_57 (
    .in(transistor_56_out), .out(pull_resistor_31_node), .gate(pull_resistor_19_node));
  Pull_Resistor #(.pull(1)) pull_resistor_32 (.node(pull_resistor_32_node));
  Transistor #(.\type ("n")) transistor_58 (
    .in(transistor_59_out), .out(pull_resistor_32_node), .gate(pull_resistor_20_node));
  Transistor #(.\type ("n")) transistor_59 (.in(1'b0), .out(transistor_59_out), .gate(in_1[2]));
  Transistor #(.\type ("n")) transistor_60 (.in(1'b0), .out(transistor_60_out), .gate(transistor_42_out));
  Pull_Resistor #(.pull(1)) pull_resistor_33 (.node(pull_resistor_33_node));
  Transistor #(.\type ("n")) transistor_61 (
    .in(transistor_52_out), .out(pull_resistor_33_node), .gate(transistor_44_out));
  Transistor #(.\type ("n")) transistor_62 (.in(1'b0), .out(transistor_62_out), .gate(pull_resistor_20_node));
  Transistor #(.\type ("n")) transistor_63 (.in(1'b0), .out(transistor_63_out), .gate(pull_resistor_32_node));
  Transistor #(.\type ("n")) transistor_64 (
    .in(transistor_60_out), .out(transistor_64_out), .gate(pull_resistor_26_node));
  Pull_Resistor #(.pull(1)) pull_resistor_34 (.node(transistor_64_out));
  Pull_Resistor #(.pull(1)) pull_resistor_35 (.node(pull_resistor_35_node));
  Transistor #(.\type ("n")) transistor_65 (
    .in(transistor_62_out), .out(pull_resistor_35_node), .gate(transistor_1_out));
  Pull_Resistor #(.pull(1)) pull_resistor_36 (.node(pull_resistor_36_node));
  Transistor #(.\type ("n")) transistor_66 (
    .in(transistor_63_out), .out(pull_resistor_36_node), .gate(pull_resistor_31_node));
  Transistor #(.\type ("n")) transistor_67 (.in(1'b0), .out(transistor_67_out), .gate(in_2[0]));
  Pull_Resistor #(.pull(1)) pull_resistor_37 (.node(transistor_67_out));
  Pull_Resistor #(.pull(1)) pull_resistor_38 (.node(pull_resistor_38_node));
  Transistor #(.\type ("n")) transistor_68 (
    .in(transistor_67_out), .out(pull_resistor_38_node), .gate(pull_resistor_39_node));
  Pull_Resistor #(.pull(1)) pull_resistor_39 (.node(pull_resistor_39_node));
  Transistor #(.\type ("n")) transistor_69 (.in(transistor_67_out), .out(pull_resistor_39_node), .gate(in_2[1]));
  Transistor #(.\type ("n")) transistor_70 (.in(1'b0), .out(transistor_70_out), .gate(pull_resistor_38_node));
  Transistor #(.\type ("n")) transistor_71 (.in(1'b0), .out(transistor_71_out), .gate(pull_resistor_39_node));
  Pull_Resistor #(.pull(1)) pull_resistor_40 (.node(transistor_71_out));
  Pull_Resistor #(.pull(1)) pull_resistor_41 (.node(pull_resistor_41_node));
  Transistor #(.\type ("n")) transistor_72 (
    .in(transistor_70_out), .out(pull_resistor_41_node), .gate(transistor_73_out));
  Transistor #(.\type ("n")) transistor_73 (.in(transistor_71_out), .out(transistor_73_out), .gate(in_2[1]));
  Pull_Resistor #(.pull(1)) pull_resistor_42 (.node(transistor_73_out));
  Transistor #(.\type ("n")) transistor_74 (.in(1'b0), .out(transistor_74_out), .gate(in_2[2]));
  Transistor #(.\type ("n")) transistor_75 (
    .in(transistor_74_out), .out(transistor_75_out), .gate(pull_resistor_41_node));
  Pull_Resistor #(.pull(1)) pull_resistor_43 (.node(transistor_75_out));
  Transistor #(.\type ("n")) transistor_76 (.in(transistor_74_out), .out(transistor_76_out), .gate(transistor_75_out));
  Pull_Resistor #(.pull(1)) pull_resistor_44 (.node(transistor_76_out));
  Transistor #(.\type ("n")) transistor_77 (.in(1'b0), .out(transistor_77_out), .gate(transistor_75_out));
  Transistor #(.\type ("n")) transistor_78 (
    .in(transistor_77_out), .out(transistor_78_out), .gate(pull_resistor_39_node));
  Pull_Resistor #(.pull(1)) pull_resistor_45 (.node(transistor_78_out));
  Transistor #(.\type ("n")) transistor_79 (.in(1'b0), .out(transistor_79_out));  // open: gate
  Transistor #(.\type ("n")) transistor_80 (.in(1'b0), .out(transistor_80_out));  // open: gate
  Pull_Resistor #(.pull(1)) pull_resistor_46 (.node(pull_resistor_46_node));
  Transistor #(.\type ("n")) transistor_81 (
    .in(transistor_77_out), .out(pull_resistor_46_node), .gate(pull_resistor_41_node));
  Transistor #(.\type ("n")) transistor_82 (.in(1'b0), .out(transistor_82_out), .gate(transistor_76_out));
  Pull_Resistor #(.pull(1)) pull_resistor_47 (.node(pull_resistor_47_node));
  Transistor #(.\type ("n")) transistor_83 (.in(transistor_79_out), .out(pull_resistor_47_node), .gate(undriven));
  Pull_Resistor #(.pull(1)) pull_resistor_48 (.node(pull_resistor_48_node));
  Transistor #(.\type ("n")) transistor_84 (.in(transistor_80_out), .out(pull_resistor_48_node), .gate(undriven_2));
  Transistor #(.\type ("n")) transistor_85 (
    .in(transistor_82_out), .out(transistor_85_out), .gate(pull_resistor_46_node));
  Pull_Resistor #(.pull(1)) pull_resistor_49 (.node(transistor_85_out));
endmodule
