// Logisim project bachelor extra.circ as structural Verilog: 1 circuit, main circuit main
module main (
  input  [2:0] in_1,
  input  in_2,
  input  in_3,
  input  in_4,
  input  in_5,
  input  in_6,
  input  in_7,
  input  in_8,
  input  in_9,
  input  in_10,
  input  in_11,
  input  in_12,
  input  in_13,
  input  in_14,
  input  in_15,
  input  in_16,
  input  in_17,
  input  in_18,
  input  in_19,
  input  SET,
  input  RESET,
  input  rst,
  input  Enable,
  input  Rising_Edge,
  input  Data_1,
  input  Data_1_2,
  input  Enable_2,
  input  Rising_Edge_2,
  input  Data,
  input  rst_2,
  input  Data_2,
  input  rst_3,
  input  in_33,
  input  Enable_3,
  input  Rising_Edge_3,
  input  Vin
);

  wire and_1_out, and_2_out, and_3_out, and_4_out, and_5_out, and_6_out, nand_1_out, nand_2_out, nand_3_out,
       nand_4_out, nand_5_out, nand_6_out, nand_7_out, nand_8_out, nand_9_out, nand_10_out, nor_1_out,
       nor_2_out, nor_3_out, nor_4_out, nor_5_out, nor_6_out, nor_7_out, nor_8_out, nor_9_out, nor_10_out,
       nor_11_out, not_1_out, not_2_out, not_3_out, not_4_out, not_5_out, not_6_out, or_1_out,
       pull_resistor_1_node, pull_resistor_2_node, pull_resistor_4_node, pull_resistor_9_node,
       pull_resistor_12_node, pull_resistor_13_node, pull_resistor_15_node, pull_resistor_16_node,
       pull_resistor_20_node, pull_resistor_21_node, pull_resistor_24_node, pull_resistor_25_node,
       pull_resistor_26_node, transistor_4_out, transistor_6_out, transistor_7_out, transistor_8_out,
       transistor_9_out, transistor_11_out, transistor_12_out, transistor_13_out, transistor_15_out,
       transistor_17_out, transistor_19_out, transistor_24_out, transistor_25_out, transistor_26_out,
       transistor_27_out, transistor_28_out, transistor_29_out, transistor_30_out, transistor_31_out,
       transistor_32_out, transistor_33_out, transistor_34_out, transistor_35_out, transistor_36_out,
       transistor_37_out, transistor_38_out, transistor_39_out, transistor_41_out, transistor_43_out,
       transistor_44_out, transistor_45_out, transistor_48_out, transistor_49_out, transistor_53_out,
       transistor_54_out, transistor_55_out, transistor_56_out, transistor_57_out, transistor_58_out,
       transistor_59_out, transistor_60_out, transistor_61_out, transistor_62_out, transistor_63_out,
       transistor_64_out, transistor_65_out, transistor_66_out, transistor_67_out;

  not not_1 (not_1_out, in_2);
  nor nor_1 (nor_1_out, in_4, in_5);
  or or_1 (or_1_out, in_8, in_10);
  nand nand_1 (nand_1_out, in_13, in_15);
  and and_1 (and_1_out, in_17, in_19);
  LED led_1 (.in(not_1_out));
  LED led_2 (.in(nor_1_out));
  LED led_3 (.in(or_1_out));
  LED led_4 (.in(nand_1_out));
  LED led_5 (.in(and_1_out));
  Pull_Resistor #(.pull(1)) pull_resistor_1 (.node(pull_resistor_1_node));
  Transistor #(.\type ("n")) transistor_1 (.in(1'b0), .out(pull_resistor_1_node), .gate(in_3));
  LED led_6 (.in(pull_resistor_1_node));
  Pull_Resistor #(.pull(1)) pull_resistor_2 (.node(pull_resistor_2_node));
  Transistor #(.\type ("n")) transistor_2 (.in(1'b0), .out(pull_resistor_2_node), .gate(in_7));
  Transistor #(.\type ("n")) transistor_3 (.in(1'b0), .out(pull_resistor_2_node), .gate(in_6));
  Transistor #(.\type ("n")) transistor_4 (.in(1'b0), .out(transistor_4_out), .gate(in_11));
  Transistor #(.\type ("n")) transistor_5 (.in(1'b0), .out(transistor_4_out), .gate(in_9));
  Pull_Resistor #(.pull(1)) pull_resistor_3 (.node(transistor_4_out));
  Transistor #(.\type ("n")) transistor_6 (.in(transistor_7_out), .out(transistor_6_out), .gate(in_12));
  Transistor #(.\type ("n")) transistor_7 (.in(1'b0), .out(transistor_7_out), .gate(in_14));
  Transistor #(.\type ("n")) transistor_8 (.in(1'b0), .out(transistor_8_out), .gate(in_18));
  Transistor #(.\type ("n")) transistor_9 (.in(transistor_8_out), .out(transistor_9_out), .gate(in_16));
  LED led_7 (.in(pull_resistor_2_node));
  Pull_Resistor #(.pull(1)) pull_resistor_4 (.node(pull_resistor_4_node));
  Transistor #(.\type ("n")) transistor_10 (.in(1'b0), .out(pull_resistor_4_node), .gate(transistor_4_out));
  LED led_8 (.in(pull_resistor_4_node));
  LED led_9 (.in(transistor_6_out));
  Pull_Resistor #(.pull(1)) pull_resistor_5 (.node(transistor_6_out));
  Transistor #(.\type ("n")) transistor_11 (.in(1'b0), .out(transistor_11_out), .gate(transistor_9_out));
  Pull_Resistor #(.pull(1)) pull_resistor_6 (.node(transistor_11_out));
  Pull_Resistor #(.pull(1)) pull_resistor_7 (.node(transistor_9_out));
  LED led_10 (.in(transistor_11_out));
  not not_2 (not_2_out, in_1[2]);
  not not_3 (not_3_out, in_1[0]);
  not not_4 (not_4_out, in_1[1]);
  nand nand_2 (nand_2_out, Enable, Rising_Edge);
  not not_5 (not_5_out, nand_2_out);
  Transistor #(.\type ("n")) transistor_12 (.in(transistor_13_out), .out(transistor_12_out), .gate(Enable_3));
  Pull_Resistor #(.pull(1)) pull_resistor_8 (.node(transistor_12_out));
  Transistor #(.\type ("n")) transistor_13 (.in(1'b0), .out(transistor_13_out), .gate(Rising_Edge_3));
  LED led_11 (.in(nand_3_out));
  nand nand_3 (nand_3_out, not_3_out, not_4_out, not_2_out);
  LED led_12 (.in(nand_4_out));
  nand nand_4 (nand_4_out, in_1[0], not_4_out, not_2_out);
  nand nand_5 (nand_5_out, not_3_out, in_1[1], not_2_out);
  LED led_13 (.in(nand_5_out));
  LED led_14 (.in(nand_6_out));
  nand nand_6 (nand_6_out, in_1[0], in_1[1], not_2_out);
  LED led_15 (.in(nand_7_out));
  nand nand_7 (nand_7_out, not_3_out, not_4_out, in_1[2]);
  nand nand_8 (nand_8_out, in_1[0], not_4_out, in_1[2]);
  LED led_16 (.in(nand_8_out));
  LED led_17 (.in(nand_9_out));
  nand nand_9 (nand_9_out, not_3_out, in_1[1], in_1[2]);
  LED led_18 (.in(nand_10_out));
  nand nand_10 (nand_10_out, in_1[0], in_1[1], in_1[2]);
  and and_2 (and_2_out, Enable_2, Rising_Edge_2);
  not not_6 (not_6_out, Data);
  Pull_Resistor #(.pull(1)) pull_resistor_9 (.node(pull_resistor_9_node));
  Transistor #(.\type ("n")) transistor_14 (.in(1'b0), .out(pull_resistor_9_node), .gate(transistor_12_out));
  nor nor_2 (nor_2_out, SET, nor_3_out);
  nor nor_3 (nor_3_out, nor_2_out, RESET);
  and and_3 (and_3_out, not_5_out, Data_1);
  and and_4 (and_4_out, not_5_out, Data_1_2);
  and and_5 (and_5_out, Data, and_2_out);
  and and_6 (and_6_out, and_2_out, not_6_out);
  Transistor #(.\type ("n"), .gate("br")) transistor_15 (.in(1'b0), .out(transistor_15_out), .gate(transistor_12_out));
  Transistor #(.\type ("n")) transistor_16 (.in(1'b0), .out(transistor_15_out), .gate(Data_2));
  Pull_Resistor #(.pull(1)) pull_resistor_10 (.node(transistor_15_out));
  LED led_19 (.in(nor_2_out));
  LED led_20 (.in(nor_3_out));
  nor nor_4 (nor_4_out, rst, nor_5_out, nor_6_out);
  nor nor_5 (nor_5_out, nand_2_out, Data_1);
  nor nor_6 (nor_6_out, nor_4_out, and_3_out);
  nor nor_7 (nor_7_out, nand_2_out, Data_1_2);
  nor nor_8 (nor_8_out, rst, nor_7_out, nor_9_out);
  nor nor_9 (nor_9_out, nor_8_out, and_4_out);
  nor nor_10 (nor_10_out, and_5_out, nor_11_out);
  LED led_21 (.in(nor_10_out));
  nor nor_11 (nor_11_out, nor_10_out, rst_2, and_6_out);
  LED led_22 (.in(nor_11_out));
  Transistor #(.\type ("n")) transistor_17 (.in(1'b0), .out(transistor_17_out), .gate(transistor_15_out));
  Transistor #(.\type ("n"), .gate("br")) transistor_18 (.in(1'b0), .out(transistor_17_out), .gate(rst_3));
  Transistor #(.\type ("n")) transistor_19 (.in(1'b0), .out(transistor_19_out), .gate(in_1[1]));
  Pull_Resistor #(.pull(1)) pull_resistor_11 (.node(transistor_19_out));
  Pull_Resistor #(.pull(1)) pull_resistor_12 (.node(pull_resistor_12_node));
  Transistor #(.\type ("n")) transistor_20 (.in(1'b0), .out(pull_resistor_12_node), .gate(in_1[2]));
  LED led_23 (.in(nor_6_out));
  LED led_24 (.in(nor_9_out));
  Pull_Resistor #(.pull(1)) pull_resistor_13 (.node(pull_resistor_13_node));
  Pull_Resistor #(.pull(1)) pull_resistor_14 (.node(transistor_17_out));
  Transistor #(.\type ("n"), .gate("br")) transistor_21 (
    .in(1'b0), .out(transistor_17_out), .gate(pull_resistor_13_node));
  Transistor #(.\type ("n")) transistor_22 (.in(1'b0), .out(pull_resistor_13_node), .gate(transistor_17_out));
  Pull_Resistor #(.pull(1)) pull_resistor_15 (.node(pull_resistor_15_node));
  Transistor #(.\type ("n")) transistor_23 (.in(1'b0), .out(pull_resistor_15_node), .gate(in_1[0]));
  Transistor #(.\type ("n")) transistor_24 (.in(transistor_25_out), .out(transistor_24_out), .gate(transistor_19_out));
  Transistor #(.\type ("n")) transistor_25 (.in(1'b0), .out(transistor_25_out), .gate(pull_resistor_12_node));
  Transistor #(.\type ("n")) transistor_26 (.in(transistor_27_out), .out(transistor_26_out), .gate(transistor_19_out));
  Transistor #(.\type ("n")) transistor_27 (.in(1'b0), .out(transistor_27_out), .gate(pull_resistor_12_node));
  Transistor #(.\type ("n")) transistor_28 (.in(1'b0), .out(transistor_28_out), .gate(pull_resistor_12_node));
  Transistor #(.\type ("n")) transistor_29 (.in(transistor_28_out), .out(transistor_29_out), .gate(in_1[1]));
  Transistor #(.\type ("n")) transistor_30 (.in(1'b0), .out(transistor_30_out), .gate(pull_resistor_12_node));
  Transistor #(.\type ("n")) transistor_31 (.in(transistor_30_out), .out(transistor_31_out), .gate(in_1[1]));
  Transistor #(.\type ("n")) transistor_32 (.in(transistor_33_out), .out(transistor_32_out), .gate(transistor_19_out));
  Transistor #(.\type ("n")) transistor_33 (.in(1'b0), .out(transistor_33_out), .gate(in_1[2]));
  Transistor #(.\type ("n")) transistor_34 (.in(transistor_35_out), .out(transistor_34_out), .gate(transistor_19_out));
  Transistor #(.\type ("n")) transistor_35 (.in(1'b0), .out(transistor_35_out), .gate(in_1[2]));
  Transistor #(.\type ("n")) transistor_36 (.in(1'b0), .out(transistor_36_out), .gate(in_1[2]));
  Transistor #(.\type ("n")) transistor_37 (.in(transistor_36_out), .out(transistor_37_out), .gate(in_1[1]));
  Transistor #(.\type ("n")) transistor_38 (.in(1'b0), .out(transistor_38_out), .gate(in_1[2]));
  Transistor #(.\type ("n")) transistor_39 (.in(transistor_38_out), .out(transistor_39_out), .gate(in_1[1]));
  Transistor #(.\type ("n"), .gate("br")) transistor_40 (
    .in(transistor_41_out), .out(pull_resistor_13_node), .gate(pull_resistor_9_node));
  Transistor #(.\type ("n"), .gate("br")) transistor_41 (.in(1'b0), .out(transistor_41_out), .gate(Data_2));
  Pull_Resistor #(.pull(1)) pull_resistor_16 (.node(pull_resistor_16_node));
  LED led_25 (.in(pull_resistor_16_node));
  Transistor #(.\type ("n")) transistor_42 (
    .in(transistor_24_out), .out(pull_resistor_16_node), .gate(pull_resistor_15_node));
  Transistor #(.\type ("n")) transistor_43 (.in(transistor_26_out), .out(transistor_43_out), .gate(in_1[0]));
  LED led_26 (.in(transistor_43_out));
  Pull_Resistor #(.pull(1)) pull_resistor_17 (.node(transistor_43_out));
  Transistor #(.\type ("n")) transistor_44 (
    .in(transistor_29_out), .out(transistor_44_out), .gate(pull_resistor_15_node));
  LED led_27 (.in(transistor_44_out));
  Pull_Resistor #(.pull(1)) pull_resistor_18 (.node(transistor_44_out));
  Transistor #(.\type ("n")) transistor_45 (.in(transistor_31_out), .out(transistor_45_out), .gate(in_1[0]));
  Pull_Resistor #(.pull(1)) pull_resistor_19 (.node(transistor_45_out));
  LED led_28 (.in(transistor_45_out));
  LED led_29 (.in(pull_resistor_20_node));
  Pull_Resistor #(.pull(1)) pull_resistor_20 (.node(pull_resistor_20_node));
  Transistor #(.\type ("n")) transistor_46 (
    .in(transistor_32_out), .out(pull_resistor_20_node), .gate(pull_resistor_15_node));
  Pull_Resistor #(.pull(1)) pull_resistor_21 (.node(pull_resistor_21_node));
  Transistor #(.\type ("n")) transistor_47 (.in(transistor_34_out), .out(pull_resistor_21_node), .gate(in_1[0]));
  LED led_30 (.in(pull_resistor_21_node));
  Transistor #(.\type ("n")) transistor_48 (
    .in(transistor_37_out), .out(transistor_48_out), .gate(pull_resistor_15_node));
  LED led_31 (.in(transistor_48_out));
  Pull_Resistor #(.pull(1)) pull_resistor_22 (.node(transistor_48_out));
  Transistor #(.\type ("n")) transistor_49 (.in(transistor_39_out), .out(transistor_49_out), .gate(in_1[0]));
  Pull_Resistor #(.pull(1)) pull_resistor_23 (.node(transistor_49_out));
  LED led_32 (.in(transistor_49_out));
  LED led_33 (.in(transistor_17_out));
  Pull_Resistor #(.pull(1)) pull_resistor_24 (.node(pull_resistor_24_node));
  LED led_34 (.in(pull_resistor_24_node));
  Transistor #(.\type ("n")) transistor_50 (.in(1'b0), .out(pull_resistor_24_node), .gate(Vin));
  Pull_Resistor #(.pull(1)) pull_resistor_25 (.node(pull_resistor_25_node));
  Transistor #(.\type ("n")) transistor_51 (.in(1'b0), .out(pull_resistor_25_node), .gate(in_1[2]));
  Pull_Resistor #(.pull(1)) pull_resistor_26 (.node(pull_resistor_26_node));
  Transistor #(.\type ("n")) transistor_52 (.in(1'b0), .out(pull_resistor_26_node), .gate(in_1[1]));
  Transistor #(.\type ("n")) transistor_53 (.in(1'b0), .out(transistor_53_out), .gate(pull_resistor_25_node));
  Transistor #(.\type ("n")) transistor_54 (.in(1'b0), .out(transistor_54_out), .gate(in_1[2]));
  Transistor #(.\type ("n")) transistor_55 (.in(1'b0), .out(transistor_55_out), .gate(in_1[0]));
  Pull_Resistor #(.pull(1)) pull_resistor_27 (.node(transistor_55_out));
  Transistor #(.\type ("n")) transistor_56 (
    .in(transistor_53_out), .out(transistor_56_out), .gate(pull_resistor_26_node));
  Transistor #(.\type ("n")) transistor_57 (.in(transistor_56_out), .out(transistor_57_out), .gate(transistor_55_out));
  Transistor #(.\type ("n")) transistor_58 (.in(transistor_56_out), .out(transistor_58_out), .gate(in_1[0]));
  Transistor #(.\type ("n")) transistor_59 (.in(transistor_60_out), .out(transistor_59_out), .gate(transistor_55_out));
  Transistor #(.\type ("n")) transistor_60 (.in(transistor_53_out), .out(transistor_60_out), .gate(in_1[1]));
  Transistor #(.\type ("n")) transistor_61 (.in(transistor_60_out), .out(transistor_61_out), .gate(in_1[0]));
  Transistor #(.\type ("n")) transistor_62 (
    .in(transistor_54_out), .out(transistor_62_out), .gate(pull_resistor_26_node));
  Transistor #(.\type ("n")) transistor_63 (.in(transistor_62_out), .out(transistor_63_out), .gate(transistor_55_out));
  Transistor #(.\type ("n")) transistor_64 (.in(transistor_62_out), .out(transistor_64_out), .gate(in_1[0]));
  Transistor #(.\type ("n")) transistor_65 (.in(transistor_54_out), .out(transistor_65_out), .gate(in_1[1]));
  Transistor #(.\type ("n")) transistor_66 (.in(transistor_65_out), .out(transistor_66_out), .gate(transistor_55_out));
  Transistor #(.\type ("n")) transistor_67 (.in(transistor_65_out), .out(transistor_67_out), .gate(in_1[0]));
  LED led_35 (.in(transistor_57_out));
  Pull_Resistor #(.pull(1)) pull_resistor_28 (.node(transistor_57_out));
  LED led_36 (.in(transistor_58_out));
  Pull_Resistor #(.pull(1)) pull_resistor_29 (.node(transistor_58_out));
  LED led_37 (.in(transistor_59_out));
  Pull_Resistor #(.pull(1)) pull_resistor_30 (.node(transistor_59_out));
  Pull_Resistor #(.pull(1)) pull_resistor_31 (.node(transistor_61_out));
  LED led_38 (.in(transistor_61_out));
  LED led_39 (.in(transistor_63_out));
  Pull_Resistor #(.pull(1)) pull_resistor_32 (.node(transistor_63_out));
  LED led_40 (.in(transistor_64_out));
  Pull_Resistor #(.pull(1)) pull_resistor_33 (.node(transistor_64_out));
  LED led_41 (.in(transistor_66_out));
  Pull_Resistor #(.pull(1)) pull_resistor_34 (.node(transistor_66_out));
  LED led_42 (.in(transistor_67_out));
  Pull_Resistor #(.pull(1)) pull_resistor_35 (.node(transistor_67_out));
  LED led_43 ();  // open: in

  // Notes on the sheet:
  //   NOT GATE
  //   NOR GATE
  //   OR GATE
  //   NAND GATE
  //   AND GATE
  //   Normal Gate
  //   TTL equivalent
  //   Logic gates
  //   !Q
  //   Q
  //   TTL equivalent
  //   !Q
  //   Q
  //   5V
  //   20kΩ
  //   Vout
  //   2N7002
  //   Simplified TTL equivalent
endmodule
