// Logisim project memory_Sim.circ as structural Verilog: 1 circuit, main circuit main
module main (
  input  in_1,
  input  in_2,
  input  in_3,
  input  in_4,
  input  [15:0] in_5,
  input  in_6,
  input  in_7
);

  wire A___ALU_A, A___ALU_B, ADD, ADR_0, ADR_1, ADR_2, ADR_3, ADR_4, ADR_5, ADR_6, ADR_7, ADR_8, ADR_9,
       ADR_10, ADR_11, ADR_12, ADR_13, ADR_14, ADR_15, ADR___0, ADR___1, ADR___2, ADR___3, ADR___4, ADR___5,
       ADR___6, ADR___7, ADR___8, ADR___9, ADR___10, ADR___11, ADR___12, ADR___13, ADR___14, ADR___15,
       ALU_B___FF, ALU_FLAG_C, ALU_FLAG_N, ALU_FLAG_O, ALU_FLAG_U, ALU_FLAG_Z, AND, and_1_out, B___ALU_A,
       B___ALU_B, bus_out____Main_bus, button_1_out, button_2_out, button_3_out, C___ALU_A, C___ALU_B,
       Carry_in, clock_1_out, clock_2_out, clock_3_out, clock_4_out, clock_7_out, clock_8_out, clock_9_out,
       clock_10_out, clock_11_out, clock_12_out, clock_13_out, clock_14_out, clock_15_out, Commit_jump,
       D___ALU_A, D___ALU_B, FLAG_C, FLAG_N, FLAG_O, FLAG_STORE_C, FLAG_STORE_N, FLAG_STORE_O, FLAG_STORE_U,
       FLAG_STORE_Z, FLAG_U, FLAG_Z, jump_type_instruction, Main_bus____bus_out, nADC, nADD, nAND, nBNC,
       nBNO, nBNU, nBNZ, nBOC, nBON, nBOO, nBOP, nBOU, nBOZ, nClear, nDEC, NEXT_ADR_0, NEXT_ADR_1,
       NEXT_ADR_2, NEXT_ADR_3, NEXT_ADR_4, NEXT_ADR_5, NEXT_ADR_6, NEXT_ADR_7, NEXT_ADR_8, NEXT_ADR_9,
       NEXT_ADR_10, NEXT_ADR_11, NEXT_ADR_12, NEXT_ADR_13, NEXT_ADR_14, NEXT_ADR_15, nINC, nJMP, nLoad, nMOV,
       nNOT, nOR, NOT, not_1_out, not_2_out, not_3_out, not_4_out, not_5_out, not_6_out, not_7_out,
       not_8_out, not_9_out, not_10_out, not_11_out, not_12_out, not_13_out, not_14_out, not_15_out,
       not_16_out, not_17_out, not_18_out, not_19_out, not_20_out, not_21_out, not_22_out, not_23_out,
       not_24_out, not_25_out, not_26_out, not_27_out, not_28_out, not_29_out, not_30_out, not_31_out,
       not_32_out, not_33_out, not_34_out, not_35_out, not_36_out, not_37_out, nRS, nStore, nTIME_STEP_0,
       nXOR, OR, pull_resistor_33_node, pull_resistor_34_node, pull_resistor_35_node, pull_resistor_36_node,
       pull_resistor_37_node, pull_resistor_40_node, pull_resistor_74_node, pull_resistor_75_node,
       pull_resistor_80_node, pull_resistor_88_node, pull_resistor_89_node, pull_resistor_92_node,
       pull_resistor_96_node, pull_resistor_98_node, pull_resistor_103_node, pull_resistor_106_node,
       pull_resistor_107_node, pull_resistor_109_node, pull_resistor_115_node, pull_resistor_116_node,
       pull_resistor_117_node, pull_resistor_118_node, pull_resistor_120_node, pull_resistor_126_node,
       pull_resistor_128_node, pull_resistor_130_node, pull_resistor_132_node, pull_resistor_133_node,
       pull_resistor_137_node, pull_resistor_138_node, pull_resistor_140_node, pull_resistor_141_node,
       pull_resistor_142_node, pull_resistor_144_node, pull_resistor_145_node, pull_resistor_147_node,
       pull_resistor_149_node, pull_resistor_150_node, pull_resistor_151_node, pull_resistor_153_node,
       pull_resistor_157_node, pull_resistor_159_node, pull_resistor_163_node, pull_resistor_165_node,
       pull_resistor_166_node, pull_resistor_167_node, pull_resistor_169_node, pull_resistor_172_node,
       pull_resistor_185_node, pull_resistor_186_node, pull_resistor_191_node, pull_resistor_194_node,
       pull_resistor_198_node, pull_resistor_200_node, pull_resistor_203_node, pull_resistor_205_node,
       pull_resistor_209_node, pull_resistor_213_node, pull_resistor_217_node, pull_resistor_219_node,
       pull_resistor_232_node, pull_resistor_233_node, pull_resistor_236_node, pull_resistor_238_node,
       pull_resistor_239_node, pull_resistor_241_node, pull_resistor_244_node, pull_resistor_246_node,
       pull_resistor_248_node, pull_resistor_250_node, pull_resistor_251_node, pull_resistor_254_node,
       pull_resistor_255_node, pull_resistor_257_node, pull_resistor_259_node, pull_resistor_262_node,
       pull_resistor_311_node, pull_resistor_313_node, pull_resistor_315_node, pull_resistor_332_node,
       pull_resistor_334_node, pull_resistor_335_node, pull_resistor_337_node, pull_resistor_338_node,
       pull_resistor_339_node, pull_resistor_343_node, pull_resistor_349_node, pull_resistor_353_node,
       pull_resistor_355_node, pull_resistor_356_node, pull_resistor_357_node, pull_resistor_358_node,
       pull_resistor_359_node, pull_resistor_361_node, pull_resistor_362_node, pull_resistor_366_node,
       pull_resistor_369_node, pull_resistor_370_node, pull_resistor_371_node, pull_resistor_373_node,
       pull_resistor_377_node, pull_resistor_380_node, pull_resistor_384_node, pull_resistor_385_node,
       pull_resistor_386_node, pull_resistor_389_node, pull_resistor_391_node, pull_resistor_392_node,
       pull_resistor_400_node, pull_resistor_401_node, pull_resistor_404_node, pull_resistor_409_node,
       pull_resistor_410_node, pull_resistor_411_node, pull_resistor_412_node, pull_resistor_414_node,
       pull_resistor_415_node, pull_resistor_416_node, pull_resistor_417_node, pull_resistor_418_node,
       pull_resistor_419_node, pull_resistor_425_node, pull_resistor_426_node, pull_resistor_427_node,
       pull_resistor_428_node, pull_resistor_438_node, pull_resistor_439_node, pull_resistor_440_node,
       pull_resistor_444_node, pull_resistor_447_node, pull_resistor_449_node, pull_resistor_450_node,
       pull_resistor_451_node, pull_resistor_453_node, pull_resistor_454_node, pull_resistor_463_node,
       pull_resistor_464_node, pull_resistor_465_node, pull_resistor_467_node, R_W_out, READ_A, READ_B,
       READ_C, READ_D, READ_FALG, Read_From_stored_Address, Read_New_Instruction, Read_Write_ins,
       REG____ALU_A, REG____ALU_B, REG_Read, RS, Store_Address_plus_plus, STORED_ADR_0, STORED_ADR_1,
       STORED_ADR_2, STORED_ADR_3, STORED_ADR_4, STORED_ADR_5, STORED_ADR_6, STORED_ADR_7, STORED_ADR_8,
       STORED_ADR_9, STORED_ADR_10, STORED_ADR_11, STORED_ADR_12, STORED_ADR_13, STORED_ADR_14,
       STORED_ADR_15, TEMP_ADR_0, TEMP_ADR_1, TEMP_ADR_2, TEMP_ADR_3, TEMP_ADR_4, TEMP_ADR_5, TEMP_ADR_6,
       TEMP_ADR_7, TEMP_ADR_8, TEMP_ADR_9, TEMP_ADR_10, TEMP_ADR_11, TEMP_ADR_12, TEMP_ADR_13, TEMP_ADR_14,
       TEMP_ADR_15, TIME_STEP_0, TIME_STEP_0or1, TIME_STEP_0or1or2, TIME_STEP_1, TIME_STEP_2, TIME_STEP_IN_0,
       TIME_STEP_IN_1, TIME_STEP_IN_2, transistor_6_out, transistor_7_out, transistor_8_out,
       transistor_9_out, transistor_10_out, transistor_12_out, transistor_13_out, transistor_14_out,
       transistor_15_out, transistor_16_out, transistor_19_out, transistor_22_out, transistor_25_out,
       transistor_28_out, transistor_29_out, transistor_30_out, transistor_31_out, transistor_32_out,
       transistor_33_out, transistor_34_out, transistor_38_out, transistor_40_out, transistor_44_out,
       transistor_45_out, transistor_46_out, transistor_47_out, transistor_49_out, transistor_52_out,
       transistor_54_out, transistor_58_out, transistor_60_out, transistor_64_out, transistor_65_out,
       transistor_68_out, transistor_71_out, transistor_73_out, transistor_74_out, transistor_75_out,
       transistor_77_out, transistor_78_out, transistor_79_out, transistor_80_out, transistor_81_out,
       transistor_82_out, transistor_95_out, transistor_96_out, transistor_97_out, transistor_98_out,
       transistor_99_out, transistor_100_out, transistor_101_out, transistor_102_out, transistor_103_out,
       transistor_104_out, transistor_105_out, transistor_106_out, transistor_107_out, transistor_110_out,
       transistor_111_out, transistor_112_out, transistor_113_out, transistor_114_out, transistor_115_out,
       transistor_116_out, transistor_117_out, transistor_118_out, transistor_119_out, transistor_122_out,
       transistor_124_out, transistor_126_out, transistor_127_out, transistor_128_out, transistor_129_out,
       transistor_131_out, transistor_132_out, transistor_133_out, transistor_134_out, transistor_135_out,
       transistor_136_out, transistor_137_out, transistor_138_out, transistor_140_out, transistor_144_out,
       transistor_145_out, transistor_146_out, transistor_147_out, transistor_149_out, transistor_150_out,
       transistor_152_out, transistor_153_out, transistor_157_out, transistor_159_out, transistor_160_out,
       transistor_162_out, transistor_164_out, transistor_165_out, transistor_166_out, transistor_169_out,
       transistor_171_out, transistor_175_out, transistor_183_out, transistor_187_out, transistor_190_out,
       transistor_194_out, transistor_195_out, transistor_197_out, transistor_199_out, transistor_202_out,
       transistor_204_out, transistor_212_out, transistor_213_out, transistor_214_out, transistor_216_out,
       transistor_219_out, transistor_225_out, transistor_226_out, transistor_229_out, transistor_230_out,
       transistor_231_out, transistor_233_out, transistor_234_out, transistor_235_out, transistor_236_out,
       transistor_238_out, transistor_241_out, transistor_246_out, transistor_250_out, transistor_253_out,
       transistor_256_out, transistor_259_out, transistor_260_out, transistor_262_out, transistor_265_out,
       transistor_268_out, transistor_270_out, transistor_271_out, transistor_274_out, transistor_277_out,
       transistor_278_out, transistor_281_out, transistor_283_out, transistor_286_out, transistor_288_out,
       transistor_292_out, transistor_295_out, transistor_297_out, transistor_299_out, transistor_302_out,
       transistor_304_out, transistor_306_out, transistor_307_out, transistor_309_out, transistor_312_out,
       transistor_314_out, transistor_317_out, transistor_319_out, transistor_321_out, transistor_322_out,
       transistor_324_out, transistor_327_out, transistor_329_out, transistor_332_out, transistor_334_out,
       transistor_336_out, transistor_338_out, transistor_340_out, transistor_342_out, transistor_345_out,
       transistor_347_out, transistor_349_out, transistor_350_out, transistor_352_out, transistor_354_out,
       transistor_356_out, transistor_357_out, transistor_358_out, transistor_359_out, transistor_360_out,
       transistor_362_out, transistor_363_out, transistor_364_out, transistor_366_out, transistor_369_out,
       transistor_374_out, transistor_376_out, transistor_381_out, transistor_383_out, transistor_385_out,
       transistor_387_out, transistor_388_out, transistor_391_out, transistor_392_out, transistor_394_out,
       transistor_395_out, transistor_397_out, transistor_400_out, transistor_402_out, transistor_405_out,
       transistor_407_out, transistor_411_out, transistor_413_out, transistor_416_out, transistor_418_out,
       transistor_420_out, transistor_421_out, transistor_423_out, transistor_426_out, transistor_428_out,
       transistor_430_out, transistor_431_out, transistor_433_out, transistor_436_out, transistor_438_out,
       transistor_440_out, transistor_441_out, transistor_443_out, transistor_446_out, transistor_448_out,
       transistor_449_out, transistor_450_out, transistor_452_out, transistor_454_out, transistor_456_out,
       transistor_458_out, transistor_459_out, transistor_461_out, transistor_463_out, transistor_464_out,
       transistor_466_out, transistor_468_out, transistor_469_out, transistor_471_out, transistor_475_out,
       transistor_476_out, transistor_478_out, transistor_480_out, transistor_482_out, transistor_483_out,
       transistor_484_out, transistor_486_out, transistor_487_out, transistor_488_out, transistor_490_out,
       transistor_491_out, transistor_492_out, transistor_494_out, transistor_495_out, transistor_496_out,
       transistor_498_out, transistor_499_out, transistor_500_out, transistor_502_out, transistor_503_out,
       transistor_504_out, transistor_506_out, transistor_507_out, transistor_508_out, transistor_510_out,
       transistor_511_out, transistor_512_out, transistor_514_out, transistor_515_out, transistor_516_out,
       transistor_518_out, transistor_519_out, transistor_520_out, transistor_522_out, transistor_523_out,
       transistor_524_out, transistor_526_out, transistor_527_out, transistor_528_out, transistor_530_out,
       transistor_531_out, transistor_532_out, transistor_534_out, transistor_535_out, transistor_536_out,
       transistor_538_out, transistor_539_out, transistor_540_out, transistor_542_out, transistor_543_out,
       transistor_592_out, transistor_604_out, transistor_610_out, transistor_611_out, transistor_612_out,
       transistor_618_out, transistor_619_out, transistor_620_out, transistor_623_out, transistor_624_out,
       transistor_629_out, transistor_630_out, transistor_631_out, transistor_632_out, transistor_634_out,
       transistor_635_out, transistor_636_out, transistor_637_out, transistor_638_out, transistor_639_out,
       transistor_640_out, transistor_642_out, transistor_643_out, transistor_644_out, transistor_646_out,
       transistor_648_out, transistor_651_out, transistor_654_out, transistor_656_out, transistor_657_out,
       transistor_658_out, transistor_661_out, transistor_662_out, transistor_664_out, transistor_666_out,
       transistor_667_out, transistor_670_out, transistor_679_out, transistor_680_out, transistor_681_out,
       transistor_682_out, transistor_684_out, transistor_685_out, transistor_686_out, transistor_688_out,
       transistor_689_out, transistor_690_out, transistor_691_out, transistor_693_out, transistor_700_out,
       transistor_702_out, transistor_704_out, transistor_705_out, transistor_706_out, transistor_709_out,
       transistor_710_out, transistor_711_out, transistor_712_out, transistor_713_out, transistor_714_out,
       transistor_715_out, transistor_716_out, transistor_717_out, transistor_718_out, transistor_719_out,
       transistor_720_out, transistor_721_out, transistor_722_out, transistor_723_out, transistor_724_out,
       transistor_725_out, transistor_726_out, transistor_729_out, transistor_730_out, transistor_732_out,
       transistor_733_out, transistor_734_out, transistor_738_out, transistor_740_out, transistor_742_out,
       transistor_743_out, transistor_750_out, transistor_751_out, transistor_752_out, transistor_753_out,
       transistor_754_out, transistor_755_out, transistor_756_out, transistor_757_out, transistor_758_out,
       transistor_759_out, transistor_760_out, transistor_761_out, transistor_762_out, transistor_764_out,
       transistor_765_out, transistor_767_out, transistor_770_out, transistor_772_out, transistor_773_out,
       transistor_774_out, transistor_775_out, transistor_776_out, transistor_777_out, transistor_778_out,
       transistor_779_out, transistor_780_out, transistor_784_out, transistor_785_out, transistor_786_out,
       transistor_787_out, transistor_788_out, transistor_789_out, transistor_790_out, transistor_791_out,
       transistor_792_out, transistor_793_out, transistor_794_out, transistor_796_out, transistor_807_out,
       transistor_808_out, transistor_809_out, transistor_810_out, transistor_812_out, transistor_816_out,
       transistor_817_out, transistor_818_out, transistor_824_out, transistor_825_out, transistor_826_out,
       transistor_833_out, transistor_834_out, transistor_835_out, transistor_840_out, transistor_841_out,
       transistor_843_out, transistor_846_out, transistor_848_out, transistor_849_out, transistor_852_out,
       transistor_854_out, transistor_855_out, transistor_861_out, transistor_862_out, transistor_864_out,
       transistor_866_out, transistor_869_out, transistor_871_out, transistor_872_out, transistor_875_out,
       transistor_877_out, transistor_885_out, transistor_886_out, transistor_887_out, transistor_888_out,
       transistor_889_out, transistor_890_out, transistor_891_out, transistor_892_out, transistor_894_out,
       transistor_903_out, transistor_904_out, transistor_905_out, transistor_906_out, transistor_909_out,
       transistor_910_out, transistor_913_out, transistor_914_out, transistor_917_out, transistor_918_out,
       transistor_921_out, transistor_922_out, transistor_925_out, transistor_926_out, transistor_927_out,
       transistor_928_out, transistor_929_out, transistor_930_out, transistor_931_out, transistor_932_out,
       transistor_936_out, transistor_937_out, transistor_938_out, transistor_942_out, transistor_943_out,
       transistor_944_out, transistor_948_out, transistor_949_out, transistor_950_out, transistor_954_out,
       transistor_955_out, transistor_956_out, transistor_960_out, transistor_961_out, transistor_962_out,
       transistor_963_out, transistor_966_out, transistor_967_out, transistor_969_out, transistor_972_out,
       transistor_974_out, transistor_975_out, transistor_978_out, transistor_979_out, transistor_980_out,
       transistor_981_out, transistor_982_out, transistor_985_out, transistor_986_out, transistor_989_out,
       transistor_990_out, transistor_993_out, transistor_994_out, transistor_997_out, transistor_998_out,
       transistor_1001_out, transistor_1002_out, transistor_1003_out, transistor_1004_out,
       transistor_1006_out, transistor_1008_out, transistor_1010_out, transistor_1012_out,
       transistor_1013_out, transistor_1016_out, transistor_1017_out, transistor_1020_out,
       transistor_1022_out, transistor_1023_out, transistor_1026_out, transistor_1027_out, XOR;
  wire [6:0] Main_bus;
  wire [7:0] ALU_A, ALU_B, Buss, register_1_q, register_7_q, register_8_q, register_9_q, register_10_q,
       transistor_26_out;
  wire [15:0] counter_2_q, multiplexer_1_out, multiplexer_2_out;

  Register #(.trigger("falling")) register_1 (
    .D(Buss), .en(Read_New_Instruction), .Q(register_1_q), .clk(clock_1_out), .clr(in_6));
  Clock clock_1 (.out(clock_1_out));
  Transistor #(.\type ("n")) transistor_1 (.in(1'b0), .out(transistor_26_out[7]), .gate(register_1_q[0]));
  Pull_Resistor #(.pull(1)) pull_resistor_1 (.node(transistor_26_out[7]));
  Pull_Resistor #(.pull(1)) pull_resistor_2 (.node(transistor_26_out[6]));
  Transistor #(.\type ("n")) transistor_2 (.in(1'b0), .out(transistor_26_out[6]), .gate(register_1_q[1]));
  Hex_Digit_Display hex_digit_display_1 (.value(register_1_q[3:0]));  // open: dp
  Hex_Digit_Display hex_digit_display_2 (.value(register_1_q[7:4]));  // open: dp
  Pull_Resistor #(.pull(1)) pull_resistor_3 (.node(transistor_26_out[5]));
  Transistor #(.\type ("n")) transistor_3 (.in(1'b0), .out(transistor_26_out[4]), .gate(register_1_q[3]));
  Transistor #(.\type ("n")) transistor_4 (.in(1'b0), .out(transistor_26_out[5]), .gate(register_1_q[2]));
  Pull_Resistor #(.pull(1)) pull_resistor_4 (.node(transistor_26_out[4]));
  Pull_Resistor #(.pull(1)) pull_resistor_5 (.node(transistor_26_out[3]));
  Transistor #(.\type ("n")) transistor_5 (.in(1'b0), .out(transistor_26_out[3]), .gate(register_1_q[4]));
  Transistor #(.\type ("n")) transistor_6 (.in(transistor_7_out), .out(transistor_6_out), .gate(transistor_26_out[1]));
  Transistor #(.\type ("n")) transistor_7 (.in(1'b0), .out(transistor_7_out), .gate(transistor_26_out[0]));
  Transistor #(.\type ("n")) transistor_8 (.in(transistor_7_out), .out(transistor_8_out), .gate(register_1_q[6]));
  Transistor #(.\type ("n")) transistor_9 (.in(1'b0), .out(transistor_9_out), .gate(register_1_q[7]));
  Transistor #(.\type ("n")) transistor_10 (
    .in(transistor_9_out), .out(transistor_10_out), .gate(transistor_26_out[1]));
  Transistor #(.\type ("n")) transistor_11 (.in(1'b0), .out(transistor_26_out[2]), .gate(register_1_q[5]));
  Pull_Resistor #(.pull(1)) pull_resistor_6 (.node(transistor_26_out[2]));
  Transistor #(.\type ("n")) transistor_12 (
    .in(transistor_13_out), .out(transistor_12_out), .gate(transistor_26_out[3]));
  Transistor #(.\type ("n")) transistor_13 (
    .in(transistor_6_out), .out(transistor_13_out), .gate(transistor_26_out[2]));
  Transistor #(.\type ("n")) transistor_14 (.in(transistor_13_out), .out(transistor_14_out), .gate(register_1_q[4]));
  Transistor #(.\type ("n")) transistor_15 (.in(transistor_6_out), .out(transistor_15_out), .gate(register_1_q[5]));
  Transistor #(.\type ("n")) transistor_16 (
    .in(transistor_15_out), .out(transistor_16_out), .gate(transistor_26_out[3]));
  Pull_Resistor #(.pull(1)) pull_resistor_7 (.node(nAND));
  Transistor #(.\type ("n")) transistor_17 (.in(transistor_15_out), .out(nAND), .gate(register_1_q[4]));
  Pull_Resistor #(.pull(1)) pull_resistor_8 (.node(nOR));
  Transistor #(.\type ("n")) transistor_18 (.in(transistor_19_out), .out(nOR), .gate(transistor_26_out[3]));
  Transistor #(.\type ("n")) transistor_19 (
    .in(transistor_8_out), .out(transistor_19_out), .gate(transistor_26_out[2]));
  Transistor #(.\type ("n")) transistor_20 (.in(transistor_19_out), .out(nXOR), .gate(register_1_q[4]));
  Pull_Resistor #(.pull(1)) pull_resistor_9 (.node(nXOR));
  Transistor #(.\type ("n")) transistor_21 (.in(transistor_22_out), .out(nADD), .gate(transistor_26_out[3]));
  Pull_Resistor #(.pull(1)) pull_resistor_10 (.node(nADD));
  Transistor #(.\type ("n")) transistor_22 (.in(transistor_8_out), .out(transistor_22_out), .gate(register_1_q[5]));
  Transistor #(.\type ("n")) transistor_23 (.in(transistor_22_out), .out(nADC), .gate(register_1_q[4]));
  Pull_Resistor #(.pull(1)) pull_resistor_11 (.node(nADC));
  Transistor #(.\type ("n")) transistor_24 (.in(transistor_25_out), .out(nMOV), .gate(transistor_26_out[3]));
  Transistor #(.\type ("n")) transistor_25 (
    .in(transistor_10_out), .out(transistor_25_out), .gate(transistor_26_out[2]));
  Pull_Resistor #(.pull(1)) pull_resistor_12 (.node(nMOV));
  Pull_Resistor #(.pull(1)) pull_resistor_13 (.node(transistor_26_out[1]));
  Transistor #(.\type ("n")) transistor_26 (.in(1'b0), .out(transistor_26_out[0]), .gate(register_1_q[7]));
  Pull_Resistor #(.pull(1)) pull_resistor_14 (.node(transistor_26_out[0]));
  Transistor #(.\type ("n")) transistor_27 (.in(1'b0), .out(transistor_26_out[1]), .gate(register_1_q[6]));
  Transistor #(.\type ("n")) transistor_28 (
    .in(transistor_29_out), .out(transistor_28_out), .gate(transistor_26_out[5]));
  Transistor #(.\type ("n")) transistor_29 (
    .in(transistor_12_out), .out(transistor_29_out), .gate(transistor_26_out[4]));
  Transistor #(.\type ("n")) transistor_30 (.in(transistor_29_out), .out(transistor_30_out), .gate(register_1_q[2]));
  Transistor #(.\type ("n")) transistor_31 (
    .in(transistor_32_out), .out(transistor_31_out), .gate(transistor_26_out[5]));
  Transistor #(.\type ("n")) transistor_32 (.in(transistor_12_out), .out(transistor_32_out), .gate(register_1_q[3]));
  Transistor #(.\type ("n")) transistor_33 (.in(transistor_32_out), .out(transistor_33_out), .gate(register_1_q[2]));
  Pull_Resistor #(.pull(1)) pull_resistor_15 (.node(nClear));
  Transistor #(.\type ("n")) transistor_34 (
    .in(transistor_14_out), .out(transistor_34_out), .gate(transistor_26_out[4]));
  Transistor #(.\type ("n")) transistor_35 (.in(transistor_34_out), .out(nClear), .gate(transistor_26_out[5]));
  Pull_Resistor #(.pull(1)) pull_resistor_16 (.node(nLoad));
  Transistor #(.\type ("n")) transistor_36 (.in(transistor_34_out), .out(nLoad), .gate(register_1_q[2]));
  Transistor #(.\type ("n")) transistor_37 (.in(transistor_38_out), .out(nStore), .gate(transistor_26_out[5]));
  Transistor #(.\type ("n")) transistor_38 (.in(transistor_14_out), .out(transistor_38_out), .gate(register_1_q[3]));
  Pull_Resistor #(.pull(1)) pull_resistor_17 (.node(nStore));
  Transistor #(.\type ("n")) transistor_39 (.in(transistor_38_out), .out(nINC), .gate(register_1_q[2]));
  Pull_Resistor #(.pull(1)) pull_resistor_18 (.node(nINC));
  Transistor #(.\type ("n")) transistor_40 (
    .in(transistor_16_out), .out(transistor_40_out), .gate(transistor_26_out[4]));
  Pull_Resistor #(.pull(1)) pull_resistor_19 (.node(nDEC));
  Transistor #(.\type ("n")) transistor_41 (.in(transistor_40_out), .out(nDEC), .gate(transistor_26_out[5]));
  Pull_Resistor #(.pull(1)) pull_resistor_20 (.node(nRS));
  Transistor #(.\type ("n")) transistor_42 (.in(transistor_40_out), .out(nRS), .gate(register_1_q[2]));
  Pull_Resistor #(.pull(1)) pull_resistor_21 (.node(nNOT));
  Transistor #(.\type ("n")) transistor_43 (.in(transistor_44_out), .out(nNOT), .gate(transistor_26_out[5]));
  Transistor #(.\type ("n")) transistor_44 (.in(transistor_16_out), .out(transistor_44_out), .gate(register_1_q[3]));
  Transistor #(.\type ("n")) transistor_45 (.in(1'b0), .out(transistor_45_out), .gate(REG_Read));
  Transistor #(.\type ("n")) transistor_46 (.in(1'b0), .out(transistor_46_out), .gate(REG____ALU_A));
  Transistor #(.\type ("n")) transistor_47 (.in(1'b0), .out(transistor_47_out), .gate(REG____ALU_B));
  Counter #(.width(20), .max('hfffff)) counter_1 (
    .count(in_4), .clk(clock_2_out), .clr(button_1_out));  // open: load, D, Q, carry
  Clock clock_2 (.out(clock_2_out));
  Button button_1 (.out(button_1_out));
  Pull_Resistor #(.pull(1)) pull_resistor_22 (.node(nJMP));
  Transistor #(.\type ("n")) transistor_48 (.in(transistor_49_out), .out(nJMP), .gate(transistor_26_out[7]));
  Transistor #(.\type ("n")) transistor_49 (.in(transistor_28_out), .out(transistor_49_out), .gate(register_1_q[1]));
  Pull_Resistor #(.pull(1)) pull_resistor_23 (.node(nBOP));
  Transistor #(.\type ("n")) transistor_50 (.in(transistor_49_out), .out(nBOP), .gate(register_1_q[0]));
  Pull_Resistor #(.pull(1)) pull_resistor_24 (.node(nBON));
  Transistor #(.\type ("n")) transistor_51 (.in(transistor_52_out), .out(nBON), .gate(transistor_26_out[7]));
  Transistor #(.\type ("n")) transistor_52 (
    .in(transistor_30_out), .out(transistor_52_out), .gate(transistor_26_out[6]));
  Pull_Resistor #(.pull(1)) pull_resistor_25 (.node(nBOZ));
  Transistor #(.\type ("n")) transistor_53 (.in(transistor_52_out), .out(nBOZ), .gate(register_1_q[0]));
  Transistor #(.\type ("n")) transistor_54 (.in(transistor_30_out), .out(transistor_54_out), .gate(register_1_q[1]));
  Pull_Resistor #(.pull(1)) pull_resistor_26 (.node(nBNZ));
  Transistor #(.\type ("n")) transistor_55 (.in(transistor_54_out), .out(nBNZ), .gate(transistor_26_out[7]));
  Pull_Resistor #(.pull(1)) pull_resistor_27 (.node(nBOO));
  Transistor #(.\type ("n")) transistor_56 (.in(transistor_54_out), .out(nBOO), .gate(register_1_q[0]));
  Pull_Resistor #(.pull(1)) pull_resistor_28 (.node(nBNO));
  Transistor #(.\type ("n")) transistor_57 (.in(transistor_58_out), .out(nBNO), .gate(transistor_26_out[7]));
  Transistor #(.\type ("n")) transistor_58 (
    .in(transistor_31_out), .out(transistor_58_out), .gate(transistor_26_out[6]));
  Pull_Resistor #(.pull(1)) pull_resistor_29 (.node(nBOU));
  Transistor #(.\type ("n")) transistor_59 (.in(transistor_58_out), .out(nBOU), .gate(register_1_q[0]));
  Transistor #(.\type ("n")) transistor_60 (.in(transistor_31_out), .out(transistor_60_out), .gate(register_1_q[1]));
  Transistor #(.\type ("n")) transistor_61 (.in(transistor_60_out), .out(nBNU), .gate(transistor_26_out[7]));
  Pull_Resistor #(.pull(1)) pull_resistor_30 (.node(nBNU));
  Pull_Resistor #(.pull(1)) pull_resistor_31 (.node(nBOC));
  Transistor #(.\type ("n")) transistor_62 (.in(transistor_60_out), .out(nBOC), .gate(register_1_q[0]));
  Transistor #(.\type ("n")) transistor_63 (.in(transistor_64_out), .out(nBNC), .gate(transistor_26_out[7]));
  Transistor #(.\type ("n")) transistor_64 (
    .in(transistor_33_out), .out(transistor_64_out), .gate(transistor_26_out[6]));
  Pull_Resistor #(.pull(1)) pull_resistor_32 (.node(nBNC));
  Transistor #(.\type ("n")) transistor_65 (
    .in(transistor_45_out), .out(transistor_65_out), .gate(transistor_26_out[6]));
  Pull_Resistor #(.pull(1)) pull_resistor_33 (.node(pull_resistor_33_node));
  Transistor #(.\type ("n")) transistor_66 (
    .in(transistor_65_out), .out(pull_resistor_33_node), .gate(transistor_26_out[7]));
  Pull_Resistor #(.pull(1)) pull_resistor_34 (.node(pull_resistor_34_node));
  Transistor #(.\type ("n")) transistor_67 (
    .in(transistor_65_out), .out(pull_resistor_34_node), .gate(register_1_q[0]));
  Transistor #(.\type ("n")) transistor_68 (.in(transistor_45_out), .out(transistor_68_out), .gate(register_1_q[1]));
  Pull_Resistor #(.pull(1)) pull_resistor_35 (.node(pull_resistor_35_node));
  Transistor #(.\type ("n")) transistor_69 (
    .in(transistor_68_out), .out(pull_resistor_35_node), .gate(transistor_26_out[7]));
  Pull_Resistor #(.pull(1)) pull_resistor_36 (.node(pull_resistor_36_node));
  Transistor #(.\type ("n")) transistor_70 (
    .in(transistor_68_out), .out(pull_resistor_36_node), .gate(register_1_q[0]));
  Transistor #(.\type ("n")) transistor_71 (
    .in(transistor_46_out), .out(transistor_71_out), .gate(transistor_26_out[6]));
  Pull_Resistor #(.pull(1)) pull_resistor_37 (.node(pull_resistor_37_node));
  Transistor #(.\type ("n")) transistor_72 (
    .in(transistor_71_out), .out(pull_resistor_37_node), .gate(transistor_26_out[7]));
  Transistor #(.\type ("n")) transistor_73 (.in(transistor_71_out), .out(transistor_73_out), .gate(register_1_q[0]));
  Pull_Resistor #(.pull(1)) pull_resistor_38 (.node(transistor_73_out));
  Transistor #(.\type ("n")) transistor_74 (.in(transistor_46_out), .out(transistor_74_out), .gate(register_1_q[1]));
  Transistor #(.\type ("n")) transistor_75 (
    .in(transistor_74_out), .out(transistor_75_out), .gate(transistor_26_out[7]));
  Pull_Resistor #(.pull(1)) pull_resistor_39 (.node(transistor_75_out));
  Pull_Resistor #(.pull(1)) pull_resistor_40 (.node(pull_resistor_40_node));
  Transistor #(.\type ("n")) transistor_76 (
    .in(transistor_74_out), .out(pull_resistor_40_node), .gate(register_1_q[0]));
  Transistor #(.\type ("n")) transistor_77 (
    .in(transistor_47_out), .out(transistor_77_out), .gate(transistor_26_out[4]));
  Transistor #(.\type ("n")) transistor_78 (
    .in(transistor_77_out), .out(transistor_78_out), .gate(transistor_26_out[5]));
  Pull_Resistor #(.pull(1)) pull_resistor_41 (.node(transistor_78_out));
  Transistor #(.\type ("n")) transistor_79 (.in(transistor_77_out), .out(transistor_79_out), .gate(register_1_q[2]));
  Pull_Resistor #(.pull(1)) pull_resistor_42 (.node(transistor_79_out));
  Transistor #(.\type ("n")) transistor_80 (
    .in(transistor_81_out), .out(transistor_80_out), .gate(transistor_26_out[5]));
  Transistor #(.\type ("n")) transistor_81 (.in(transistor_47_out), .out(transistor_81_out), .gate(register_1_q[3]));
  Pull_Resistor #(.pull(1)) pull_resistor_43 (.node(transistor_80_out));
  Transistor #(.\type ("n")) transistor_82 (.in(transistor_81_out), .out(transistor_82_out), .gate(register_1_q[2]));
  Pull_Resistor #(.pull(1)) pull_resistor_44 (.node(transistor_82_out));
  LED led_1 (.in(not_1_out));
  not not_1 (not_1_out, nJMP);
  LED led_2 (.in(not_2_out));
  not not_2 (not_2_out, nBOP);
  LED led_3 (.in(not_3_out));
  not not_3 (not_3_out, nBON);
  not not_4 (not_4_out, nBOZ);
  LED led_4 (.in(not_4_out));
  not not_5 (not_5_out, nBNZ);
  LED led_5 (.in(not_5_out));
  not not_6 (not_6_out, nBOO);
  LED led_6 (.in(not_6_out));
  not not_7 (not_7_out, nBNO);
  LED led_7 (.in(not_7_out));
  not not_8 (not_8_out, nBOU);
  LED led_8 (.in(not_8_out));
  LED led_9 (.in(not_9_out));
  not not_9 (not_9_out, nBNU);
  LED led_10 (.in(not_10_out));
  not not_10 (not_10_out, nBOC);
  LED led_11 (.in(not_11_out));
  not not_11 (not_11_out, nBNC);
  LED led_12 (.in(not_12_out));
  not not_12 (not_12_out, nClear);
  LED led_13 (.in(not_13_out));
  not not_13 (not_13_out, nLoad);
  not not_14 (not_14_out, nStore);
  LED led_14 (.in(not_14_out));
  LED led_15 (.in(not_15_out));
  not not_15 (not_15_out, nINC);
  LED led_16 (.in(not_16_out));
  not not_16 (not_16_out, nDEC);
  LED led_17 (.in(not_17_out));
  not not_17 (not_17_out, nRS);
  not not_18 (not_18_out, nNOT);
  LED led_18 (.in(not_18_out));
  not not_19 (not_19_out, nAND);
  LED led_19 (.in(not_19_out));
  LED led_20 (.in(not_20_out));
  not not_20 (not_20_out, nOR);
  not not_21 (not_21_out, nXOR);
  LED led_21 (.in(not_21_out));
  not not_22 (not_22_out, nADD);
  LED led_22 (.in(not_22_out));
  not not_23 (not_23_out, nADC);
  LED led_23 (.in(not_23_out));
  LED led_24 (.in(not_24_out));
  not not_24 (not_24_out, nMOV);
  LED led_25 (.in(not_25_out));
  not not_25 (not_25_out, pull_resistor_33_node);
  Transistor #(.\type ("n")) transistor_83 (.in(1'b0), .out(READ_A), .gate(pull_resistor_33_node));
  Pull_Resistor #(.pull(1)) pull_resistor_45 (.node(READ_A));
  LED led_26 (.in(not_26_out));
  not not_26 (not_26_out, pull_resistor_34_node);
  Transistor #(.\type ("n")) transistor_84 (.in(1'b0), .out(READ_B), .gate(pull_resistor_34_node));
  Pull_Resistor #(.pull(1)) pull_resistor_46 (.node(READ_B));
  LED led_27 (.in(not_27_out));
  not not_27 (not_27_out, pull_resistor_35_node);
  Transistor #(.\type ("n")) transistor_85 (.in(1'b0), .out(READ_C), .gate(pull_resistor_35_node));
  Pull_Resistor #(.pull(1)) pull_resistor_47 (.node(READ_C));
  LED led_28 (.in(not_28_out));
  not not_28 (not_28_out, pull_resistor_36_node);
  Transistor #(.\type ("n")) transistor_86 (.in(1'b0), .out(READ_D), .gate(pull_resistor_36_node));
  Pull_Resistor #(.pull(1)) pull_resistor_48 (.node(READ_D));
  not not_29 (not_29_out, pull_resistor_37_node);
  LED led_29 (.in(not_29_out));
  Pull_Resistor #(.pull(1)) pull_resistor_49 (.node(A___ALU_A));
  Transistor #(.\type ("n")) transistor_87 (.in(1'b0), .out(A___ALU_A), .gate(pull_resistor_37_node));
  not not_30 (not_30_out, transistor_73_out);
  LED led_30 (.in(not_30_out));
  Pull_Resistor #(.pull(1)) pull_resistor_50 (.node(B___ALU_A));
  Transistor #(.\type ("n")) transistor_88 (.in(1'b0), .out(B___ALU_A), .gate(transistor_73_out));
  not not_31 (not_31_out, transistor_75_out);
  LED led_31 (.in(not_31_out));
  Pull_Resistor #(.pull(1)) pull_resistor_51 (.node(C___ALU_A));
  Transistor #(.\type ("n")) transistor_89 (.in(1'b0), .out(C___ALU_A), .gate(transistor_75_out));
  LED led_32 (.in(not_32_out));
  not not_32 (not_32_out, pull_resistor_40_node);
  Transistor #(.\type ("n")) transistor_90 (.in(1'b0), .out(D___ALU_A), .gate(pull_resistor_40_node));
  Pull_Resistor #(.pull(1)) pull_resistor_52 (.node(D___ALU_A));
  LED led_33 (.in(not_33_out));
  not not_33 (not_33_out, transistor_78_out);
  Transistor #(.\type ("n")) transistor_91 (.in(1'b0), .out(A___ALU_B), .gate(transistor_78_out));
  Pull_Resistor #(.pull(1)) pull_resistor_53 (.node(A___ALU_B));
  LED led_34 (.in(not_34_out));
  not not_34 (not_34_out, transistor_79_out);
  Transistor #(.\type ("n")) transistor_92 (.in(1'b0), .out(B___ALU_B), .gate(transistor_79_out));
  Pull_Resistor #(.pull(1)) pull_resistor_54 (.node(B___ALU_B));
  not not_35 (not_35_out, transistor_80_out);
  LED led_35 (.in(not_35_out));
  Transistor #(.\type ("n")) transistor_93 (.in(1'b0), .out(C___ALU_B), .gate(transistor_80_out));
  Pull_Resistor #(.pull(1)) pull_resistor_55 (.node(C___ALU_B));
  not not_36 (not_36_out, transistor_82_out);
  LED led_36 (.in(not_36_out));
  Transistor #(.\type ("n")) transistor_94 (.in(1'b0), .out(D___ALU_B), .gate(transistor_82_out));
  Pull_Resistor #(.pull(1)) pull_resistor_56 (.node(D___ALU_B));
  Counter #(.width(16), .max('hffff)) counter_2 (
    .count(in_2), .Q(counter_2_q), .clk(clock_3_out), .clr(button_2_out));  // open: load, D, carry
  Clock clock_3 (.out(clock_3_out));
  Button button_2 (.out(button_2_out));
  Multiplexer #(.width(16)) multiplexer_1 (
    .in0(counter_2_q), .in1(in_5), .out(multiplexer_1_out), .sel(in_3), .en(1'b1));
  Transistor #(.\type ("n")) transistor_95 (.in(1'b0), .out(transistor_95_out), .gate(nClear));
  Transistor #(.\type ("n")) transistor_96 (.in(1'b0), .out(transistor_96_out), .gate(nStore));
  Transistor #(.\type ("n")) transistor_97 (.in(1'b0), .out(transistor_97_out), .gate(nAND));
  Transistor #(.\type ("n")) transistor_98 (.in(1'b0), .out(transistor_98_out), .gate(nINC));
  Multiplexer #(.width(16)) multiplexer_2 (
    .in0({ADR_15, ADR_14, ADR_13, ADR_12, ADR_11, ADR_10, ADR_9, ADR_8, ADR_7, ADR_6, ADR_5, ADR_4, ADR_3, ADR_2, ADR_1, ADR_0}),
    .in1(multiplexer_1_out), .out(multiplexer_2_out), .sel(in_2), .en(1'b1));
  Pull_Resistor #(.pull(1)) pull_resistor_57 (.node(Buss[7]));
  Pull_Resistor #(.pull(1)) pull_resistor_58 (.node(Buss[6]));
  Pull_Resistor #(.pull(1)) pull_resistor_59 (.node(Buss[5]));
  Pull_Resistor #(.pull(1)) pull_resistor_60 (.node(Buss[4]));
  Pull_Resistor #(.pull(1)) pull_resistor_61 (.node(Buss[3]));
  Pull_Resistor #(.pull(1)) pull_resistor_62 (.node(Buss[2]));
  Pull_Resistor #(.pull(1)) pull_resistor_63 (.node(Buss[1]));
  Pull_Resistor #(.pull(1)) pull_resistor_64 (.node(Buss[0]));
  Pull_Resistor #(.pull(1)) pull_resistor_65 (.node(ALU_FLAG_N));
  Pull_Resistor #(.pull(1)) pull_resistor_66 (.node(Main_bus[6]));
  Pull_Resistor #(.pull(1)) pull_resistor_67 (.node(Main_bus[5]));
  Pull_Resistor #(.pull(1)) pull_resistor_68 (.node(Main_bus[4]));
  Pull_Resistor #(.pull(1)) pull_resistor_69 (.node(Main_bus[3]));
  Pull_Resistor #(.pull(1)) pull_resistor_70 (.node(Main_bus[2]));
  Pull_Resistor #(.pull(1)) pull_resistor_71 (.node(Main_bus[1]));
  Pull_Resistor #(.pull(1)) pull_resistor_72 (.node(Main_bus[0]));
  Transistor #(.\type ("n")) transistor_99 (.in(transistor_95_out), .out(transistor_99_out), .gate(nLoad));
  Transistor #(.\type ("n")) transistor_100 (.in(transistor_99_out), .out(transistor_100_out), .gate(nINC));
  Transistor #(.\type ("n")) transistor_101 (.in(transistor_96_out), .out(transistor_101_out), .gate(nINC));
  Transistor #(.\type ("n")) transistor_102 (.in(transistor_101_out), .out(transistor_102_out), .gate(nDEC));
  Transistor #(.\type ("n")) transistor_103 (.in(transistor_104_out), .out(transistor_103_out), .gate(nXOR));
  Transistor #(.\type ("n")) transistor_104 (.in(transistor_97_out), .out(transistor_104_out), .gate(nOR));
  Transistor #(.\type ("n")) transistor_105 (.in(transistor_98_out), .out(transistor_105_out), .gate(nDEC));
  Transistor #(.\type ("n")) transistor_106 (.in(transistor_105_out), .out(transistor_106_out), .gate(nRS));
  Pull_Resistor pull_resistor_73 (.node(in_1));
  Clock clock_4 (.out(clock_4_out));
  Transistor #(.\type ("n")) transistor_107 (.in(1'b0), .out(transistor_107_out), .gate(nBOP));
  Pull_Resistor #(.pull(1)) pull_resistor_74 (.node(pull_resistor_74_node));
  Transistor #(.\type ("n")) transistor_108 (
    .in(transistor_110_out), .out(pull_resistor_74_node), .gate(pull_resistor_75_node));
  Pull_Resistor #(.pull(1)) pull_resistor_75 (.node(pull_resistor_75_node));
  Transistor #(.\type ("n")) transistor_109 (.in(1'b0), .out(pull_resistor_75_node), .gate(nLoad));
  Transistor #(.\type ("n")) transistor_110 (.in(1'b0), .out(transistor_110_out), .gate(TIME_STEP_2));
  Transistor #(.\type ("n")) transistor_111 (.in(transistor_112_out), .out(transistor_111_out), .gate(nRS));
  Transistor #(.\type ("n")) transistor_112 (.in(transistor_100_out), .out(transistor_112_out), .gate(nDEC));
  Transistor #(.\type ("n")) transistor_113 (.in(transistor_114_out), .out(transistor_113_out), .gate(nNOT));
  Transistor #(.\type ("n")) transistor_114 (.in(transistor_102_out), .out(transistor_114_out), .gate(nRS));
  Transistor #(.\type ("n")) transistor_115 (.in(transistor_103_out), .out(transistor_115_out), .gate(nADD));
  Transistor #(.\type ("n")) transistor_116 (.in(transistor_115_out), .out(transistor_116_out), .gate(nADC));
  Transistor #(.\type ("n")) transistor_117 (.in(transistor_118_out), .out(transistor_117_out), .gate(nAND));
  Transistor #(.\type ("n")) transistor_118 (.in(transistor_106_out), .out(transistor_118_out), .gate(nNOT));
  ROM #(.addrWidth(16)) rom_1 (.addr(multiplexer_2_out), .data(Buss), .sel(in_1));
  RAM #(.addrWidth(16)) ram_1 (
    .addr(multiplexer_2_out), .data(Buss), .sel(1'b1), .clk(clock_4_out), .ld(and_1_out), .clr(button_3_out));
  Button button_3 (.out(button_3_out));
  and and_1 (and_1_out, not_37_out, R_W_out);
  not not_37 (not_37_out, in_2);
  Transistor #(.\type ("n")) transistor_119 (.in(1'b0), .out(transistor_119_out), .gate(transistor_107_out));
  Pull_Resistor #(.pull(1)) pull_resistor_76 (.node(transistor_107_out));
  Transistor #(.\type ("n"), .gate("br")) transistor_120 (.in(1'b0), .out(transistor_107_out), .gate(FLAG_Z));
  Transistor #(.\type ("n"), .gate("br")) transistor_121 (.in(1'b0), .out(transistor_107_out), .gate(FLAG_N));
  Transistor #(.\type ("n")) transistor_122 (.in(1'b0), .out(transistor_122_out), .gate(nJMP));
  Transistor #(.\type ("n")) transistor_123 (.in(transistor_124_out), .out(Read_Write_ins), .gate(nStore));
  Pull_Resistor #(.pull(1)) pull_resistor_77 (.node(Read_Write_ins));
  Transistor #(.\type ("n")) transistor_124 (.in(1'b0), .out(transistor_124_out), .gate(nLoad));
  Transistor #(.\type ("n")) transistor_125 (.in(1'b0), .out(bus_out____Main_bus), .gate(pull_resistor_74_node));
  Pull_Resistor #(.pull(1)) pull_resistor_78 (.node(bus_out____Main_bus));
  Transistor #(.\type ("n")) transistor_126 (.in(transistor_127_out), .out(transistor_126_out), .gate(nAND));
  Transistor #(.\type ("n")) transistor_127 (.in(transistor_111_out), .out(transistor_127_out), .gate(nNOT));
  Transistor #(.\type ("n")) transistor_128 (.in(transistor_129_out), .out(transistor_128_out), .gate(nOR));
  Transistor #(.\type ("n")) transistor_129 (.in(transistor_113_out), .out(transistor_129_out), .gate(nAND));
  Transistor #(.\type ("n")) transistor_130 (.in(transistor_116_out), .out(REG____ALU_B), .gate(nMOV));
  Transistor #(.\type ("n")) transistor_131 (.in(transistor_117_out), .out(transistor_131_out), .gate(nOR));
  Transistor #(.\type ("n")) transistor_132 (.in(transistor_131_out), .out(transistor_132_out), .gate(nXOR));
  Transistor #(.\type ("n")) transistor_133 (.in(transistor_122_out), .out(transistor_133_out), .gate(nBOP));
  Transistor #(.\type ("n")) transistor_134 (.in(transistor_133_out), .out(transistor_134_out), .gate(nBON));
  Transistor #(.\type ("n")) transistor_135 (.in(transistor_126_out), .out(transistor_135_out), .gate(nOR));
  Transistor #(.\type ("n")) transistor_136 (.in(transistor_135_out), .out(transistor_136_out), .gate(nXOR));
  Transistor #(.\type ("n")) transistor_137 (.in(transistor_138_out), .out(transistor_137_out), .gate(nADD));
  Transistor #(.\type ("n")) transistor_138 (.in(transistor_128_out), .out(transistor_138_out), .gate(nXOR));
  Pull_Resistor #(.pull(1)) pull_resistor_79 (.node(REG____ALU_B));
  Transistor #(.\type ("n")) transistor_139 (.in(transistor_140_out), .out(READ_FALG), .gate(nADC));
  Transistor #(.\type ("n")) transistor_140 (.in(transistor_132_out), .out(transistor_140_out), .gate(nADD));
  Transistor #(.\type ("n")) transistor_141 (.in(1'b0), .out(transistor_119_out), .gate(pull_resistor_80_node));
  Pull_Resistor #(.pull(1)) pull_resistor_80 (.node(pull_resistor_80_node));
  Transistor #(.\type ("n"), .gate("br")) transistor_142 (
    .in(1'b0), .out(pull_resistor_80_node), .gate(transistor_144_out));
  Transistor #(.\type ("n")) transistor_143 (.in(1'b0), .out(pull_resistor_80_node), .gate(nBON));
  Transistor #(.\type ("n")) transistor_144 (.in(1'b0), .out(transistor_144_out), .gate(FLAG_N));
  Pull_Resistor #(.pull(1)) pull_resistor_81 (.node(transistor_144_out));
  Transistor #(.\type ("n")) transistor_145 (.in(transistor_134_out), .out(transistor_145_out), .gate(nBOZ));
  Transistor #(.\type ("n")) transistor_146 (.in(transistor_145_out), .out(transistor_146_out), .gate(nBNZ));
  Transistor #(.\type ("n")) transistor_147 (.in(1'b0), .out(transistor_147_out), .gate(TIME_STEP_0));
  Pull_Resistor #(.pull(1)) pull_resistor_82 (.node(transistor_147_out));
  Transistor #(.\type ("n")) transistor_148 (.in(1'b0), .out(transistor_147_out), .gate(TIME_STEP_1));
  Transistor #(.\type ("n")) transistor_149 (.in(transistor_150_out), .out(transistor_149_out), .gate(nADC));
  Transistor #(.\type ("n")) transistor_150 (.in(transistor_136_out), .out(transistor_150_out), .gate(nADD));
  Transistor #(.\type ("n")) transistor_151 (.in(transistor_137_out), .out(REG____ALU_A), .gate(nADC));
  Pull_Resistor #(.pull(1)) pull_resistor_83 (.node(READ_FALG));
  Transistor #(.\type ("n")) transistor_152 (.in(transistor_146_out), .out(transistor_152_out), .gate(nBOO));
  Transistor #(.\type ("n")) transistor_153 (.in(transistor_152_out), .out(transistor_153_out), .gate(nBNO));
  Transistor #(.\type ("n")) transistor_154 (.in(1'b0), .out(TIME_STEP_0or1), .gate(transistor_147_out));
  Pull_Resistor #(.pull(1)) pull_resistor_84 (.node(TIME_STEP_0or1));
  Pull_Resistor #(.pull(1)) pull_resistor_85 (.node(REG_Read));
  Transistor #(.\type ("n")) transistor_155 (.in(transistor_149_out), .out(REG_Read), .gate(nMOV));
  Pull_Resistor #(.pull(1)) pull_resistor_86 (.node(REG____ALU_A));
  LED led_37 (.in(FLAG_C));
  LED led_38 (.in(FLAG_O));
  LED led_39 (.in(FLAG_U));
  LED led_40 (.in(FLAG_Z));
  LED led_41 (.in(FLAG_N));
  Hex_Digit_Display hex_digit_display_3 (.value({ADR_11, ADR_10, ADR_9, ADR_8}));  // open: dp
  Hex_Digit_Display hex_digit_display_4 (.value({ADR_15, ADR_14, ADR_13, ADR_12}));  // open: dp
  Transistor #(.\type ("n")) transistor_156 (.in(1'b0), .out(transistor_119_out), .gate(transistor_157_out));
  Transistor #(.\type ("n"), .gate("br")) transistor_157 (
    .in(1'b0), .out(transistor_157_out), .gate(transistor_164_out));
  Transistor #(.\type ("n")) transistor_158 (.in(1'b0), .out(transistor_157_out), .gate(nBOZ));
  Pull_Resistor #(.pull(1)) pull_resistor_87 (.node(transistor_157_out));
  Transistor #(.\type ("n")) transistor_159 (.in(transistor_160_out), .out(transistor_159_out), .gate(nBOU));
  Transistor #(.\type ("n")) transistor_160 (.in(transistor_153_out), .out(transistor_160_out), .gate(nBOU));
  Pull_Resistor #(.pull(1)) pull_resistor_88 (.node(pull_resistor_88_node));
  Transistor #(.\type ("n")) transistor_161 (
    .in(transistor_162_out), .out(pull_resistor_88_node), .gate(jump_type_instruction));
  Transistor #(.\type ("n")) transistor_162 (.in(1'b0), .out(transistor_162_out), .gate(transistor_147_out));
  Hex_Digit_Display hex_digit_display_5 (.value({ADR_7, ADR_6, ADR_5, ADR_4}));  // open: dp
  Hex_Digit_Display hex_digit_display_6 (.value({ADR_3, ADR_2, ADR_1, ADR_0}));  // open: dp
  Pull_Resistor #(.pull(1)) pull_resistor_89 (.node(pull_resistor_89_node));
  Transistor #(.\type ("n")) transistor_163 (.in(1'b0), .out(pull_resistor_89_node), .gate(nBNZ));
  Transistor #(.\type ("n")) transistor_164 (.in(1'b0), .out(transistor_164_out), .gate(FLAG_Z));
  Pull_Resistor #(.pull(1)) pull_resistor_90 (.node(transistor_164_out));
  Transistor #(.\type ("n")) transistor_165 (.in(transistor_159_out), .out(transistor_165_out), .gate(nBNU));
  Transistor #(.\type ("n")) transistor_166 (.in(transistor_165_out), .out(transistor_166_out), .gate(nBOC));
  Transistor #(.\type ("n")) transistor_167 (.in(1'b0), .out(TIME_STEP_IN_0), .gate(pull_resistor_88_node));
  Pull_Resistor #(.pull(1)) pull_resistor_91 (.node(TIME_STEP_IN_0));
  Transistor #(.\type ("n"), .gate("br")) transistor_168 (
    .in(transistor_169_out), .out(pull_resistor_88_node), .gate(Read_Write_ins));
  Transistor #(.\type ("n"), .gate("br")) transistor_169 (
    .in(1'b0), .out(transistor_169_out), .gate(transistor_175_out));
  Pull_Resistor #(.pull(1)) pull_resistor_92 (.node(pull_resistor_92_node));
  Transistor #(.\type ("n")) transistor_170 (
    .in(transistor_110_out), .out(pull_resistor_92_node), .gate(transistor_171_out));
  Transistor #(.\type ("n")) transistor_171 (.in(1'b0), .out(transistor_171_out), .gate(nStore));
  Pull_Resistor #(.pull(1)) pull_resistor_93 (.node(transistor_171_out));
  Transistor #(.\type ("n")) transistor_172 (.in(1'b0), .out(transistor_119_out), .gate(pull_resistor_89_node));
  Transistor #(.\type ("n"), .gate("br")) transistor_173 (.in(1'b0), .out(pull_resistor_89_node), .gate(FLAG_Z));
  Transistor #(.\type ("n")) transistor_174 (.in(transistor_166_out), .out(jump_type_instruction), .gate(nBNC));
  Pull_Resistor #(.pull(1)) pull_resistor_94 (.node(jump_type_instruction));
  Transistor #(.\type ("n")) transistor_175 (.in(1'b0), .out(transistor_175_out), .gate(TIME_STEP_2));
  Transistor #(.\type ("n")) transistor_176 (.in(1'b0), .out(Main_bus____bus_out), .gate(pull_resistor_92_node));
  Pull_Resistor #(.pull(1)) pull_resistor_95 (.node(Main_bus____bus_out));
  Clock clock_5 ();  // open: out
  Transistor #(.\type ("n")) transistor_177 (.in(1'b0), .out(transistor_119_out), .gate(pull_resistor_96_node));
  Pull_Resistor #(.pull(1)) pull_resistor_96 (.node(pull_resistor_96_node));
  Transistor #(.\type ("n")) transistor_178 (.in(1'b0), .out(pull_resistor_96_node), .gate(nBOO));
  Transistor #(.\type ("n"), .gate("br")) transistor_179 (
    .in(1'b0), .out(pull_resistor_96_node), .gate(transistor_183_out));
  Pull_Resistor #(.pull(1)) pull_resistor_97 (.node(transistor_175_out));
  Transistor #(.\type ("n")) transistor_180 (.in(1'b0), .out(transistor_175_out), .gate(TIME_STEP_0));
  Transistor #(.\type ("n")) transistor_181 (.in(1'b0), .out(transistor_175_out), .gate(TIME_STEP_1));
  Clock clock_6 ();  // open: out
  Pull_Resistor #(.pull(1)) pull_resistor_98 (.node(pull_resistor_98_node));
  Transistor #(.\type ("n")) transistor_182 (.in(1'b0), .out(pull_resistor_98_node), .gate(nBNO));
  Transistor #(.\type ("n")) transistor_183 (.in(1'b0), .out(transistor_183_out), .gate(FLAG_O));
  Pull_Resistor #(.pull(1)) pull_resistor_99 (.node(transistor_183_out));
  Pull_Resistor #(.pull(1)) pull_resistor_100 (.node(TIME_STEP_0or1or2));
  Transistor #(.\type ("n")) transistor_184 (.in(1'b0), .out(TIME_STEP_0or1or2), .gate(transistor_175_out));
  Transistor #(.\type ("n")) transistor_185 (.in(1'b0), .out(transistor_119_out), .gate(pull_resistor_98_node));
  Transistor #(.\type ("n"), .gate("br")) transistor_186 (.in(1'b0), .out(pull_resistor_98_node), .gate(FLAG_O));
  Transistor #(.\type ("n")) transistor_187 (.in(1'b0), .out(transistor_187_out), .gate(nDEC));
  Transistor #(.\type ("n")) transistor_188 (.in(1'b0), .out(ALU_B___FF), .gate(nDEC));
  Pull_Resistor #(.pull(1)) pull_resistor_101 (.node(ALU_B___FF));
  Pull_Resistor #(.pull(1)) pull_resistor_102 (.node(NOT));
  Transistor #(.\type ("n")) transistor_189 (.in(1'b0), .out(NOT), .gate(nNOT));
  Transistor #(.\type ("n")) transistor_190 (.in(1'b0), .out(transistor_190_out), .gate(nAND));
  Transistor #(.\type ("n")) transistor_191 (.in(1'b0), .out(transistor_119_out), .gate(pull_resistor_103_node));
  Pull_Resistor #(.pull(1)) pull_resistor_103 (.node(pull_resistor_103_node));
  Transistor #(.\type ("n")) transistor_192 (.in(1'b0), .out(pull_resistor_103_node), .gate(nBOU));
  Transistor #(.\type ("n"), .gate("br")) transistor_193 (
    .in(1'b0), .out(pull_resistor_103_node), .gate(transistor_204_out));
  Transistor #(.\type ("n")) transistor_194 (.in(transistor_195_out), .out(transistor_194_out), .gate(nADD));
  Transistor #(.\type ("n")) transistor_195 (.in(transistor_187_out), .out(transistor_195_out), .gate(nINC));
  Transistor #(.\type ("n")) transistor_196 (.in(transistor_190_out), .out(AND), .gate(nClear));
  Pull_Resistor #(.pull(1)) pull_resistor_104 (.node(AND));
  Transistor #(.\type ("n")) transistor_197 (.in(1'b0), .out(transistor_197_out), .gate(Main_bus[0]));
  Transistor #(.\type ("n")) transistor_198 (.in(transistor_199_out), .out(Buss[0]), .gate(transistor_197_out));
  Pull_Resistor #(.pull(1)) pull_resistor_105 (.node(transistor_197_out));
  Transistor #(.\type ("n")) transistor_199 (.in(1'b0), .out(transistor_199_out), .gate(Main_bus____bus_out));
  Transistor #(.\type ("n")) transistor_200 (.in(transistor_202_out), .out(Main_bus[0]), .gate(pull_resistor_106_node));
  Pull_Resistor #(.pull(1)) pull_resistor_106 (.node(pull_resistor_106_node));
  Transistor #(.\type ("n")) transistor_201 (.in(1'b0), .out(pull_resistor_106_node), .gate(Buss[0]));
  Transistor #(.\type ("n")) transistor_202 (.in(1'b0), .out(transistor_202_out), .gate(bus_out____Main_bus));
  Pull_Resistor #(.pull(1)) pull_resistor_107 (.node(pull_resistor_107_node));
  Transistor #(.\type ("n")) transistor_203 (.in(1'b0), .out(pull_resistor_107_node), .gate(nBNU));
  Transistor #(.\type ("n")) transistor_204 (.in(1'b0), .out(transistor_204_out), .gate(FLAG_U));
  Pull_Resistor #(.pull(1)) pull_resistor_108 (.node(transistor_204_out));
  Pull_Resistor #(.pull(1)) pull_resistor_109 (.node(pull_resistor_109_node));
  Transistor #(.\type ("n")) transistor_205 (.in(1'b0), .out(pull_resistor_109_node), .gate(nStore));
  Transistor #(.\type ("n")) transistor_206 (.in(transistor_194_out), .out(ADD), .gate(nADC));
  Pull_Resistor #(.pull(1)) pull_resistor_110 (.node(ADD));
  Transistor #(.\type ("n")) transistor_207 (.in(1'b0), .out(transistor_119_out), .gate(pull_resistor_107_node));
  Transistor #(.\type ("n"), .gate("br")) transistor_208 (.in(1'b0), .out(pull_resistor_107_node), .gate(FLAG_U));
  Pull_Resistor #(.pull(1)) pull_resistor_111 (.node(R_W_out));
  Transistor #(.\type ("n")) transistor_209 (.in(transistor_233_out), .out(R_W_out), .gate(pull_resistor_109_node));
  Pull_Resistor #(.pull(1)) pull_resistor_112 (.node(XOR));
  Transistor #(.\type ("n")) transistor_210 (.in(1'b0), .out(XOR), .gate(nXOR));
  Transistor #(.\type ("n")) transistor_211 (.in(1'b0), .out(RS), .gate(nRS));
  Pull_Resistor #(.pull(1)) pull_resistor_113 (.node(RS));
  Transistor #(.\type ("n")) transistor_212 (.in(transistor_213_out), .out(transistor_212_out), .gate(nMOV));
  Transistor #(.\type ("n")) transistor_213 (.in(1'b0), .out(transistor_213_out), .gate(nStore));
  Transistor #(.\type ("n")) transistor_214 (.in(1'b0), .out(transistor_214_out), .gate(Main_bus[1]));
  Transistor #(.\type ("n")) transistor_215 (.in(transistor_216_out), .out(Buss[1]), .gate(transistor_214_out));
  Pull_Resistor #(.pull(1)) pull_resistor_114 (.node(transistor_214_out));
  Transistor #(.\type ("n")) transistor_216 (.in(1'b0), .out(transistor_216_out), .gate(Main_bus____bus_out));
  Pull_Resistor #(.pull(1)) pull_resistor_115 (.node(pull_resistor_115_node));
  Transistor #(.\type ("n")) transistor_217 (.in(transistor_219_out), .out(Main_bus[1]), .gate(pull_resistor_115_node));
  Transistor #(.\type ("n")) transistor_218 (.in(1'b0), .out(pull_resistor_115_node), .gate(Buss[1]));
  Transistor #(.\type ("n")) transistor_219 (.in(1'b0), .out(transistor_219_out), .gate(bus_out____Main_bus));
  Transistor #(.\type ("n")) transistor_220 (.in(1'b0), .out(transistor_119_out), .gate(pull_resistor_116_node));
  Pull_Resistor #(.pull(1)) pull_resistor_116 (.node(pull_resistor_116_node));
  Transistor #(.\type ("n"), .gate("br")) transistor_221 (
    .in(1'b0), .out(pull_resistor_116_node), .gate(transistor_229_out));
  Transistor #(.\type ("n")) transistor_222 (.in(1'b0), .out(pull_resistor_116_node), .gate(nBOC));
  Pull_Resistor #(.pull(1)) pull_resistor_117 (.node(pull_resistor_117_node));
  Pull_Resistor #(.pull(1)) pull_resistor_118 (.node(pull_resistor_118_node));
  Transistor #(.\type ("n")) transistor_223 (
    .in(transistor_226_out), .out(pull_resistor_118_node), .gate(TIME_STEP_0or1));
  Transistor #(.\type ("n"), .gate("br")) transistor_224 (
    .in(transistor_225_out), .out(pull_resistor_118_node), .gate(TIME_STEP_0or1or2));
  Transistor #(.\type ("n"), .gate("br")) transistor_225 (.in(1'b0), .out(transistor_225_out), .gate(Read_Write_ins));
  Transistor #(.\type ("n")) transistor_226 (.in(1'b0), .out(transistor_226_out), .gate(jump_type_instruction));
  Transistor #(.\type ("n")) transistor_227 (.in(transistor_212_out), .out(OR), .gate(nOR));
  Pull_Resistor #(.pull(1)) pull_resistor_119 (.node(OR));
  Pull_Resistor #(.pull(1)) pull_resistor_120 (.node(pull_resistor_120_node));
  Transistor #(.\type ("n")) transistor_228 (.in(1'b0), .out(pull_resistor_120_node), .gate(nBNC));
  Transistor #(.\type ("n")) transistor_229 (.in(1'b0), .out(transistor_229_out), .gate(FLAG_C));
  Pull_Resistor #(.pull(1)) pull_resistor_121 (.node(transistor_229_out));
  Transistor #(.\type ("n")) transistor_230 (
    .in(transistor_231_out), .out(transistor_230_out), .gate(pull_resistor_117_node));
  Pull_Resistor #(.pull(1)) pull_resistor_122 (.node(transistor_230_out));
  Transistor #(.\type ("n")) transistor_231 (.in(1'b0), .out(transistor_231_out), .gate(pull_resistor_118_node));
  Transistor #(.\type ("n")) transistor_232 (
    .in(transistor_233_out), .out(Read_From_stored_Address), .gate(Read_Write_ins));
  Pull_Resistor #(.pull(1)) pull_resistor_123 (.node(Read_From_stored_Address));
  Transistor #(.\type ("n")) transistor_233 (.in(transistor_234_out), .out(transistor_233_out), .gate(nTIME_STEP_0));
  Transistor #(.\type ("n")) transistor_234 (.in(1'b0), .out(transistor_234_out), .gate(TIME_STEP_2));
  Transistor #(.\type ("n")) transistor_235 (.in(1'b0), .out(transistor_235_out), .gate(nADC));
  Pull_Resistor #(.pull(1)) pull_resistor_124 (.node(transistor_235_out));
  Transistor #(.\type ("n")) transistor_236 (.in(1'b0), .out(transistor_236_out), .gate(Main_bus[2]));
  Transistor #(.\type ("n")) transistor_237 (.in(transistor_238_out), .out(Buss[2]), .gate(transistor_236_out));
  Pull_Resistor #(.pull(1)) pull_resistor_125 (.node(transistor_236_out));
  Transistor #(.\type ("n")) transistor_238 (.in(1'b0), .out(transistor_238_out), .gate(Main_bus____bus_out));
  Pull_Resistor #(.pull(1)) pull_resistor_126 (.node(pull_resistor_126_node));
  Transistor #(.\type ("n")) transistor_239 (.in(1'b0), .out(pull_resistor_126_node), .gate(Buss[2]));
  Transistor #(.\type ("n")) transistor_240 (.in(transistor_241_out), .out(Main_bus[2]), .gate(pull_resistor_126_node));
  Transistor #(.\type ("n")) transistor_241 (.in(1'b0), .out(transistor_241_out), .gate(bus_out____Main_bus));
  Transistor #(.\type ("n")) transistor_242 (.in(1'b0), .out(transistor_119_out), .gate(pull_resistor_120_node));
  Transistor #(.\type ("n"), .gate("br")) transistor_243 (.in(1'b0), .out(pull_resistor_120_node), .gate(FLAG_C));
  Transistor #(.\type ("n")) transistor_244 (.in(1'b0), .out(Read_New_Instruction), .gate(transistor_230_out));
  Pull_Resistor #(.pull(1)) pull_resistor_127 (.node(Read_New_Instruction));
  Pull_Resistor #(.pull(1)) pull_resistor_128 (.node(pull_resistor_128_node));
  Transistor #(.\type ("n")) transistor_245 (
    .in(transistor_246_out), .out(pull_resistor_128_node), .gate(transistor_235_out));
  Transistor #(.\type ("n")) transistor_246 (.in(1'b0), .out(transistor_246_out), .gate(FLAG_C));
  Transistor #(.\type ("n")) transistor_247 (.in(1'b0), .out(transistor_119_out), .gate(pull_resistor_130_node));
  Pull_Resistor #(.pull(1)) pull_resistor_129 (.node(transistor_119_out));
  Pull_Resistor #(.pull(1)) pull_resistor_130 (.node(pull_resistor_130_node));
  Transistor #(.\type ("n")) transistor_248 (.in(1'b0), .out(pull_resistor_130_node), .gate(nJMP));
  Transistor #(.\type ("n")) transistor_249 (.in(transistor_250_out), .out(Carry_in), .gate(nINC));
  Pull_Resistor #(.pull(1)) pull_resistor_131 (.node(Carry_in));
  Transistor #(.\type ("n")) transistor_250 (.in(1'b0), .out(transistor_250_out), .gate(pull_resistor_128_node));
  Pull_Resistor #(.pull(1)) pull_resistor_132 (.node(pull_resistor_132_node));
  Transistor #(.\type ("n")) transistor_251 (.in(transistor_253_out), .out(Buss[3]), .gate(pull_resistor_132_node));
  Transistor #(.\type ("n")) transistor_252 (.in(1'b0), .out(pull_resistor_132_node), .gate(Main_bus[3]));
  Transistor #(.\type ("n")) transistor_253 (.in(1'b0), .out(transistor_253_out), .gate(Main_bus____bus_out));
  Transistor #(.\type ("n")) transistor_254 (.in(transistor_256_out), .out(Main_bus[3]), .gate(pull_resistor_133_node));
  Pull_Resistor #(.pull(1)) pull_resistor_133 (.node(pull_resistor_133_node));
  Transistor #(.\type ("n")) transistor_255 (.in(1'b0), .out(pull_resistor_133_node), .gate(Buss[3]));
  Transistor #(.\type ("n")) transistor_256 (.in(1'b0), .out(transistor_256_out), .gate(bus_out____Main_bus));
  Transistor #(.\type ("n")) transistor_257 (.in(1'b0), .out(Commit_jump), .gate(transistor_119_out));
  Pull_Resistor #(.pull(1)) pull_resistor_134 (.node(Commit_jump));
  Transistor #(.\type ("n")) transistor_258 (
    .in(transistor_259_out), .out(Store_Address_plus_plus), .gate(TIME_STEP_IN_2));
  Pull_Resistor #(.pull(1)) pull_resistor_135 (.node(Store_Address_plus_plus));
  Transistor #(.\type ("n")) transistor_259 (.in(1'b0), .out(transistor_259_out), .gate(Commit_jump));
  Transistor #(.\type ("n")) transistor_260 (.in(1'b0), .out(transistor_260_out), .gate(Main_bus[4]));
  Pull_Resistor #(.pull(1)) pull_resistor_136 (.node(transistor_260_out));
  Transistor #(.\type ("n")) transistor_261 (.in(transistor_262_out), .out(Buss[4]), .gate(transistor_260_out));
  Transistor #(.\type ("n")) transistor_262 (.in(1'b0), .out(transistor_262_out), .gate(Main_bus____bus_out));
  Transistor #(.\type ("n")) transistor_263 (.in(transistor_265_out), .out(Main_bus[4]), .gate(pull_resistor_137_node));
  Pull_Resistor #(.pull(1)) pull_resistor_137 (.node(pull_resistor_137_node));
  Transistor #(.\type ("n")) transistor_264 (.in(1'b0), .out(pull_resistor_137_node), .gate(Buss[4]));
  Transistor #(.\type ("n")) transistor_265 (.in(1'b0), .out(transistor_265_out), .gate(bus_out____Main_bus));
  Pull_Resistor #(.pull(1)) pull_resistor_138 (.node(pull_resistor_138_node));
  Transistor #(.\type ("n")) transistor_266 (.in(1'b0), .out(pull_resistor_138_node), .gate(Main_bus[5]));
  Transistor #(.\type ("n")) transistor_267 (.in(transistor_268_out), .out(Buss[5]), .gate(pull_resistor_138_node));
  Transistor #(.\type ("n")) transistor_268 (.in(1'b0), .out(transistor_268_out), .gate(Main_bus____bus_out));
  Transistor #(.\type ("n")) transistor_269 (.in(transistor_271_out), .out(Main_bus[5]), .gate(transistor_270_out));
  Transistor #(.\type ("n")) transistor_270 (.in(1'b0), .out(transistor_270_out), .gate(Buss[5]));
  Pull_Resistor #(.pull(1)) pull_resistor_139 (.node(transistor_270_out));
  Transistor #(.\type ("n")) transistor_271 (.in(1'b0), .out(transistor_271_out), .gate(bus_out____Main_bus));
  Register register_2 (
    .D({NEXT_ADR_7, NEXT_ADR_6, NEXT_ADR_5, NEXT_ADR_4, NEXT_ADR_3, NEXT_ADR_2, NEXT_ADR_1, NEXT_ADR_0}),
    .en(pull_resistor_140_node),
    .Q({STORED_ADR_7, STORED_ADR_6, STORED_ADR_5, STORED_ADR_4, STORED_ADR_3, STORED_ADR_2, STORED_ADR_1, STORED_ADR_0}),
    .clk(clock_7_out), .clr(in_6));
  Pull_Resistor #(.pull(1)) pull_resistor_140 (.node(pull_resistor_140_node));
  Clock clock_7 (.out(clock_7_out));
  Pull_Resistor #(.pull(1)) pull_resistor_141 (.node(pull_resistor_141_node));
  Transistor #(.\type ("n")) transistor_272 (.in(transistor_274_out), .out(Buss[6]), .gate(pull_resistor_141_node));
  Transistor #(.\type ("n")) transistor_273 (.in(1'b0), .out(pull_resistor_141_node), .gate(Main_bus[6]));
  Transistor #(.\type ("n")) transistor_274 (.in(1'b0), .out(transistor_274_out), .gate(Main_bus____bus_out));
  Pull_Resistor #(.pull(1)) pull_resistor_142 (.node(pull_resistor_142_node));
  Transistor #(.\type ("n")) transistor_275 (.in(1'b0), .out(pull_resistor_142_node), .gate(Buss[6]));
  Transistor #(.\type ("n")) transistor_276 (.in(transistor_277_out), .out(Main_bus[6]), .gate(pull_resistor_142_node));
  Transistor #(.\type ("n")) transistor_277 (.in(1'b0), .out(transistor_277_out), .gate(bus_out____Main_bus));
  Transistor #(.\type ("n")) transistor_278 (.in(1'b0), .out(transistor_278_out), .gate(Store_Address_plus_plus));
  Pull_Resistor #(.pull(1)) pull_resistor_143 (.node(transistor_278_out));
  Pull_Resistor #(.pull(1)) pull_resistor_144 (.node(pull_resistor_144_node));
  Transistor #(.\type ("n")) transistor_279 (.in(1'b0), .out(pull_resistor_144_node), .gate(Read_From_stored_Address));
  Register #(.trigger("falling")) register_3 (
    .D(Buss), .en(TIME_STEP_1),
    .Q({TEMP_ADR_7, TEMP_ADR_6, TEMP_ADR_5, TEMP_ADR_4, TEMP_ADR_3, TEMP_ADR_2, TEMP_ADR_1, TEMP_ADR_0}),
    .clk(clock_8_out), .clr(in_6));
  Clock clock_8 (.out(clock_8_out));
  Pull_Resistor #(.pull(1)) pull_resistor_145 (.node(pull_resistor_145_node));
  Transistor #(.\type ("n")) transistor_280 (.in(transistor_281_out), .out(pull_resistor_145_node), .gate(ADR___0));
  Transistor #(.\type ("n")) transistor_281 (.in(1'b0), .out(transistor_281_out), .gate(Store_Address_plus_plus));
  Transistor #(.\type ("n")) transistor_282 (.in(transistor_283_out), .out(pull_resistor_145_node), .gate(TEMP_ADR_0));
  Transistor #(.\type ("n")) transistor_283 (.in(1'b0), .out(transistor_283_out), .gate(transistor_278_out));
  Pull_Resistor #(.pull(1)) pull_resistor_146 (.node(NEXT_ADR_0));
  Transistor #(.\type ("n")) transistor_284 (.in(1'b0), .out(NEXT_ADR_0), .gate(pull_resistor_145_node));
  Pull_Resistor #(.pull(1)) pull_resistor_147 (.node(pull_resistor_147_node));
  Transistor #(.\type ("n")) transistor_285 (
    .in(transistor_286_out), .out(pull_resistor_147_node), .gate(STORED_ADR_0));
  Transistor #(.\type ("n")) transistor_286 (.in(1'b0), .out(transistor_286_out), .gate(Read_From_stored_Address));
  Transistor #(.\type ("n")) transistor_287 (.in(transistor_288_out), .out(pull_resistor_147_node), .gate(TEMP_ADR_0));
  Transistor #(.\type ("n")) transistor_288 (.in(1'b0), .out(transistor_288_out), .gate(pull_resistor_144_node));
  Pull_Resistor #(.pull(1)) pull_resistor_148 (.node(ADR_0));
  Transistor #(.\type ("n")) transistor_289 (.in(1'b0), .out(ADR_0), .gate(pull_resistor_147_node));
  Pull_Resistor #(.pull(1)) pull_resistor_149 (.node(pull_resistor_149_node));
  Transistor #(.\type ("n")) transistor_290 (.in(transistor_292_out), .out(Buss[7]), .gate(pull_resistor_149_node));
  Transistor #(.\type ("n")) transistor_291 (.in(1'b0), .out(pull_resistor_149_node), .gate(ALU_FLAG_N));
  Transistor #(.\type ("n")) transistor_292 (.in(1'b0), .out(transistor_292_out), .gate(Main_bus____bus_out));
  Transistor #(.\type ("n")) transistor_293 (.in(transistor_295_out), .out(ALU_FLAG_N), .gate(pull_resistor_150_node));
  Pull_Resistor #(.pull(1)) pull_resistor_150 (.node(pull_resistor_150_node));
  Transistor #(.\type ("n")) transistor_294 (.in(1'b0), .out(pull_resistor_150_node), .gate(Buss[7]));
  Transistor #(.\type ("n")) transistor_295 (.in(1'b0), .out(transistor_295_out), .gate(bus_out____Main_bus));
  Pull_Resistor #(.pull(1)) pull_resistor_151 (.node(pull_resistor_151_node));
  Transistor #(.\type ("n")) transistor_296 (.in(transistor_297_out), .out(pull_resistor_151_node), .gate(ADR___1));
  Transistor #(.\type ("n")) transistor_297 (.in(1'b0), .out(transistor_297_out), .gate(Store_Address_plus_plus));
  Transistor #(.\type ("n")) transistor_298 (.in(transistor_299_out), .out(pull_resistor_151_node), .gate(TEMP_ADR_1));
  Transistor #(.\type ("n")) transistor_299 (.in(1'b0), .out(transistor_299_out), .gate(transistor_278_out));
  Transistor #(.\type ("n")) transistor_300 (.in(1'b0), .out(NEXT_ADR_1), .gate(pull_resistor_151_node));
  Pull_Resistor #(.pull(1)) pull_resistor_152 (.node(NEXT_ADR_1));
  Pull_Resistor #(.pull(1)) pull_resistor_153 (.node(pull_resistor_153_node));
  Transistor #(.\type ("n")) transistor_301 (
    .in(transistor_302_out), .out(pull_resistor_153_node), .gate(STORED_ADR_1));
  Transistor #(.\type ("n")) transistor_302 (.in(1'b0), .out(transistor_302_out), .gate(Read_From_stored_Address));
  Transistor #(.\type ("n")) transistor_303 (.in(transistor_304_out), .out(pull_resistor_153_node), .gate(TEMP_ADR_1));
  Transistor #(.\type ("n")) transistor_304 (.in(1'b0), .out(transistor_304_out), .gate(pull_resistor_144_node));
  Transistor #(.\type ("n")) transistor_305 (.in(1'b0), .out(ADR_1), .gate(pull_resistor_153_node));
  Pull_Resistor #(.pull(1)) pull_resistor_154 (.node(ADR_1));
  Transistor #(.\type ("n")) transistor_306 (.in(transistor_307_out), .out(transistor_306_out), .gate(ADR___2));
  Pull_Resistor #(.pull(1)) pull_resistor_155 (.node(transistor_306_out));
  Transistor #(.\type ("n")) transistor_307 (.in(1'b0), .out(transistor_307_out), .gate(Store_Address_plus_plus));
  Transistor #(.\type ("n")) transistor_308 (.in(transistor_309_out), .out(transistor_306_out), .gate(TEMP_ADR_2));
  Transistor #(.\type ("n")) transistor_309 (.in(1'b0), .out(transistor_309_out), .gate(transistor_278_out));
  Pull_Resistor #(.pull(1)) pull_resistor_156 (.node(NEXT_ADR_2));
  Transistor #(.\type ("n")) transistor_310 (.in(1'b0), .out(NEXT_ADR_2), .gate(transistor_306_out));
  Pull_Resistor #(.pull(1)) pull_resistor_157 (.node(pull_resistor_157_node));
  Transistor #(.\type ("n")) transistor_311 (
    .in(transistor_312_out), .out(pull_resistor_157_node), .gate(STORED_ADR_2));
  Transistor #(.\type ("n")) transistor_312 (.in(1'b0), .out(transistor_312_out), .gate(Read_From_stored_Address));
  Transistor #(.\type ("n")) transistor_313 (.in(transistor_314_out), .out(pull_resistor_157_node), .gate(TEMP_ADR_2));
  Transistor #(.\type ("n")) transistor_314 (.in(1'b0), .out(transistor_314_out), .gate(pull_resistor_144_node));
  Transistor #(.\type ("n")) transistor_315 (.in(1'b0), .out(ADR_2), .gate(pull_resistor_157_node));
  Pull_Resistor #(.pull(1)) pull_resistor_158 (.node(ADR_2));
  Pull_Resistor #(.pull(1)) pull_resistor_159 (.node(pull_resistor_159_node));
  Transistor #(.\type ("n")) transistor_316 (.in(transistor_317_out), .out(pull_resistor_159_node), .gate(ADR___3));
  Transistor #(.\type ("n")) transistor_317 (.in(1'b0), .out(transistor_317_out), .gate(Store_Address_plus_plus));
  Transistor #(.\type ("n")) transistor_318 (.in(transistor_319_out), .out(pull_resistor_159_node), .gate(TEMP_ADR_3));
  Transistor #(.\type ("n")) transistor_319 (.in(1'b0), .out(transistor_319_out), .gate(transistor_278_out));
  Pull_Resistor #(.pull(1)) pull_resistor_160 (.node(NEXT_ADR_3));
  Transistor #(.\type ("n")) transistor_320 (.in(1'b0), .out(NEXT_ADR_3), .gate(pull_resistor_159_node));
  Transistor #(.\type ("n")) transistor_321 (.in(transistor_322_out), .out(transistor_321_out), .gate(STORED_ADR_3));
  Pull_Resistor #(.pull(1)) pull_resistor_161 (.node(transistor_321_out));
  Transistor #(.\type ("n")) transistor_322 (.in(1'b0), .out(transistor_322_out), .gate(Read_From_stored_Address));
  Transistor #(.\type ("n")) transistor_323 (.in(transistor_324_out), .out(transistor_321_out), .gate(TEMP_ADR_3));
  Transistor #(.\type ("n")) transistor_324 (.in(1'b0), .out(transistor_324_out), .gate(pull_resistor_144_node));
  Pull_Resistor #(.pull(1)) pull_resistor_162 (.node(ADR_3));
  Transistor #(.\type ("n")) transistor_325 (.in(1'b0), .out(ADR_3), .gate(transistor_321_out));
  Pull_Resistor #(.pull(1)) pull_resistor_163 (.node(pull_resistor_163_node));
  Transistor #(.\type ("n")) transistor_326 (.in(transistor_327_out), .out(pull_resistor_163_node), .gate(ADR___4));
  Transistor #(.\type ("n")) transistor_327 (.in(1'b0), .out(transistor_327_out), .gate(Store_Address_plus_plus));
  Transistor #(.\type ("n")) transistor_328 (.in(transistor_329_out), .out(pull_resistor_163_node), .gate(TEMP_ADR_4));
  Transistor #(.\type ("n")) transistor_329 (.in(1'b0), .out(transistor_329_out), .gate(transistor_278_out));
  Transistor #(.\type ("n")) transistor_330 (.in(1'b0), .out(NEXT_ADR_4), .gate(pull_resistor_163_node));
  Pull_Resistor #(.pull(1)) pull_resistor_164 (.node(NEXT_ADR_4));
  Pull_Resistor #(.pull(1)) pull_resistor_165 (.node(pull_resistor_165_node));
  Transistor #(.\type ("n")) transistor_331 (
    .in(transistor_332_out), .out(pull_resistor_165_node), .gate(STORED_ADR_4));
  Transistor #(.\type ("n")) transistor_332 (.in(1'b0), .out(transistor_332_out), .gate(Read_From_stored_Address));
  Transistor #(.\type ("n")) transistor_333 (.in(transistor_334_out), .out(pull_resistor_165_node), .gate(TEMP_ADR_4));
  Transistor #(.\type ("n")) transistor_334 (.in(1'b0), .out(transistor_334_out), .gate(pull_resistor_144_node));
  Register register_4 (
    .D({FLAG_STORE_C, FLAG_STORE_O, FLAG_STORE_U, FLAG_STORE_Z, FLAG_STORE_N, TIME_STEP_IN_2, TIME_STEP_IN_1, TIME_STEP_IN_0}),
    .en(1'b1), .Q({FLAG_C, FLAG_O, FLAG_U, FLAG_Z, FLAG_N, TIME_STEP_2, TIME_STEP_1, TIME_STEP_0}),
    .clk(clock_9_out), .clr(in_6));
  Clock clock_9 (.out(clock_9_out));
  Pull_Resistor #(.pull(1)) pull_resistor_166 (.node(pull_resistor_166_node));
  Transistor #(.\type ("n")) transistor_335 (.in(transistor_336_out), .out(pull_resistor_166_node), .gate(ADR___5));
  Transistor #(.\type ("n")) transistor_336 (.in(1'b0), .out(transistor_336_out), .gate(Store_Address_plus_plus));
  Transistor #(.\type ("n")) transistor_337 (.in(transistor_338_out), .out(pull_resistor_166_node), .gate(TEMP_ADR_5));
  Transistor #(.\type ("n")) transistor_338 (.in(1'b0), .out(transistor_338_out), .gate(transistor_278_out));
  Pull_Resistor #(.pull(1)) pull_resistor_167 (.node(pull_resistor_167_node));
  Transistor #(.\type ("n")) transistor_339 (
    .in(transistor_340_out), .out(pull_resistor_167_node), .gate(STORED_ADR_5));
  Transistor #(.\type ("n")) transistor_340 (.in(1'b0), .out(transistor_340_out), .gate(Read_From_stored_Address));
  Transistor #(.\type ("n")) transistor_341 (.in(transistor_342_out), .out(pull_resistor_167_node), .gate(TEMP_ADR_5));
  Transistor #(.\type ("n")) transistor_342 (.in(1'b0), .out(transistor_342_out), .gate(pull_resistor_144_node));
  Transistor #(.\type ("n")) transistor_343 (.in(1'b0), .out(ADR_4), .gate(pull_resistor_165_node));
  Pull_Resistor #(.pull(1)) pull_resistor_168 (.node(ADR_4));
  Pull_Resistor #(.pull(1)) pull_resistor_169 (.node(pull_resistor_169_node));
  Transistor #(.\type ("n")) transistor_344 (.in(transistor_345_out), .out(pull_resistor_169_node), .gate(ADR___6));
  Transistor #(.\type ("n")) transistor_345 (.in(1'b0), .out(transistor_345_out), .gate(Store_Address_plus_plus));
  Transistor #(.\type ("n")) transistor_346 (.in(transistor_347_out), .out(pull_resistor_169_node), .gate(TEMP_ADR_6));
  Transistor #(.\type ("n")) transistor_347 (.in(1'b0), .out(transistor_347_out), .gate(transistor_278_out));
  Transistor #(.\type ("n")) transistor_348 (.in(1'b0), .out(NEXT_ADR_5), .gate(pull_resistor_166_node));
  Pull_Resistor #(.pull(1)) pull_resistor_170 (.node(NEXT_ADR_5));
  Transistor #(.\type ("n")) transistor_349 (.in(transistor_350_out), .out(transistor_349_out), .gate(STORED_ADR_6));
  Transistor #(.\type ("n")) transistor_350 (.in(1'b0), .out(transistor_350_out), .gate(Read_From_stored_Address));
  Transistor #(.\type ("n")) transistor_351 (.in(transistor_352_out), .out(transistor_349_out), .gate(TEMP_ADR_6));
  Transistor #(.\type ("n")) transistor_352 (.in(1'b0), .out(transistor_352_out), .gate(pull_resistor_144_node));
  Transistor #(.\type ("n")) transistor_353 (.in(1'b0), .out(ADR_5), .gate(pull_resistor_167_node));
  Pull_Resistor #(.pull(1)) pull_resistor_171 (.node(ADR_5));
  Pull_Resistor #(.pull(1)) pull_resistor_172 (.node(pull_resistor_172_node));
  Clock clock_10 (.out(clock_10_out));
  Transistor #(.\type ("n")) transistor_354 (.in(1'b0), .out(transistor_354_out), .gate(nTIME_STEP_0));
  Pull_Resistor #(.pull(1)) pull_resistor_173 (.node(nTIME_STEP_0));
  Pull_Resistor #(.pull(1)) pull_resistor_174 (.node(transistor_354_out));
  Transistor #(.\type ("n")) transistor_355 (.in(1'b0), .out(nTIME_STEP_0), .gate(TIME_STEP_0));
  Transistor #(.\type ("n")) transistor_356 (.in(1'b0), .out(transistor_356_out), .gate(transistor_357_out));
  Transistor #(.\type ("n")) transistor_357 (.in(1'b0), .out(transistor_357_out), .gate(TIME_STEP_1));
  Pull_Resistor #(.pull(1)) pull_resistor_175 (.node(transistor_357_out));
  Pull_Resistor #(.pull(1)) pull_resistor_176 (.node(transistor_356_out));
  Transistor #(.\type ("n")) transistor_358 (.in(transistor_359_out), .out(transistor_358_out), .gate(FLAG_N));
  Pull_Resistor #(.pull(1)) pull_resistor_177 (.node(transistor_358_out));
  Transistor #(.\type ("n")) transistor_359 (.in(1'b0), .out(transistor_359_out), .gate(transistor_360_out));
  Transistor #(.\type ("n")) transistor_360 (.in(1'b0), .out(transistor_360_out), .gate(READ_FALG));
  Pull_Resistor #(.pull(1)) pull_resistor_178 (.node(transistor_360_out));
  Transistor #(.\type ("n")) transistor_361 (.in(transistor_362_out), .out(transistor_358_out), .gate(ALU_FLAG_N));
  Transistor #(.\type ("n")) transistor_362 (.in(1'b0), .out(transistor_362_out), .gate(READ_FALG));
  Transistor #(.\type ("n")) transistor_363 (.in(transistor_364_out), .out(transistor_363_out), .gate(ADR___7));
  Transistor #(.\type ("n")) transistor_364 (.in(1'b0), .out(transistor_364_out), .gate(Store_Address_plus_plus));
  Transistor #(.\type ("n")) transistor_365 (.in(transistor_366_out), .out(transistor_363_out), .gate(TEMP_ADR_7));
  Transistor #(.\type ("n")) transistor_366 (.in(1'b0), .out(transistor_366_out), .gate(transistor_278_out));
  Transistor #(.\type ("n")) transistor_367 (.in(1'b0), .out(NEXT_ADR_6), .gate(pull_resistor_169_node));
  Pull_Resistor #(.pull(1)) pull_resistor_179 (.node(NEXT_ADR_6));
  Pull_Resistor #(.pull(1)) pull_resistor_180 (.node(transistor_349_out));
  Pull_Resistor #(.pull(1)) pull_resistor_181 (.node(ADR_6));
  Transistor #(.\type ("n")) transistor_368 (.in(1'b0), .out(ADR_6), .gate(transistor_349_out));
  Register register_5 (
    .D({NEXT_ADR_15, NEXT_ADR_14, NEXT_ADR_13, NEXT_ADR_12, NEXT_ADR_11, NEXT_ADR_10, NEXT_ADR_9, NEXT_ADR_8}),
    .en(pull_resistor_172_node),
    .Q({STORED_ADR_15, STORED_ADR_14, STORED_ADR_13, STORED_ADR_12, STORED_ADR_11, STORED_ADR_10, STORED_ADR_9, STORED_ADR_8}),
    .clk(clock_10_out), .clr(in_6));
  Pull_Resistor #(.pull(1)) pull_resistor_182 (.node(TIME_STEP_IN_1));
  Transistor #(.\type ("n")) transistor_369 (.in(1'b0), .out(transistor_369_out), .gate(transistor_354_out));
  Transistor #(.\type ("n")) transistor_370 (.in(1'b0), .out(TIME_STEP_IN_1), .gate(transistor_369_out));
  Pull_Resistor #(.pull(1)) pull_resistor_183 (.node(transistor_369_out));
  Pull_Resistor #(.pull(1)) pull_resistor_184 (.node(TIME_STEP_IN_2));
  Pull_Resistor #(.pull(1)) pull_resistor_185 (.node(pull_resistor_185_node));
  Transistor #(.\type ("n")) transistor_371 (.in(1'b0), .out(pull_resistor_185_node), .gate(transistor_356_out));
  Transistor #(.\type ("n")) transistor_372 (.in(1'b0), .out(TIME_STEP_IN_2), .gate(pull_resistor_185_node));
  Pull_Resistor #(.pull(1)) pull_resistor_186 (.node(pull_resistor_186_node));
  Transistor #(.\type ("n")) transistor_373 (.in(transistor_374_out), .out(pull_resistor_186_node), .gate(FLAG_Z));
  Transistor #(.\type ("n")) transistor_374 (.in(1'b0), .out(transistor_374_out), .gate(transistor_360_out));
  Transistor #(.\type ("n")) transistor_375 (.in(transistor_376_out), .out(pull_resistor_186_node), .gate(ALU_FLAG_Z));
  Transistor #(.\type ("n")) transistor_376 (.in(1'b0), .out(transistor_376_out), .gate(READ_FALG));
  Pull_Resistor #(.pull(1)) pull_resistor_187 (.node(FLAG_STORE_N));
  Transistor #(.\type ("n")) transistor_377 (.in(1'b0), .out(FLAG_STORE_N), .gate(transistor_358_out));
  Transistor #(.\type ("n")) transistor_378 (.in(1'b0), .out(FLAG_STORE_Z), .gate(pull_resistor_186_node));
  Pull_Resistor #(.pull(1)) pull_resistor_188 (.node(FLAG_STORE_Z));
  Pull_Resistor #(.pull(1)) pull_resistor_189 (.node(transistor_363_out));
  Pull_Resistor #(.pull(1)) pull_resistor_190 (.node(NEXT_ADR_7));
  Transistor #(.\type ("n")) transistor_379 (.in(1'b0), .out(NEXT_ADR_7), .gate(transistor_363_out));
  Pull_Resistor #(.pull(1)) pull_resistor_191 (.node(pull_resistor_191_node));
  Transistor #(.\type ("n")) transistor_380 (
    .in(transistor_381_out), .out(pull_resistor_191_node), .gate(STORED_ADR_7));
  Transistor #(.\type ("n")) transistor_381 (.in(1'b0), .out(transistor_381_out), .gate(Read_From_stored_Address));
  Transistor #(.\type ("n")) transistor_382 (.in(transistor_383_out), .out(pull_resistor_191_node), .gate(TEMP_ADR_7));
  Transistor #(.\type ("n")) transistor_383 (.in(1'b0), .out(transistor_383_out), .gate(pull_resistor_144_node));
  Transistor #(.\type ("n")) transistor_384 (.in(1'b0), .out(ADR_7), .gate(pull_resistor_191_node));
  Pull_Resistor #(.pull(1)) pull_resistor_192 (.node(ADR_7));
  Clock clock_11 (.out(clock_11_out));
  Transistor #(.\type ("n")) transistor_385 (.in(transistor_387_out), .out(transistor_385_out), .gate(FLAG_U));
  Pull_Resistor #(.pull(1)) pull_resistor_193 (.node(transistor_385_out));
  Pull_Resistor #(.pull(1)) pull_resistor_194 (.node(pull_resistor_194_node));
  Transistor #(.\type ("n")) transistor_386 (.in(transistor_388_out), .out(pull_resistor_194_node), .gate(FLAG_O));
  Transistor #(.\type ("n")) transistor_387 (.in(1'b0), .out(transistor_387_out), .gate(transistor_360_out));
  Transistor #(.\type ("n")) transistor_388 (.in(1'b0), .out(transistor_388_out), .gate(transistor_360_out));
  Transistor #(.\type ("n")) transistor_389 (.in(transistor_392_out), .out(transistor_385_out), .gate(ALU_FLAG_U));
  Transistor #(.\type ("n")) transistor_390 (.in(transistor_391_out), .out(pull_resistor_194_node), .gate(ALU_FLAG_O));
  Transistor #(.\type ("n")) transistor_391 (.in(1'b0), .out(transistor_391_out), .gate(READ_FALG));
  Transistor #(.\type ("n")) transistor_392 (.in(1'b0), .out(transistor_392_out), .gate(READ_FALG));
  Pull_Resistor #(.pull(1)) pull_resistor_195 (.node(FLAG_STORE_U));
  Transistor #(.\type ("n")) transistor_393 (.in(1'b0), .out(FLAG_STORE_U), .gate(transistor_385_out));
  Transistor #(.\type ("n")) transistor_394 (.in(transistor_395_out), .out(transistor_394_out), .gate(ADR___8));
  Pull_Resistor #(.pull(1)) pull_resistor_196 (.node(transistor_394_out));
  Transistor #(.\type ("n")) transistor_395 (.in(1'b0), .out(transistor_395_out), .gate(Store_Address_plus_plus));
  Transistor #(.\type ("n")) transistor_396 (.in(transistor_397_out), .out(transistor_394_out), .gate(TEMP_ADR_8));
  Transistor #(.\type ("n")) transistor_397 (.in(1'b0), .out(transistor_397_out), .gate(transistor_278_out));
  Transistor #(.\type ("n")) transistor_398 (.in(1'b0), .out(NEXT_ADR_8), .gate(transistor_394_out));
  Pull_Resistor #(.pull(1)) pull_resistor_197 (.node(NEXT_ADR_8));
  Pull_Resistor #(.pull(1)) pull_resistor_198 (.node(pull_resistor_198_node));
  Transistor #(.\type ("n")) transistor_399 (
    .in(transistor_400_out), .out(pull_resistor_198_node), .gate(STORED_ADR_8));
  Transistor #(.\type ("n")) transistor_400 (.in(1'b0), .out(transistor_400_out), .gate(Read_From_stored_Address));
  Transistor #(.\type ("n")) transistor_401 (.in(transistor_402_out), .out(pull_resistor_198_node), .gate(TEMP_ADR_8));
  Transistor #(.\type ("n")) transistor_402 (.in(1'b0), .out(transistor_402_out), .gate(pull_resistor_144_node));
  Transistor #(.\type ("n")) transistor_403 (.in(1'b0), .out(ADR_8), .gate(pull_resistor_198_node));
  Pull_Resistor #(.pull(1)) pull_resistor_199 (.node(ADR_8));
  Register #(.trigger("falling")) register_6 (
    .D(Buss), .en(TIME_STEP_0),
    .Q({TEMP_ADR_15, TEMP_ADR_14, TEMP_ADR_13, TEMP_ADR_12, TEMP_ADR_11, TEMP_ADR_10, TEMP_ADR_9, TEMP_ADR_8}),
    .clk(clock_11_out), .clr(in_6));
  Pull_Resistor #(.pull(1)) pull_resistor_200 (.node(pull_resistor_200_node));
  Transistor #(.\type ("n")) transistor_404 (.in(transistor_405_out), .out(pull_resistor_200_node), .gate(FLAG_C));
  Transistor #(.\type ("n")) transistor_405 (.in(1'b0), .out(transistor_405_out), .gate(transistor_360_out));
  Transistor #(.\type ("n")) transistor_406 (.in(transistor_407_out), .out(pull_resistor_200_node), .gate(ALU_FLAG_C));
  Transistor #(.\type ("n")) transistor_407 (.in(1'b0), .out(transistor_407_out), .gate(READ_FALG));
  Pull_Resistor #(.pull(1)) pull_resistor_201 (.node(FLAG_STORE_C));
  Transistor #(.\type ("n")) transistor_408 (.in(1'b0), .out(FLAG_STORE_O), .gate(pull_resistor_194_node));
  Pull_Resistor #(.pull(1)) pull_resistor_202 (.node(FLAG_STORE_O));
  Transistor #(.\type ("n")) transistor_409 (.in(1'b0), .out(FLAG_STORE_C), .gate(pull_resistor_200_node));
  Pull_Resistor #(.pull(1)) pull_resistor_203 (.node(pull_resistor_203_node));
  Transistor #(.\type ("n")) transistor_410 (.in(transistor_411_out), .out(pull_resistor_203_node), .gate(ADR___9));
  Transistor #(.\type ("n")) transistor_411 (.in(1'b0), .out(transistor_411_out), .gate(Store_Address_plus_plus));
  Transistor #(.\type ("n")) transistor_412 (.in(transistor_413_out), .out(pull_resistor_203_node), .gate(TEMP_ADR_9));
  Transistor #(.\type ("n")) transistor_413 (.in(1'b0), .out(transistor_413_out), .gate(transistor_278_out));
  Pull_Resistor #(.pull(1)) pull_resistor_204 (.node(NEXT_ADR_9));
  Transistor #(.\type ("n")) transistor_414 (.in(1'b0), .out(NEXT_ADR_9), .gate(pull_resistor_203_node));
  Pull_Resistor #(.pull(1)) pull_resistor_205 (.node(pull_resistor_205_node));
  Transistor #(.\type ("n")) transistor_415 (
    .in(transistor_416_out), .out(pull_resistor_205_node), .gate(STORED_ADR_9));
  Transistor #(.\type ("n")) transistor_416 (.in(1'b0), .out(transistor_416_out), .gate(Read_From_stored_Address));
  Transistor #(.\type ("n")) transistor_417 (.in(transistor_418_out), .out(pull_resistor_205_node), .gate(TEMP_ADR_9));
  Transistor #(.\type ("n")) transistor_418 (.in(1'b0), .out(transistor_418_out), .gate(pull_resistor_144_node));
  Pull_Resistor #(.pull(1)) pull_resistor_206 (.node(ADR_9));
  Transistor #(.\type ("n")) transistor_419 (.in(1'b0), .out(ADR_9), .gate(pull_resistor_205_node));
  Transistor #(.\type ("n")) transistor_420 (.in(transistor_421_out), .out(transistor_420_out), .gate(ADR___10));
  Pull_Resistor #(.pull(1)) pull_resistor_207 (.node(transistor_420_out));
  Transistor #(.\type ("n")) transistor_421 (.in(1'b0), .out(transistor_421_out), .gate(Store_Address_plus_plus));
  Transistor #(.\type ("n")) transistor_422 (.in(transistor_423_out), .out(transistor_420_out), .gate(TEMP_ADR_10));
  Transistor #(.\type ("n")) transistor_423 (.in(1'b0), .out(transistor_423_out), .gate(transistor_278_out));
  Transistor #(.\type ("n")) transistor_424 (.in(1'b0), .out(NEXT_ADR_10), .gate(transistor_420_out));
  Pull_Resistor #(.pull(1)) pull_resistor_208 (.node(NEXT_ADR_10));
  Pull_Resistor #(.pull(1)) pull_resistor_209 (.node(pull_resistor_209_node));
  Transistor #(.\type ("n")) transistor_425 (
    .in(transistor_426_out), .out(pull_resistor_209_node), .gate(STORED_ADR_10));
  Transistor #(.\type ("n")) transistor_426 (.in(1'b0), .out(transistor_426_out), .gate(Read_From_stored_Address));
  Transistor #(.\type ("n")) transistor_427 (.in(transistor_428_out), .out(pull_resistor_209_node), .gate(TEMP_ADR_10));
  Transistor #(.\type ("n")) transistor_428 (.in(1'b0), .out(transistor_428_out), .gate(pull_resistor_144_node));
  Transistor #(.\type ("n")) transistor_429 (.in(1'b0), .out(ADR_10), .gate(pull_resistor_209_node));
  Pull_Resistor #(.pull(1)) pull_resistor_210 (.node(ADR_10));
  Transistor #(.\type ("n")) transistor_430 (.in(transistor_431_out), .out(transistor_430_out), .gate(ADR___11));
  Pull_Resistor #(.pull(1)) pull_resistor_211 (.node(transistor_430_out));
  Transistor #(.\type ("n")) transistor_431 (.in(1'b0), .out(transistor_431_out), .gate(Store_Address_plus_plus));
  Transistor #(.\type ("n")) transistor_432 (.in(transistor_433_out), .out(transistor_430_out), .gate(TEMP_ADR_11));
  Transistor #(.\type ("n")) transistor_433 (.in(1'b0), .out(transistor_433_out), .gate(transistor_278_out));
  Pull_Resistor #(.pull(1)) pull_resistor_212 (.node(NEXT_ADR_11));
  Transistor #(.\type ("n")) transistor_434 (.in(1'b0), .out(NEXT_ADR_11), .gate(transistor_430_out));
  Pull_Resistor #(.pull(1)) pull_resistor_213 (.node(pull_resistor_213_node));
  Transistor #(.\type ("n")) transistor_435 (
    .in(transistor_436_out), .out(pull_resistor_213_node), .gate(STORED_ADR_11));
  Transistor #(.\type ("n")) transistor_436 (.in(1'b0), .out(transistor_436_out), .gate(Read_From_stored_Address));
  Transistor #(.\type ("n")) transistor_437 (.in(transistor_438_out), .out(pull_resistor_213_node), .gate(TEMP_ADR_11));
  Transistor #(.\type ("n")) transistor_438 (.in(1'b0), .out(transistor_438_out), .gate(pull_resistor_144_node));
  Transistor #(.\type ("n")) transistor_439 (.in(1'b0), .out(ADR_11), .gate(pull_resistor_213_node));
  Pull_Resistor #(.pull(1)) pull_resistor_214 (.node(ADR_11));
  Transistor #(.\type ("n")) transistor_440 (.in(transistor_441_out), .out(transistor_440_out), .gate(ADR___12));
  Pull_Resistor #(.pull(1)) pull_resistor_215 (.node(transistor_440_out));
  Transistor #(.\type ("n")) transistor_441 (.in(1'b0), .out(transistor_441_out), .gate(Store_Address_plus_plus));
  Transistor #(.\type ("n")) transistor_442 (.in(transistor_443_out), .out(transistor_440_out), .gate(TEMP_ADR_12));
  Transistor #(.\type ("n")) transistor_443 (.in(1'b0), .out(transistor_443_out), .gate(transistor_278_out));
  Pull_Resistor #(.pull(1)) pull_resistor_216 (.node(NEXT_ADR_12));
  Transistor #(.\type ("n")) transistor_444 (.in(1'b0), .out(NEXT_ADR_12), .gate(transistor_440_out));
  Pull_Resistor #(.pull(1)) pull_resistor_217 (.node(pull_resistor_217_node));
  Transistor #(.\type ("n")) transistor_445 (
    .in(transistor_446_out), .out(pull_resistor_217_node), .gate(STORED_ADR_12));
  Transistor #(.\type ("n")) transistor_446 (.in(1'b0), .out(transistor_446_out), .gate(Read_From_stored_Address));
  Transistor #(.\type ("n")) transistor_447 (.in(transistor_448_out), .out(pull_resistor_217_node), .gate(TEMP_ADR_12));
  Transistor #(.\type ("n")) transistor_448 (.in(1'b0), .out(transistor_448_out), .gate(pull_resistor_144_node));
  Transistor #(.\type ("n")) transistor_449 (.in(transistor_450_out), .out(transistor_449_out), .gate(ADR___13));
  Pull_Resistor #(.pull(1)) pull_resistor_218 (.node(transistor_449_out));
  Transistor #(.\type ("n")) transistor_450 (.in(1'b0), .out(transistor_450_out), .gate(Store_Address_plus_plus));
  Transistor #(.\type ("n")) transistor_451 (.in(transistor_452_out), .out(transistor_449_out), .gate(TEMP_ADR_13));
  Transistor #(.\type ("n")) transistor_452 (.in(1'b0), .out(transistor_452_out), .gate(transistor_278_out));
  Pull_Resistor #(.pull(1)) pull_resistor_219 (.node(pull_resistor_219_node));
  Transistor #(.\type ("n")) transistor_453 (
    .in(transistor_454_out), .out(pull_resistor_219_node), .gate(STORED_ADR_13));
  Transistor #(.\type ("n")) transistor_454 (.in(1'b0), .out(transistor_454_out), .gate(Read_From_stored_Address));
  Transistor #(.\type ("n")) transistor_455 (.in(transistor_456_out), .out(pull_resistor_219_node), .gate(TEMP_ADR_13));
  Transistor #(.\type ("n")) transistor_456 (.in(1'b0), .out(transistor_456_out), .gate(pull_resistor_144_node));
  Transistor #(.\type ("n")) transistor_457 (.in(1'b0), .out(ADR_12), .gate(pull_resistor_217_node));
  Pull_Resistor #(.pull(1)) pull_resistor_220 (.node(ADR_12));
  Transistor #(.\type ("n")) transistor_458 (.in(transistor_459_out), .out(transistor_458_out), .gate(ADR___14));
  Pull_Resistor #(.pull(1)) pull_resistor_221 (.node(transistor_458_out));
  Transistor #(.\type ("n")) transistor_459 (.in(1'b0), .out(transistor_459_out), .gate(Store_Address_plus_plus));
  Transistor #(.\type ("n")) transistor_460 (.in(transistor_461_out), .out(transistor_458_out), .gate(TEMP_ADR_14));
  Transistor #(.\type ("n")) transistor_461 (.in(1'b0), .out(transistor_461_out), .gate(transistor_278_out));
  Pull_Resistor #(.pull(1)) pull_resistor_222 (.node(NEXT_ADR_13));
  Transistor #(.\type ("n")) transistor_462 (.in(1'b0), .out(NEXT_ADR_13), .gate(transistor_449_out));
  Transistor #(.\type ("n")) transistor_463 (.in(transistor_464_out), .out(transistor_463_out), .gate(STORED_ADR_14));
  Transistor #(.\type ("n")) transistor_464 (.in(1'b0), .out(transistor_464_out), .gate(Read_From_stored_Address));
  Transistor #(.\type ("n")) transistor_465 (.in(transistor_466_out), .out(transistor_463_out), .gate(TEMP_ADR_14));
  Transistor #(.\type ("n")) transistor_466 (.in(1'b0), .out(transistor_466_out), .gate(pull_resistor_144_node));
  Pull_Resistor #(.pull(1)) pull_resistor_223 (.node(ADR_13));
  Transistor #(.\type ("n")) transistor_467 (.in(1'b0), .out(ADR_13), .gate(pull_resistor_219_node));
  Transistor #(.\type ("n")) transistor_468 (.in(transistor_469_out), .out(transistor_468_out), .gate(ADR___15));
  Transistor #(.\type ("n")) transistor_469 (.in(1'b0), .out(transistor_469_out), .gate(Store_Address_plus_plus));
  Transistor #(.\type ("n")) transistor_470 (.in(transistor_471_out), .out(transistor_468_out), .gate(TEMP_ADR_15));
  Transistor #(.\type ("n")) transistor_471 (.in(1'b0), .out(transistor_471_out), .gate(transistor_278_out));
  Pull_Resistor #(.pull(1)) pull_resistor_224 (.node(NEXT_ADR_14));
  Transistor #(.\type ("n")) transistor_472 (.in(1'b0), .out(NEXT_ADR_14), .gate(transistor_458_out));
  Pull_Resistor #(.pull(1)) pull_resistor_225 (.node(transistor_463_out));
  Pull_Resistor #(.pull(1)) pull_resistor_226 (.node(ADR_14));
  Transistor #(.\type ("n")) transistor_473 (.in(1'b0), .out(ADR_14), .gate(transistor_463_out));
  Pull_Resistor #(.pull(1)) pull_resistor_227 (.node(transistor_468_out));
  Pull_Resistor #(.pull(1)) pull_resistor_228 (.node(NEXT_ADR_15));
  Transistor #(.\type ("n")) transistor_474 (.in(1'b0), .out(NEXT_ADR_15), .gate(transistor_468_out));
  Transistor #(.\type ("n")) transistor_475 (.in(transistor_476_out), .out(transistor_475_out), .gate(STORED_ADR_15));
  Pull_Resistor #(.pull(1)) pull_resistor_229 (.node(transistor_475_out));
  Transistor #(.\type ("n")) transistor_476 (.in(1'b0), .out(transistor_476_out), .gate(Read_From_stored_Address));
  Transistor #(.\type ("n")) transistor_477 (.in(transistor_478_out), .out(transistor_475_out), .gate(TEMP_ADR_15));
  Transistor #(.\type ("n")) transistor_478 (.in(1'b0), .out(transistor_478_out), .gate(pull_resistor_144_node));
  Pull_Resistor #(.pull(1)) pull_resistor_230 (.node(ADR_15));
  Transistor #(.\type ("n")) transistor_479 (.in(1'b0), .out(ADR_15), .gate(transistor_475_out));
  Transistor #(.\type ("n")) transistor_480 (.in(1'b0), .out(transistor_480_out), .gate(pull_resistor_233_node));
  Transistor #(.\type ("n")) transistor_481 (.in(1'b0), .out(transistor_480_out), .gate(STORED_ADR_15));
  Transistor #(.\type ("n")) transistor_482 (
    .in(transistor_483_out), .out(transistor_482_out), .gate(pull_resistor_233_node));
  Transistor #(.\type ("n")) transistor_483 (.in(1'b0), .out(transistor_483_out), .gate(STORED_ADR_15));
  Transistor #(.\type ("n")) transistor_484 (.in(1'b0), .out(transistor_484_out), .gate(STORED_ADR_14));
  Transistor #(.\type ("n")) transistor_485 (.in(1'b0), .out(transistor_484_out), .gate(pull_resistor_236_node));
  Transistor #(.\type ("n")) transistor_486 (
    .in(transistor_487_out), .out(transistor_486_out), .gate(pull_resistor_236_node));
  Transistor #(.\type ("n")) transistor_487 (.in(1'b0), .out(transistor_487_out), .gate(STORED_ADR_14));
  Transistor #(.\type ("n")) transistor_488 (.in(1'b0), .out(transistor_488_out), .gate(STORED_ADR_13));
  Transistor #(.\type ("n")) transistor_489 (.in(1'b0), .out(transistor_488_out), .gate(pull_resistor_238_node));
  Transistor #(.\type ("n")) transistor_490 (
    .in(transistor_491_out), .out(transistor_490_out), .gate(pull_resistor_238_node));
  Transistor #(.\type ("n")) transistor_491 (.in(1'b0), .out(transistor_491_out), .gate(STORED_ADR_13));
  Transistor #(.\type ("n")) transistor_492 (.in(1'b0), .out(transistor_492_out), .gate(pull_resistor_239_node));
  Transistor #(.\type ("n")) transistor_493 (.in(1'b0), .out(transistor_492_out), .gate(STORED_ADR_12));
  Transistor #(.\type ("n")) transistor_494 (
    .in(transistor_495_out), .out(transistor_494_out), .gate(pull_resistor_239_node));
  Transistor #(.\type ("n")) transistor_495 (.in(1'b0), .out(transistor_495_out), .gate(STORED_ADR_12));
  Transistor #(.\type ("n")) transistor_496 (.in(1'b0), .out(transistor_496_out), .gate(STORED_ADR_11));
  Transistor #(.\type ("n")) transistor_497 (.in(1'b0), .out(transistor_496_out), .gate(pull_resistor_241_node));
  Transistor #(.\type ("n")) transistor_498 (
    .in(transistor_499_out), .out(transistor_498_out), .gate(pull_resistor_241_node));
  Transistor #(.\type ("n")) transistor_499 (.in(1'b0), .out(transistor_499_out), .gate(STORED_ADR_11));
  Transistor #(.\type ("n")) transistor_500 (.in(1'b0), .out(transistor_500_out), .gate(STORED_ADR_10));
  Transistor #(.\type ("n")) transistor_501 (.in(1'b0), .out(transistor_500_out), .gate(pull_resistor_244_node));
  Transistor #(.\type ("n")) transistor_502 (
    .in(transistor_503_out), .out(transistor_502_out), .gate(pull_resistor_244_node));
  Transistor #(.\type ("n")) transistor_503 (.in(1'b0), .out(transistor_503_out), .gate(STORED_ADR_10));
  Transistor #(.\type ("n")) transistor_504 (.in(1'b0), .out(transistor_504_out), .gate(pull_resistor_246_node));
  Transistor #(.\type ("n")) transistor_505 (.in(1'b0), .out(transistor_504_out), .gate(STORED_ADR_9));
  Transistor #(.\type ("n")) transistor_506 (.in(1'b0), .out(transistor_506_out), .gate(STORED_ADR_9));
  Transistor #(.\type ("n")) transistor_507 (
    .in(transistor_506_out), .out(transistor_507_out), .gate(pull_resistor_246_node));
  Transistor #(.\type ("n")) transistor_508 (.in(1'b0), .out(transistor_508_out), .gate(STORED_ADR_8));
  Transistor #(.\type ("n")) transistor_509 (.in(1'b0), .out(transistor_508_out), .gate(pull_resistor_248_node));
  Transistor #(.\type ("n")) transistor_510 (.in(1'b0), .out(transistor_510_out), .gate(STORED_ADR_8));
  Transistor #(.\type ("n")) transistor_511 (
    .in(transistor_510_out), .out(transistor_511_out), .gate(pull_resistor_248_node));
  Transistor #(.\type ("n")) transistor_512 (.in(1'b0), .out(transistor_512_out), .gate(pull_resistor_250_node));
  Transistor #(.\type ("n")) transistor_513 (.in(1'b0), .out(transistor_512_out), .gate(STORED_ADR_7));
  Transistor #(.\type ("n")) transistor_514 (.in(1'b0), .out(transistor_514_out), .gate(STORED_ADR_7));
  Transistor #(.\type ("n")) transistor_515 (
    .in(transistor_514_out), .out(transistor_515_out), .gate(pull_resistor_250_node));
  Transistor #(.\type ("n")) transistor_516 (.in(1'b0), .out(transistor_516_out), .gate(pull_resistor_251_node));
  Transistor #(.\type ("n")) transistor_517 (.in(1'b0), .out(transistor_516_out), .gate(STORED_ADR_6));
  Transistor #(.\type ("n")) transistor_518 (
    .in(transistor_519_out), .out(transistor_518_out), .gate(pull_resistor_251_node));
  Transistor #(.\type ("n")) transistor_519 (.in(1'b0), .out(transistor_519_out), .gate(STORED_ADR_6));
  Transistor #(.\type ("n")) transistor_520 (.in(1'b0), .out(transistor_520_out), .gate(STORED_ADR_5));
  Transistor #(.\type ("n")) transistor_521 (.in(1'b0), .out(transistor_520_out), .gate(pull_resistor_254_node));
  Transistor #(.\type ("n")) transistor_522 (.in(1'b0), .out(transistor_522_out), .gate(STORED_ADR_5));
  Transistor #(.\type ("n")) transistor_523 (
    .in(transistor_522_out), .out(transistor_523_out), .gate(pull_resistor_254_node));
  Transistor #(.\type ("n")) transistor_524 (.in(1'b0), .out(transistor_524_out), .gate(STORED_ADR_4));
  Transistor #(.\type ("n")) transistor_525 (.in(1'b0), .out(transistor_524_out), .gate(pull_resistor_255_node));
  Transistor #(.\type ("n")) transistor_526 (
    .in(transistor_527_out), .out(transistor_526_out), .gate(pull_resistor_255_node));
  Transistor #(.\type ("n")) transistor_527 (.in(1'b0), .out(transistor_527_out), .gate(STORED_ADR_4));
  Transistor #(.\type ("n")) transistor_528 (.in(1'b0), .out(transistor_528_out), .gate(STORED_ADR_3));
  Transistor #(.\type ("n")) transistor_529 (.in(1'b0), .out(transistor_528_out), .gate(pull_resistor_257_node));
  Transistor #(.\type ("n")) transistor_530 (
    .in(transistor_531_out), .out(transistor_530_out), .gate(pull_resistor_257_node));
  Transistor #(.\type ("n")) transistor_531 (.in(1'b0), .out(transistor_531_out), .gate(STORED_ADR_3));
  Transistor #(.\type ("n")) transistor_532 (.in(1'b0), .out(transistor_532_out), .gate(STORED_ADR_2));
  Transistor #(.\type ("n")) transistor_533 (.in(1'b0), .out(transistor_532_out), .gate(pull_resistor_259_node));
  Transistor #(.\type ("n")) transistor_534 (.in(1'b0), .out(transistor_534_out), .gate(STORED_ADR_2));
  Transistor #(.\type ("n")) transistor_535 (
    .in(transistor_534_out), .out(transistor_535_out), .gate(pull_resistor_259_node));
  Transistor #(.\type ("n")) transistor_536 (.in(1'b0), .out(transistor_536_out), .gate(STORED_ADR_1));
  Transistor #(.\type ("n")) transistor_537 (.in(1'b0), .out(transistor_536_out), .gate(pull_resistor_262_node));
  Transistor #(.\type ("n")) transistor_538 (
    .in(transistor_539_out), .out(transistor_538_out), .gate(pull_resistor_262_node));
  Transistor #(.\type ("n")) transistor_539 (.in(1'b0), .out(transistor_539_out), .gate(STORED_ADR_1));
  Transistor #(.\type ("n")) transistor_540 (.in(1'b0), .out(transistor_540_out), .gate(Read_From_stored_Address));
  Transistor #(.\type ("n")) transistor_541 (.in(1'b0), .out(transistor_540_out), .gate(STORED_ADR_0));
  Transistor #(.\type ("n")) transistor_542 (.in(1'b0), .out(transistor_542_out), .gate(STORED_ADR_0));
  Transistor #(.\type ("n")) transistor_543 (
    .in(transistor_542_out), .out(transistor_543_out), .gate(Read_From_stored_Address));
  Pull_Resistor #(.pull(1)) pull_resistor_231 (.node(transistor_482_out));
  Pull_Resistor #(.pull(1)) pull_resistor_232 (.node(pull_resistor_232_node));
  Transistor #(.\type ("n")) transistor_544 (.in(1'b0), .out(pull_resistor_232_node), .gate(transistor_482_out));
  Pull_Resistor #(.pull(1)) pull_resistor_233 (.node(pull_resistor_233_node));
  Pull_Resistor #(.pull(1)) pull_resistor_234 (.node(transistor_486_out));
  Transistor #(.\type ("n")) transistor_545 (.in(1'b0), .out(pull_resistor_233_node), .gate(transistor_486_out));
  Pull_Resistor #(.pull(1)) pull_resistor_235 (.node(transistor_490_out));
  Pull_Resistor #(.pull(1)) pull_resistor_236 (.node(pull_resistor_236_node));
  Transistor #(.\type ("n")) transistor_546 (.in(1'b0), .out(pull_resistor_236_node), .gate(transistor_490_out));
  Pull_Resistor #(.pull(1)) pull_resistor_237 (.node(transistor_494_out));
  Pull_Resistor #(.pull(1)) pull_resistor_238 (.node(pull_resistor_238_node));
  Transistor #(.\type ("n")) transistor_547 (.in(1'b0), .out(pull_resistor_238_node), .gate(transistor_494_out));
  Pull_Resistor #(.pull(1)) pull_resistor_239 (.node(pull_resistor_239_node));
  Pull_Resistor #(.pull(1)) pull_resistor_240 (.node(transistor_498_out));
  Transistor #(.\type ("n")) transistor_548 (.in(1'b0), .out(pull_resistor_239_node), .gate(transistor_498_out));
  Pull_Resistor #(.pull(1)) pull_resistor_241 (.node(pull_resistor_241_node));
  Pull_Resistor #(.pull(1)) pull_resistor_242 (.node(transistor_502_out));
  Transistor #(.\type ("n")) transistor_549 (.in(1'b0), .out(pull_resistor_241_node), .gate(transistor_502_out));
  Pull_Resistor #(.pull(1)) pull_resistor_243 (.node(transistor_507_out));
  Pull_Resistor #(.pull(1)) pull_resistor_244 (.node(pull_resistor_244_node));
  Transistor #(.\type ("n")) transistor_550 (.in(1'b0), .out(pull_resistor_244_node), .gate(transistor_507_out));
  Pull_Resistor #(.pull(1)) pull_resistor_245 (.node(transistor_511_out));
  Pull_Resistor #(.pull(1)) pull_resistor_246 (.node(pull_resistor_246_node));
  Transistor #(.\type ("n")) transistor_551 (.in(1'b0), .out(pull_resistor_246_node), .gate(transistor_511_out));
  Pull_Resistor #(.pull(1)) pull_resistor_247 (.node(transistor_515_out));
  Pull_Resistor #(.pull(1)) pull_resistor_248 (.node(pull_resistor_248_node));
  Transistor #(.\type ("n")) transistor_552 (.in(1'b0), .out(pull_resistor_248_node), .gate(transistor_515_out));
  Pull_Resistor #(.pull(1)) pull_resistor_249 (.node(transistor_518_out));
  Pull_Resistor #(.pull(1)) pull_resistor_250 (.node(pull_resistor_250_node));
  Transistor #(.\type ("n")) transistor_553 (.in(1'b0), .out(pull_resistor_250_node), .gate(transistor_518_out));
  Pull_Resistor #(.pull(1)) pull_resistor_251 (.node(pull_resistor_251_node));
  Pull_Resistor #(.pull(1)) pull_resistor_252 (.node(transistor_523_out));
  Transistor #(.\type ("n")) transistor_554 (.in(1'b0), .out(pull_resistor_251_node), .gate(transistor_523_out));
  Pull_Resistor #(.pull(1)) pull_resistor_253 (.node(transistor_526_out));
  Pull_Resistor #(.pull(1)) pull_resistor_254 (.node(pull_resistor_254_node));
  Transistor #(.\type ("n")) transistor_555 (.in(1'b0), .out(pull_resistor_254_node), .gate(transistor_526_out));
  Pull_Resistor #(.pull(1)) pull_resistor_255 (.node(pull_resistor_255_node));
  Pull_Resistor #(.pull(1)) pull_resistor_256 (.node(transistor_530_out));
  Transistor #(.\type ("n")) transistor_556 (.in(1'b0), .out(pull_resistor_255_node), .gate(transistor_530_out));
  Pull_Resistor #(.pull(1)) pull_resistor_257 (.node(pull_resistor_257_node));
  Pull_Resistor #(.pull(1)) pull_resistor_258 (.node(transistor_535_out));
  Transistor #(.\type ("n")) transistor_557 (.in(1'b0), .out(pull_resistor_257_node), .gate(transistor_535_out));
  Pull_Resistor #(.pull(1)) pull_resistor_259 (.node(pull_resistor_259_node));
  Pull_Resistor #(.pull(1)) pull_resistor_260 (.node(transistor_538_out));
  Transistor #(.\type ("n")) transistor_558 (.in(1'b0), .out(pull_resistor_259_node), .gate(transistor_538_out));
  Pull_Resistor #(.pull(1)) pull_resistor_261 (.node(transistor_543_out));
  Pull_Resistor #(.pull(1)) pull_resistor_262 (.node(pull_resistor_262_node));
  Transistor #(.\type ("n")) transistor_559 (.in(1'b0), .out(pull_resistor_262_node), .gate(transistor_543_out));
  Transistor #(.\type ("n")) transistor_560 (.in(1'b0), .out(ADR___15), .gate(transistor_480_out));
  Pull_Resistor #(.pull(1)) pull_resistor_263 (.node(transistor_480_out));
  Transistor #(.\type ("n")) transistor_561 (.in(1'b0), .out(ADR___14), .gate(transistor_484_out));
  Pull_Resistor #(.pull(1)) pull_resistor_264 (.node(transistor_484_out));
  Transistor #(.\type ("n")) transistor_562 (.in(1'b0), .out(ADR___13), .gate(transistor_488_out));
  Pull_Resistor #(.pull(1)) pull_resistor_265 (.node(transistor_488_out));
  Transistor #(.\type ("n")) transistor_563 (.in(1'b0), .out(ADR___12), .gate(transistor_492_out));
  Pull_Resistor #(.pull(1)) pull_resistor_266 (.node(transistor_492_out));
  Transistor #(.\type ("n")) transistor_564 (.in(1'b0), .out(ADR___11), .gate(transistor_496_out));
  Pull_Resistor #(.pull(1)) pull_resistor_267 (.node(transistor_496_out));
  Transistor #(.\type ("n")) transistor_565 (.in(1'b0), .out(ADR___10), .gate(transistor_500_out));
  Pull_Resistor #(.pull(1)) pull_resistor_268 (.node(transistor_500_out));
  Transistor #(.\type ("n")) transistor_566 (.in(1'b0), .out(ADR___9), .gate(transistor_504_out));
  Pull_Resistor #(.pull(1)) pull_resistor_269 (.node(transistor_504_out));
  Transistor #(.\type ("n")) transistor_567 (.in(1'b0), .out(ADR___8), .gate(transistor_508_out));
  Pull_Resistor #(.pull(1)) pull_resistor_270 (.node(transistor_508_out));
  Transistor #(.\type ("n")) transistor_568 (.in(1'b0), .out(ADR___7), .gate(transistor_512_out));
  Pull_Resistor #(.pull(1)) pull_resistor_271 (.node(transistor_512_out));
  Transistor #(.\type ("n")) transistor_569 (.in(1'b0), .out(ADR___6), .gate(transistor_516_out));
  Pull_Resistor #(.pull(1)) pull_resistor_272 (.node(transistor_516_out));
  Transistor #(.\type ("n")) transistor_570 (.in(1'b0), .out(ADR___5), .gate(transistor_520_out));
  Pull_Resistor #(.pull(1)) pull_resistor_273 (.node(transistor_520_out));
  Transistor #(.\type ("n")) transistor_571 (.in(1'b0), .out(ADR___4), .gate(transistor_524_out));
  Pull_Resistor #(.pull(1)) pull_resistor_274 (.node(transistor_524_out));
  Transistor #(.\type ("n")) transistor_572 (.in(1'b0), .out(ADR___3), .gate(transistor_528_out));
  Pull_Resistor #(.pull(1)) pull_resistor_275 (.node(transistor_528_out));
  Transistor #(.\type ("n")) transistor_573 (.in(1'b0), .out(ADR___2), .gate(transistor_532_out));
  Pull_Resistor #(.pull(1)) pull_resistor_276 (.node(transistor_532_out));
  Transistor #(.\type ("n")) transistor_574 (.in(1'b0), .out(ADR___1), .gate(transistor_536_out));
  Pull_Resistor #(.pull(1)) pull_resistor_277 (.node(transistor_536_out));
  Transistor #(.\type ("n")) transistor_575 (.in(1'b0), .out(ADR___0), .gate(transistor_540_out));
  Pull_Resistor #(.pull(1)) pull_resistor_278 (.node(transistor_540_out));
  Pull_Resistor #(.pull(1)) pull_resistor_279 (.node(ADR___15));
  Transistor #(.\type ("n")) transistor_576 (.in(1'b0), .out(ADR___15), .gate(pull_resistor_232_node));
  Transistor #(.\type ("n")) transistor_577 (.in(1'b0), .out(ADR___14), .gate(pull_resistor_233_node));
  Pull_Resistor #(.pull(1)) pull_resistor_280 (.node(ADR___14));
  Pull_Resistor #(.pull(1)) pull_resistor_281 (.node(ADR___13));
  Transistor #(.\type ("n")) transistor_578 (.in(1'b0), .out(ADR___13), .gate(pull_resistor_236_node));
  Pull_Resistor #(.pull(1)) pull_resistor_282 (.node(ADR___12));
  Transistor #(.\type ("n")) transistor_579 (.in(1'b0), .out(ADR___12), .gate(pull_resistor_238_node));
  Transistor #(.\type ("n")) transistor_580 (.in(1'b0), .out(ADR___11), .gate(pull_resistor_239_node));
  Pull_Resistor #(.pull(1)) pull_resistor_283 (.node(ADR___11));
  Transistor #(.\type ("n")) transistor_581 (.in(1'b0), .out(ADR___10), .gate(pull_resistor_241_node));
  Pull_Resistor #(.pull(1)) pull_resistor_284 (.node(ADR___10));
  Pull_Resistor #(.pull(1)) pull_resistor_285 (.node(ADR___9));
  Transistor #(.\type ("n")) transistor_582 (.in(1'b0), .out(ADR___9), .gate(pull_resistor_244_node));
  Pull_Resistor #(.pull(1)) pull_resistor_286 (.node(ADR___8));
  Transistor #(.\type ("n")) transistor_583 (.in(1'b0), .out(ADR___8), .gate(pull_resistor_246_node));
  Transistor #(.\type ("n")) transistor_584 (.in(1'b0), .out(ADR___7), .gate(pull_resistor_248_node));
  Pull_Resistor #(.pull(1)) pull_resistor_287 (.node(ADR___7));
  Transistor #(.\type ("n")) transistor_585 (.in(1'b0), .out(ADR___6), .gate(pull_resistor_250_node));
  Pull_Resistor #(.pull(1)) pull_resistor_288 (.node(ADR___6));
  Transistor #(.\type ("n")) transistor_586 (.in(1'b0), .out(ADR___5), .gate(pull_resistor_251_node));
  Pull_Resistor #(.pull(1)) pull_resistor_289 (.node(ADR___5));
  Transistor #(.\type ("n")) transistor_587 (.in(1'b0), .out(ADR___4), .gate(pull_resistor_254_node));
  Pull_Resistor #(.pull(1)) pull_resistor_290 (.node(ADR___4));
  Transistor #(.\type ("n")) transistor_588 (.in(1'b0), .out(ADR___3), .gate(pull_resistor_255_node));
  Pull_Resistor #(.pull(1)) pull_resistor_291 (.node(ADR___3));
  Transistor #(.\type ("n")) transistor_589 (.in(1'b0), .out(ADR___2), .gate(pull_resistor_257_node));
  Pull_Resistor #(.pull(1)) pull_resistor_292 (.node(ADR___2));
  Transistor #(.\type ("n")) transistor_590 (.in(1'b0), .out(ADR___1), .gate(pull_resistor_259_node));
  Pull_Resistor #(.pull(1)) pull_resistor_293 (.node(ADR___1));
  Transistor #(.\type ("n")) transistor_591 (.in(1'b0), .out(ADR___0), .gate(pull_resistor_262_node));
  Pull_Resistor #(.pull(1)) pull_resistor_294 (.node(ADR___0));
  Pull_Resistor #(.pull(1)) pull_resistor_295 (.node(ALU_A[0]));
  Pull_Resistor #(.pull(1)) pull_resistor_296 (.node(ALU_A[1]));
  Pull_Resistor #(.pull(1)) pull_resistor_297 (.node(ALU_A[2]));
  Pull_Resistor #(.pull(1)) pull_resistor_298 (.node(ALU_A[3]));
  Pull_Resistor #(.pull(1)) pull_resistor_299 (.node(ALU_A[4]));
  Pull_Resistor #(.pull(1)) pull_resistor_300 (.node(ALU_A[5]));
  Pull_Resistor #(.pull(1)) pull_resistor_301 (.node(ALU_A[6]));
  Pull_Resistor #(.pull(1)) pull_resistor_302 (.node(ALU_A[7]));
  Pull_Resistor #(.pull(1)) pull_resistor_303 (.node(ALU_B[0]));
  Pull_Resistor #(.pull(1)) pull_resistor_304 (.node(ALU_B[1]));
  Pull_Resistor #(.pull(1)) pull_resistor_305 (.node(ALU_B[2]));
  Pull_Resistor #(.pull(1)) pull_resistor_306 (.node(ALU_B[3]));
  Pull_Resistor #(.pull(1)) pull_resistor_307 (.node(ALU_B[4]));
  Pull_Resistor #(.pull(1)) pull_resistor_308 (.node(ALU_B[5]));
  Pull_Resistor #(.pull(1)) pull_resistor_309 (.node(ALU_B[6]));
  Pull_Resistor #(.pull(1)) pull_resistor_310 (.node(ALU_B[7]));
  Pull_Resistor #(.pull(1)) pull_resistor_311 (.node(pull_resistor_311_node));
  Transistor #(.\type ("n"), .gate("br")) transistor_592 (.in(1'b0), .out(transistor_592_out), .gate(ALU_B[7]));
  Pull_Resistor #(.pull(1)) pull_resistor_312 (.node(transistor_592_out));
  Pull_Resistor #(.pull(1)) pull_resistor_313 (.node(pull_resistor_313_node));
  Transistor #(.\type ("n"), .gate("br")) transistor_593 (.in(1'b0), .out(pull_resistor_313_node), .gate(ALU_A[7]));
  Pull_Resistor #(.pull(1)) pull_resistor_314 (.node(ALU_FLAG_O));
  Transistor #(.\type ("n"), .gate("br")) transistor_594 (.in(1'b0), .out(ALU_FLAG_O), .gate(pull_resistor_315_node));
  Pull_Resistor #(.pull(1)) pull_resistor_315 (.node(pull_resistor_315_node));
  Pull_Resistor #(.pull(1)) pull_resistor_316 (.node(ALU_A[7]));
  Pull_Resistor #(.pull(1)) pull_resistor_317 (.node(ALU_A[6]));
  Transistor #(.\type ("n")) transistor_595 (.in(1'b0), .out(ALU_A[7]), .gate(transistor_725_out));
  Transistor #(.\type ("n")) transistor_596 (.in(1'b0), .out(ALU_A[6]), .gate(transistor_724_out));
  Pull_Resistor #(.pull(1)) pull_resistor_318 (.node(ALU_B[7]));
  Pull_Resistor #(.pull(1)) pull_resistor_319 (.node(ALU_B[6]));
  Transistor #(.\type ("n")) transistor_597 (.in(1'b0), .out(ALU_B[7]), .gate(transistor_779_out));
  Transistor #(.\type ("n")) transistor_598 (.in(1'b0), .out(ALU_B[6]), .gate(transistor_778_out));
  Transistor #(.\type ("n")) transistor_599 (.in(transistor_604_out), .out(pull_resistor_315_node), .gate(ALU_FLAG_N));
  Pull_Resistor #(.pull(1)) pull_resistor_320 (.node(ALU_A[5]));
  Pull_Resistor #(.pull(1)) pull_resistor_321 (.node(ALU_A[4]));
  Transistor #(.\type ("n")) transistor_600 (.in(1'b0), .out(ALU_A[5]), .gate(transistor_722_out));
  Transistor #(.\type ("n")) transistor_601 (.in(1'b0), .out(ALU_A[4]), .gate(transistor_719_out));
  Pull_Resistor #(.pull(1)) pull_resistor_322 (.node(ALU_B[5]));
  Pull_Resistor #(.pull(1)) pull_resistor_323 (.node(ALU_B[4]));
  Transistor #(.\type ("n")) transistor_602 (.in(1'b0), .out(ALU_B[5]), .gate(transistor_777_out));
  Transistor #(.\type ("n")) transistor_603 (.in(1'b0), .out(ALU_B[4]), .gate(transistor_776_out));
  Transistor #(.\type ("n")) transistor_604 (
    .in(transistor_610_out), .out(transistor_604_out), .gate(transistor_592_out));
  Transistor #(.\type ("n")) transistor_605 (
    .in(transistor_611_out), .out(pull_resistor_315_node), .gate(transistor_634_out));
  Pull_Resistor #(.pull(1)) pull_resistor_324 (.node(ALU_A[3]));
  Pull_Resistor #(.pull(1)) pull_resistor_325 (.node(ALU_A[2]));
  Transistor #(.\type ("n")) transistor_606 (.in(1'b0), .out(ALU_A[3]), .gate(transistor_717_out));
  Transistor #(.\type ("n")) transistor_607 (.in(1'b0), .out(ALU_A[2]), .gate(transistor_715_out));
  Pull_Resistor #(.pull(1)) pull_resistor_326 (.node(ALU_B[3]));
  Pull_Resistor #(.pull(1)) pull_resistor_327 (.node(ALU_B[2]));
  Transistor #(.\type ("n")) transistor_608 (.in(1'b0), .out(ALU_B[3]), .gate(transistor_775_out));
  Transistor #(.\type ("n")) transistor_609 (.in(1'b0), .out(ALU_B[2]), .gate(transistor_774_out));
  Transistor #(.\type ("n")) transistor_610 (.in(1'b0), .out(transistor_610_out), .gate(pull_resistor_313_node));
  Transistor #(.\type ("n")) transistor_611 (.in(transistor_612_out), .out(transistor_611_out), .gate(ALU_B[7]));
  Transistor #(.\type ("n")) transistor_612 (.in(1'b0), .out(transistor_612_out), .gate(ALU_A[7]));
  Pull_Resistor #(.pull(1)) pull_resistor_328 (.node(ALU_A[1]));
  Pull_Resistor #(.pull(1)) pull_resistor_329 (.node(ALU_A[0]));
  Transistor #(.\type ("n")) transistor_613 (.in(1'b0), .out(ALU_A[1]), .gate(transistor_714_out));
  Transistor #(.\type ("n")) transistor_614 (.in(1'b0), .out(ALU_A[0]), .gate(transistor_712_out));
  Pull_Resistor #(.pull(1)) pull_resistor_330 (.node(ALU_B[1]));
  Pull_Resistor #(.pull(1)) pull_resistor_331 (.node(ALU_B[0]));
  Transistor #(.\type ("n")) transistor_615 (.in(1'b0), .out(ALU_B[1]), .gate(transistor_773_out));
  Transistor #(.\type ("n")) transistor_616 (.in(1'b0), .out(ALU_B[0]), .gate(transistor_772_out));
  Pull_Resistor #(.pull(1)) pull_resistor_332 (.node(pull_resistor_332_node));
  Transistor #(.\type ("n"), .gate("br")) transistor_617 (
    .in(pull_resistor_338_node), .out(pull_resistor_332_node), .gate(pull_resistor_339_node));
  Transistor #(.\type ("n"), .gate("br")) transistor_618 (
    .in(1'b0), .out(transistor_618_out), .gate(pull_resistor_332_node));
  Transistor #(.\type ("n"), .gate("br")) transistor_619 (
    .in(transistor_618_out), .out(transistor_619_out), .gate(transistor_630_out));
  Pull_Resistor #(.pull(1)) pull_resistor_333 (.node(transistor_619_out));
  Transistor #(.\type ("n"), .gate("br")) transistor_620 (.in(1'b0), .out(transistor_620_out), .gate(Carry_in));
  Pull_Resistor #(.pull(1)) pull_resistor_334 (.node(pull_resistor_334_node));
  Transistor #(.\type ("n"), .gate("br")) transistor_621 (
    .in(transistor_620_out), .out(pull_resistor_334_node), .gate(transistor_631_out));
  Pull_Resistor #(.pull(1)) pull_resistor_335 (.node(pull_resistor_335_node));
  Transistor #(.\type ("n"), .gate("br")) transistor_622 (
    .in(transistor_632_out), .out(pull_resistor_335_node), .gate(pull_resistor_339_node));
  Transistor #(.\type ("n"), .gate("br")) transistor_623 (
    .in(1'b0), .out(transistor_623_out), .gate(pull_resistor_334_node));
  Transistor #(.\type ("n"), .gate("br")) transistor_624 (
    .in(transistor_623_out), .out(transistor_624_out), .gate(pull_resistor_343_node));
  Pull_Resistor #(.pull(1)) pull_resistor_336 (.node(transistor_624_out));
  Pull_Resistor #(.pull(1)) pull_resistor_337 (.node(pull_resistor_337_node));
  Transistor #(.\type ("n"), .gate("br")) transistor_625 (.in(1'b0), .out(pull_resistor_337_node), .gate(ALU_B[0]));
  Transistor #(.\type ("n")) transistor_626 (.in(1'b0), .out(pull_resistor_337_node), .gate(ALU_A[0]));
  Pull_Resistor #(.pull(1)) pull_resistor_338 (.node(pull_resistor_338_node));
  Transistor #(.\type ("n"), .gate("br")) transistor_627 (.in(1'b0), .out(pull_resistor_338_node), .gate(ALU_A[0]));
  Pull_Resistor #(.pull(1)) pull_resistor_339 (.node(pull_resistor_339_node));
  Transistor #(.\type ("n"), .gate("br")) transistor_628 (
    .in(pull_resistor_338_node), .out(pull_resistor_339_node), .gate(ALU_B[0]));
  Transistor #(.\type ("n"), .gate("br")) transistor_629 (
    .in(1'b0), .out(transistor_629_out), .gate(pull_resistor_339_node));
  Pull_Resistor #(.pull(1)) pull_resistor_340 (.node(transistor_629_out));
  Transistor #(.\type ("n"), .gate("br")) transistor_630 (
    .in(transistor_629_out), .out(transistor_630_out), .gate(ALU_B[0]));
  Pull_Resistor #(.pull(1)) pull_resistor_341 (.node(transistor_630_out));
  Transistor #(.\type ("n"), .gate("br")) transistor_631 (
    .in(transistor_620_out), .out(transistor_631_out), .gate(transistor_619_out));
  Pull_Resistor #(.pull(1)) pull_resistor_342 (.node(transistor_631_out));
  Transistor #(.\type ("n"), .gate("br")) transistor_632 (
    .in(1'b0), .out(transistor_632_out), .gate(transistor_631_out));
  Pull_Resistor #(.pull(1)) pull_resistor_343 (.node(pull_resistor_343_node));
  Transistor #(.\type ("n"), .gate("br")) transistor_633 (
    .in(transistor_632_out), .out(pull_resistor_343_node), .gate(transistor_619_out));
  Transistor #(.\type ("n")) transistor_634 (.in(1'b0), .out(transistor_634_out), .gate(ALU_FLAG_N));
  Pull_Resistor #(.pull(1)) pull_resistor_344 (.node(transistor_634_out));
  Transistor #(.\type ("n")) transistor_635 (.in(1'b0), .out(transistor_635_out), .gate(pull_resistor_337_node));
  Pull_Resistor #(.pull(1)) pull_resistor_345 (.node(transistor_635_out));
  Transistor #(.\type ("n"), .gate("br")) transistor_636 (
    .in(transistor_646_out), .out(transistor_636_out), .gate(pull_resistor_353_node));
  Pull_Resistor #(.pull(1)) pull_resistor_346 (.node(transistor_636_out));
  Transistor #(.\type ("n"), .gate("br")) transistor_637 (
    .in(1'b0), .out(transistor_637_out), .gate(transistor_636_out));
  Transistor #(.\type ("n"), .gate("br")) transistor_638 (
    .in(transistor_637_out), .out(transistor_638_out), .gate(pull_resistor_355_node));
  Pull_Resistor #(.pull(1)) pull_resistor_347 (.node(transistor_638_out));
  Transistor #(.\type ("n"), .gate("br")) transistor_639 (
    .in(1'b0), .out(transistor_639_out), .gate(pull_resistor_335_node));
  Transistor #(.\type ("n"), .gate("br")) transistor_640 (
    .in(transistor_639_out), .out(transistor_640_out), .gate(pull_resistor_356_node));
  Pull_Resistor #(.pull(1)) pull_resistor_348 (.node(transistor_640_out));
  Pull_Resistor #(.pull(1)) pull_resistor_349 (.node(pull_resistor_349_node));
  Transistor #(.\type ("n"), .gate("br")) transistor_641 (
    .in(transistor_651_out), .out(pull_resistor_349_node), .gate(pull_resistor_353_node));
  Transistor #(.\type ("n"), .gate("br")) transistor_642 (
    .in(1'b0), .out(transistor_642_out), .gate(transistor_640_out));
  Transistor #(.\type ("n"), .gate("br")) transistor_643 (
    .in(transistor_642_out), .out(transistor_643_out), .gate(pull_resistor_357_node));
  Pull_Resistor #(.pull(1)) pull_resistor_350 (.node(transistor_643_out));
  Transistor #(.\type ("n")) transistor_644 (.in(1'b0), .out(transistor_644_out), .gate(ALU_A[1]));
  Pull_Resistor #(.pull(1)) pull_resistor_351 (.node(transistor_644_out));
  Transistor #(.\type ("n"), .gate("br")) transistor_645 (.in(1'b0), .out(transistor_644_out), .gate(ALU_B[1]));
  Transistor #(.\type ("n"), .gate("br")) transistor_646 (.in(1'b0), .out(transistor_646_out), .gate(ALU_A[1]));
  Pull_Resistor #(.pull(1)) pull_resistor_352 (.node(transistor_646_out));
  Pull_Resistor #(.pull(1)) pull_resistor_353 (.node(pull_resistor_353_node));
  Transistor #(.\type ("n"), .gate("br")) transistor_647 (
    .in(transistor_646_out), .out(pull_resistor_353_node), .gate(ALU_B[1]));
  Transistor #(.\type ("n"), .gate("br")) transistor_648 (
    .in(1'b0), .out(transistor_648_out), .gate(pull_resistor_353_node));
  Pull_Resistor #(.pull(1)) pull_resistor_354 (.node(transistor_648_out));
  Pull_Resistor #(.pull(1)) pull_resistor_355 (.node(pull_resistor_355_node));
  Transistor #(.\type ("n"), .gate("br")) transistor_649 (
    .in(transistor_648_out), .out(pull_resistor_355_node), .gate(ALU_B[1]));
  Pull_Resistor #(.pull(1)) pull_resistor_356 (.node(pull_resistor_356_node));
  Transistor #(.\type ("n"), .gate("br")) transistor_650 (
    .in(transistor_639_out), .out(pull_resistor_356_node), .gate(transistor_638_out));
  Transistor #(.\type ("n"), .gate("br")) transistor_651 (
    .in(1'b0), .out(transistor_651_out), .gate(pull_resistor_356_node));
  Pull_Resistor #(.pull(1)) pull_resistor_357 (.node(pull_resistor_357_node));
  Transistor #(.\type ("n"), .gate("br")) transistor_652 (
    .in(transistor_651_out), .out(pull_resistor_357_node), .gate(transistor_638_out));
  Pull_Resistor #(.pull(1)) pull_resistor_358 (.node(pull_resistor_358_node));
  Transistor #(.\type ("n")) transistor_653 (.in(1'b0), .out(pull_resistor_358_node), .gate(transistor_644_out));
  Transistor #(.\type ("n")) transistor_654 (.in(1'b0), .out(transistor_654_out), .gate(ALU_A[2]));
  Pull_Resistor #(.pull(1)) pull_resistor_359 (.node(pull_resistor_359_node));
  Transistor #(.\type ("n"), .gate("br")) transistor_655 (
    .in(pull_resistor_366_node), .out(pull_resistor_359_node), .gate(transistor_666_out));
  Transistor #(.\type ("n"), .gate("br")) transistor_656 (
    .in(1'b0), .out(transistor_656_out), .gate(pull_resistor_359_node));
  Transistor #(.\type ("n"), .gate("br")) transistor_657 (
    .in(transistor_656_out), .out(transistor_657_out), .gate(pull_resistor_369_node));
  Pull_Resistor #(.pull(1)) pull_resistor_360 (.node(transistor_657_out));
  Transistor #(.\type ("n"), .gate("br")) transistor_658 (
    .in(1'b0), .out(transistor_658_out), .gate(pull_resistor_349_node));
  Pull_Resistor #(.pull(1)) pull_resistor_361 (.node(pull_resistor_361_node));
  Transistor #(.\type ("n"), .gate("br")) transistor_659 (
    .in(transistor_658_out), .out(pull_resistor_361_node), .gate(pull_resistor_370_node));
  Pull_Resistor #(.pull(1)) pull_resistor_362 (.node(pull_resistor_362_node));
  Transistor #(.\type ("n"), .gate("br")) transistor_660 (
    .in(transistor_670_out), .out(pull_resistor_362_node), .gate(transistor_666_out));
  Transistor #(.\type ("n"), .gate("br")) transistor_661 (
    .in(1'b0), .out(transistor_661_out), .gate(pull_resistor_361_node));
  Transistor #(.\type ("n"), .gate("br")) transistor_662 (
    .in(transistor_661_out), .out(transistor_662_out), .gate(pull_resistor_371_node));
  Pull_Resistor #(.pull(1)) pull_resistor_363 (.node(transistor_662_out));
  Transistor #(.\type ("n"), .gate("br")) transistor_663 (.in(1'b0), .out(transistor_654_out), .gate(ALU_B[2]));
  Transistor #(.\type ("n")) transistor_664 (.in(1'b0), .out(transistor_664_out), .gate(transistor_654_out));
  Pull_Resistor #(.pull(1)) pull_resistor_364 (.node(transistor_654_out));
  Pull_Resistor #(.pull(1)) pull_resistor_365 (.node(transistor_664_out));
  Pull_Resistor #(.pull(1)) pull_resistor_366 (.node(pull_resistor_366_node));
  Transistor #(.\type ("n"), .gate("br")) transistor_665 (.in(1'b0), .out(pull_resistor_366_node), .gate(ALU_A[2]));
  Transistor #(.\type ("n"), .gate("br")) transistor_666 (
    .in(pull_resistor_366_node), .out(transistor_666_out), .gate(ALU_B[2]));
  Pull_Resistor #(.pull(1)) pull_resistor_367 (.node(transistor_666_out));
  Transistor #(.\type ("n"), .gate("br")) transistor_667 (
    .in(1'b0), .out(transistor_667_out), .gate(transistor_666_out));
  Pull_Resistor #(.pull(1)) pull_resistor_368 (.node(transistor_667_out));
  Pull_Resistor #(.pull(1)) pull_resistor_369 (.node(pull_resistor_369_node));
  Transistor #(.\type ("n"), .gate("br")) transistor_668 (
    .in(transistor_667_out), .out(pull_resistor_369_node), .gate(ALU_B[2]));
  Pull_Resistor #(.pull(1)) pull_resistor_370 (.node(pull_resistor_370_node));
  Transistor #(.\type ("n"), .gate("br")) transistor_669 (
    .in(transistor_658_out), .out(pull_resistor_370_node), .gate(transistor_657_out));
  Transistor #(.\type ("n"), .gate("br")) transistor_670 (
    .in(1'b0), .out(transistor_670_out), .gate(pull_resistor_370_node));
  Pull_Resistor #(.pull(1)) pull_resistor_371 (.node(pull_resistor_371_node));
  Transistor #(.\type ("n"), .gate("br")) transistor_671 (
    .in(transistor_670_out), .out(pull_resistor_371_node), .gate(transistor_657_out));
  Transistor #(.\type ("n")) transistor_672 (.in(1'b0), .out(ALU_FLAG_Z), .gate(Main_bus[0]));
  Transistor #(.\type ("n")) transistor_673 (.in(1'b0), .out(ALU_FLAG_Z), .gate(Main_bus[1]));
  Pull_Resistor #(.pull(1)) pull_resistor_372 (.node(ALU_FLAG_Z));
  Pull_Resistor #(.pull(1)) pull_resistor_373 (.node(pull_resistor_373_node));
  Transistor #(.\type ("n")) transistor_674 (.in(1'b0), .out(pull_resistor_373_node), .gate(ALU_A[3]));
  Transistor #(.\type ("n"), .gate("br")) transistor_675 (.in(1'b0), .out(pull_resistor_373_node), .gate(ALU_B[3]));
  Transistor #(.\type ("n")) transistor_676 (.in(1'b0), .out(ALU_FLAG_Z), .gate(Main_bus[3]));
  Transistor #(.\type ("n")) transistor_677 (.in(1'b0), .out(ALU_FLAG_Z), .gate(Main_bus[2]));
  Transistor #(.\type ("n")) transistor_678 (.in(1'b0), .out(ALU_FLAG_Z), .gate(Main_bus[4]));
  Transistor #(.\type ("n")) transistor_679 (.in(1'b0), .out(transistor_679_out), .gate(pull_resistor_373_node));
  Pull_Resistor #(.pull(1)) pull_resistor_374 (.node(transistor_679_out));
  Transistor #(.\type ("n"), .gate("br")) transistor_680 (
    .in(transistor_681_out), .out(transistor_680_out), .gate(pull_resistor_377_node));
  Transistor #(.\type ("n"), .gate("br")) transistor_681 (.in(1'b0), .out(transistor_681_out), .gate(ALU_A[3]));
  Pull_Resistor #(.pull(1)) pull_resistor_375 (.node(transistor_681_out));
  Pull_Resistor #(.pull(1)) pull_resistor_376 (.node(transistor_680_out));
  Pull_Resistor #(.pull(1)) pull_resistor_377 (.node(pull_resistor_377_node));
  Transistor #(.\type ("n"), .gate("br")) transistor_682 (
    .in(1'b0), .out(transistor_682_out), .gate(transistor_680_out));
  Transistor #(.\type ("n"), .gate("br")) transistor_683 (
    .in(transistor_681_out), .out(pull_resistor_377_node), .gate(ALU_B[3]));
  Transistor #(.\type ("n"), .gate("br")) transistor_684 (
    .in(1'b0), .out(transistor_684_out), .gate(pull_resistor_377_node));
  Transistor #(.\type ("n"), .gate("br")) transistor_685 (
    .in(transistor_682_out), .out(transistor_685_out), .gate(pull_resistor_380_node));
  Pull_Resistor #(.pull(1)) pull_resistor_378 (.node(transistor_684_out));
  Pull_Resistor #(.pull(1)) pull_resistor_379 (.node(transistor_685_out));
  Transistor #(.\type ("n"), .gate("br")) transistor_686 (
    .in(1'b0), .out(transistor_686_out), .gate(pull_resistor_362_node));
  Pull_Resistor #(.pull(1)) pull_resistor_380 (.node(pull_resistor_380_node));
  Transistor #(.\type ("n"), .gate("br")) transistor_687 (
    .in(transistor_684_out), .out(pull_resistor_380_node), .gate(ALU_B[3]));
  Transistor #(.\type ("n"), .gate("br")) transistor_688 (
    .in(transistor_686_out), .out(transistor_688_out), .gate(transistor_689_out));
  Transistor #(.\type ("n"), .gate("br")) transistor_689 (
    .in(transistor_686_out), .out(transistor_689_out), .gate(transistor_685_out));
  Pull_Resistor #(.pull(1)) pull_resistor_381 (.node(transistor_689_out));
  Pull_Resistor #(.pull(1)) pull_resistor_382 (.node(transistor_688_out));
  Transistor #(.\type ("n"), .gate("br")) transistor_690 (
    .in(1'b0), .out(transistor_690_out), .gate(transistor_689_out));
  Transistor #(.\type ("n"), .gate("br")) transistor_691 (
    .in(transistor_690_out), .out(transistor_691_out), .gate(pull_resistor_377_node));
  Pull_Resistor #(.pull(1)) pull_resistor_383 (.node(transistor_691_out));
  Pull_Resistor #(.pull(1)) pull_resistor_384 (.node(pull_resistor_384_node));
  Transistor #(.\type ("n"), .gate("br")) transistor_692 (
    .in(transistor_690_out), .out(pull_resistor_384_node), .gate(transistor_685_out));
  Transistor #(.\type ("n"), .gate("br")) transistor_693 (
    .in(1'b0), .out(transistor_693_out), .gate(transistor_688_out));
  Pull_Resistor #(.pull(1)) pull_resistor_385 (.node(pull_resistor_385_node));
  Transistor #(.\type ("n"), .gate("br")) transistor_694 (
    .in(transistor_693_out), .out(pull_resistor_385_node), .gate(pull_resistor_384_node));
  Transistor #(.\type ("n")) transistor_695 (.in(1'b0), .out(ALU_FLAG_Z), .gate(Main_bus[6]));
  Transistor #(.\type ("n")) transistor_696 (.in(1'b0), .out(ALU_FLAG_Z), .gate(Main_bus[5]));
  Pull_Resistor #(.pull(1)) pull_resistor_386 (.node(pull_resistor_386_node));
  Transistor #(.\type ("n"), .gate("br")) transistor_697 (.in(1'b0), .out(pull_resistor_386_node), .gate(ALU_B[4]));
  Transistor #(.\type ("n")) transistor_698 (.in(1'b0), .out(pull_resistor_386_node), .gate(ALU_A[4]));
  Transistor #(.\type ("n")) transistor_699 (.in(1'b0), .out(ALU_FLAG_Z), .gate(ALU_FLAG_N));
  Transistor #(.\type ("n")) transistor_700 (.in(1'b0), .out(transistor_700_out), .gate(ALU_A[5]));
  Pull_Resistor #(.pull(1)) pull_resistor_387 (.node(transistor_700_out));
  Transistor #(.\type ("n"), .gate("br")) transistor_701 (.in(1'b0), .out(transistor_700_out), .gate(ALU_B[5]));
  Transistor #(.\type ("n")) transistor_702 (.in(1'b0), .out(transistor_702_out), .gate(pull_resistor_386_node));
  Pull_Resistor #(.pull(1)) pull_resistor_388 (.node(transistor_702_out));
  Pull_Resistor #(.pull(1)) pull_resistor_389 (.node(pull_resistor_389_node));
  Transistor #(.\type ("n"), .gate("br")) transistor_703 (
    .in(pull_resistor_401_node), .out(pull_resistor_389_node), .gate(transistor_729_out));
  Transistor #(.\type ("n"), .gate("br")) transistor_704 (
    .in(1'b0), .out(transistor_704_out), .gate(pull_resistor_389_node));
  Transistor #(.\type ("n"), .gate("br")) transistor_705 (
    .in(transistor_704_out), .out(transistor_705_out), .gate(pull_resistor_404_node));
  Pull_Resistor #(.pull(1)) pull_resistor_390 (.node(transistor_705_out));
  Transistor #(.\type ("n"), .gate("br")) transistor_706 (
    .in(1'b0), .out(transistor_706_out), .gate(transistor_691_out));
  Pull_Resistor #(.pull(1)) pull_resistor_391 (.node(pull_resistor_391_node));
  Transistor #(.\type ("n"), .gate("br")) transistor_707 (
    .in(transistor_706_out), .out(pull_resistor_391_node), .gate(transistor_732_out));
  Pull_Resistor #(.pull(1)) pull_resistor_392 (.node(pull_resistor_392_node));
  Transistor #(.\type ("n"), .gate("br")) transistor_708 (
    .in(transistor_733_out), .out(pull_resistor_392_node), .gate(transistor_729_out));
  Transistor #(.\type ("n"), .gate("br")) transistor_709 (
    .in(1'b0), .out(transistor_709_out), .gate(pull_resistor_391_node));
  Transistor #(.\type ("n"), .gate("br")) transistor_710 (
    .in(transistor_709_out), .out(transistor_710_out), .gate(transistor_734_out));
  Pull_Resistor #(.pull(1)) pull_resistor_393 (.node(transistor_710_out));
  Transistor #(.\type ("n")) transistor_711 (.in(1'b0), .out(transistor_711_out), .gate(A___ALU_A));
  Transistor #(.\type ("n")) transistor_712 (.in(transistor_711_out), .out(transistor_712_out), .gate(register_7_q[0]));
  Transistor #(.\type ("n")) transistor_713 (.in(1'b0), .out(transistor_713_out), .gate(A___ALU_A));
  Transistor #(.\type ("n")) transistor_714 (.in(transistor_713_out), .out(transistor_714_out), .gate(register_7_q[1]));
  Transistor #(.\type ("n")) transistor_715 (.in(transistor_716_out), .out(transistor_715_out), .gate(register_7_q[2]));
  Transistor #(.\type ("n")) transistor_716 (.in(1'b0), .out(transistor_716_out), .gate(A___ALU_A));
  Transistor #(.\type ("n")) transistor_717 (.in(transistor_718_out), .out(transistor_717_out), .gate(register_7_q[3]));
  Transistor #(.\type ("n")) transistor_718 (.in(1'b0), .out(transistor_718_out), .gate(A___ALU_A));
  Transistor #(.\type ("n")) transistor_719 (.in(transistor_720_out), .out(transistor_719_out), .gate(register_7_q[4]));
  Transistor #(.\type ("n")) transistor_720 (.in(1'b0), .out(transistor_720_out), .gate(A___ALU_A));
  Transistor #(.\type ("n")) transistor_721 (.in(1'b0), .out(transistor_721_out), .gate(A___ALU_A));
  Transistor #(.\type ("n")) transistor_722 (.in(transistor_721_out), .out(transistor_722_out), .gate(register_7_q[5]));
  Transistor #(.\type ("n")) transistor_723 (.in(1'b0), .out(transistor_723_out), .gate(A___ALU_A));
  Transistor #(.\type ("n")) transistor_724 (.in(transistor_723_out), .out(transistor_724_out), .gate(register_7_q[6]));
  Transistor #(.\type ("n")) transistor_725 (.in(transistor_726_out), .out(transistor_725_out), .gate(register_7_q[7]));
  Transistor #(.\type ("n")) transistor_726 (.in(1'b0), .out(transistor_726_out), .gate(A___ALU_A));
  Pull_Resistor #(.pull(1)) pull_resistor_394 (.node(transistor_725_out));
  Pull_Resistor #(.pull(1)) pull_resistor_395 (.node(transistor_724_out));
  Pull_Resistor #(.pull(1)) pull_resistor_396 (.node(transistor_722_out));
  Pull_Resistor #(.pull(1)) pull_resistor_397 (.node(transistor_719_out));
  Pull_Resistor #(.pull(1)) pull_resistor_398 (.node(transistor_717_out));
  Pull_Resistor #(.pull(1)) pull_resistor_399 (.node(transistor_715_out));
  Pull_Resistor #(.pull(1)) pull_resistor_400 (.node(pull_resistor_400_node));
  Transistor #(.\type ("n")) transistor_727 (.in(1'b0), .out(pull_resistor_400_node), .gate(transistor_700_out));
  Pull_Resistor #(.pull(1)) pull_resistor_401 (.node(pull_resistor_401_node));
  Transistor #(.\type ("n"), .gate("br")) transistor_728 (.in(1'b0), .out(pull_resistor_401_node), .gate(ALU_A[4]));
  Transistor #(.\type ("n"), .gate("br")) transistor_729 (
    .in(pull_resistor_401_node), .out(transistor_729_out), .gate(ALU_B[4]));
  Pull_Resistor #(.pull(1)) pull_resistor_402 (.node(transistor_729_out));
  Transistor #(.\type ("n"), .gate("br")) transistor_730 (
    .in(1'b0), .out(transistor_730_out), .gate(transistor_729_out));
  Pull_Resistor #(.pull(1)) pull_resistor_403 (.node(transistor_730_out));
  Pull_Resistor #(.pull(1)) pull_resistor_404 (.node(pull_resistor_404_node));
  Transistor #(.\type ("n"), .gate("br")) transistor_731 (
    .in(transistor_730_out), .out(pull_resistor_404_node), .gate(ALU_B[4]));
  Transistor #(.\type ("n"), .gate("br")) transistor_732 (
    .in(transistor_706_out), .out(transistor_732_out), .gate(transistor_705_out));
  Pull_Resistor #(.pull(1)) pull_resistor_405 (.node(transistor_732_out));
  Transistor #(.\type ("n"), .gate("br")) transistor_733 (
    .in(1'b0), .out(transistor_733_out), .gate(transistor_732_out));
  Transistor #(.\type ("n"), .gate("br")) transistor_734 (
    .in(transistor_733_out), .out(transistor_734_out), .gate(transistor_705_out));
  Pull_Resistor #(.pull(1)) pull_resistor_406 (.node(transistor_734_out));
  Register register_7 (.D({ALU_FLAG_N, Main_bus}), .en(READ_A), .Q(register_7_q), .clk(clock_12_out), .clr(in_6));
  Clock clock_12 (.out(clock_12_out));
  Pull_Resistor #(.pull(1)) pull_resistor_407 (.node(transistor_714_out));
  Pull_Resistor #(.pull(1)) pull_resistor_408 (.node(transistor_712_out));
  Pull_Resistor #(.pull(1)) pull_resistor_409 (.node(pull_resistor_409_node));
  Transistor #(.\type ("n")) transistor_735 (.in(1'b0), .out(pull_resistor_409_node), .gate(ALU_A[6]));
  Transistor #(.\type ("n"), .gate("br")) transistor_736 (.in(1'b0), .out(pull_resistor_409_node), .gate(ALU_B[6]));
  Pull_Resistor #(.pull(1)) pull_resistor_410 (.node(pull_resistor_410_node));
  Transistor #(.\type ("n"), .gate("br")) transistor_737 (
    .in(pull_resistor_416_node), .out(pull_resistor_410_node), .gate(pull_resistor_417_node));
  Transistor #(.\type ("n"), .gate("br")) transistor_738 (
    .in(1'b0), .out(transistor_738_out), .gate(pull_resistor_410_node));
  Pull_Resistor #(.pull(1)) pull_resistor_411 (.node(pull_resistor_411_node));
  Transistor #(.\type ("n"), .gate("br")) transistor_739 (
    .in(transistor_738_out), .out(pull_resistor_411_node), .gate(pull_resistor_419_node));
  Transistor #(.\type ("n"), .gate("br")) transistor_740 (
    .in(1'b0), .out(transistor_740_out), .gate(pull_resistor_392_node));
  Pull_Resistor #(.pull(1)) pull_resistor_412 (.node(pull_resistor_412_node));
  Transistor #(.\type ("n"), .gate("br")) transistor_741 (
    .in(transistor_740_out), .out(pull_resistor_412_node), .gate(transistor_750_out));
  Transistor #(.\type ("n"), .gate("br")) transistor_742 (
    .in(transistor_751_out), .out(transistor_742_out), .gate(pull_resistor_417_node));
  Pull_Resistor #(.pull(1)) pull_resistor_413 (.node(transistor_742_out));
  Transistor #(.\type ("n"), .gate("br")) transistor_743 (
    .in(1'b0), .out(transistor_743_out), .gate(pull_resistor_412_node));
  Pull_Resistor #(.pull(1)) pull_resistor_414 (.node(pull_resistor_414_node));
  Transistor #(.\type ("n"), .gate("br")) transistor_744 (
    .in(transistor_743_out), .out(pull_resistor_414_node), .gate(transistor_752_out));
  Pull_Resistor #(.pull(1)) pull_resistor_415 (.node(pull_resistor_415_node));
  Transistor #(.\type ("n")) transistor_745 (.in(1'b0), .out(pull_resistor_415_node), .gate(pull_resistor_409_node));
  Pull_Resistor #(.pull(1)) pull_resistor_416 (.node(pull_resistor_416_node));
  Transistor #(.\type ("n"), .gate("br")) transistor_746 (.in(1'b0), .out(pull_resistor_416_node), .gate(ALU_A[5]));
  Pull_Resistor #(.pull(1)) pull_resistor_417 (.node(pull_resistor_417_node));
  Transistor #(.\type ("n"), .gate("br")) transistor_747 (
    .in(pull_resistor_416_node), .out(pull_resistor_417_node), .gate(ALU_B[5]));
  Pull_Resistor #(.pull(1)) pull_resistor_418 (.node(pull_resistor_418_node));
  Transistor #(.\type ("n"), .gate("br")) transistor_748 (
    .in(1'b0), .out(pull_resistor_418_node), .gate(pull_resistor_417_node));
  Pull_Resistor #(.pull(1)) pull_resistor_419 (.node(pull_resistor_419_node));
  Transistor #(.\type ("n"), .gate("br")) transistor_749 (
    .in(pull_resistor_418_node), .out(pull_resistor_419_node), .gate(ALU_B[5]));
  Transistor #(.\type ("n"), .gate("br")) transistor_750 (
    .in(transistor_740_out), .out(transistor_750_out), .gate(pull_resistor_411_node));
  Pull_Resistor #(.pull(1)) pull_resistor_420 (.node(transistor_750_out));
  Transistor #(.\type ("n"), .gate("br")) transistor_751 (
    .in(1'b0), .out(transistor_751_out), .gate(transistor_750_out));
  Transistor #(.\type ("n"), .gate("br")) transistor_752 (
    .in(transistor_751_out), .out(transistor_752_out), .gate(pull_resistor_411_node));
  Pull_Resistor #(.pull(1)) pull_resistor_421 (.node(transistor_752_out));
  Transistor #(.\type ("n")) transistor_753 (.in(1'b0), .out(transistor_753_out), .gate(A___ALU_B));
  Transistor #(.\type ("n")) transistor_754 (.in(1'b0), .out(transistor_754_out), .gate(A___ALU_B));
  Transistor #(.\type ("n")) transistor_755 (.in(1'b0), .out(transistor_755_out), .gate(A___ALU_B));
  Transistor #(.\type ("n")) transistor_756 (.in(1'b0), .out(transistor_756_out), .gate(A___ALU_B));
  Transistor #(.\type ("n")) transistor_757 (.in(1'b0), .out(transistor_757_out), .gate(A___ALU_B));
  Transistor #(.\type ("n")) transistor_758 (.in(1'b0), .out(transistor_758_out), .gate(A___ALU_B));
  Transistor #(.\type ("n")) transistor_759 (.in(1'b0), .out(transistor_759_out), .gate(A___ALU_B));
  Transistor #(.\type ("n")) transistor_760 (.in(1'b0), .out(transistor_760_out), .gate(A___ALU_B));
  Transistor #(.\type ("n")) transistor_761 (.in(1'b0), .out(transistor_761_out), .gate(transistor_762_out));
  Transistor #(.\type ("n")) transistor_762 (.in(1'b0), .out(transistor_762_out), .gate(ALU_A[7]));
  Pull_Resistor #(.pull(1)) pull_resistor_422 (.node(transistor_762_out));
  Transistor #(.\type ("n"), .gate("br")) transistor_763 (.in(1'b0), .out(transistor_762_out), .gate(ALU_B[7]));
  Pull_Resistor #(.pull(1)) pull_resistor_423 (.node(transistor_761_out));
  Transistor #(.\type ("n"), .gate("br")) transistor_764 (
    .in(transistor_780_out), .out(transistor_764_out), .gate(pull_resistor_438_node));
  Pull_Resistor #(.pull(1)) pull_resistor_424 (.node(transistor_764_out));
  Transistor #(.\type ("n"), .gate("br")) transistor_765 (
    .in(1'b0), .out(transistor_765_out), .gate(transistor_764_out));
  Pull_Resistor #(.pull(1)) pull_resistor_425 (.node(pull_resistor_425_node));
  Transistor #(.\type ("n"), .gate("br")) transistor_766 (
    .in(transistor_765_out), .out(pull_resistor_425_node), .gate(pull_resistor_440_node));
  Transistor #(.\type ("n"), .gate("br")) transistor_767 (
    .in(1'b0), .out(transistor_767_out), .gate(transistor_742_out));
  Pull_Resistor #(.pull(1)) pull_resistor_426 (.node(pull_resistor_426_node));
  Transistor #(.\type ("n"), .gate("br")) transistor_768 (
    .in(transistor_767_out), .out(pull_resistor_426_node), .gate(transistor_784_out));
  Pull_Resistor #(.pull(1)) pull_resistor_427 (.node(pull_resistor_427_node));
  Transistor #(.\type ("n"), .gate("br")) transistor_769 (
    .in(transistor_785_out), .out(pull_resistor_427_node), .gate(pull_resistor_438_node));
  Transistor #(.\type ("n"), .gate("br")) transistor_770 (
    .in(1'b0), .out(transistor_770_out), .gate(pull_resistor_426_node));
  Pull_Resistor #(.pull(1)) pull_resistor_428 (.node(pull_resistor_428_node));
  Transistor #(.\type ("n"), .gate("br")) transistor_771 (
    .in(transistor_770_out), .out(pull_resistor_428_node), .gate(transistor_786_out));
  Transistor #(.\type ("n")) transistor_772 (.in(transistor_753_out), .out(transistor_772_out), .gate(register_7_q[0]));
  Transistor #(.\type ("n")) transistor_773 (.in(transistor_754_out), .out(transistor_773_out), .gate(register_7_q[1]));
  Transistor #(.\type ("n")) transistor_774 (.in(transistor_755_out), .out(transistor_774_out), .gate(register_7_q[2]));
  Transistor #(.\type ("n")) transistor_775 (.in(transistor_756_out), .out(transistor_775_out), .gate(register_7_q[3]));
  Transistor #(.\type ("n")) transistor_776 (.in(transistor_757_out), .out(transistor_776_out), .gate(register_7_q[4]));
  Transistor #(.\type ("n")) transistor_777 (.in(transistor_758_out), .out(transistor_777_out), .gate(register_7_q[5]));
  Transistor #(.\type ("n")) transistor_778 (.in(transistor_759_out), .out(transistor_778_out), .gate(register_7_q[6]));
  Transistor #(.\type ("n")) transistor_779 (.in(transistor_760_out), .out(transistor_779_out), .gate(register_7_q[7]));
  Pull_Resistor #(.pull(1)) pull_resistor_429 (.node(transistor_779_out));
  Pull_Resistor #(.pull(1)) pull_resistor_430 (.node(transistor_778_out));
  Pull_Resistor #(.pull(1)) pull_resistor_431 (.node(transistor_777_out));
  Pull_Resistor #(.pull(1)) pull_resistor_432 (.node(transistor_776_out));
  Pull_Resistor #(.pull(1)) pull_resistor_433 (.node(transistor_775_out));
  Pull_Resistor #(.pull(1)) pull_resistor_434 (.node(transistor_774_out));
  Pull_Resistor #(.pull(1)) pull_resistor_435 (.node(transistor_773_out));
  Pull_Resistor #(.pull(1)) pull_resistor_436 (.node(transistor_772_out));
  Transistor #(.\type ("n"), .gate("br")) transistor_780 (.in(1'b0), .out(transistor_780_out), .gate(ALU_A[6]));
  Pull_Resistor #(.pull(1)) pull_resistor_437 (.node(transistor_780_out));
  Pull_Resistor #(.pull(1)) pull_resistor_438 (.node(pull_resistor_438_node));
  Transistor #(.\type ("n"), .gate("br")) transistor_781 (
    .in(transistor_780_out), .out(pull_resistor_438_node), .gate(ALU_B[6]));
  Pull_Resistor #(.pull(1)) pull_resistor_439 (.node(pull_resistor_439_node));
  Transistor #(.\type ("n"), .gate("br")) transistor_782 (
    .in(1'b0), .out(pull_resistor_439_node), .gate(pull_resistor_438_node));
  Pull_Resistor #(.pull(1)) pull_resistor_440 (.node(pull_resistor_440_node));
  Transistor #(.\type ("n"), .gate("br")) transistor_783 (
    .in(pull_resistor_439_node), .out(pull_resistor_440_node), .gate(ALU_B[6]));
  Transistor #(.\type ("n"), .gate("br")) transistor_784 (
    .in(transistor_767_out), .out(transistor_784_out), .gate(pull_resistor_425_node));
  Pull_Resistor #(.pull(1)) pull_resistor_441 (.node(transistor_784_out));
  Transistor #(.\type ("n"), .gate("br")) transistor_785 (
    .in(1'b0), .out(transistor_785_out), .gate(transistor_784_out));
  Transistor #(.\type ("n"), .gate("br")) transistor_786 (
    .in(transistor_785_out), .out(transistor_786_out), .gate(pull_resistor_425_node));
  Pull_Resistor #(.pull(1)) pull_resistor_442 (.node(transistor_786_out));
  Transistor #(.\type ("n")) transistor_787 (.in(1'b0), .out(transistor_787_out), .gate(B___ALU_A));
  Transistor #(.\type ("n")) transistor_788 (.in(1'b0), .out(transistor_788_out), .gate(B___ALU_A));
  Transistor #(.\type ("n")) transistor_789 (.in(1'b0), .out(transistor_789_out), .gate(B___ALU_A));
  Transistor #(.\type ("n")) transistor_790 (.in(1'b0), .out(transistor_790_out), .gate(B___ALU_A));
  Transistor #(.\type ("n")) transistor_791 (.in(1'b0), .out(transistor_791_out), .gate(B___ALU_A));
  Transistor #(.\type ("n")) transistor_792 (.in(1'b0), .out(transistor_792_out), .gate(B___ALU_A));
  Transistor #(.\type ("n")) transistor_793 (.in(1'b0), .out(transistor_793_out), .gate(B___ALU_A));
  Transistor #(.\type ("n")) transistor_794 (.in(1'b0), .out(transistor_794_out), .gate(B___ALU_A));
  Pull_Resistor #(.pull(1)) pull_resistor_443 (.node(Main_bus[0]));
  Transistor #(.\type ("n")) transistor_795 (.in(transistor_796_out), .out(Main_bus[0]), .gate(transistor_904_out));
  Transistor #(.\type ("n")) transistor_796 (.in(1'b0), .out(transistor_796_out), .gate(pull_resistor_463_node));
  Clock clock_13 (.out(clock_13_out));
  Transistor #(.\type ("n")) transistor_797 (.in(transistor_787_out), .out(transistor_712_out), .gate(register_8_q[0]));
  Transistor #(.\type ("n")) transistor_798 (.in(transistor_788_out), .out(transistor_714_out), .gate(register_8_q[1]));
  Transistor #(.\type ("n")) transistor_799 (.in(transistor_789_out), .out(transistor_715_out), .gate(register_8_q[2]));
  Transistor #(.\type ("n")) transistor_800 (.in(transistor_790_out), .out(transistor_717_out), .gate(register_8_q[3]));
  Transistor #(.\type ("n")) transistor_801 (.in(transistor_791_out), .out(transistor_719_out), .gate(register_8_q[4]));
  Transistor #(.\type ("n")) transistor_802 (.in(transistor_792_out), .out(transistor_722_out), .gate(register_8_q[5]));
  Transistor #(.\type ("n")) transistor_803 (.in(transistor_793_out), .out(transistor_724_out), .gate(register_8_q[6]));
  Transistor #(.\type ("n")) transistor_804 (.in(transistor_794_out), .out(transistor_725_out), .gate(register_8_q[7]));
  Transistor #(.\type ("n")) transistor_805 (.in(1'b0), .out(transistor_779_out), .gate(ALU_B___FF));
  Pull_Resistor #(.pull(1)) pull_resistor_444 (.node(pull_resistor_444_node));
  Transistor #(.\type ("n"), .gate("br")) transistor_806 (.in(1'b0), .out(pull_resistor_444_node), .gate(ALU_A[7]));
  Transistor #(.\type ("n"), .gate("br")) transistor_807 (
    .in(pull_resistor_444_node), .out(transistor_807_out), .gate(transistor_808_out));
  Pull_Resistor #(.pull(1)) pull_resistor_445 (.node(transistor_807_out));
  Transistor #(.\type ("n"), .gate("br")) transistor_808 (
    .in(pull_resistor_444_node), .out(transistor_808_out), .gate(ALU_B[7]));
  Transistor #(.\type ("n"), .gate("br")) transistor_809 (
    .in(1'b0), .out(transistor_809_out), .gate(transistor_807_out));
  Pull_Resistor #(.pull(1)) pull_resistor_446 (.node(transistor_808_out));
  Transistor #(.\type ("n"), .gate("br")) transistor_810 (
    .in(transistor_809_out), .out(transistor_810_out), .gate(pull_resistor_449_node));
  Pull_Resistor #(.pull(1)) pull_resistor_447 (.node(pull_resistor_447_node));
  Pull_Resistor #(.pull(1)) pull_resistor_448 (.node(transistor_810_out));
  Transistor #(.\type ("n"), .gate("br")) transistor_811 (
    .in(1'b0), .out(pull_resistor_447_node), .gate(transistor_808_out));
  Pull_Resistor #(.pull(1)) pull_resistor_449 (.node(pull_resistor_449_node));
  Transistor #(.\type ("n"), .gate("br")) transistor_812 (
    .in(1'b0), .out(transistor_812_out), .gate(pull_resistor_427_node));
  Transistor #(.\type ("n"), .gate("br")) transistor_813 (
    .in(pull_resistor_447_node), .out(pull_resistor_449_node), .gate(ALU_B[7]));
  Pull_Resistor #(.pull(1)) pull_resistor_450 (.node(pull_resistor_450_node));
  Transistor #(.\type ("n"), .gate("br")) transistor_814 (
    .in(transistor_812_out), .out(pull_resistor_450_node), .gate(pull_resistor_451_node));
  Pull_Resistor #(.pull(1)) pull_resistor_451 (.node(pull_resistor_451_node));
  Transistor #(.\type ("n"), .gate("br")) transistor_815 (
    .in(transistor_812_out), .out(pull_resistor_451_node), .gate(transistor_810_out));
  Transistor #(.\type ("n"), .gate("br")) transistor_816 (
    .in(1'b0), .out(transistor_816_out), .gate(pull_resistor_451_node));
  Transistor #(.\type ("n"), .gate("br")) transistor_817 (
    .in(transistor_816_out), .out(transistor_817_out), .gate(transistor_808_out));
  Pull_Resistor #(.pull(1)) pull_resistor_452 (.node(transistor_817_out));
  Transistor #(.\type ("n"), .gate("br")) transistor_818 (
    .in(1'b0), .out(transistor_818_out), .gate(pull_resistor_450_node));
  Pull_Resistor #(.pull(1)) pull_resistor_453 (.node(pull_resistor_453_node));
  Transistor #(.\type ("n"), .gate("br")) transistor_819 (
    .in(transistor_816_out), .out(pull_resistor_453_node), .gate(transistor_810_out));
  Pull_Resistor #(.pull(1)) pull_resistor_454 (.node(pull_resistor_454_node));
  Transistor #(.\type ("n"), .gate("br")) transistor_820 (
    .in(transistor_818_out), .out(pull_resistor_454_node), .gate(pull_resistor_453_node));
  Pull_Resistor #(.pull(1)) pull_resistor_455 (.node(Main_bus[1]));
  Pull_Resistor #(.pull(1)) pull_resistor_456 (.node(Main_bus[2]));
  Pull_Resistor #(.pull(1)) pull_resistor_457 (.node(Main_bus[3]));
  Transistor #(.\type ("n")) transistor_821 (.in(transistor_824_out), .out(Main_bus[1]), .gate(transistor_903_out));
  Transistor #(.\type ("n")) transistor_822 (.in(transistor_826_out), .out(Main_bus[3]), .gate(transistor_927_out));
  Transistor #(.\type ("n")) transistor_823 (.in(transistor_825_out), .out(Main_bus[2]), .gate(transistor_929_out));
  Transistor #(.\type ("n")) transistor_824 (.in(1'b0), .out(transistor_824_out), .gate(pull_resistor_463_node));
  Transistor #(.\type ("n")) transistor_825 (.in(1'b0), .out(transistor_825_out), .gate(pull_resistor_463_node));
  Transistor #(.\type ("n")) transistor_826 (.in(1'b0), .out(transistor_826_out), .gate(pull_resistor_463_node));
  Register register_8 (.D({ALU_FLAG_N, Main_bus}), .en(READ_B), .Q(register_8_q), .clk(clock_13_out), .clr(in_6));
  Transistor #(.\type ("n")) transistor_827 (.in(1'b0), .out(transistor_778_out), .gate(ALU_B___FF));
  Transistor #(.\type ("n")) transistor_828 (.in(1'b0), .out(transistor_776_out), .gate(ALU_B___FF));
  Transistor #(.\type ("n")) transistor_829 (.in(1'b0), .out(transistor_777_out), .gate(ALU_B___FF));
  Pull_Resistor #(.pull(1)) pull_resistor_458 (.node(Main_bus[4]));
  Pull_Resistor #(.pull(1)) pull_resistor_459 (.node(Main_bus[5]));
  Pull_Resistor #(.pull(1)) pull_resistor_460 (.node(Main_bus[6]));
  Transistor #(.\type ("n")) transistor_830 (.in(transistor_834_out), .out(Main_bus[6]), .gate(transistor_980_out));
  Transistor #(.\type ("n")) transistor_831 (.in(transistor_833_out), .out(Main_bus[5]), .gate(transistor_979_out));
  Transistor #(.\type ("n")) transistor_832 (.in(transistor_835_out), .out(Main_bus[4]), .gate(transistor_928_out));
  Transistor #(.\type ("n")) transistor_833 (.in(1'b0), .out(transistor_833_out), .gate(pull_resistor_463_node));
  Transistor #(.\type ("n")) transistor_834 (.in(1'b0), .out(transistor_834_out), .gate(pull_resistor_463_node));
  Transistor #(.\type ("n")) transistor_835 (.in(1'b0), .out(transistor_835_out), .gate(pull_resistor_463_node));
  Transistor #(.\type ("n")) transistor_836 (.in(1'b0), .out(transistor_774_out), .gate(ALU_B___FF));
  Transistor #(.\type ("n")) transistor_837 (.in(1'b0), .out(transistor_773_out), .gate(ALU_B___FF));
  Transistor #(.\type ("n")) transistor_838 (.in(1'b0), .out(transistor_775_out), .gate(ALU_B___FF));
  Pull_Resistor #(.pull(1)) pull_resistor_461 (.node(ALU_FLAG_N));
  Transistor #(.\type ("n")) transistor_839 (.in(transistor_840_out), .out(ALU_FLAG_N), .gate(transistor_1003_out));
  Transistor #(.\type ("n")) transistor_840 (.in(1'b0), .out(transistor_840_out), .gate(pull_resistor_463_node));
  Transistor #(.\type ("n")) transistor_841 (.in(1'b0), .out(transistor_841_out), .gate(B___ALU_B));
  Transistor #(.\type ("n")) transistor_842 (.in(transistor_841_out), .out(transistor_772_out), .gate(register_8_q[0]));
  Transistor #(.\type ("n")) transistor_843 (.in(1'b0), .out(transistor_843_out), .gate(B___ALU_B));
  Transistor #(.\type ("n")) transistor_844 (.in(transistor_843_out), .out(transistor_773_out), .gate(register_8_q[1]));
  Transistor #(.\type ("n")) transistor_845 (.in(transistor_846_out), .out(transistor_774_out), .gate(register_8_q[2]));
  Transistor #(.\type ("n")) transistor_846 (.in(1'b0), .out(transistor_846_out), .gate(B___ALU_B));
  Transistor #(.\type ("n")) transistor_847 (.in(transistor_848_out), .out(transistor_775_out), .gate(register_8_q[3]));
  Transistor #(.\type ("n")) transistor_848 (.in(1'b0), .out(transistor_848_out), .gate(B___ALU_B));
  Transistor #(.\type ("n")) transistor_849 (.in(1'b0), .out(transistor_849_out), .gate(B___ALU_B));
  Transistor #(.\type ("n")) transistor_850 (.in(transistor_849_out), .out(transistor_776_out), .gate(register_8_q[4]));
  Transistor #(.\type ("n")) transistor_851 (.in(transistor_852_out), .out(transistor_777_out), .gate(register_8_q[5]));
  Transistor #(.\type ("n")) transistor_852 (.in(1'b0), .out(transistor_852_out), .gate(B___ALU_B));
  Transistor #(.\type ("n")) transistor_853 (.in(transistor_854_out), .out(transistor_778_out), .gate(register_8_q[6]));
  Transistor #(.\type ("n")) transistor_854 (.in(1'b0), .out(transistor_854_out), .gate(B___ALU_B));
  Transistor #(.\type ("n")) transistor_855 (.in(1'b0), .out(transistor_855_out), .gate(B___ALU_B));
  Transistor #(.\type ("n")) transistor_856 (.in(transistor_855_out), .out(transistor_779_out), .gate(register_8_q[7]));
  Transistor #(.\type ("n")) transistor_857 (.in(1'b0), .out(transistor_772_out), .gate(ALU_B___FF));
  Pull_Resistor #(.pull(1)) pull_resistor_462 (.node(ALU_FLAG_C));
  Transistor #(.\type ("n"), .gate("br")) transistor_858 (.in(1'b0), .out(ALU_FLAG_C), .gate(pull_resistor_465_node));
  Pull_Resistor #(.pull(1)) pull_resistor_463 (.node(pull_resistor_463_node));
  Transistor #(.\type ("n"), .gate("br")) transistor_859 (
    .in(1'b0), .out(pull_resistor_463_node), .gate(pull_resistor_464_node));
  Pull_Resistor #(.pull(1)) pull_resistor_464 (.node(pull_resistor_464_node));
  Transistor #(.\type ("n")) transistor_860 (.in(transistor_861_out), .out(transistor_712_out), .gate(register_9_q[0]));
  Transistor #(.\type ("n")) transistor_861 (.in(1'b0), .out(transistor_861_out), .gate(C___ALU_A));
  Transistor #(.\type ("n")) transistor_862 (.in(1'b0), .out(transistor_862_out), .gate(C___ALU_A));
  Transistor #(.\type ("n")) transistor_863 (.in(transistor_862_out), .out(transistor_714_out), .gate(register_9_q[1]));
  Transistor #(.\type ("n")) transistor_864 (.in(1'b0), .out(transistor_864_out), .gate(C___ALU_A));
  Transistor #(.\type ("n")) transistor_865 (.in(transistor_864_out), .out(transistor_715_out), .gate(register_9_q[2]));
  Transistor #(.\type ("n")) transistor_866 (.in(1'b0), .out(transistor_866_out), .gate(C___ALU_A));
  Transistor #(.\type ("n")) transistor_867 (.in(transistor_866_out), .out(transistor_717_out), .gate(register_9_q[3]));
  Transistor #(.\type ("n")) transistor_868 (.in(transistor_869_out), .out(transistor_719_out), .gate(register_9_q[4]));
  Transistor #(.\type ("n")) transistor_869 (.in(1'b0), .out(transistor_869_out), .gate(C___ALU_A));
  Transistor #(.\type ("n")) transistor_870 (.in(transistor_871_out), .out(transistor_722_out), .gate(register_9_q[5]));
  Transistor #(.\type ("n")) transistor_871 (.in(1'b0), .out(transistor_871_out), .gate(C___ALU_A));
  Transistor #(.\type ("n")) transistor_872 (.in(1'b0), .out(transistor_872_out), .gate(C___ALU_A));
  Transistor #(.\type ("n")) transistor_873 (.in(transistor_872_out), .out(transistor_724_out), .gate(register_9_q[6]));
  Transistor #(.\type ("n")) transistor_874 (.in(transistor_875_out), .out(transistor_725_out), .gate(register_9_q[7]));
  Transistor #(.\type ("n")) transistor_875 (.in(1'b0), .out(transistor_875_out), .gate(C___ALU_A));
  Pull_Resistor #(.pull(1)) pull_resistor_465 (.node(pull_resistor_465_node));
  Transistor #(.\type ("n")) transistor_876 (
    .in(transistor_877_out), .out(pull_resistor_465_node), .gate(transistor_817_out));
  Transistor #(.\type ("n")) transistor_877 (.in(1'b0), .out(transistor_877_out), .gate(ADD));
  Transistor #(.\type ("n")) transistor_878 (.in(1'b0), .out(pull_resistor_464_node), .gate(RS));
  Transistor #(.\type ("n")) transistor_879 (.in(1'b0), .out(pull_resistor_464_node), .gate(OR));
  Transistor #(.\type ("n")) transistor_880 (.in(1'b0), .out(pull_resistor_464_node), .gate(AND));
  Clock clock_14 (.out(clock_14_out));
  Transistor #(.\type ("n")) transistor_881 (.in(1'b0), .out(pull_resistor_464_node), .gate(NOT));
  Transistor #(.\type ("n")) transistor_882 (.in(1'b0), .out(pull_resistor_464_node), .gate(ADD));
  Transistor #(.\type ("n")) transistor_883 (.in(1'b0), .out(pull_resistor_464_node), .gate(XOR));
  Register register_9 (.D({ALU_FLAG_N, Main_bus}), .en(READ_C), .Q(register_9_q), .clk(clock_14_out), .clr(in_6));
  Pull_Resistor #(.pull(1)) pull_resistor_466 (.node(ALU_FLAG_U));
  Transistor #(.\type ("n"), .gate("br")) transistor_884 (.in(1'b0), .out(ALU_FLAG_U), .gate(pull_resistor_467_node));
  Transistor #(.\type ("n")) transistor_885 (.in(1'b0), .out(transistor_885_out), .gate(C___ALU_B));
  Transistor #(.\type ("n")) transistor_886 (.in(1'b0), .out(transistor_886_out), .gate(C___ALU_B));
  Transistor #(.\type ("n")) transistor_887 (.in(1'b0), .out(transistor_887_out), .gate(C___ALU_B));
  Transistor #(.\type ("n")) transistor_888 (.in(1'b0), .out(transistor_888_out), .gate(C___ALU_B));
  Transistor #(.\type ("n")) transistor_889 (.in(1'b0), .out(transistor_889_out), .gate(C___ALU_B));
  Transistor #(.\type ("n")) transistor_890 (.in(1'b0), .out(transistor_890_out), .gate(C___ALU_B));
  Transistor #(.\type ("n")) transistor_891 (.in(1'b0), .out(transistor_891_out), .gate(C___ALU_B));
  Transistor #(.\type ("n")) transistor_892 (.in(1'b0), .out(transistor_892_out), .gate(C___ALU_B));
  Pull_Resistor #(.pull(1)) pull_resistor_467 (.node(pull_resistor_467_node));
  Transistor #(.\type ("n")) transistor_893 (.in(transistor_894_out), .out(pull_resistor_467_node), .gate(ALU_A[0]));
  Transistor #(.\type ("n")) transistor_894 (.in(1'b0), .out(transistor_894_out), .gate(RS));
  Transistor #(.\type ("n")) transistor_895 (.in(transistor_885_out), .out(transistor_772_out), .gate(register_9_q[0]));
  Transistor #(.\type ("n")) transistor_896 (.in(transistor_886_out), .out(transistor_773_out), .gate(register_9_q[1]));
  Transistor #(.\type ("n")) transistor_897 (.in(transistor_887_out), .out(transistor_774_out), .gate(register_9_q[2]));
  Transistor #(.\type ("n")) transistor_898 (.in(transistor_888_out), .out(transistor_775_out), .gate(register_9_q[3]));
  Transistor #(.\type ("n")) transistor_899 (.in(transistor_889_out), .out(transistor_776_out), .gate(register_9_q[4]));
  Transistor #(.\type ("n")) transistor_900 (.in(transistor_890_out), .out(transistor_777_out), .gate(register_9_q[5]));
  Transistor #(.\type ("n")) transistor_901 (.in(transistor_891_out), .out(transistor_778_out), .gate(register_9_q[6]));
  Transistor #(.\type ("n")) transistor_902 (.in(transistor_892_out), .out(transistor_779_out), .gate(register_9_q[7]));
  Transistor #(.\type ("n")) transistor_903 (
    .in(transistor_906_out), .out(transistor_903_out), .gate(pull_resistor_358_node));
  Transistor #(.\type ("n")) transistor_904 (
    .in(transistor_905_out), .out(transistor_904_out), .gate(transistor_635_out));
  Transistor #(.\type ("n")) transistor_905 (.in(1'b0), .out(transistor_905_out), .gate(OR));
  Transistor #(.\type ("n")) transistor_906 (.in(1'b0), .out(transistor_906_out), .gate(OR));
  Transistor #(.\type ("n")) transistor_907 (
    .in(transistor_909_out), .out(transistor_904_out), .gate(transistor_629_out));
  Transistor #(.\type ("n")) transistor_908 (
    .in(transistor_910_out), .out(transistor_903_out), .gate(transistor_648_out));
  Transistor #(.\type ("n")) transistor_909 (.in(1'b0), .out(transistor_909_out), .gate(AND));
  Transistor #(.\type ("n")) transistor_910 (.in(1'b0), .out(transistor_910_out), .gate(AND));
  Transistor #(.\type ("n")) transistor_911 (.in(transistor_913_out), .out(transistor_904_out), .gate(ALU_A[1]));
  Transistor #(.\type ("n")) transistor_912 (.in(transistor_914_out), .out(transistor_903_out), .gate(ALU_A[2]));
  Transistor #(.\type ("n")) transistor_913 (.in(1'b0), .out(transistor_913_out), .gate(RS));
  Transistor #(.\type ("n")) transistor_914 (.in(1'b0), .out(transistor_914_out), .gate(RS));
  Transistor #(.\type ("n")) transistor_915 (
    .in(transistor_918_out), .out(transistor_903_out), .gate(transistor_646_out));
  Transistor #(.\type ("n")) transistor_916 (
    .in(transistor_917_out), .out(transistor_904_out), .gate(pull_resistor_338_node));
  Transistor #(.\type ("n")) transistor_917 (.in(1'b0), .out(transistor_917_out), .gate(NOT));
  Transistor #(.\type ("n")) transistor_918 (.in(1'b0), .out(transistor_918_out), .gate(NOT));
  Transistor #(.\type ("n")) transistor_919 (
    .in(transistor_921_out), .out(transistor_903_out), .gate(transistor_638_out));
  Transistor #(.\type ("n")) transistor_920 (
    .in(transistor_922_out), .out(transistor_904_out), .gate(transistor_619_out));
  Transistor #(.\type ("n")) transistor_921 (.in(1'b0), .out(transistor_921_out), .gate(XOR));
  Transistor #(.\type ("n")) transistor_922 (.in(1'b0), .out(transistor_922_out), .gate(XOR));
  Transistor #(.\type ("n")) transistor_923 (
    .in(transistor_925_out), .out(transistor_904_out), .gate(transistor_624_out));
  Transistor #(.\type ("n")) transistor_924 (
    .in(transistor_926_out), .out(transistor_903_out), .gate(transistor_643_out));
  Transistor #(.\type ("n")) transistor_925 (.in(1'b0), .out(transistor_925_out), .gate(ADD));
  Transistor #(.\type ("n")) transistor_926 (.in(1'b0), .out(transistor_926_out), .gate(ADD));
  Transistor #(.\type ("n")) transistor_927 (
    .in(transistor_932_out), .out(transistor_927_out), .gate(transistor_679_out));
  Transistor #(.\type ("n")) transistor_928 (
    .in(transistor_930_out), .out(transistor_928_out), .gate(transistor_702_out));
  Transistor #(.\type ("n")) transistor_929 (
    .in(transistor_931_out), .out(transistor_929_out), .gate(transistor_664_out));
  Transistor #(.\type ("n")) transistor_930 (.in(1'b0), .out(transistor_930_out), .gate(OR));
  Transistor #(.\type ("n")) transistor_931 (.in(1'b0), .out(transistor_931_out), .gate(OR));
  Transistor #(.\type ("n")) transistor_932 (.in(1'b0), .out(transistor_932_out), .gate(OR));
  Transistor #(.\type ("n")) transistor_933 (
    .in(transistor_938_out), .out(transistor_927_out), .gate(transistor_684_out));
  Transistor #(.\type ("n")) transistor_934 (
    .in(transistor_937_out), .out(transistor_929_out), .gate(transistor_667_out));
  Transistor #(.\type ("n")) transistor_935 (
    .in(transistor_936_out), .out(transistor_928_out), .gate(transistor_730_out));
  Transistor #(.\type ("n")) transistor_936 (.in(1'b0), .out(transistor_936_out), .gate(AND));
  Transistor #(.\type ("n")) transistor_937 (.in(1'b0), .out(transistor_937_out), .gate(AND));
  Transistor #(.\type ("n")) transistor_938 (.in(1'b0), .out(transistor_938_out), .gate(AND));
  Transistor #(.\type ("n")) transistor_939 (.in(transistor_943_out), .out(transistor_928_out), .gate(ALU_A[5]));
  Transistor #(.\type ("n")) transistor_940 (.in(transistor_942_out), .out(transistor_929_out), .gate(ALU_A[3]));
  Transistor #(.\type ("n")) transistor_941 (.in(transistor_944_out), .out(transistor_927_out), .gate(ALU_A[4]));
  Transistor #(.\type ("n")) transistor_942 (.in(1'b0), .out(transistor_942_out), .gate(RS));
  Transistor #(.\type ("n")) transistor_943 (.in(1'b0), .out(transistor_943_out), .gate(RS));
  Transistor #(.\type ("n")) transistor_944 (.in(1'b0), .out(transistor_944_out), .gate(RS));
  Transistor #(.\type ("n")) transistor_945 (
    .in(transistor_948_out), .out(transistor_927_out), .gate(transistor_681_out));
  Transistor #(.\type ("n")) transistor_946 (
    .in(transistor_949_out), .out(transistor_928_out), .gate(pull_resistor_401_node));
  Transistor #(.\type ("n")) transistor_947 (
    .in(transistor_950_out), .out(transistor_929_out), .gate(pull_resistor_366_node));
  Transistor #(.\type ("n")) transistor_948 (.in(1'b0), .out(transistor_948_out), .gate(NOT));
  Transistor #(.\type ("n")) transistor_949 (.in(1'b0), .out(transistor_949_out), .gate(NOT));
  Transistor #(.\type ("n")) transistor_950 (.in(1'b0), .out(transistor_950_out), .gate(NOT));
  Transistor #(.\type ("n")) transistor_951 (
    .in(transistor_954_out), .out(transistor_929_out), .gate(transistor_657_out));
  Transistor #(.\type ("n")) transistor_952 (
    .in(transistor_955_out), .out(transistor_928_out), .gate(transistor_705_out));
  Transistor #(.\type ("n")) transistor_953 (
    .in(transistor_956_out), .out(transistor_927_out), .gate(transistor_685_out));
  Transistor #(.\type ("n")) transistor_954 (.in(1'b0), .out(transistor_954_out), .gate(XOR));
  Transistor #(.\type ("n")) transistor_955 (.in(1'b0), .out(transistor_955_out), .gate(XOR));
  Transistor #(.\type ("n")) transistor_956 (.in(1'b0), .out(transistor_956_out), .gate(XOR));
  Transistor #(.\type ("n")) transistor_957 (
    .in(transistor_960_out), .out(transistor_927_out), .gate(pull_resistor_385_node));
  Transistor #(.\type ("n")) transistor_958 (
    .in(transistor_961_out), .out(transistor_929_out), .gate(transistor_662_out));
  Transistor #(.\type ("n")) transistor_959 (
    .in(transistor_962_out), .out(transistor_928_out), .gate(transistor_710_out));
  Transistor #(.\type ("n")) transistor_960 (.in(1'b0), .out(transistor_960_out), .gate(ADD));
  Transistor #(.\type ("n")) transistor_961 (.in(1'b0), .out(transistor_961_out), .gate(ADD));
  Transistor #(.\type ("n")) transistor_962 (.in(1'b0), .out(transistor_962_out), .gate(ADD));
  Transistor #(.\type ("n")) transistor_963 (.in(1'b0), .out(transistor_963_out), .gate(D___ALU_A));
  Transistor #(.\type ("n")) transistor_964 (
    .in(transistor_963_out), .out(transistor_712_out), .gate(register_10_q[0]));
  Transistor #(.\type ("n")) transistor_965 (
    .in(transistor_966_out), .out(transistor_714_out), .gate(register_10_q[1]));
  Transistor #(.\type ("n")) transistor_966 (.in(1'b0), .out(transistor_966_out), .gate(D___ALU_A));
  Transistor #(.\type ("n")) transistor_967 (.in(1'b0), .out(transistor_967_out), .gate(D___ALU_A));
  Transistor #(.\type ("n")) transistor_968 (
    .in(transistor_967_out), .out(transistor_715_out), .gate(register_10_q[2]));
  Transistor #(.\type ("n")) transistor_969 (.in(1'b0), .out(transistor_969_out), .gate(D___ALU_A));
  Transistor #(.\type ("n")) transistor_970 (
    .in(transistor_969_out), .out(transistor_717_out), .gate(register_10_q[3]));
  Transistor #(.\type ("n")) transistor_971 (
    .in(transistor_972_out), .out(transistor_719_out), .gate(register_10_q[4]));
  Transistor #(.\type ("n")) transistor_972 (.in(1'b0), .out(transistor_972_out), .gate(D___ALU_A));
  Transistor #(.\type ("n")) transistor_973 (
    .in(transistor_974_out), .out(transistor_722_out), .gate(register_10_q[5]));
  Transistor #(.\type ("n")) transistor_974 (.in(1'b0), .out(transistor_974_out), .gate(D___ALU_A));
  Transistor #(.\type ("n")) transistor_975 (.in(1'b0), .out(transistor_975_out), .gate(D___ALU_A));
  Transistor #(.\type ("n")) transistor_976 (
    .in(transistor_975_out), .out(transistor_724_out), .gate(register_10_q[6]));
  Transistor #(.\type ("n")) transistor_977 (
    .in(transistor_978_out), .out(transistor_725_out), .gate(register_10_q[7]));
  Transistor #(.\type ("n")) transistor_978 (.in(1'b0), .out(transistor_978_out), .gate(D___ALU_A));
  Transistor #(.\type ("n")) transistor_979 (
    .in(transistor_982_out), .out(transistor_979_out), .gate(pull_resistor_400_node));
  Transistor #(.\type ("n")) transistor_980 (
    .in(transistor_981_out), .out(transistor_980_out), .gate(pull_resistor_415_node));
  Transistor #(.\type ("n")) transistor_981 (.in(1'b0), .out(transistor_981_out), .gate(OR));
  Transistor #(.\type ("n")) transistor_982 (.in(1'b0), .out(transistor_982_out), .gate(OR));
  Transistor #(.\type ("n")) transistor_983 (
    .in(transistor_985_out), .out(transistor_979_out), .gate(pull_resistor_418_node));
  Transistor #(.\type ("n")) transistor_984 (
    .in(transistor_986_out), .out(transistor_980_out), .gate(pull_resistor_439_node));
  Transistor #(.\type ("n")) transistor_985 (.in(1'b0), .out(transistor_985_out), .gate(AND));
  Transistor #(.\type ("n")) transistor_986 (.in(1'b0), .out(transistor_986_out), .gate(AND));
  Transistor #(.\type ("n")) transistor_987 (.in(transistor_989_out), .out(transistor_980_out), .gate(ALU_A[7]));
  Transistor #(.\type ("n")) transistor_988 (.in(transistor_990_out), .out(transistor_979_out), .gate(ALU_A[6]));
  Transistor #(.\type ("n")) transistor_989 (.in(1'b0), .out(transistor_989_out), .gate(RS));
  Transistor #(.\type ("n")) transistor_990 (.in(1'b0), .out(transistor_990_out), .gate(RS));
  Transistor #(.\type ("n")) transistor_991 (
    .in(transistor_993_out), .out(transistor_979_out), .gate(pull_resistor_416_node));
  Transistor #(.\type ("n")) transistor_992 (
    .in(transistor_994_out), .out(transistor_980_out), .gate(transistor_780_out));
  Transistor #(.\type ("n")) transistor_993 (.in(1'b0), .out(transistor_993_out), .gate(NOT));
  Transistor #(.\type ("n")) transistor_994 (.in(1'b0), .out(transistor_994_out), .gate(NOT));
  Transistor #(.\type ("n")) transistor_995 (
    .in(transistor_997_out), .out(transistor_979_out), .gate(pull_resistor_411_node));
  Transistor #(.\type ("n")) transistor_996 (
    .in(transistor_998_out), .out(transistor_980_out), .gate(pull_resistor_425_node));
  Transistor #(.\type ("n")) transistor_997 (.in(1'b0), .out(transistor_997_out), .gate(XOR));
  Transistor #(.\type ("n")) transistor_998 (.in(1'b0), .out(transistor_998_out), .gate(XOR));
  Transistor #(.\type ("n")) transistor_999 (
    .in(transistor_1002_out), .out(transistor_979_out), .gate(pull_resistor_414_node));
  Transistor #(.\type ("n")) transistor_1000 (
    .in(transistor_1001_out), .out(transistor_980_out), .gate(pull_resistor_428_node));
  Transistor #(.\type ("n")) transistor_1001 (.in(1'b0), .out(transistor_1001_out), .gate(ADD));
  Transistor #(.\type ("n")) transistor_1002 (.in(1'b0), .out(transistor_1002_out), .gate(ADD));
  Register register_10 (.D({ALU_FLAG_N, Main_bus}), .en(READ_D), .Q(register_10_q), .clk(clock_15_out), .clr(in_6));
  Clock clock_15 (.out(clock_15_out));
  Transistor #(.\type ("n")) transistor_1003 (
    .in(transistor_1004_out), .out(transistor_1003_out), .gate(transistor_761_out));
  Transistor #(.\type ("n")) transistor_1004 (.in(1'b0), .out(transistor_1004_out), .gate(OR));
  Transistor #(.\type ("n")) transistor_1005 (
    .in(transistor_1006_out), .out(transistor_1003_out), .gate(pull_resistor_447_node));
  Transistor #(.\type ("n")) transistor_1006 (.in(1'b0), .out(transistor_1006_out), .gate(AND));
  Transistor #(.\type ("n")) transistor_1007 (
    .in(transistor_1008_out), .out(transistor_1003_out), .gate(pull_resistor_444_node));
  Transistor #(.\type ("n")) transistor_1008 (.in(1'b0), .out(transistor_1008_out), .gate(NOT));
  Transistor #(.\type ("n")) transistor_1009 (
    .in(transistor_1010_out), .out(transistor_1003_out), .gate(transistor_810_out));
  Transistor #(.\type ("n")) transistor_1010 (.in(1'b0), .out(transistor_1010_out), .gate(XOR));
  Transistor #(.\type ("n")) transistor_1011 (
    .in(transistor_1012_out), .out(transistor_1003_out), .gate(pull_resistor_454_node));
  Transistor #(.\type ("n")) transistor_1012 (.in(1'b0), .out(transistor_1012_out), .gate(ADD));
  Transistor #(.\type ("n")) transistor_1013 (.in(1'b0), .out(transistor_1013_out), .gate(D___ALU_B));
  Transistor #(.\type ("n")) transistor_1014 (
    .in(transistor_1013_out), .out(transistor_772_out), .gate(register_10_q[0]));
  Transistor #(.\type ("n")) transistor_1015 (
    .in(transistor_1016_out), .out(transistor_773_out), .gate(register_10_q[1]));
  Transistor #(.\type ("n")) transistor_1016 (.in(1'b0), .out(transistor_1016_out), .gate(D___ALU_B));
  Transistor #(.\type ("n")) transistor_1017 (.in(1'b0), .out(transistor_1017_out), .gate(D___ALU_B));
  Transistor #(.\type ("n")) transistor_1018 (
    .in(transistor_1017_out), .out(transistor_774_out), .gate(register_10_q[2]));
  Transistor #(.\type ("n")) transistor_1019 (
    .in(transistor_1020_out), .out(transistor_775_out), .gate(register_10_q[3]));
  Transistor #(.\type ("n")) transistor_1020 (.in(1'b0), .out(transistor_1020_out), .gate(D___ALU_B));
  Transistor #(.\type ("n")) transistor_1021 (
    .in(transistor_1022_out), .out(transistor_776_out), .gate(register_10_q[4]));
  Transistor #(.\type ("n")) transistor_1022 (.in(1'b0), .out(transistor_1022_out), .gate(D___ALU_B));
  Transistor #(.\type ("n")) transistor_1023 (.in(1'b0), .out(transistor_1023_out), .gate(D___ALU_B));
  Transistor #(.\type ("n")) transistor_1024 (
    .in(transistor_1023_out), .out(transistor_777_out), .gate(register_10_q[5]));
  Transistor #(.\type ("n")) transistor_1025 (
    .in(transistor_1026_out), .out(transistor_778_out), .gate(register_10_q[6]));
  Transistor #(.\type ("n")) transistor_1026 (.in(1'b0), .out(transistor_1026_out), .gate(D___ALU_B));
  Transistor #(.\type ("n")) transistor_1027 (.in(1'b0), .out(transistor_1027_out), .gate(D___ALU_B));
  Transistor #(.\type ("n")) transistor_1028 (
    .in(transistor_1027_out), .out(transistor_779_out), .gate(register_10_q[7]));
  Pull_Resistor #(.pull(1)) pull_resistor_468 (.node(transistor_979_out));
  Pull_Resistor #(.pull(1)) pull_resistor_469 (.node(transistor_928_out));
  Pull_Resistor #(.pull(1)) pull_resistor_470 (.node(transistor_904_out));
  Pull_Resistor #(.pull(1)) pull_resistor_471 (.node(transistor_980_out));
  Pull_Resistor #(.pull(1)) pull_resistor_472 (.node(transistor_927_out));
  Pull_Resistor #(.pull(1)) pull_resistor_473 (.node(transistor_903_out));
  Pull_Resistor #(.pull(1)) pull_resistor_474 (.node(transistor_929_out));
  Pull_Resistor #(.pull(1)) pull_resistor_475 (.node(transistor_1003_out));

  // Other names for the same wires on the sheet: ADR_out[15:0] = {ADR_15, ADR_14, ADR_13, ADR_12, ADR_11, ADR_10, ADR_9, ADR_8, ADR_7, ADR_6, ADR_5, ADR_4, ADR_3, ADR_2, ADR_1, ADR_0};
  //   Main_bus_0 = Main_bus[0]; Main_bus_1 = Main_bus[1]; Main_bus_2 = Main_bus[2]; Main_bus_3 = Main_bus[3];
  //   Main_bus_4 = Main_bus[4]; Main_bus_5 = Main_bus[5]; Main_bus_6 = Main_bus[6]; Main_bus[7] = ALU_FLAG_N;
  //   Main_bus_7 = ALU_FLAG_N; rst = in_6

  // Notes on the sheet:
  //   contents of rom_1 (hex, n*v repeats v):
  //   0 14 0 1b 15 0 1c 54 18 0 1a 0 2 0 b 2 0 0 0 2 0 12 5*0 a 37
endmodule
